// Logisim project 实验一先行进位电路.circ as structural Verilog: 2 circuits, main circuit main
module main (
  input  A3,
  input  B3,
  input  A2,
  input  B2,
  input  A1,
  input  B1,
  input  A0,
  input  B0,
  input  C0,
  output Co,
  output S3,
  output S2,
  output S1,
  output S0
);

  wire and_1_out, and_2_out, and_3_out, and_4_out, and_5_out, and_6_out, and_7_out, and_8_out, and_9_out,
       and_10_out, and_11_out, and_12_out, and_13_out, and_14_out, xor_1_out, xor_2_out, xor_3_out,
       xor_4_out, xor_6_out, xor_7_out, xor_8_out;

  and and_1 (and_1_out, A3, B3);
  and and_2 (and_2_out, A2, B2);
  and and_3 (and_3_out, A1, B1);
  and and_4 (and_4_out, A0, B0);
  xor xor_1 (xor_1_out, A3, B3);
  xor xor_2 (xor_2_out, A2, B2);
  xor xor_3 (xor_3_out, A1, B1);
  xor xor_4 (xor_4_out, A0, B0);
  and and_5 (and_5_out, xor_1_out, and_2_out);
  and and_6 (and_6_out, xor_1_out, and_3_out, xor_2_out);
  and and_7 (and_7_out, xor_1_out, xor_2_out, and_4_out, xor_3_out);
  and and_8 (and_8_out, xor_1_out, xor_2_out, xor_3_out, xor_4_out, C0);
  and and_9 (and_9_out, xor_2_out, and_3_out);
  and and_10 (and_10_out, and_4_out, xor_2_out, xor_3_out);
  and and_11 (and_11_out, xor_3_out, xor_4_out, C0, xor_2_out);
  and and_12 (and_12_out, and_4_out, xor_3_out);
  and and_13 (and_13_out, xor_4_out, xor_3_out, C0);
  and and_14 (and_14_out, xor_4_out, C0);
  ExactlyOne xor_5 (.out(Co), .in0(and_1_out), .in1(and_5_out), .in2(and_6_out), .in3(and_7_out), .in4(and_8_out));
  ExactlyOne xor_6 (.out(xor_6_out), .in0(and_2_out), .in1(and_9_out), .in2(and_10_out), .in3(and_11_out));
  ExactlyOne xor_7 (.out(xor_7_out), .in0(and_12_out), .in1(and_3_out), .in2(and_13_out));
  xor xor_8 (xor_8_out, and_4_out, and_14_out);
  xor xor_9 (S3, xor_1_out, xor_6_out);
  xor xor_10 (S2, xor_2_out, xor_7_out);
  xor xor_11 (S1, xor_3_out, xor_8_out);
  xor xor_12 (S0, xor_4_out, C0);
endmodule

module \四位二进制并行加法器  (
  input  in_1,
  input  in_2,
  input  in_3,
  input  in_4,
  input  in_5,
  input  in_6,
  input  in_7,
  input  in_8,
  input  in_9,
  output out_10,
  output out_11,
  output out_12,
  output out_13,
  output out_14
);

  main main_1 (
    .A3(in_2), .B3(in_6), .A2(in_3), .B2(in_7), .A1(in_4), .B1(in_8), .A0(in_5), .B0(in_9), .C0(in_1),
    .Co(out_14), .S3(out_10), .S2(out_11), .S1(out_12), .S0(out_13));
endmodule
