// Logisim project 四位二进制转8421码.circ as structural Verilog: 2 circuits, main circuit main
module main (
  input  A3,
  input  A2,
  input  A1,
  input  A0,
  output S80,
  output S40,
  output S20,
  output S10,
  output S8,
  output S4,
  output S2,
  output S1
);

  wire and_1_out, or_1_out;

  \实验一先行进位电路_main  main_1 (
    .A3(A3), .B3(1'b0), .A2(A2), .B2(and_1_out), .A1(A1), .B1(and_1_out), .A0(A0), .B0(1'b0), .C0(1'b0),
    .Co(S10), .S3(S8), .S2(S4), .S1(S2), .S0(S1));
  and and_1 (and_1_out, A3, or_1_out);
  or or_1 (or_1_out, A1, A2);

  assign S20 = 1'b0;
  assign S40 = 1'b0;
  assign S80 = 1'b0;
endmodule

module \四位二进制转8421码  (
  input  in_1,
  input  in_2,
  input  in_3,
  input  in_4,
  output out_5,
  output out_6,
  output out_7,
  output out_8,
  output out_9,
  output out_10,
  output out_11,
  output out_12
);

  main main_1 (
    .S80(out_5), .S40(out_6), .S20(out_7), .S10(out_8), .S8(out_9), .S4(out_10), .S2(out_11), .S1(out_12),
    .A3(in_1), .A2(in_2), .A1(in_3), .A0(in_4));

  // Notes on the sheet:
  //   十位
  //   个位
endmodule
