// Logisim project 报警电路.circ as structural Verilog: 2 circuits, main circuit main
module main (
  input  U,
  input  CLR,
  input  D,
  output out_4,
  output out_5,
  output out_6,
  output out_7,
  output out_8
);

  wire and_2_out, and_3_out, and_4_out, not_1_out, or_1_out;

  and and_1 (out_8, U, and_2_out);
  not not_1 (not_1_out, and_2_out);
  or or_1 (or_1_out, out_4, out_5, out_6, out_7);
  and and_2 (and_2_out, out_4, out_5, out_6, out_7);
  and and_3 (and_3_out, not_1_out, U);
  and and_4 (and_4_out, or_1_out, D);
  \四位二进制可逆计数器_main  main_1 (
    .A0(out_7), .A2(out_6), .A3(out_5), .A4(out_4), .CPd(and_4_out), .CPu(and_3_out), .CLR(CLR));
endmodule

module \报警电路  (
  input  in_1,
  input  in_2,
  input  in_3,
  output out_4,
  output out_5,
  output out_6,
  output out_7
);

  wire main_1_out_8;

  LED led_1 (.in(main_1_out_8));
  main main_1 (
    .U(in_1), .CLR(in_2), .D(in_3), .out_4(out_4), .out_5(out_5), .out_6(out_6), .out_7(out_7),
    .out_8(main_1_out_8));
endmodule
