// Logisim project 4X4除法器设计.circ as structural Verilog: 4 circuits, main circuit main
module main (
  input  [3:0] \被除数 ,
  input  [3:0] \除数 ,
  output [3:0] \商 ,
  output [3:0] \余 
);

  wire comparator_1_lt, comparator_2_lt, comparator_3_lt, comparator_4_lt, not_1_out, not_2_out, not_3_out,
       not_4_out;
  wire [3:0] adder_2_out, bit_extender_2_out, bit_extender_3_out, bit_extender_4_out, bit_extender_5_out,
       subtractor_1_out, subtractor_2_out, subtractor_3_out, subtractor_4_out;
  wire [7:0] adder_1_out, adder_3_out, bit_extender_1_out, shifter_1_out, shifter_2_out, shifter_3_out,
       shifter_4_out;
  wire [7:4] multiplexer_2_out;

  assign bit_extender_1_out = {{4{1'b0}}, \被除数 };  // Bit_Extender bit_extender_1
  Shifter shifter_1 (.in(bit_extender_1_out), .\dist (3'b001), .out(shifter_1_out));
  Shifter shifter_2 (.in(adder_1_out), .\dist (3'b001), .out(shifter_2_out));
  Shifter shifter_3 (.in({multiplexer_2_out, adder_2_out}), .\dist (3'b001), .out(shifter_3_out));
  Shifter shifter_4 (.in(adder_3_out), .\dist (3'b001), .out(shifter_4_out));
  Comparator #(.width(4)) comparator_1 (.a(shifter_1_out[7:4]), .b(\除数 ), .lt(comparator_1_lt));  // open: gt, eq
  Subtractor #(.width(4)) subtractor_1 (.a(shifter_1_out[7:4]), .b(\除数 ), .out(subtractor_1_out));  // open: bin, bout
  Comparator #(.width(4)) comparator_2 (.a(shifter_2_out[7:4]), .b(\除数 ), .lt(comparator_2_lt));  // open: gt, eq
  Subtractor #(.width(4)) subtractor_2 (.a(shifter_2_out[7:4]), .b(\除数 ), .out(subtractor_2_out));  // open: bin, bout
  Comparator #(.width(4)) comparator_3 (.a(shifter_3_out[7:4]), .b(\除数 ), .lt(comparator_3_lt));  // open: gt, eq
  Subtractor #(.width(4)) subtractor_3 (.a(shifter_3_out[7:4]), .b(\除数 ), .out(subtractor_3_out));  // open: bin, bout
  Comparator #(.width(4)) comparator_4 (.a(shifter_4_out[7:4]), .b(\除数 ), .lt(comparator_4_lt));  // open: gt, eq
  Subtractor #(.width(4)) subtractor_4 (.a(shifter_4_out[7:4]), .b(\除数 ), .out(subtractor_4_out));  // open: bin, bout
  Multiplexer #(.width(4), .enable("false")) multiplexer_1 (
    .in0(subtractor_1_out), .in1(shifter_1_out[7:4]), .out(adder_1_out[7:4]), .sel(comparator_1_lt));
  Multiplexer #(.width(4), .enable("false")) multiplexer_2 (
    .in0(subtractor_2_out), .in1(shifter_2_out[7:4]), .out(multiplexer_2_out), .sel(comparator_2_lt));
  Multiplexer #(.width(4), .enable("false")) multiplexer_3 (
    .in0(subtractor_3_out), .in1(shifter_3_out[7:4]), .out(adder_3_out[7:4]), .sel(comparator_3_lt));
  Multiplexer #(.width(4), .enable("false")) multiplexer_4 (
    .in0(subtractor_4_out), .in1(shifter_4_out[7:4]), .out(\余 ), .sel(comparator_4_lt));
  not not_1 (not_1_out, comparator_1_lt);
  not not_2 (not_2_out, comparator_2_lt);
  assign bit_extender_2_out = {{3{1'b0}}, not_1_out};  // Bit_Extender bit_extender_2
  assign bit_extender_3_out = {{3{1'b0}}, not_2_out};  // Bit_Extender bit_extender_3
  not not_3 (not_3_out, comparator_3_lt);
  assign bit_extender_4_out = {{3{1'b0}}, not_3_out};  // Bit_Extender bit_extender_4
  not not_4 (not_4_out, comparator_4_lt);
  assign bit_extender_5_out = {{3{1'b0}}, not_4_out};  // Bit_Extender bit_extender_5
  Adder #(.width(4)) adder_1 (
    .a(shifter_1_out[3:0]), .b(bit_extender_2_out), .out(adder_1_out[3:0]));  // open: cin, cout
  Adder #(.width(4)) adder_2 (.a(shifter_2_out[3:0]), .b(bit_extender_3_out), .out(adder_2_out));  // open: cin, cout
  Adder #(.width(4)) adder_3 (
    .a(shifter_3_out[3:0]), .b(bit_extender_4_out), .out(adder_3_out[3:0]));  // open: cin, cout
  Adder #(.width(4)) adder_4 (.a(shifter_4_out[3:0]), .b(bit_extender_5_out), .out(\商 ));  // open: cin, cout
endmodule

module \_4X4除法器  (
  input  [3:0] in_1,
  input  [3:0] in_2,
  input  [31:0] in_3,
  input  [31:0] in_4,
  output [3:0] out_5,
  output [3:0] out_6,
  output [31:0] out_7,
  output [31:0] out_8
);

  main main_1 (.\被除数 (in_1), .\余 (out_6), .\除数 (in_2), .\商 (out_5));
  \_32X32除法器  \u_32x32除法器_1  (.\被除数 (in_3), .\除数 (in_4), .\商 (out_7), .\余数 (out_8));
endmodule

module \_32X32除法器  (
  input  [31:0] \被除数 ,
  input  [31:0] \除数 ,
  output [31:0] \商 ,
  output [31:0] \余数 
);

  wire [31:0] \n32x32除法器单元_1_out_4 , \n32x32除法器单元_1_out_5 , \n32x32除法器单元_2_out_4 , \n32x32除法器单元_2_out_5 ,
       \n32x32除法器单元_3_out_4 , \n32x32除法器单元_3_out_5 , \n32x32除法器单元_4_out_4 , \n32x32除法器单元_4_out_5 ,
       \n32x32除法器单元_5_out_4 , \n32x32除法器单元_5_out_5 , \n32x32除法器单元_6_out_4 , \n32x32除法器单元_6_out_5 ,
       \n32x32除法器单元_7_out_4 , \n32x32除法器单元_7_out_5 , \n32x32除法器单元_8_out_4 , \n32x32除法器单元_8_out_5 ,
       \n32x32除法器单元_9_out_4 , \n32x32除法器单元_9_out_5 , \n32x32除法器单元_10_out_4 , \n32x32除法器单元_10_out_5 ,
       \n32x32除法器单元_11_out_4 , \n32x32除法器单元_11_out_5 , \n32x32除法器单元_13_out_4 , \n32x32除法器单元_13_out_5 ,
       \n32x32除法器单元_14_out_4 , \n32x32除法器单元_14_out_5 , \n32x32除法器单元_15_out_4 , \n32x32除法器单元_15_out_5 ,
       \n32x32除法器单元_16_out_4 , \n32x32除法器单元_16_out_5 , \n32x32除法器单元_17_out_4 , \n32x32除法器单元_17_out_5 ,
       \n32x32除法器单元_18_out_4 , \n32x32除法器单元_18_out_5 , \n32x32除法器单元_19_out_4 , \n32x32除法器单元_19_out_5 ,
       \n32x32除法器单元_20_out_4 , \n32x32除法器单元_20_out_5 , \n32x32除法器单元_21_out_4 , \n32x32除法器单元_21_out_5 ,
       \n32x32除法器单元_22_out_4 , \n32x32除法器单元_22_out_5 , \n32x32除法器单元_23_out_4 , \n32x32除法器单元_23_out_5 ,
       \n32x32除法器单元_24_out_4 , \n32x32除法器单元_24_out_5 , \n32x32除法器单元_25_out_4 , \n32x32除法器单元_25_out_5 ,
       \n32x32除法器单元_26_out_4 , \n32x32除法器单元_26_out_5 , \n32x32除法器单元_27_out_4 , \n32x32除法器单元_27_out_5 ,
       \n32x32除法器单元_28_out_4 , \n32x32除法器单元_28_out_5 , \n32x32除法器单元_29_out_4 , \n32x32除法器单元_29_out_5 ,
       \n32x32除法器单元_30_out_4 , \n32x32除法器单元_30_out_5 , \n32x32除法器单元_31_out_4 , \n32x32除法器单元_31_out_5 ,
       \n32x32除法器单元_32_out_4 , \n32x32除法器单元_32_out_5 ;

  \_32X32除法器单元  \u_32x32除法器单元_1  (
    .\被除数 (\被除数 ), .\除数 (\除数 ), .\加数 ({32{1'b0}}), .out_4(\n32x32除法器单元_1_out_4 ),
    .out_5(\n32x32除法器单元_1_out_5 ));
  \_32X32除法器单元  \u_32x32除法器单元_2  (
    .\被除数 (\n32x32除法器单元_28_out_4 ), .\除数 (\除数 ), .\加数 (\n32x32除法器单元_28_out_5 ),
    .out_4(\n32x32除法器单元_2_out_4 ), .out_5(\n32x32除法器单元_2_out_5 ));
  \_32X32除法器单元  \u_32x32除法器单元_3  (
    .\被除数 (\n32x32除法器单元_29_out_4 ), .\除数 (\除数 ), .\加数 (\n32x32除法器单元_29_out_5 ),
    .out_4(\n32x32除法器单元_3_out_4 ), .out_5(\n32x32除法器单元_3_out_5 ));
  \_32X32除法器单元  \u_32x32除法器单元_4  (
    .\被除数 (\n32x32除法器单元_30_out_4 ), .\除数 (\除数 ), .\加数 (\n32x32除法器单元_30_out_5 ),
    .out_4(\n32x32除法器单元_4_out_4 ), .out_5(\n32x32除法器单元_4_out_5 ));
  \_32X32除法器单元  \u_32x32除法器单元_5  (
    .\被除数 (\n32x32除法器单元_31_out_4 ), .\除数 (\除数 ), .\加数 (\n32x32除法器单元_31_out_5 ),
    .out_4(\n32x32除法器单元_5_out_4 ), .out_5(\n32x32除法器单元_5_out_5 ));
  \_32X32除法器单元  \u_32x32除法器单元_6  (
    .\被除数 (\n32x32除法器单元_32_out_4 ), .\除数 (\除数 ), .\加数 (\n32x32除法器单元_32_out_5 ),
    .out_4(\n32x32除法器单元_6_out_4 ), .out_5(\n32x32除法器单元_6_out_5 ));
  \_32X32除法器单元  \u_32x32除法器单元_7  (
    .\被除数 (\n32x32除法器单元_1_out_4 ), .\除数 (\除数 ), .\加数 (\n32x32除法器单元_1_out_5 ), .out_4(\n32x32除法器单元_7_out_4 ),
    .out_5(\n32x32除法器单元_7_out_5 ));
  \_32X32除法器单元  \u_32x32除法器单元_8  (
    .\被除数 (\n32x32除法器单元_2_out_4 ), .\除数 (\除数 ), .\加数 (\n32x32除法器单元_2_out_5 ), .out_4(\n32x32除法器单元_8_out_4 ),
    .out_5(\n32x32除法器单元_8_out_5 ));
  \_32X32除法器单元  \u_32x32除法器单元_9  (
    .\被除数 (\n32x32除法器单元_3_out_4 ), .\除数 (\除数 ), .\加数 (\n32x32除法器单元_3_out_5 ), .out_4(\n32x32除法器单元_9_out_4 ),
    .out_5(\n32x32除法器单元_9_out_5 ));
  \_32X32除法器单元  \u_32x32除法器单元_10  (
    .\被除数 (\n32x32除法器单元_4_out_4 ), .\除数 (\除数 ), .\加数 (\n32x32除法器单元_4_out_5 ), .out_4(\n32x32除法器单元_10_out_4 ),
    .out_5(\n32x32除法器单元_10_out_5 ));
  \_32X32除法器单元  \u_32x32除法器单元_11  (
    .\被除数 (\n32x32除法器单元_5_out_4 ), .\除数 (\除数 ), .\加数 (\n32x32除法器单元_5_out_5 ), .out_4(\n32x32除法器单元_11_out_4 ),
    .out_5(\n32x32除法器单元_11_out_5 ));
  \_32X32除法器单元  \u_32x32除法器单元_12  (
    .\被除数 (\n32x32除法器单元_6_out_4 ), .\除数 (\除数 ), .\加数 (\n32x32除法器单元_6_out_5 ), .out_4(\商 ), .out_5(\余数 ));
  \_32X32除法器单元  \u_32x32除法器单元_13  (
    .\被除数 (\n32x32除法器单元_7_out_4 ), .\除数 (\除数 ), .\加数 (\n32x32除法器单元_7_out_5 ), .out_4(\n32x32除法器单元_13_out_4 ),
    .out_5(\n32x32除法器单元_13_out_5 ));
  \_32X32除法器单元  \u_32x32除法器单元_14  (
    .\被除数 (\n32x32除法器单元_8_out_4 ), .\除数 (\除数 ), .\加数 (\n32x32除法器单元_8_out_5 ), .out_4(\n32x32除法器单元_14_out_4 ),
    .out_5(\n32x32除法器单元_14_out_5 ));
  \_32X32除法器单元  \u_32x32除法器单元_15  (
    .\被除数 (\n32x32除法器单元_9_out_4 ), .\除数 (\除数 ), .\加数 (\n32x32除法器单元_9_out_5 ), .out_4(\n32x32除法器单元_15_out_4 ),
    .out_5(\n32x32除法器单元_15_out_5 ));
  \_32X32除法器单元  \u_32x32除法器单元_16  (
    .\被除数 (\n32x32除法器单元_10_out_4 ), .\除数 (\除数 ), .\加数 (\n32x32除法器单元_10_out_5 ),
    .out_4(\n32x32除法器单元_16_out_4 ), .out_5(\n32x32除法器单元_16_out_5 ));
  \_32X32除法器单元  \u_32x32除法器单元_17  (
    .\被除数 (\n32x32除法器单元_11_out_4 ), .\除数 (\除数 ), .\加数 (\n32x32除法器单元_11_out_5 ),
    .out_4(\n32x32除法器单元_17_out_4 ), .out_5(\n32x32除法器单元_17_out_5 ));
  \_32X32除法器单元  \u_32x32除法器单元_18  (
    .\被除数 (\n32x32除法器单元_13_out_4 ), .\除数 (\除数 ), .\加数 (\n32x32除法器单元_13_out_5 ),
    .out_4(\n32x32除法器单元_18_out_4 ), .out_5(\n32x32除法器单元_18_out_5 ));
  \_32X32除法器单元  \u_32x32除法器单元_19  (
    .\被除数 (\n32x32除法器单元_14_out_4 ), .\除数 (\除数 ), .\加数 (\n32x32除法器单元_14_out_5 ),
    .out_4(\n32x32除法器单元_19_out_4 ), .out_5(\n32x32除法器单元_19_out_5 ));
  \_32X32除法器单元  \u_32x32除法器单元_20  (
    .\被除数 (\n32x32除法器单元_15_out_4 ), .\除数 (\除数 ), .\加数 (\n32x32除法器单元_15_out_5 ),
    .out_4(\n32x32除法器单元_20_out_4 ), .out_5(\n32x32除法器单元_20_out_5 ));
  \_32X32除法器单元  \u_32x32除法器单元_21  (
    .\被除数 (\n32x32除法器单元_16_out_4 ), .\除数 (\除数 ), .\加数 (\n32x32除法器单元_16_out_5 ),
    .out_4(\n32x32除法器单元_21_out_4 ), .out_5(\n32x32除法器单元_21_out_5 ));
  \_32X32除法器单元  \u_32x32除法器单元_22  (
    .\被除数 (\n32x32除法器单元_17_out_4 ), .\除数 (\除数 ), .\加数 (\n32x32除法器单元_17_out_5 ),
    .out_4(\n32x32除法器单元_22_out_4 ), .out_5(\n32x32除法器单元_22_out_5 ));
  \_32X32除法器单元  \u_32x32除法器单元_23  (
    .\被除数 (\n32x32除法器单元_18_out_4 ), .\除数 (\除数 ), .\加数 (\n32x32除法器单元_18_out_5 ),
    .out_4(\n32x32除法器单元_23_out_4 ), .out_5(\n32x32除法器单元_23_out_5 ));
  \_32X32除法器单元  \u_32x32除法器单元_24  (
    .\被除数 (\n32x32除法器单元_19_out_4 ), .\除数 (\除数 ), .\加数 (\n32x32除法器单元_19_out_5 ),
    .out_4(\n32x32除法器单元_24_out_4 ), .out_5(\n32x32除法器单元_24_out_5 ));
  \_32X32除法器单元  \u_32x32除法器单元_25  (
    .\被除数 (\n32x32除法器单元_20_out_4 ), .\除数 (\除数 ), .\加数 (\n32x32除法器单元_20_out_5 ),
    .out_4(\n32x32除法器单元_25_out_4 ), .out_5(\n32x32除法器单元_25_out_5 ));
  \_32X32除法器单元  \u_32x32除法器单元_26  (
    .\被除数 (\n32x32除法器单元_21_out_4 ), .\除数 (\除数 ), .\加数 (\n32x32除法器单元_21_out_5 ),
    .out_4(\n32x32除法器单元_26_out_4 ), .out_5(\n32x32除法器单元_26_out_5 ));
  \_32X32除法器单元  \u_32x32除法器单元_27  (
    .\被除数 (\n32x32除法器单元_22_out_4 ), .\除数 (\除数 ), .\加数 (\n32x32除法器单元_22_out_5 ),
    .out_4(\n32x32除法器单元_27_out_4 ), .out_5(\n32x32除法器单元_27_out_5 ));
  \_32X32除法器单元  \u_32x32除法器单元_28  (
    .\被除数 (\n32x32除法器单元_23_out_4 ), .\除数 (\除数 ), .\加数 (\n32x32除法器单元_23_out_5 ),
    .out_4(\n32x32除法器单元_28_out_4 ), .out_5(\n32x32除法器单元_28_out_5 ));
  \_32X32除法器单元  \u_32x32除法器单元_29  (
    .\被除数 (\n32x32除法器单元_24_out_4 ), .\除数 (\除数 ), .\加数 (\n32x32除法器单元_24_out_5 ),
    .out_4(\n32x32除法器单元_29_out_4 ), .out_5(\n32x32除法器单元_29_out_5 ));
  \_32X32除法器单元  \u_32x32除法器单元_30  (
    .\被除数 (\n32x32除法器单元_25_out_4 ), .\除数 (\除数 ), .\加数 (\n32x32除法器单元_25_out_5 ),
    .out_4(\n32x32除法器单元_30_out_4 ), .out_5(\n32x32除法器单元_30_out_5 ));
  \_32X32除法器单元  \u_32x32除法器单元_31  (
    .\被除数 (\n32x32除法器单元_26_out_4 ), .\除数 (\除数 ), .\加数 (\n32x32除法器单元_26_out_5 ),
    .out_4(\n32x32除法器单元_31_out_4 ), .out_5(\n32x32除法器单元_31_out_5 ));
  \_32X32除法器单元  \u_32x32除法器单元_32  (
    .\被除数 (\n32x32除法器单元_27_out_4 ), .\除数 (\除数 ), .\加数 (\n32x32除法器单元_27_out_5 ),
    .out_4(\n32x32除法器单元_32_out_4 ), .out_5(\n32x32除法器单元_32_out_5 ));
endmodule

module \_32X32除法器单元  (
  input  [31:0] \被除数 ,
  input  [31:0] \除数 ,
  input  [31:0] \加数 ,
  output [31:0] out_4,
  output [31:0] out_5
);

  wire comparator_1_lt, not_1_out;
  wire [31:0] bit_extender_1_out, subtractor_1_out;

  Subtractor #(.width(32)) subtractor_1 (
    .a({\加数 [30:0], \被除数 [31]}), .b(\除数 ), .out(subtractor_1_out));  // open: bin, bout
  Comparator #(.width(32)) comparator_1 (.a({\加数 [30:0], \被除数 [31]}), .b(\除数 ), .lt(comparator_1_lt));  // open: gt, eq
  Multiplexer #(.width(32), .enable("false")) multiplexer_1 (
    .in0(subtractor_1_out), .in1({\加数 [30:0], \被除数 [31]}), .out(out_5), .sel(comparator_1_lt));
  not not_1 (not_1_out, comparator_1_lt);
  assign bit_extender_1_out = {{31{1'b0}}, not_1_out};  // Bit_Extender bit_extender_1
  Adder #(.width(32)) adder_1 (.a({\被除数 [30:0], 1'b0}), .b(bit_extender_1_out), .out(out_4));  // open: cin, cout
endmodule
