// Logisim project 多功能电子钟系统设计.circ as structural Verilog: 10 circuits, main circuit main
module main (
  input  CPU,
  input  CLR,
  input  CPD,
  input  Adj,
  output out_5,
  output out_6,
  output out_7,
  output out_8,
  output out_9,
  output out_10,
  output out_11,
  output out_12,
  output QCC
);

  wire and_1_out, and_2_out, and_3_out, and_4_out, and_5_out, nor_1_out, nor_2_out, not_1_out, or_1_out;

  and and_1 (and_1_out, out_11, out_10);
  or or_1 (or_1_out, and_1_out, CLR, and_3_out);
  and and_2 (and_2_out, CPD, Adj);
  and and_3 (and_3_out, and_2_out, nor_1_out, nor_2_out);
  \四位二进制可逆计数器  \u_四位二进制可逆计数器_1  (
    .A0(out_8), .A2(out_7), .A3(out_6), .A4(out_5), .CPu(CPU), .CPd(and_2_out), .CLR(or_1_out));
  not not_1 (not_1_out, nor_2_out);
  and and_4 (and_4_out, CPU, out_5, out_8);
  nor nor_1 (nor_1_out, out_6, out_5, out_7, out_8);
  and and_5 (and_5_out, not_1_out, nor_1_out, and_2_out);
  nor nor_2 (nor_2_out, out_12, out_11, out_10, out_9);
  \四位二进制可逆计数器  \u_四位二进制可逆计数器_2  (
    .A0(out_12), .A2(out_11), .A3(out_10), .A4(out_9), .CPu(and_4_out), .CPd(and_5_out), .CLR(or_1_out));
  and and_6 (QCC, out_10, out_12, and_4_out);
endmodule

module \四位二进制可逆计数器  (
  input  CPd,
  input  CPu,
  input  CLR,
  output A0,
  output A2,
  output A3,
  output A4
);

  wire and_1_out, and_2_out, and_3_out, and_4_out, and_5_out, and_6_out, and_7_out, d_ff_1_qn, d_ff_2_qn,
       d_ff_3_qn, d_ff_4_qn, nand_1_out, or_1_out, or_2_out, or_3_out, or_4_out, or_5_out, or_6_out;

  or or_1 (or_1_out, A0, A2, A3, A4);
  D_Flip_Flop #(.trigger("falling")) d_ff_1 (
    .clk(or_2_out), .D(d_ff_1_qn), .Q(A0), .Qn(d_ff_1_qn), .reset(or_5_out));  // open: preset, en
  or or_2 (or_2_out, CPd, CPu);
  D_Flip_Flop #(.trigger("falling")) d_ff_2 (
    .clk(or_3_out), .D(d_ff_2_qn), .Q(A2), .Qn(d_ff_2_qn), .reset(or_5_out));  // open: preset, en
  or or_3 (or_3_out, and_1_out, and_2_out);
  and and_1 (and_1_out, CPd, or_1_out, d_ff_1_qn);
  and and_2 (and_2_out, A0, CPu);
  and and_3 (and_3_out, CPd, or_1_out, d_ff_1_qn, d_ff_2_qn);
  D_Flip_Flop #(.trigger("falling")) d_ff_3 (
    .clk(or_4_out), .D(d_ff_3_qn), .Q(A3), .Qn(d_ff_3_qn), .reset(or_5_out));  // open: preset, en
  or or_4 (or_4_out, and_3_out, and_4_out);
  and and_4 (and_4_out, A0, A2, CPu);
  or or_5 (or_5_out, CLR, and_7_out);
  nand nand_1 (nand_1_out, A0, A3);
  D_Flip_Flop #(.trigger("falling")) d_ff_4 (
    .clk(or_6_out), .D(d_ff_4_qn), .Q(A4), .Qn(d_ff_4_qn), .reset(or_5_out));  // open: preset, en
  or or_6 (or_6_out, and_5_out, and_6_out);
  and and_5 (and_5_out, CPd, d_ff_1_qn, d_ff_2_qn, d_ff_3_qn);
  and and_6 (and_6_out, A0, A2, A3, CPu);
  and and_7 (and_7_out, A2, nand_1_out, A4);
endmodule

module \四位二级制可逆计数器2  (
  input  CPd,
  input  CPu,
  input  CLR,
  output A0,
  output A2,
  output A3,
  output A4
);

  wire and_1_out, and_2_out, and_3_out, and_4_out, and_5_out, and_6_out, and_7_out, d_ff_1_qn, d_ff_2_qn,
       d_ff_3_qn, d_ff_4_qn, nand_1_out, or_1_out, or_2_out, or_3_out, or_4_out, or_5_out, or_6_out;

  or or_1 (or_1_out, A0, A2, A3, A4);
  D_Flip_Flop #(.trigger("falling")) d_ff_1 (
    .clk(or_2_out), .D(d_ff_1_qn), .Q(A0), .Qn(d_ff_1_qn), .reset(or_5_out));  // open: preset, en
  or or_2 (or_2_out, CPd, CPu);
  D_Flip_Flop #(.trigger("falling")) d_ff_2 (
    .clk(or_3_out), .D(d_ff_2_qn), .Q(A2), .Qn(d_ff_2_qn), .reset(or_5_out));  // open: preset, en
  or or_3 (or_3_out, and_1_out, and_2_out);
  and and_1 (and_1_out, CPd, or_1_out, d_ff_1_qn);
  and and_2 (and_2_out, A0, CPu);
  and and_3 (and_3_out, CPd, d_ff_1_qn, d_ff_2_qn);
  D_Flip_Flop #(.trigger("falling")) d_ff_3 (
    .clk(or_4_out), .D(d_ff_3_qn), .Q(A3), .Qn(d_ff_3_qn), .reset(or_5_out));  // open: preset, en
  or or_4 (or_4_out, and_3_out, and_4_out);
  and and_4 (and_4_out, A0, A2, CPu);
  or or_5 (or_5_out, CLR, and_7_out);
  nand nand_1 (nand_1_out, A0, A3);
  D_Flip_Flop #(.trigger("falling")) d_ff_4 (
    .clk(or_6_out), .D(d_ff_4_qn), .Q(A4), .Qn(d_ff_4_qn), .reset(or_5_out));  // open: preset, en
  or or_6 (or_6_out, and_6_out, and_5_out);
  and and_5 (and_5_out, A0, A2, A3, CPu);
  and and_6 (and_6_out, CPd, d_ff_1_qn, or_1_out, d_ff_2_qn, d_ff_3_qn);
  and and_7 (and_7_out, A2, nand_1_out, A4);
endmodule

module \十二进制计数器或二十四进制的计数器电路  (
  input  SET,
  input  CPU,
  input  CLR,
  input  CPD,
  input  adj,
  output out_6,
  output out_7,
  output out_8,
  output out_9,
  output out_10,
  output out_11,
  output out_12,
  output out_13,
  output QCC
);

  wire _0A, _0B, _0C, _0D, _1A, _1B, _1C, _1D, and_1_out, and_2_out, and_3_out, and_4_out, and_5_out,
       and_6_out, and_7_out, and_8_out, and_9_out, and_10_out, and_11_out, nor_1_out, nor_2_out, nor_3_out,
       nor_4_out, not_1_out, not_2_out, or_1_out, or_2_out, QCC_t, \四位二进制可逆计数器_1_a0 , \四位二进制可逆计数器_1_a2 ,
       \四位二进制可逆计数器_1_a3 , \四位二进制可逆计数器_1_a4 , \四位二进制可逆计数器_4_a0 , \四位二进制可逆计数器_4_a2 , \四位二进制可逆计数器_4_a3 ,
       \四位二进制可逆计数器_4_a4 ;

  and and_1 (and_1_out, \四位二进制可逆计数器_4_a0 , \四位二进制可逆计数器_1_a2 );
  or or_1 (or_1_out, and_1_out, CLR, and_6_out);
  and and_2 (and_2_out, CPD, adj);
  and and_3 (and_3_out, _1B, _0C);
  or or_2 (or_2_out, and_3_out, CLR, and_5_out);
  and and_4 (and_4_out, CPD, adj);
  and and_5 (and_5_out, and_4_out, nor_1_out, nor_4_out);
  Multiplexer #(.enable("false")) multiplexer_1 (.in0(\四位二进制可逆计数器_1_a4 ), .in1(_0D), .out(out_6), .sel(SET));
  Multiplexer #(.enable("false")) multiplexer_2 (.in0(\四位二进制可逆计数器_1_a3 ), .in1(_0C), .out(out_7), .sel(SET));
  and and_6 (and_6_out, and_2_out, nor_2_out, nor_3_out);
  Multiplexer #(.enable("false")) multiplexer_3 (.in0(\四位二进制可逆计数器_1_a2 ), .in1(_0B), .out(out_8), .sel(SET));
  Multiplexer #(.enable("false")) multiplexer_4 (.in0(\四位二进制可逆计数器_1_a0 ), .in1(_0A), .out(out_9), .sel(SET));
  \四位二进制可逆计数器  \u_四位二进制可逆计数器_1  (
    .A0(\四位二进制可逆计数器_1_a0 ), .A2(\四位二进制可逆计数器_1_a2 ), .A3(\四位二进制可逆计数器_1_a3 ), .A4(\四位二进制可逆计数器_1_a4 ),
    .CPu(CPU), .CPd(and_2_out), .CLR(or_1_out));
  \四位二进制可逆计数器  \u_四位二进制可逆计数器_2  (.A0(_0A), .A2(_0B), .A3(_0C), .A4(_0D), .CPu(CPU), .CPd(and_4_out), .CLR(or_2_out));
  nor nor_1 (nor_1_out, _0A, _0C, _0D, _0B);
  Multiplexer #(.enable("false")) multiplexer_5 (.in0(\四位二进制可逆计数器_4_a4 ), .in1(_1D), .out(out_10), .sel(SET));
  Multiplexer #(.enable("false")) multiplexer_6 (.in0(\四位二进制可逆计数器_4_a3 ), .in1(_1C), .out(out_11), .sel(SET));
  and and_7 (and_7_out, \四位二进制可逆计数器_1_a4 , \四位二进制可逆计数器_1_a2 );
  nor nor_2 (nor_2_out, \四位二进制可逆计数器_1_a0 , \四位二进制可逆计数器_1_a3 , \四位二进制可逆计数器_1_a4 , \四位二进制可逆计数器_1_a2 );
  not not_1 (not_1_out, nor_3_out);
  and and_8 (and_8_out, _0D, _0B);
  not not_2 (not_2_out, nor_4_out);
  Multiplexer #(.enable("false")) multiplexer_7 (.in0(\四位二进制可逆计数器_4_a2 ), .in1(_1B), .out(out_12), .sel(SET));
  and and_9 (and_9_out, nor_2_out, and_2_out, not_1_out);
  and and_10 (and_10_out, nor_1_out, and_4_out, not_2_out);
  Multiplexer #(.enable("false")) multiplexer_8 (.in0(\四位二进制可逆计数器_4_a0 ), .in1(_1A), .out(out_13), .sel(SET));
  \四位二进制可逆计数器  \u_四位二进制可逆计数器_3  (
    .A0(_1A), .A2(_1B), .A3(_1C), .A4(_1D), .CPu(and_8_out), .CPd(and_10_out), .CLR(or_2_out));
  nor nor_3 (nor_3_out, \四位二进制可逆计数器_4_a0 , \四位二进制可逆计数器_4_a2 , \四位二进制可逆计数器_4_a3 , \四位二进制可逆计数器_4_a4 );
  \四位二进制可逆计数器  \u_四位二进制可逆计数器_4  (
    .A0(\四位二进制可逆计数器_4_a0 ), .A2(\四位二进制可逆计数器_4_a2 ), .A3(\四位二进制可逆计数器_4_a3 ), .A4(\四位二进制可逆计数器_4_a4 ),
    .CPu(and_7_out), .CPd(and_9_out), .CLR(or_1_out));
  nor nor_4 (nor_4_out, _1A, _1B, _1C, _1D);
  Multiplexer #(.enable("false")) multiplexer_9 (.in0(and_11_out), .in1(QCC_t), .out(QCC), .sel(SET));
  and and_11 (and_11_out, \四位二进制可逆计数器_4_a0 , \四位二进制可逆计数器_1_a0 , CPU);
  and and_12 (QCC_t, _1B, _0A, CPU, _0B);
endmodule

module \测试  (
  input  in_1,
  input  in_2,
  input  in_3,
  input  in_4,
  input  in_5,
  input  in_6,
  input  in_7,
  input  in_8,
  input  in_9,
  output out_10,
  output out_11,
  output out_12
);

  wire button_1_out, button_2_out, button_3_out, button_4_out, button_5_out, button_6_out, button_7_out,
       button_8_out, button_9_out, clock_1_out, clock_2_out, clock_3_out, \多功能电子钟_1_out_18 , \整点报时_1_out_3 ;
  wire [3:0] main_1_out_8, main_1_out_12, \十二进制计数器或二十四进制的计数器电路_1_out_9 , \十二进制计数器或二十四进制的计数器电路_1_out_13 ,
       \多功能电子钟_1_out_12 , \多功能电子钟_1_out_13 , \多功能电子钟_1_out_14 , \多功能电子钟_1_out_15 , \多功能电子钟_1_out_16 ,
       \多功能电子钟_1_out_17 ;
  wire [4:0] led_1_p1, led_1_p3, led_1_p4, led_1_p6, \多功能电子钟_1_out_8 , \多功能电子钟_1_out_9 , \多功能电子钟_1_out_10 ,
       \多功能电子钟_1_out_11 ;

  Button button_1 (.out(button_1_out));
  Button button_2 (.out(button_2_out));
  Button button_3 (.out(button_3_out));
  Button button_4 (.out(button_4_out));
  Clock clock_1 (.out(clock_1_out));
  Hex_Digit_Display hex_digit_display_1 (.value(main_1_out_12));  // open: dp
  Hex_Digit_Display hex_digit_display_2 (.value(\十二进制计数器或二十四进制的计数器电路_1_out_13 ));  // open: dp
  Hex_Digit_Display hex_digit_display_3 (.value(main_1_out_8));  // open: dp
  Hex_Digit_Display hex_digit_display_4 (.value(\十二进制计数器或二十四进制的计数器电路_1_out_9 ));  // open: dp
  \秒计时脉冲产生电路  \u_秒计时脉冲产生电路_1  (.in_1(clock_1_out), .out_2(out_12));
  main main_1 (
    .QCC(out_10), .out_5(main_1_out_8[3]), .out_6(main_1_out_8[2]), .out_7(main_1_out_8[1]),
    .out_8(main_1_out_8[0]), .out_9(main_1_out_12[3]), .out_10(main_1_out_12[2]), .out_11(main_1_out_12[1]),
    .out_12(main_1_out_12[0]), .CPU(button_1_out), .CLR(button_5_out), .CPD(button_2_out), .Adj(in_1));
  Button button_5 (.out(button_5_out));
  \十二进制计数器或二十四进制的计数器电路  \u_十二进制计数器或二十四进制的计数器电路_1  (
    .SET(in_6), .CPU(button_3_out), .CLR(button_6_out), .CPD(button_4_out), .adj(in_5),
    .out_6(\十二进制计数器或二十四进制的计数器电路_1_out_9 [3]), .out_7(\十二进制计数器或二十四进制的计数器电路_1_out_9 [2]),
    .out_8(\十二进制计数器或二十四进制的计数器电路_1_out_9 [1]), .out_9(\十二进制计数器或二十四进制的计数器电路_1_out_9 [0]),
    .out_10(\十二进制计数器或二十四进制的计数器电路_1_out_13 [3]), .out_11(\十二进制计数器或二十四进制的计数器电路_1_out_13 [2]),
    .out_12(\十二进制计数器或二十四进制的计数器电路_1_out_13 [1]), .out_13(\十二进制计数器或二十四进制的计数器电路_1_out_13 [0]), .QCC(out_11));
  Button button_6 (.out(button_6_out));
  DotMatrix #(.matrixcols(4), .matrixrows(5)) dotmatrix_1 (
    .col0(led_1_p1), .col1(led_1_p3), .col2(led_1_p4), .col3(led_1_p6));
  // LED led_1: pin names not known; wires that end beside it: led_1_p1, in_3, led_1_p3, led_1_p4, in_4, led_1_p6
  DotMatrix #(.matrixcols(4), .matrixrows(5)) dotmatrix_2 (
    .col0(\多功能电子钟_1_out_8 ), .col1(\多功能电子钟_1_out_9 ), .col2(\多功能电子钟_1_out_10 ), .col3(\多功能电子钟_1_out_11 ));
  Clock clock_2 (.out(clock_2_out));
  Hex_Digit_Display hex_digit_display_5 (.value(\多功能电子钟_1_out_13 ));  // open: dp
  Hex_Digit_Display hex_digit_display_6 (.value(\多功能电子钟_1_out_12 ));  // open: dp
  Button button_7 (.out(button_7_out));
  Button button_8 (.out(button_8_out));
  Hex_Digit_Display hex_digit_display_7 (.value(\多功能电子钟_1_out_15 ));  // open: dp
  Hex_Digit_Display hex_digit_display_8 (.value(\多功能电子钟_1_out_14 ));  // open: dp
  Button button_9 (.out(button_9_out));
  Clock clock_3 (.out(clock_3_out));
  Hex_Digit_Display hex_digit_display_9 (.value(\多功能电子钟_1_out_17 ));  // open: dp
  Hex_Digit_Display hex_digit_display_10 (.value(\多功能电子钟_1_out_16 ));  // open: dp
  \多功能电子钟  \u_多功能电子钟_1  (
    .SET(in_9), .CPd(button_8_out), .Adj0(in_7), .Adj1(in_8), .CLR(button_9_out), .CPu(button_7_out),
    .out_8(\多功能电子钟_1_out_8 ), .out_9(\多功能电子钟_1_out_9 ), .out_10(\多功能电子钟_1_out_10 ),
    .out_11(\多功能电子钟_1_out_11 ), .out_14(\多功能电子钟_1_out_14 ), .out_15(\多功能电子钟_1_out_15 ),
    .out_16(\多功能电子钟_1_out_16 ), .out_17(\多功能电子钟_1_out_17 ), .CP(clock_2_out), .out_18(\多功能电子钟_1_out_18 ),
    .out_12(\多功能电子钟_1_out_12 ), .out_13(\多功能电子钟_1_out_13 ));
  LED_part led_2 (.in(\多功能电子钟_1_out_18 ));
  \整点报时  \u_整点报时_1  (.in_1(clock_3_out), .in_2(in_2), .out_3(\整点报时_1_out_3 ));
  LED_part led_3 (.in(\整点报时_1_out_3 ));
endmodule

module \整点报时  (
  input  in_1,
  input  in_2,
  output out_3
);

  wire and_2_out, and_3_out, d_ff_1_q, d_ff_1_qn, \四位二进制可逆计数器_1_a2 , \四位二进制可逆计数器_1_a4 ;

  and and_1 (out_3, in_1, d_ff_1_q);
  D_Flip_Flop #(.trigger("falling")) d_ff_1 (
    .clk(in_2), .D(d_ff_1_qn), .Q(d_ff_1_q), .Qn(d_ff_1_qn), .preset(d_ff_1_q), .reset(and_3_out));  // open: en
  and and_2 (and_2_out, in_1, d_ff_1_q);
  and and_3 (and_3_out, \四位二进制可逆计数器_1_a4 , \四位二进制可逆计数器_1_a2 );
  \四位二进制可逆计数器  \u_四位二进制可逆计数器_1  (
    .A2(\四位二进制可逆计数器_1_a2 ), .A4(\四位二进制可逆计数器_1_a4 ), .CPu(and_2_out), .CPd(1'b0), .CLR(1'b0));  // open: A0, A3
endmodule

module \秒计时脉冲产生电路  (
  input  in_1,
  output out_2
);

  wire d_ff_1_q, d_ff_1_qn, d_ff_2_q, d_ff_2_qn, d_ff_3_qn;

  D_Flip_Flop d_ff_1 (.clk(in_1), .D(d_ff_1_qn), .Q(d_ff_1_q), .Qn(d_ff_1_qn));  // open: preset, en, reset
  D_Flip_Flop d_ff_2 (.clk(d_ff_1_q), .D(d_ff_2_qn), .Q(d_ff_2_q), .Qn(d_ff_2_qn));  // open: preset, en, reset
  D_Flip_Flop d_ff_3 (.clk(d_ff_2_q), .D(d_ff_3_qn), .Q(out_2), .Qn(d_ff_3_qn));  // open: preset, en, reset
endmodule

module LED (
  input  AM_FM,
  input  TT,
  output [4:0] out_3,
  output [4:0] out_4,
  output [4:0] out_5,
  output [4:0] out_6
);

  Multiplexer #(.width(5), .disabled(0)) multiplexer_1 (
    .in0(5'b00001), .in1(5'b10000), .out(out_3), .sel(AM_FM), .en(TT));
  Multiplexer #(.width(5), .disabled(0)) multiplexer_2 (
    .in0({5{1'b1}}), .in1({5{1'b1}}), .out(out_4), .sel(AM_FM), .en(TT));
  Multiplexer #(.width(5), .disabled(0)) multiplexer_3 (
    .in0(5'b00101), .in1(5'b10100), .out(out_5), .sel(AM_FM), .en(TT));
  Multiplexer #(.width(5), .disabled(0)) multiplexer_4 (
    .in0(5'b00001), .in1(5'b10000), .out(out_6), .sel(AM_FM), .en(TT));
endmodule

module \多功能电子钟  (
  input  SET,
  input  Adj0,
  input  Adj1,
  input  CLR,
  input  CPu,
  input  CPd,
  input  CP,
  output [4:0] out_8,
  output [4:0] out_9,
  output [4:0] out_10,
  output [4:0] out_11,
  output [3:0] out_12,
  output [3:0] out_13,
  output [3:0] out_14,
  output [3:0] out_15,
  output [3:0] out_16,
  output [3:0] out_17,
  output out_18
);

  wire _1HZ, _50, _59, AF, and_1_out, and_2_out, and_3_out, and_4_out, and_5_out, and_6_out, and_7_out,
       and_9_out, and_10_out, comparator_1_eq, comparator_2_eq, comparator_3_eq, CPd1, CPd2, d_ff_1_qn,
       multiplexer_1_out, multiplexer_3_out, not_1_out, not_2_out, not_3_out, not_4_out, not_5_out,
       not_6_out, not_7_out, not_8_out, not_9_out, or_1_out, Q, QCC, QM, QS;
  wire [7:0] X;

  not not_1 (not_1_out, CPd2);
  or or_1 (or_1_out, QCC, Q);
  not not_2 (not_2_out, Adj0);
  and and_1 (and_1_out, not_2_out, QM);
  not not_3 (not_3_out, Adj1);
  and and_2 (and_2_out, not_1_out, or_1_out);
  D_Flip_Flop d_ff_1 (.clk(and_2_out), .D(d_ff_1_qn), .Q(AF), .Qn(d_ff_1_qn), .reset(CLR));  // open: preset, en
  Multiplexer #(.enable("false")) multiplexer_1 (.in0(and_1_out), .in1(CPu), .out(multiplexer_1_out), .sel(and_3_out));
  and and_3 (and_3_out, not_3_out, Adj0);
  LED led_1 (.out_3(out_8), .out_4(out_9), .out_5(out_10), .out_6(out_11), .AM_FM(AF), .TT(not_4_out));
  not not_4 (not_4_out, SET);
  Comparator comparator_1 (.a(X), .b({8{1'b0}}), .eq(comparator_1_eq));  // open: gt, lt
  not not_5 (not_5_out, Adj0);
  and and_4 (and_4_out, not_5_out, QS);
  Multiplexer #(.width(8), .enable("false")) multiplexer_2 (
    .in0(X), .in1(8'h12), .out({out_12, out_13}), .sel(and_5_out));
  and and_5 (and_5_out, comparator_1_eq, not_6_out);
  not not_6 (not_6_out, SET);
  \十二进制或二十四进制计数器  \u_十二进制或二十四进制计数器_1  (
    .SET(SET), .CPU(multiplexer_1_out), .CLR(CLR), .CPD(CPd2), .adj(Adj0), .out_6(X[7]), .out_7(X[6]),
    .out_8(X[5]), .out_9(X[4]), .out_10(X[3]), .out_11(X[2]), .out_12(X[1]), .out_13(X[0]), .out_14(QCC));
  and and_6 (and_6_out, Adj1, Adj0);
  Multiplexer #(.enable("false")) multiplexer_3 (.in0(and_4_out), .in1(CPu), .out(multiplexer_3_out), .sel(and_6_out));
  and and_7 (and_7_out, _59, _50);
  and u__59 (_59, out_14[2], out_15[3], out_15[0], out_14[0]);
  main main_1 (
    .QCC(QM), .out_5(out_15[3]), .out_6(out_15[2]), .out_7(out_15[1]), .out_8(out_15[0]), .out_9(out_14[3]),
    .out_10(out_14[2]), .out_11(out_14[1]), .out_12(out_14[0]), .CPU(multiplexer_3_out), .CLR(CLR),
    .CPD(CPd1), .Adj(Adj0));
  Comparator comparator_2 (.a(X), .b({8{1'b0}}), .eq(comparator_2_eq));  // open: gt, lt
  Comparator comparator_3 (.a(X), .b(8'h12), .eq(comparator_3_eq));  // open: gt, lt
  \整点报时  \u_整点报时_1  (.in_1(_1HZ), .in_2(and_7_out), .out_3(out_18));
  \秒计时脉冲产生电路  \u_秒计时脉冲产生电路_1  (.in_1(CP), .out_2(_1HZ));
  not not_7 (not_7_out, Adj1);
  not not_8 (not_8_out, Adj1);
  and and_8 (CPd2, not_9_out, CPd);
  not not_9 (not_9_out, Adj1);
  and and_9 (and_9_out, AF, not_7_out, Adj0, comparator_2_eq, CPd);
  or or_2 (Q, and_9_out, and_10_out);
  and and_10 (and_10_out, AF, comparator_3_eq, Adj0, not_8_out, CPd);
  and u__50 (_50, out_16[2], out_17[0], out_17[3]);
  main main_2 (
    .QCC(QS), .out_5(out_17[3]), .out_6(out_17[2]), .out_7(out_17[1]), .out_8(out_17[0]), .out_9(out_16[3]),
    .out_10(out_16[2]), .out_11(out_16[1]), .out_12(out_16[0]), .CPU(_1HZ), .CLR(CLR), .CPD(1'b0), .Adj(1'b0));
  and and_11 (CPd1, Adj1, CPd);
endmodule

module \十二进制或二十四进制计数器  (
  input  SET,
  input  CPU,
  input  CLR,
  input  CPD,
  input  adj,
  output out_6,
  output out_7,
  output out_8,
  output out_9,
  output out_10,
  output out_11,
  output out_12,
  output out_13,
  output out_14
);

  wire and_1_out, and_2_out, and_3_out, and_4_out, and_5_out, and_6_out, and_7_out, and_8_out, and_9_out,
       and_10_out, and_11_out, and_12_out, comparator_1_eq, comparator_2_eq, comparator_3_gt,
       comparator_4_lt, comparator_5_gt, comparator_6_eq, nor_1_out, nor_2_out, not_2_out, not_3_out,
       not_4_out, not_5_out, or_1_out, or_2_out, SET_t;
  wire [7:0] multiplexer_1_out, multiplexer_2_out, multiplexer_3_out, subtractor_1_out, \四位二进制可逆计数器_1_a0 ;

  not not_1 (SET_t, SET);
  and and_1 (and_1_out, \四位二进制可逆计数器_1_a0 [5], \四位二进制可逆计数器_1_a0 [2]);
  or or_1 (or_1_out, and_1_out, CLR, and_3_out);
  and and_2 (and_2_out, CPD, adj);
  and and_3 (and_3_out, and_2_out, nor_1_out, nor_2_out);
  Subtractor subtractor_1 (.a(\四位二进制可逆计数器_1_a0 ), .b(8'h12), .out(subtractor_1_out));  // open: bin, bout
  Comparator comparator_1 (.a(\四位二进制可逆计数器_1_a0 ), .b(8'h20), .eq(comparator_1_eq));  // open: gt, lt
  Comparator comparator_2 (.a(\四位二进制可逆计数器_1_a0 ), .b(8'h21), .eq(comparator_2_eq));  // open: gt, lt
  Multiplexer #(.width(8), .enable("false")) multiplexer_1 (
    .in0(\四位二进制可逆计数器_1_a0 ), .in1(subtractor_1_out), .out(multiplexer_1_out), .sel(or_2_out));
  Comparator comparator_3 (.a(\四位二进制可逆计数器_1_a0 ), .b(8'h21), .gt(comparator_3_gt));  // open: eq, lt
  Comparator comparator_4 (.a(\四位二进制可逆计数器_1_a0 ), .b(8'h20), .lt(comparator_4_lt));  // open: gt, eq
  Comparator comparator_5 (.a(\四位二进制可逆计数器_1_a0 ), .b(8'h11), .gt(comparator_5_gt));  // open: eq, lt
  and and_4 (and_4_out, SET_t, comparator_1_eq);
  and and_5 (and_5_out, SET_t, comparator_2_eq);
  and and_6 (and_6_out, comparator_3_gt, SET_t);
  Multiplexer #(.width(8), .enable("false")) multiplexer_2 (
    .in0(multiplexer_1_out), .in1(8'h8), .out(multiplexer_2_out), .sel(and_4_out));
  Multiplexer #(.width(8), .enable("false")) multiplexer_3 (
    .in0(multiplexer_1_out), .in1(8'h9), .out(multiplexer_3_out), .sel(and_5_out));
  or or_2 (or_2_out, and_6_out, and_7_out);
  and and_7 (and_7_out, SET_t, comparator_4_lt, comparator_5_gt);
  not not_2 (not_2_out, \四位二进制可逆计数器_1_a0 [3]);
  not not_3 (not_3_out, \四位二进制可逆计数器_1_a0 [2]);
  not not_4 (not_4_out, \四位二进制可逆计数器_1_a0 [1]);
  \四位二进制可逆计数器  \u_四位二进制可逆计数器_1  (
    .A0(\四位二进制可逆计数器_1_a0 [0]), .A2(\四位二进制可逆计数器_1_a0 [1]), .A3(\四位二进制可逆计数器_1_a0 [2]),
    .A4(\四位二进制可逆计数器_1_a0 [3]), .CPu(CPU), .CPd(and_2_out), .CLR(or_1_out));
  Comparator comparator_6 (.a(\四位二进制可逆计数器_1_a0 ), .b(8'h21), .eq(comparator_6_eq));  // open: gt, lt
  and and_8 (and_8_out, not_2_out, not_3_out, not_4_out, \四位二进制可逆计数器_1_a0 [0]);
  nor nor_1 (nor_1_out, \四位二进制可逆计数器_1_a0 [0], \四位二进制可逆计数器_1_a0 [2], \四位二进制可逆计数器_1_a0 [3], \四位二进制可逆计数器_1_a0 [1]);
  Multiplexer #(.width(8), .enable("false")) multiplexer_4 (
    .in0(multiplexer_2_out), .in1(multiplexer_3_out),
    .out({out_6, out_7, out_8, out_9, out_10, out_11, out_12, out_13}), .sel(comparator_6_eq));
  and and_9 (and_9_out, \四位二进制可逆计数器_1_a0 [3], \四位二进制可逆计数器_1_a0 [1]);
  not not_5 (not_5_out, nor_2_out);
  and and_10 (and_10_out, nor_1_out, and_2_out, not_5_out);
  \四位二进制可逆计数器  \u_四位二进制可逆计数器_2  (
    .A0(\四位二进制可逆计数器_1_a0 [4]), .A2(\四位二进制可逆计数器_1_a0 [5]), .A3(\四位二进制可逆计数器_1_a0 [6]),
    .A4(\四位二进制可逆计数器_1_a0 [7]), .CPu(and_9_out), .CPd(and_10_out), .CLR(or_1_out));
  nor nor_2 (nor_2_out, \四位二进制可逆计数器_1_a0 [4], \四位二进制可逆计数器_1_a0 [5], \四位二进制可逆计数器_1_a0 [6], \四位二进制可逆计数器_1_a0 [7]);
  and and_11 (and_11_out, and_8_out, \四位二进制可逆计数器_1_a0 [4], CPU);
  and and_12 (and_12_out, \四位二进制可逆计数器_1_a0 [5], \四位二进制可逆计数器_1_a0 [0], CPU, \四位二进制可逆计数器_1_a0 [1]);
  or or_3 (out_14, and_11_out, and_12_out);
endmodule
