// Logisim project 斐波那契数列计算器设计.circ as structural Verilog: 8 circuits, main circuit main
module main (
  input  [5:0] in_1
);

  wire button_1_out, button_2_out, controller_1_clear_2, controller_1_clk, controller_1_ni_1,
       controller_1_start;
  wire [3:0] \fibonacci数显示模块_1_out_2 , \fibonacci数显示模块_1_out_3 , \fibonacci数显示模块_1_out_4 ,
       \fibonacci数显示模块_1_out_5 , \fibonacci数显示模块_1_out_6 , \fibonacci数显示模块_1_out_7 ,
       \fibonacci数显示模块_1_out_8 , \fibonacci数显示模块_1_out_9 , \fibonacci数显示模块_1_out_10 ,
       \fibonacci数显示模块_1_out_11 ;
  wire [31:0] \矩阵快速幂算法迭代模块_1_out_5 ;

  Button button_1 (.out(button_1_out));
  Button button_2 (.out(button_2_out));
  Controller_2 controller_1 (
    .clock(button_2_out), .ni_1(controller_1_ni_1), .start(controller_1_start), .clk(controller_1_clk),
    .in_1(in_1), .clear(button_1_out), .clear_2(controller_1_clear_2));
  \矩阵快速幂算法迭代模块  \u_矩阵快速幂算法迭代模块_1  (
    .start(controller_1_start), .clr(controller_1_clear_2), .clk(controller_1_clk), .ni_1(controller_1_ni_1),
    .out_5(\矩阵快速幂算法迭代模块_1_out_5 ));
  \Fibonacci数显示模块  \fibonacci数显示模块_1  (
    .out_2(\fibonacci数显示模块_1_out_2 ), .out_3(\fibonacci数显示模块_1_out_3 ), .in_1(\矩阵快速幂算法迭代模块_1_out_5 ),
    .out_4(\fibonacci数显示模块_1_out_4 ), .out_5(\fibonacci数显示模块_1_out_5 ), .out_6(\fibonacci数显示模块_1_out_6 ),
    .out_7(\fibonacci数显示模块_1_out_7 ), .out_8(\fibonacci数显示模块_1_out_8 ), .out_9(\fibonacci数显示模块_1_out_9 ),
    .out_10(\fibonacci数显示模块_1_out_10 ), .out_11(\fibonacci数显示模块_1_out_11 ));
  Hex_Digit_Display hex_digit_display_1 (.value(\fibonacci数显示模块_1_out_11 ));  // open: dp
  Hex_Digit_Display hex_digit_display_2 (.value(\fibonacci数显示模块_1_out_10 ));  // open: dp
  Hex_Digit_Display hex_digit_display_3 (.value(\fibonacci数显示模块_1_out_8 ));  // open: dp
  Hex_Digit_Display hex_digit_display_4 (.value(\fibonacci数显示模块_1_out_9 ));  // open: dp
  Hex_Digit_Display hex_digit_display_5 (.value(\fibonacci数显示模块_1_out_6 ));  // open: dp
  Hex_Digit_Display hex_digit_display_6 (.value(\fibonacci数显示模块_1_out_7 ));  // open: dp
  Hex_Digit_Display hex_digit_display_7 (.value(\fibonacci数显示模块_1_out_5 ));  // open: dp
  Hex_Digit_Display hex_digit_display_8 (.value(\fibonacci数显示模块_1_out_4 ));  // open: dp
  Hex_Digit_Display hex_digit_display_9 (.value(\fibonacci数显示模块_1_out_2 ));  // open: dp
  Hex_Digit_Display hex_digit_display_10 (.value(\fibonacci数显示模块_1_out_3 ));  // open: dp
endmodule

module sqrX (
  input  [31:0] a,
  input  [31:0] b,
  input  [31:0] c,
  input  [31:0] d,
  output [31:0] a_tilde,
  output [31:0] b_tilde,
  output [31:0] c_tilde,
  output [31:0] d_tilde
);

  wire [31:0] multiplier_1_out, multiplier_2_out, multiplier_3_out, multiplier_4_out, multiplier_5_out,
       multiplier_6_out, multiplier_7_out;

  Multiplier #(.width(32)) multiplier_1 (.a(a), .b(a), .out(multiplier_1_out));  // open: cin, cout
  Multiplier #(.width(32)) multiplier_2 (.a(a), .b(b), .out(multiplier_2_out));  // open: cin, cout
  Multiplier #(.width(32)) multiplier_3 (.a(a), .b(c), .out(multiplier_3_out));  // open: cin, cout
  Multiplier #(.width(32)) multiplier_4 (.a(b), .b(d), .out(multiplier_4_out));  // open: cin, cout
  Multiplier #(.width(32)) multiplier_5 (.a(b), .b(c), .out(multiplier_5_out));  // open: cin, cout
  Multiplier #(.width(32)) multiplier_6 (.a(c), .b(d), .out(multiplier_6_out));  // open: cin, cout
  Multiplier #(.width(32)) multiplier_7 (.a(d), .b(d), .out(multiplier_7_out));  // open: cin, cout
  Adder #(.width(32)) adder_1 (.a(multiplier_1_out), .b(multiplier_5_out), .out(a_tilde));  // open: cin, cout
  Adder #(.width(32)) adder_2 (.a(multiplier_2_out), .b(multiplier_4_out), .out(b_tilde));  // open: cin, cout
  Adder #(.width(32)) adder_3 (.a(multiplier_3_out), .b(multiplier_6_out), .out(c_tilde));  // open: cin, cout
  Adder #(.width(32)) adder_4 (.a(multiplier_5_out), .b(multiplier_7_out), .out(d_tilde));  // open: cin, cout
endmodule

module sqrX_A (
  input  [31:0] a,
  input  [31:0] b,
  input  [31:0] c,
  input  [31:0] d,
  output [31:0] a_tilde,
  output [31:0] b_tilde,
  output [31:0] c_tilde,
  output [31:0] d_tilde
);

  wire [31:0] adder_2_out, adder_4_out, adder_6_out, adder_8_out, multiplier_1_out, multiplier_2_out,
       multiplier_3_out, multiplier_4_out, multiplier_5_out, multiplier_6_out, multiplier_7_out;

  Multiplier #(.width(32)) multiplier_1 (.a(a), .b(b), .out(multiplier_1_out));  // open: cin, cout
  Multiplier #(.width(32)) multiplier_2 (.a(b), .b(d), .out(multiplier_2_out));  // open: cin, cout
  Multiplier #(.width(32)) multiplier_3 (.a(a), .b(a), .out(multiplier_3_out));  // open: cin, cout
  Multiplier #(.width(32)) multiplier_4 (.a(b), .b(c), .out(multiplier_4_out));  // open: cin, cout
  Multiplier #(.width(32)) multiplier_5 (.a(d), .b(d), .out(multiplier_5_out));  // open: cin, cout
  Multiplier #(.width(32)) multiplier_6 (.a(a), .b(c), .out(multiplier_6_out));  // open: cin, cout
  Multiplier #(.width(32)) multiplier_7 (.a(c), .b(d), .out(multiplier_7_out));  // open: cin, cout
  Adder #(.width(32)) adder_1 (.a(multiplier_1_out), .b(multiplier_2_out), .out(a_tilde));  // open: cin, cout
  Adder #(.width(32)) adder_2 (.a(multiplier_1_out), .b(multiplier_2_out), .out(adder_2_out));  // open: cin, cout
  Adder #(.width(32)) adder_3 (.a(adder_2_out), .b(adder_4_out), .out(b_tilde));  // open: cin, cout
  Adder #(.width(32)) adder_4 (.a(multiplier_3_out), .b(multiplier_4_out), .out(adder_4_out));  // open: cin, cout
  Adder #(.width(32)) adder_5 (.a(multiplier_4_out), .b(multiplier_5_out), .out(c_tilde));  // open: cin, cout
  Adder #(.width(32)) adder_6 (.a(multiplier_5_out), .b(multiplier_6_out), .out(adder_6_out));  // open: cin, cout
  Adder #(.width(32)) adder_7 (.a(adder_6_out), .b(adder_8_out), .out(d_tilde));  // open: cin, cout
  Adder #(.width(32)) adder_8 (.a(multiplier_7_out), .b(multiplier_4_out), .out(adder_8_out));  // open: cin, cout

  // Notes on the sheet:
  //   cd
  //   ab
  //   bd
  //   aa
  //   bc
  //   dd
  //   ac
endmodule

module \矩阵快速幂算法迭代模块  (
  input  start,
  input  ni_1,
  input  clr,
  input  clk,
  output [31:0] out_5
);

  wire [31:0] ena_1_a_2, ena_1_b_2, ena_1_c_2, ena_1_d_2, multiplexer_1_out, multiplexer_2_out,
       multiplexer_3_out, multiplexer_4_out, multiplexer_5_out, multiplexer_6_out, multiplexer_7_out,
       multiplexer_8_out, sqrx_1_a_tilde, sqrx_1_b_tilde, sqrx_1_c_tilde, sqrx_1_d_tilde, sqrx_a_1_a_tilde,
       sqrx_a_1_b_tilde, sqrx_a_1_c_tilde, sqrx_a_1_d_tilde;

  Multiplexer #(.width(32), .enable("false")) multiplexer_1 (
    .in0({32{1'b0}}), .in1(multiplexer_5_out), .out(multiplexer_1_out), .sel(start));
  Multiplexer #(.width(32), .enable("false")) multiplexer_2 (
    .in0(32'h1), .in1(multiplexer_6_out), .out(multiplexer_2_out), .sel(start));
  Multiplexer #(.width(32), .enable("false")) multiplexer_3 (
    .in0(32'h1), .in1(multiplexer_7_out), .out(multiplexer_3_out), .sel(start));
  Multiplexer #(.width(32), .enable("false")) multiplexer_4 (
    .in0(32'h1), .in1(multiplexer_8_out), .out(multiplexer_4_out), .sel(start));
  ENA ena_1 (
    .a(multiplexer_1_out), .b(multiplexer_2_out), .c(multiplexer_3_out), .d(multiplexer_4_out), .clr(clr),
    .clk(clk), .a_2(ena_1_a_2), .b_2(ena_1_b_2), .c_2(ena_1_c_2), .d_2(ena_1_d_2));
  sqrX sqrx_1 (
    .a(ena_1_a_2), .b(ena_1_b_2), .c(ena_1_c_2), .d(ena_1_d_2), .a_tilde(sqrx_1_a_tilde),
    .b_tilde(sqrx_1_b_tilde), .c_tilde(sqrx_1_c_tilde), .d_tilde(sqrx_1_d_tilde));
  sqrX_A sqrx_a_1 (
    .a(ena_1_a_2), .b(ena_1_b_2), .c(ena_1_c_2), .d(ena_1_d_2), .a_tilde(sqrx_a_1_a_tilde),
    .b_tilde(sqrx_a_1_b_tilde), .c_tilde(sqrx_a_1_c_tilde), .d_tilde(sqrx_a_1_d_tilde));
  Multiplexer #(.width(32), .enable("false")) multiplexer_5 (
    .in0(sqrx_1_a_tilde), .in1(sqrx_a_1_a_tilde), .out(multiplexer_5_out), .sel(ni_1));
  Multiplexer #(.width(32), .enable("false")) multiplexer_6 (
    .in0(sqrx_1_b_tilde), .in1(sqrx_a_1_b_tilde), .out(multiplexer_6_out), .sel(ni_1));
  Multiplexer #(.width(32), .enable("false")) multiplexer_7 (
    .in0(sqrx_1_c_tilde), .in1(sqrx_a_1_c_tilde), .out(multiplexer_7_out), .sel(ni_1));
  Multiplexer #(.width(32), .enable("false")) multiplexer_8 (
    .in0(sqrx_1_d_tilde), .in1(sqrx_a_1_d_tilde), .out(multiplexer_8_out), .sel(ni_1));
  Multiplexer #(.width(32), .enable("false")) multiplexer_9 (
    .in0({32{1'b0}}), .in1(ena_1_b_2), .out(out_5), .sel(start));

  // Other names for the same wires on the sheet: s = start
endmodule

module \Fibonacci数显示模块  (
  input  [31:0] in_1,
  output [3:0] out_2,
  output [3:0] out_3,
  output [3:0] out_4,
  output [3:0] out_5,
  output [3:0] out_6,
  output [3:0] out_7,
  output [3:0] out_8,
  output [3:0] out_9,
  output [3:0] out_10,
  output [3:0] out_11
);

  wire [31:0] divider_1_out, divider_2_out, divider_3_out, divider_4_out, divider_5_out, divider_6_out,
       divider_7_out, divider_8_out, divider_9_out;
  wire [31:4] divider_1_rem, divider_2_rem, divider_3_rem, divider_4_rem, divider_5_rem, divider_6_rem,
       divider_7_rem, divider_8_rem, divider_9_rem, divider_10_rem;

  Divider #(.width(32)) divider_1 (
    .a(in_1), .b(32'ha), .out(divider_1_out), .rem({divider_1_rem, out_2}));  // open: upper
  Divider #(.width(32)) divider_2 (
    .a(divider_1_out), .b(32'ha), .out(divider_2_out), .rem({divider_2_rem, out_3}));  // open: upper
  Divider #(.width(32)) divider_3 (
    .a(divider_2_out), .b(32'ha), .out(divider_3_out), .rem({divider_3_rem, out_4}));  // open: upper
  Divider #(.width(32)) divider_4 (
    .a(divider_3_out), .b(32'ha), .out(divider_4_out), .rem({divider_4_rem, out_5}));  // open: upper
  Divider #(.width(32)) divider_5 (
    .a(divider_4_out), .b(32'ha), .out(divider_5_out), .rem({divider_5_rem, out_6}));  // open: upper
  Divider #(.width(32)) divider_6 (
    .a(divider_5_out), .b(32'ha), .out(divider_6_out), .rem({divider_6_rem, out_7}));  // open: upper
  Divider #(.width(32)) divider_7 (
    .a(divider_6_out), .b(32'ha), .out(divider_7_out), .rem({divider_7_rem, out_8}));  // open: upper
  Divider #(.width(32)) divider_8 (
    .a(divider_7_out), .b(32'ha), .out(divider_8_out), .rem({divider_8_rem, out_9}));  // open: upper
  Divider #(.width(32)) divider_9 (
    .a(divider_8_out), .b(32'ha), .out(divider_9_out), .rem({divider_9_rem, out_10}));  // open: upper
  Divider #(.width(32)) divider_10 (.a(divider_9_out), .b(32'ha), .rem({divider_10_rem, out_11}));  // open: out, upper
endmodule

module Controller (
  input  [5:0] in_1,
  input  clear,
  input  clock,
  output Ni_1,
  output start,
  output clr,
  output clear_2
);

  wire _5, and_1_out, and_3_out, and_4_out, and_5_out, buffer_1_out, buffer_2_out, buffer_3_out,
       buffer_4_out, buffer_5_out, buffer_6_out, buffer_7_out, buffer_9_out, buffer_10_out, D, d_ff_1_qn,
       main_1_a0, main_1_a3, not_1_out, not_2_out, or_1_out, or_2_out, or_3_out, shift_register_1_out,
       shift_register_1_q5;

  or or_1 (or_1_out, _5, clear);
  and and_1 (and_1_out, D, clock);
  buf buffer_1 (buffer_1_out, clock);
  D_Flip_Flop d_ff_1 (.clk(clear), .D(d_ff_1_qn), .Q(D), .Qn(d_ff_1_qn), .reset(_5));  // open: preset, en
  and and_2 (_5, main_1_a3, main_1_a0);
  \四位二进制可逆计数器_main  main_1 (
    .A0(main_1_a0), .A3(main_1_a3), .CPd(1'b0), .CPu(and_1_out), .CLR(or_1_out));  // open: A2, A4
  and and_3 (and_3_out, clear, D);
  and and_4 (and_4_out, buffer_1_out, D);
  buf buffer_2 (buffer_2_out, clear);
  Shift_Register #(.length(6)) shift_register_1 (
    .in(1'b0), .clk(or_2_out), .out(shift_register_1_out), .load(clear), .d0(in_1[0]), .d1(in_1[1]),
    .d2(in_1[2]), .d3(in_1[3]), .d4(in_1[4]), .d5(in_1[5]), .q5(shift_register_1_q5));  // open: shift, clr, q0, q1, q2, q3, q4
  or or_2 (or_2_out, and_3_out, and_4_out);
  buf buffer_3 (buffer_3_out, buffer_2_out);
  not not_1 (not_1_out, start);
  buf buffer_4 (buffer_4_out, clock);
  or or_3 (or_3_out, buffer_3_out, and_5_out);
  and and_5 (and_5_out, not_1_out, buffer_4_out);
  buf buffer_5 (buffer_5_out, buffer_6_out);
  buf buffer_6 (buffer_6_out, buffer_7_out);
  buf buffer_7 (buffer_7_out, shift_register_1_out);
  D_Flip_Flop #(.trigger("falling")) d_ff_2 (
    .clk(or_3_out), .D(shift_register_1_q5), .Q(start));  // open: Qn, preset, en, reset
  not not_2 (not_2_out, or_3_out);
  buf buffer_8 (clear_2, buffer_9_out);
  buf buffer_9 (buffer_9_out, buffer_10_out);
  buf buffer_10 (buffer_10_out, clear);
  buf buffer_11 (Ni_1, buffer_5_out);
  and and_6 (clr, clock, not_2_out, D);
endmodule

module ENA (
  input  [31:0] a,
  input  [31:0] b,
  input  [31:0] c,
  input  [31:0] d,
  input  clr,
  input  clk,
  output [31:0] a_2,
  output [31:0] b_2,
  output [31:0] c_2,
  output [31:0] d_2
);

  wire or_1_out;
  wire [31:0] multiplexer_1_out, multiplexer_2_out, multiplexer_3_out, multiplexer_4_out;

  Multiplexer #(.width(32), .enable("false")) multiplexer_1 (
    .in0(a), .in1({32{1'b0}}), .out(multiplexer_1_out), .sel(clr));
  Multiplexer #(.width(32), .enable("false")) multiplexer_2 (.in0(b), .in1(32'h1), .out(multiplexer_2_out), .sel(clr));
  Multiplexer #(.width(32), .enable("false")) multiplexer_3 (.in0(c), .in1(32'h1), .out(multiplexer_3_out), .sel(clr));
  Multiplexer #(.width(32), .enable("false")) multiplexer_4 (.in0(d), .in1(32'h1), .out(multiplexer_4_out), .sel(clr));
  or or_1 (or_1_out, clr, clk);
  Register #(.width(32), .trigger("falling")) register_1 (
    .D(multiplexer_1_out), .Q(a_2), .clk(or_1_out));  // open: en, clr
  Register #(.width(32), .trigger("falling")) register_2 (
    .D(multiplexer_2_out), .Q(b_2), .clk(or_1_out));  // open: en, clr
  Register #(.width(32), .trigger("falling")) register_3 (
    .D(multiplexer_3_out), .Q(c_2), .clk(or_1_out));  // open: en, clr
  Register #(.width(32), .trigger("falling")) register_4 (
    .D(multiplexer_4_out), .Q(d_2), .clk(or_1_out));  // open: en, clr
endmodule

module Controller_2 (
  input  [5:0] in_1,
  input  clear,
  input  clock,
  output start,
  output ni_1,
  output clear_2,
  output clk
);

  wire _5, and_1_out, and_2_out, and_3_out, buffer_1_out, buffer_3_out, buffer_4_out, D, d_ff_1_qn,
       main_1_a2, main_1_a3, not_1_out, not_2_out, not_3_out, or_1_out, or_2_out, or_3_out, s_r_ff_1_q,
       shift_register_1_out, shift_register_1_q5;

  or or_1 (or_1_out, _5, clear);
  S_R_Flip_Flop #(.trigger("falling")) s_r_ff_1 (
    .Q(s_r_ff_1_q), .preset(clear), .reset(clock));  // open: S, clk, R, Qn, en
  and and_1 (and_1_out, D, clock);
  and and_2 (and_2_out, clock, D);
  buf or_2 (or_2_out, and_2_out);  // OR_Gate
  not not_1 (not_1_out, start);
  and and_3 (and_3_out, not_1_out, clock);
  D_Flip_Flop #(.trigger("falling")) d_ff_1 (
    .D(d_ff_1_qn), .Q(D), .Qn(d_ff_1_qn), .preset(clear), .reset(_5));  // open: clk, en
  and and_4 (_5, main_1_a3, main_1_a2);
  \四位二进制可逆计数器_main  main_1 (
    .A2(main_1_a2), .A3(main_1_a3), .CPd(1'b0), .CPu(and_1_out), .CLR(or_1_out));  // open: A0, A4
  Shift_Register #(.length(6)) shift_register_1 (
    .in(1'b0), .clk(or_2_out), .out(shift_register_1_out), .load(s_r_ff_1_q), .clr(not_2_out), .d0(in_1[0]),
    .d1(in_1[1]), .d2(in_1[2]), .d3(in_1[3]), .d4(in_1[4]), .d5(in_1[5]), .q5(shift_register_1_q5));  // open: shift, q0, q1, q2, q3, q4
  not not_2 (not_2_out, D);
  or or_3 (or_3_out, clear, and_3_out);
  D_Flip_Flop #(.trigger("falling")) d_ff_2 (
    .clk(or_3_out), .D(shift_register_1_out), .Q(start), .reset(clear));  // open: Qn, preset, en
  buf buffer_1 (buffer_1_out, shift_register_1_q5);
  buf buffer_2 (ni_1, buffer_3_out);
  buf buffer_3 (buffer_3_out, buffer_4_out);
  buf buffer_4 (buffer_4_out, buffer_1_out);
  not not_3 (not_3_out, or_3_out);
  and and_5 (clk, clock, not_3_out, D);

  assign clear_2 = clear;
endmodule
