// Logisim project 数电实验一.circ as structural Verilog: 3 circuits, main circuit main
module main (
  input  A,
  input  B,
  input  C,
  output S,
  output Co
);

  wire and_1_out, and_2_out, and_3_out, xor_1_out;

  xor xor_1 (xor_1_out, A, B);
  and and_1 (and_1_out, B, A);
  and and_2 (and_2_out, C, A);
  xor xor_2 (S, xor_1_out, C);
  and and_3 (and_3_out, C, B);
  or or_1 (Co, and_1_out, and_2_out, and_3_out);

  // Notes on the sheet:
  //   C0
endmodule

module _1 (
  input  B,
  input  A,
  output S,
  output C
);

  xor xor_1 (S, B, A);
  and and_1 (C, B, A);
endmodule

module _3 (
  input  A3,
  input  B3,
  input  A2,
  input  B2,
  input  A1,
  input  B1,
  input  A0,
  input  B0,
  input  C0,
  output S3,
  output C4,
  output S2,
  output S1,
  output S0
);

  wire main_2_co, main_3_co, main_4_co;

  main main_1 (.A(A3), .B(B3), .C(main_2_co), .S(S3), .Co(C4));
  main main_2 (.A(A2), .B(B2), .C(main_3_co), .S(S2), .Co(main_2_co));
  main main_3 (.A(A1), .B(B1), .C(main_4_co), .S(S1), .Co(main_3_co));
  main main_4 (.A(A0), .B(B0), .C(C0), .S(S0), .Co(main_4_co));
endmodule
