// Logisim project 32x32乘法器设计.circ as structural Verilog: 2 circuits, main circuit main
module main (
  input  [31:0] a_31_0,
  input  [31:0] b_31_0,
  output [31:0] p_31_0
);

  wire [31:0] adder_1_out, adder_2_out, adder_3_out, adder_4_out, adder_5_out, adder_6_out, main_1_p_31_0,
       main_2_p_31_0, main_3_p_31_0, main_4_p_31_0, main_5_p_31_0, main_6_p_31_0, main_7_p_31_0,
       main_8_p_31_0, shifter_1_out, shifter_2_out, shifter_3_out, shifter_4_out, shifter_5_out,
       shifter_6_out, shifter_7_out;

  \_32x4乘法器设计_main  main_1 (.a_3_0(a_31_0[31:28]), .b_31_0(b_31_0), .p_31_0(main_1_p_31_0));
  \_32x4乘法器设计_main  main_2 (.a_3_0(a_31_0[27:24]), .b_31_0(b_31_0), .p_31_0(main_2_p_31_0));
  \_32x4乘法器设计_main  main_3 (.a_3_0(a_31_0[23:20]), .b_31_0(b_31_0), .p_31_0(main_3_p_31_0));
  \_32x4乘法器设计_main  main_4 (.a_3_0(a_31_0[19:16]), .b_31_0(b_31_0), .p_31_0(main_4_p_31_0));
  \_32x4乘法器设计_main  main_5 (.a_3_0(a_31_0[15:12]), .b_31_0(b_31_0), .p_31_0(main_5_p_31_0));
  \_32x4乘法器设计_main  main_6 (.a_3_0(a_31_0[11:8]), .b_31_0(b_31_0), .p_31_0(main_6_p_31_0));
  \_32x4乘法器设计_main  main_7 (.a_3_0(a_31_0[7:4]), .b_31_0(b_31_0), .p_31_0(main_7_p_31_0));
  \_32x4乘法器设计_main  main_8 (.a_3_0(a_31_0[3:0]), .b_31_0(b_31_0), .p_31_0(main_8_p_31_0));
  Shifter #(.width(32)) shifter_1 (.in(main_1_p_31_0), .\dist (5'b11100), .out(shifter_1_out));
  Shifter #(.width(32)) shifter_2 (.in(main_2_p_31_0), .\dist (5'b11000), .out(shifter_2_out));
  Shifter #(.width(32)) shifter_3 (.in(main_3_p_31_0), .\dist (5'b10100), .out(shifter_3_out));
  Shifter #(.width(32)) shifter_4 (.in(main_4_p_31_0), .\dist (5'b10000), .out(shifter_4_out));
  Shifter #(.width(32)) shifter_5 (.in(main_5_p_31_0), .\dist (5'b01100), .out(shifter_5_out));
  Shifter #(.width(32)) shifter_6 (.in(main_6_p_31_0), .\dist (5'b01000), .out(shifter_6_out));
  Shifter #(.width(32)) shifter_7 (.in(main_7_p_31_0), .\dist (5'b00100), .out(shifter_7_out));
  Adder #(.width(32)) adder_1 (.a(shifter_1_out), .b(shifter_2_out), .out(adder_1_out));  // open: cin, cout
  Adder #(.width(32)) adder_2 (.a(shifter_3_out), .b(shifter_4_out), .out(adder_2_out));  // open: cin, cout
  Adder #(.width(32)) adder_3 (.a(shifter_5_out), .b(shifter_6_out), .out(adder_3_out));  // open: cin, cout
  Adder #(.width(32)) adder_4 (.a(shifter_7_out), .b(main_8_p_31_0), .out(adder_4_out));  // open: cin, cout
  Adder #(.width(32)) adder_5 (.a(adder_1_out), .b(adder_2_out), .out(adder_5_out));  // open: cin, cout
  Adder #(.width(32)) adder_6 (.a(adder_3_out), .b(adder_4_out), .out(adder_6_out));  // open: cin, cout
  Adder #(.width(32)) adder_7 (.a(adder_5_out), .b(adder_6_out), .out(p_31_0));  // open: cin, cout
endmodule

module \_32X32c乘法器设计  (
  input  [31:0] in_1,
  input  [31:0] in_2,
  output [31:0] out_3
);

  main main_1 (.b_31_0(in_2), .p_31_0(out_3), .a_31_0(in_1));
endmodule
