// Logisim project 32x4乘法器设计.circ as structural Verilog: 2 circuits, main circuit main
module main (
  input  [3:0] a_3_0,
  input  [31:0] b_31_0,
  output [31:0] p_31_0
);

  wire [31:0] adder_1_out, adder_2_out, adder_3_out, adder_4_out, multiplexer_1_out, multiplexer_2_out,
       multiplexer_3_out, shifter_1_out, shifter_2_out, shifter_3_out;

  Adder #(.width(32)) adder_1 (.a({32{1'b0}}), .b(b_31_0), .out(adder_1_out));  // open: cin, cout
  Shifter #(.width(32)) shifter_1 (.in(b_31_0), .\dist (5'b00001), .out(shifter_1_out));
  Multiplexer #(.width(32), .enable("false")) multiplexer_1 (
    .in0({32{1'b0}}), .in1(adder_1_out), .out(multiplexer_1_out), .sel(a_3_0[0]));
  Adder #(.width(32)) adder_2 (.a(multiplexer_1_out), .b(shifter_1_out), .out(adder_2_out));  // open: cin, cout
  Shifter #(.width(32)) shifter_2 (.in(shifter_1_out), .\dist (5'b00001), .out(shifter_2_out));
  Multiplexer #(.width(32), .enable("false")) multiplexer_2 (
    .in0(multiplexer_1_out), .in1(adder_2_out), .out(multiplexer_2_out), .sel(a_3_0[1]));
  Multiplexer #(.width(32), .enable("false")) multiplexer_3 (
    .in0(multiplexer_2_out), .in1(adder_3_out), .out(multiplexer_3_out), .sel(a_3_0[2]));
  Adder #(.width(32)) adder_3 (.a(multiplexer_2_out), .b(shifter_2_out), .out(adder_3_out));  // open: cin, cout
  Shifter #(.width(32)) shifter_3 (.in(shifter_2_out), .\dist (5'b00001), .out(shifter_3_out));
  Adder #(.width(32)) adder_4 (.a(multiplexer_3_out), .b(shifter_3_out), .out(adder_4_out));  // open: cin, cout
  Shifter #(.width(32)) shifter_4 (.in(shifter_3_out), .\dist (5'b00001));  // open: out
  Multiplexer #(.width(32), .enable("false")) multiplexer_4 (
    .in0(multiplexer_3_out), .in1(adder_4_out), .out(p_31_0), .sel(a_3_0[3]));
endmodule

module \_32X4乘法设计  (
  input  [3:0] in_1,
  input  [31:0] in_2,
  output [31:0] out_3
);

  main main_1 (.a_3_0(in_1), .b_31_0(in_2), .p_31_0(out_3));
endmodule
