// Logisim project 7段译码器.circ as structural Verilog: 3 circuits, main circuit main
module main (
  input  A3,
  input  A2,
  input  A1,
  input  A0,
  output A,
  output B,
  output C,
  output D,
  output E,
  output F,
  output G
);

  wire and_1_out, and_2_out, and_3_out, and_4_out, and_5_out, and_6_out, and_7_out, and_8_out, and_9_out,
       and_10_out, and_11_out, and_12_out, and_13_out, and_14_out, and_15_out, and_16_out, and_17_out,
       and_18_out, and_19_out, and_20_out, and_21_out, not_1_out, not_2_out, not_3_out, not_4_out;

  not not_1 (not_1_out, A2);
  not not_2 (not_2_out, A3);
  not not_3 (not_3_out, A0);
  not not_4 (not_4_out, A1);
  and and_1 (and_1_out, not_1_out, not_4_out, not_3_out);
  and and_2 (and_2_out, not_2_out, not_1_out, A1);
  and and_3 (and_3_out, not_2_out, A2, A0);
  and and_4 (and_4_out, A3, not_4_out, A0);
  and and_5 (and_5_out, not_2_out, A1, A0);
  and and_6 (and_6_out, not_2_out, not_1_out);
  and and_7 (and_7_out, not_4_out, not_3_out);
  and and_8 (and_8_out, not_1_out, not_4_out);
  and and_9 (and_9_out, not_2_out, A2);
  and and_10 (and_10_out, not_1_out, A0);
  and and_11 (and_11_out, not_1_out, not_3_out);
  and and_12 (and_12_out, A2, not_4_out, A0);
  and and_13 (and_13_out, not_1_out, A1, A0);
  and and_14 (and_14_out, A2, A1, not_3_out);
  and and_15 (and_15_out, A1, not_3_out);
  and and_16 (and_16_out, not_4_out, not_3_out);
  and and_17 (and_17_out, A2, not_4_out);
  and and_18 (and_18_out, A2, not_3_out);
  and and_19 (and_19_out, A3, not_1_out, not_4_out);
  and and_20 (and_20_out, not_1_out, A3);
  and and_21 (and_21_out, not_1_out, A1);
  or or_1 (A, and_1_out, and_2_out, and_3_out, and_4_out);
  or or_2 (B, and_5_out, and_6_out, and_7_out, and_8_out);
  or or_3 (C, and_8_out, and_9_out, and_10_out);
  or or_4 (D, and_11_out, and_12_out, and_13_out, and_14_out);
  or or_5 (E, and_11_out, and_15_out);
  or or_6 (F, and_16_out, and_17_out, and_18_out, and_19_out);
  or or_7 (G, and_15_out, and_17_out, and_20_out, and_21_out);
endmodule

module \_7段译码器  (
  input  in_1,
  input  in_2,
  input  in_3,
  input  in_4,
  output out_5,
  output out_6,
  output out_7,
  output out_8,
  output out_9,
  output out_10,
  output out_11
);

  main main_1 (
    .A3(in_1), .A2(in_2), .A1(in_3), .A0(in_4), .A(out_5), .B(out_6), .C(out_7), .D(out_8), .E(out_9),
    .F(out_10), .G(out_11));
endmodule

module \_7段数码显示管显示人数电路  (
  input  in_1,
  input  in_2,
  input  in_3,
  input  in_4
);

  wire main_1_a, main_1_b, main_1_c, main_1_d, main_1_e, main_1_f, main_1_g, main_2_s1, main_2_s2, main_2_s4,
       main_2_s8, main_2_s10, main_2_s20, main_2_s40, main_2_s80, main_3_a, main_3_b, main_3_c, main_3_d,
       main_3_e, main_3_f, main_3_g;

  _7_Segment_Display u_7_segment_display_1 (
    .g(main_1_g), .f(main_1_f), .a(main_1_a), .b(main_1_b), .e(main_1_e), .d(main_1_d), .c(main_1_c));  // open: dp
  main main_1 (
    .A3(main_2_s80), .A2(main_2_s40), .A1(main_2_s20), .A0(main_2_s10), .A(main_1_a), .B(main_1_b),
    .C(main_1_c), .D(main_1_d), .E(main_1_e), .F(main_1_f), .G(main_1_g));
  \四位二进制转8421码_main  main_2 (
    .S80(main_2_s80), .S40(main_2_s40), .S20(main_2_s20), .S10(main_2_s10), .S8(main_2_s8), .S4(main_2_s4),
    .S2(main_2_s2), .S1(main_2_s1), .A3(in_1), .A2(in_2), .A1(in_3), .A0(in_4));
  _7_Segment_Display u_7_segment_display_2 (
    .g(main_3_g), .f(main_3_f), .a(main_3_a), .b(main_3_b), .e(main_3_e), .d(main_3_d), .c(main_3_c));  // open: dp
  main main_3 (
    .A3(main_2_s8), .A2(main_2_s4), .A1(main_2_s2), .A0(main_2_s1), .A(main_3_a), .B(main_3_b), .C(main_3_c),
    .D(main_3_d), .E(main_3_e), .F(main_3_f), .G(main_3_g));
endmodule
