// Logisim project 四位二进制可逆计数器.circ as structural Verilog: 2 circuits, main circuit main
module main (
  input  CPd,
  input  CPu,
  input  CLR,
  output A0,
  output A2,
  output A3,
  output A4
);

  wire and_1_out, and_2_out, and_3_out, and_4_out, and_5_out, and_6_out, d_ff_1_qn, d_ff_2_qn, d_ff_3_qn,
       d_ff_4_qn, or_1_out, or_2_out, or_3_out, or_4_out;

  D_Flip_Flop #(.trigger("falling")) d_ff_1 (
    .clk(or_1_out), .D(d_ff_1_qn), .Q(A0), .Qn(d_ff_1_qn), .reset(CLR));  // open: preset, en
  or or_1 (or_1_out, CPd, CPu);
  D_Flip_Flop #(.trigger("falling")) d_ff_2 (
    .clk(or_2_out), .D(d_ff_2_qn), .Q(A2), .Qn(d_ff_2_qn), .reset(CLR));  // open: preset, en
  or or_2 (or_2_out, and_1_out, and_2_out);
  and and_1 (and_1_out, CPd, d_ff_1_qn);
  and and_2 (and_2_out, A0, CPu);
  and and_3 (and_3_out, CPd, d_ff_1_qn, d_ff_2_qn);
  D_Flip_Flop #(.trigger("falling")) d_ff_3 (
    .clk(or_3_out), .D(d_ff_3_qn), .Q(A3), .Qn(d_ff_3_qn), .reset(CLR));  // open: preset, en
  or or_3 (or_3_out, and_3_out, and_4_out);
  and and_4 (and_4_out, A0, A2, CPu);
  D_Flip_Flop #(.trigger("falling")) d_ff_4 (
    .clk(or_4_out), .D(d_ff_4_qn), .Q(A4), .Qn(d_ff_4_qn), .reset(CLR));  // open: preset, en
  or or_4 (or_4_out, and_6_out, and_5_out);
  and and_5 (and_5_out, A0, A2, A3, CPu);
  and and_6 (and_6_out, CPd, d_ff_1_qn, d_ff_2_qn, d_ff_3_qn);
endmodule

module \四位二进制可逆计数器  (
  input  in_1,
  input  in_2,
  input  in_3,
  output out_4,
  output out_5,
  output out_6,
  output out_7
);

  main main_1 (.A0(out_7), .A2(out_6), .A3(out_5), .A4(out_4), .CPd(in_3), .CPu(in_1), .CLR(in_2));
endmodule
