// Logisim project 小型实验室门禁系统电路.circ as structural Verilog: 2 circuits, main circuit main
module main (
  input  in_1,
  input  in_2,
  input  in_3,
  output out_4,
  output out_5,
  output out_6,
  output out_7,
  output out_8,
  output out_9,
  output out_10,
  output out_11,
  output out_12,
  output out_13,
  output out_14,
  output out_15,
  output out_16,
  output out_17,
  output out_18
);

  wire main_2_s1, main_2_s2, main_2_s4, main_2_s8, main_2_s10, main_2_s20, main_2_s40, main_2_s80,
       main_3_out_4, main_3_out_5, main_3_out_6, main_3_out_7;

  \_7段译码器_main  main_1 (
    .A3(main_2_s80), .A2(main_2_s40), .A1(main_2_s20), .A0(main_2_s10), .A(out_4), .B(out_5), .C(out_6),
    .D(out_7), .E(out_8), .F(out_9), .G(out_10));
  \四位二进制转8421码_main  main_2 (
    .S80(main_2_s80), .S40(main_2_s40), .S20(main_2_s20), .S10(main_2_s10), .S8(main_2_s8), .S4(main_2_s4),
    .S2(main_2_s2), .S1(main_2_s1), .A3(main_3_out_4), .A2(main_3_out_5), .A1(main_3_out_6), .A0(main_3_out_7));
  \报警电路_main  main_3 (
    .U(in_1), .CLR(in_2), .D(in_3), .out_4(main_3_out_4), .out_5(main_3_out_5), .out_6(main_3_out_6),
    .out_7(main_3_out_7), .out_8(out_18));
  \_7段译码器_main  main_4 (
    .A3(main_2_s8), .A2(main_2_s4), .A1(main_2_s2), .A0(main_2_s1), .A(out_11), .B(out_12), .C(out_13),
    .D(out_14), .E(out_15), .F(out_16), .G(out_17));
endmodule

module \小型实验室门禁系统电路  (
  input  in_1
);

  wire button_1_out, button_2_out, main_1_out_4, main_1_out_5, main_1_out_6, main_1_out_7, main_1_out_8,
       main_1_out_9, main_1_out_10, main_1_out_11, main_1_out_12, main_1_out_13, main_1_out_14,
       main_1_out_15, main_1_out_16, main_1_out_17, main_1_out_18;

  Button button_1 (.out(button_1_out));
  Button button_2 (.out(button_2_out));
  _7_Segment_Display u_7_segment_display_1 (
    .g(main_1_out_10), .f(main_1_out_9), .a(main_1_out_4), .b(main_1_out_5), .e(main_1_out_8),
    .d(main_1_out_7), .c(main_1_out_6));  // open: dp
  _7_Segment_Display u_7_segment_display_2 (
    .g(main_1_out_17), .f(main_1_out_16), .a(main_1_out_11), .b(main_1_out_12), .e(main_1_out_15),
    .d(main_1_out_14), .c(main_1_out_13));  // open: dp
  main main_1 (
    .in_1(button_1_out), .in_2(in_1), .in_3(button_2_out), .out_18(main_1_out_18), .out_4(main_1_out_4),
    .out_5(main_1_out_5), .out_6(main_1_out_6), .out_7(main_1_out_7), .out_8(main_1_out_8),
    .out_9(main_1_out_9), .out_10(main_1_out_10), .out_11(main_1_out_11), .out_12(main_1_out_12),
    .out_13(main_1_out_13), .out_14(main_1_out_14), .out_15(main_1_out_15), .out_16(main_1_out_16),
    .out_17(main_1_out_17));
  LED led_1 (.in(main_1_out_18));
endmodule
