// Logisim project 多功能电子钟系统设计.circ as structural Verilog: 7 circuits, main circuit main
module main (
  input  CPU,
  input  CLR,
  input  CPD,
  input  adj,
  output out_5,
  output out_6,
  output out_7,
  output out_8,
  output out_9,
  output out_10,
  output out_11,
  output out_12,
  output QCC
);

  wire and_1_out, and_2_out, and_3_out, and_4_out, and_5_out, nor_1_out, nor_2_out, not_1_out, or_1_out;

  and and_1 (and_1_out, out_11, out_10);
  or or_1 (or_1_out, and_1_out, CLR, and_3_out);
  and and_2 (and_2_out, CPD, adj);
  and and_3 (and_3_out, and_2_out, nor_1_out, nor_2_out);
  \四位二进制可逆计数器  \u_四位二进制可逆计数器_1  (
    .A0(out_8), .A2(out_7), .A3(out_6), .A4(out_5), .CPu(CPU), .CPd(and_2_out), .CLR(or_1_out));
  and and_4 (and_4_out, CPU, out_5, out_8);
  nor nor_1 (nor_1_out, out_7, out_6, out_5, out_8);
  not not_1 (not_1_out, nor_2_out);
  and and_5 (and_5_out, nor_1_out, and_2_out, not_1_out);
  \四位二进制可逆计数器_main  main_1 (
    .A0(out_12), .A2(out_11), .A3(out_10), .A4(out_9), .CPd(and_5_out), .CPu(and_4_out), .CLR(or_1_out));
  and and_6 (QCC, out_10, out_12, and_4_out);
  nor nor_2 (nor_2_out, out_12, out_11, out_10, out_9);
endmodule

module \四位二进制可逆计数器  (
  input  CPd,
  input  CPu,
  input  CLR,
  output A0,
  output A2,
  output A3,
  output A4
);

  wire and_1_out, and_2_out, and_3_out, and_4_out, and_5_out, and_6_out, and_7_out, d_ff_1_qn, d_ff_2_qn,
       d_ff_3_qn, d_ff_4_qn, nand_1_out, or_1_out, or_2_out, or_3_out, or_4_out, or_5_out, or_6_out;

  or or_1 (or_1_out, A0, A2, A3, A4);
  D_Flip_Flop #(.trigger("falling")) d_ff_1 (
    .clk(or_2_out), .D(d_ff_1_qn), .Q(A0), .Qn(d_ff_1_qn), .reset(or_5_out));  // open: preset, en
  or or_2 (or_2_out, CPd, CPu);
  D_Flip_Flop #(.trigger("falling")) d_ff_2 (
    .clk(or_3_out), .D(d_ff_2_qn), .Q(A2), .Qn(d_ff_2_qn), .reset(or_5_out));  // open: preset, en
  or or_3 (or_3_out, and_1_out, and_2_out);
  and and_1 (and_1_out, CPd, or_1_out, d_ff_1_qn);
  and and_2 (and_2_out, A0, CPu);
  and and_3 (and_3_out, CPd, or_1_out, d_ff_1_qn, d_ff_2_qn);
  D_Flip_Flop #(.trigger("falling")) d_ff_3 (
    .clk(or_4_out), .D(d_ff_3_qn), .Q(A3), .Qn(d_ff_3_qn), .reset(or_5_out));  // open: preset, en
  or or_4 (or_4_out, and_3_out, and_4_out);
  and and_4 (and_4_out, A0, A2, CPu);
  or or_5 (or_5_out, CLR, and_7_out);
  nand nand_1 (nand_1_out, A0, A3);
  D_Flip_Flop #(.trigger("falling")) d_ff_4 (
    .clk(or_6_out), .D(d_ff_4_qn), .Q(A4), .Qn(d_ff_4_qn), .reset(or_5_out));  // open: preset, en
  or or_6 (or_6_out, and_6_out, and_5_out);
  and and_5 (and_5_out, A0, A2, A3, CPu);
  and and_6 (and_6_out, CPd, d_ff_1_qn, d_ff_2_qn, d_ff_3_qn);
  and and_7 (and_7_out, A2, nand_1_out, A4);
endmodule

module \四位二级制可逆计数器2  (
  input  CPd,
  input  CPu,
  input  CLR,
  output A0,
  output A2,
  output A3,
  output A4
);

  wire and_1_out, and_2_out, and_3_out, and_4_out, and_5_out, and_6_out, and_7_out, d_ff_1_qn, d_ff_2_qn,
       d_ff_3_qn, d_ff_4_qn, nand_1_out, or_1_out, or_2_out, or_3_out, or_4_out, or_5_out, or_6_out;

  or or_1 (or_1_out, A0, A2, A3, A4);
  D_Flip_Flop #(.trigger("falling")) d_ff_1 (
    .clk(or_2_out), .D(d_ff_1_qn), .Q(A0), .Qn(d_ff_1_qn), .reset(or_5_out));  // open: preset, en
  or or_2 (or_2_out, CPd, CPu);
  D_Flip_Flop #(.trigger("falling")) d_ff_2 (
    .clk(or_3_out), .D(d_ff_2_qn), .Q(A2), .Qn(d_ff_2_qn), .reset(or_5_out));  // open: preset, en
  or or_3 (or_3_out, and_1_out, and_2_out);
  and and_1 (and_1_out, CPd, or_1_out, d_ff_1_qn);
  and and_2 (and_2_out, A0, CPu);
  and and_3 (and_3_out, CPd, d_ff_1_qn, d_ff_2_qn);
  D_Flip_Flop #(.trigger("falling")) d_ff_3 (
    .clk(or_4_out), .D(d_ff_3_qn), .Q(A3), .Qn(d_ff_3_qn), .reset(or_5_out));  // open: preset, en
  or or_4 (or_4_out, and_3_out, and_4_out);
  and and_4 (and_4_out, A0, A2, CPu);
  or or_5 (or_5_out, CLR, and_7_out);
  nand nand_1 (nand_1_out, A0, A3);
  D_Flip_Flop #(.trigger("falling")) d_ff_4 (
    .clk(or_6_out), .D(d_ff_4_qn), .Q(A4), .Qn(d_ff_4_qn), .reset(or_5_out));  // open: preset, en
  or or_6 (or_6_out, and_5_out, and_6_out);
  and and_5 (and_5_out, CPd, d_ff_1_qn, or_1_out, d_ff_2_qn, d_ff_3_qn);
  and and_6 (and_6_out, A0, A2, A3, CPu);
  and and_7 (and_7_out, A2, nand_1_out, A4);
endmodule

module test (
  input  in_1,
  input  in_2,
  output out_3,
  output out_4,
  output out_5,
  output out_6,
  output out_7,
  output out_8,
  output out_9,
  output out_10,
  output out_11
);

  wire and_1_out, and_3_out, and_4_out, and_5_out, and_6_out, and_7_out, button_1_out, nand_1_out, nor_1_out,
       or_1_out, undriven;

  and and_1 (and_1_out, out_5, out_5);
  and and_2 (out_11, out_6, and_4_out, out_4);
  or or_1 (or_1_out, and_1_out, and_6_out, in_2);
  and and_3 (and_3_out, out_9, out_7);
  and and_4 (and_4_out, out_10, out_7, in_1);
  and and_5 (and_5_out, out_9, out_7);
  \四位二级制可逆计数器2  \u_四位二级制可逆计数器2_1  (
    .A0(out_6), .A2(out_5), .A3(out_4), .A4(out_3), .CPd(and_7_out), .CPu(and_5_out), .CLR(or_1_out));
  Button button_1 (.out(button_1_out));
  // OR_Gate or_2 has open pins: in0=and_3_out, in1=and_6_out, out=open
  and and_6 (and_6_out, button_1_out, nand_1_out);
  \四位二进制可逆计数器  \u_四位二进制可逆计数器_1  (
    .A0(out_10), .A2(out_9), .A3(out_8), .A4(out_7), .CPu(in_1), .CPd(button_1_out), .CLR(undriven));
  nand nand_1 (nand_1_out, out_10, out_9, out_8, out_7);
  nor nor_1 (nor_1_out, out_7, out_8, out_9, out_10);
  and and_7 (and_7_out, nor_1_out, button_1_out);
endmodule

module \十二进制计数器或二十四进制的计数器电路  (
);

  \四位二进制可逆计数器  \u_四位二进制可逆计数器_1  ();  // open: A0, A2, A3, A4, CPu, CPd, CLR
  \四位二进制可逆计数器  \u_四位二进制可逆计数器_2  ();  // open: A0, A2, A3, A4, CPu, CPd, CLR
endmodule

module \测试  (
  input  in_1,
  output out_2,
  output out_3,
  output out_4,
  output out_5,
  output out_6,
  output out_7,
  output out_8,
  output out_9,
  output out_10
);

  wire button_1_out, button_2_out, button_3_out;

  Button button_1 (.out(button_1_out));
  main main_1 (
    .QCC(out_10), .out_5(out_6), .out_6(out_7), .out_7(out_8), .out_8(out_9), .out_9(out_2), .out_10(out_3),
    .out_11(out_4), .out_12(out_5), .CPU(button_2_out), .CLR(button_3_out), .CPD(button_1_out), .adj(in_1));
  Button button_2 (.out(button_2_out));
  Button button_3 (.out(button_3_out));
endmodule

module \整点报时  (
  input  in_1,
  input  in_2,
  output out_3
);

  wire and_2_out, and_3_out, d_ff_1_q, d_ff_1_qn, \四位二进制可逆计数器_1_a2 , \四位二进制可逆计数器_1_a4 ;

  and and_1 (out_3, in_1, d_ff_1_q);
  D_Flip_Flop #(.trigger("falling")) d_ff_1 (
    .clk(in_2), .D(d_ff_1_qn), .Q(d_ff_1_q), .Qn(d_ff_1_qn), .preset(d_ff_1_q), .reset(and_3_out));  // open: en
  and and_2 (and_2_out, in_1, d_ff_1_q);
  and and_3 (and_3_out, \四位二进制可逆计数器_1_a4 , \四位二进制可逆计数器_1_a2 );
  \四位二进制可逆计数器  \u_四位二进制可逆计数器_1  (
    .A2(\四位二进制可逆计数器_1_a2 ), .A4(\四位二进制可逆计数器_1_a4 ), .CPu(and_2_out), .CPd(1'b0), .CLR(1'b0));  // open: A0, A3
endmodule
