// Logisim project cpu24.circ as structural Verilog: 27 circuits, main circuit ◇单周期MIPS
module \单周期MIPS  (
  output RegWrite,
  output MemWrite,
  output [31:0] PC,
  output [31:0] IR,
  output [31:0] RDin,
  output [31:0] MDin,
  output [31:0] LedData
);

  wire and_1_out, and_2_out, BGTZ, CLK, comparator_1_eq, comparator_2_gt, Go, IR1, IR2, IR3, JAL, JMP, JR,
       JUMP, LH, mips_alu_1_equal, multiplexer_4_out, not_1_out, RegDst, SignedExt, SLLV, Syscall, W1, W2,
       W3, XORI, \中止 , \单周期硬布线控制器_1_alu_src , \单周期硬布线控制器_1_beq , \单周期硬布线控制器_1_bne , \单周期硬布线控制器_1_memtoreg ,
       \有条件分支 ;
  wire [3:0] \单周期硬布线控制器_1_alu_op ;
  wire [4:0] multiplexer_5_out, multiplexer_6_out, multiplexer_7_out, multiplexer_8_out, multiplexer_11_out;
  wire [15:0] multiplexer_14_out, \总周期数 ;
  wire [27:0] PC_4;
  wire [31:0] bit_extender_1_out, bit_extender_2_out, bit_extender_3_out, J, JR_address, mips_alu_1_result,
       multiplexer_1_out, multiplexer_2_out, multiplexer_3_out, multiplexer_9_out, multiplexer_10_out,
       multiplexer_12_out, multiplexer_13_out, ram_1_data, shifter_1_out;
  wire [31:28] J_JAL;

  Clock #(.highDuration(1), .lowDuration(1)) clock_1 (.out(CLK));
  Button _1 (.out(IR1));
  Button _2 (.out(IR2));
  Button _3 (.out(IR3));
  Button \u_继续运行  (.out(Go));
  LED #(.active("true")) led_1 (.in(W1));
  LED #(.active("true")) led_2 (.in(W2));
  LED #(.active("true")) led_3 (.in(W3));
  Multiplexer #(.select(1), .width(32), .disabled("Z"), .enable("false")) multiplexer_1 (
    .in0({J_JAL, PC_4}), .in1(J), .out(multiplexer_1_out), .sel(\有条件分支 ));
  Multiplexer #(.select(1), .width(32), .disabled("Z"), .enable("false")) multiplexer_2 (
    .in0({J_JAL, IR[25:0], 2'b00}), .in1(JR_address), .out(multiplexer_2_out), .sel(JR));
  Hex_Digit_Display hex_digit_display_1 (.value(LedData[31:28]));  // open: dp
  Multiplexer #(.select(1), .width(32), .disabled("Z"), .enable("false")) multiplexer_3 (
    .in0(multiplexer_1_out), .in1(multiplexer_2_out), .out(multiplexer_3_out), .sel(JMP));
  Comparator #(.width(32), .mode("twosComplement")) comparator_1 (
    .a(JR_address), .b(32'h22), .eq(comparator_1_eq));  // open: gt, lt
  Hex_Digit_Display hex_digit_display_2 (.value(LedData[23:20]));  // open: dp
  Hex_Digit_Display hex_digit_display_3 (.value(LedData[27:24]));  // open: dp
  Counter #(.width(16), .max('hffff), .ongoal("wrap"), .trigger("rising"), .behavior("old")) counter_1 (
    .count(\中止 ), .Q(\总周期数 ), .clk(CLK));  // open: load, D, carry, clr, preset
  Register #(.width(32), .trigger("rising"), .Select("low")) u_PC (
    .D(multiplexer_3_out), .en(\中止 ), .Q(PC), .clk(CLK));  // open: clr
  Multiplexer #(.select(1), .width(1), .disabled("Z"), .enable("false")) multiplexer_4 (
    .in0(1'b0), .in1(comparator_1_eq), .out(multiplexer_4_out), .sel(Syscall));
  Hex_Digit_Display hex_digit_display_4 (.value(LedData[15:12]));  // open: dp
  Hex_Digit_Display hex_digit_display_5 (.value(LedData[19:16]));  // open: dp
  Adder #(.width(32)) adder_1 (.a(PC), .b(32'h4), .out({J_JAL, PC_4}));  // open: cin, cout
  Register #(.width(32), .trigger("rising"), .Select("low")) register_1 (
    .D(MDin), .en(multiplexer_4_out), .Q(LedData), .clk(CLK));  // open: clr
  Hex_Digit_Display hex_digit_display_6 (.value(LedData[11:8]));  // open: dp
  Hex_Digit_Display hex_digit_display_7 (.value(LedData[7:4]));  // open: dp
  // Probe on \总周期数 
  ROM #(.addrWidth(10), .dataWidth(32), .Select("high")) rom_1 (.addr(PC[11:2]), .data(IR));
  or or_1 (\中止 , multiplexer_4_out, Go, ~Syscall);  // OR_Gate
  Hex_Digit_Display hex_digit_display_8 (.value(LedData[3:0]));  // open: dp
  assign bit_extender_1_out = {{16{1'b0}}, IR[15:0]};  // Bit_Extender bit_extender_1
  assign bit_extender_2_out = {{16{IR[15]}}, IR[15:0]};  // Bit_Extender bit_extender_2
  Multiplexer #(.select(1), .width(5), .disabled("Z"), .enable("false")) multiplexer_5 (
    .in0(IR[20:16]), .in1(IR[15:11]), .out(multiplexer_5_out), .sel(RegDst));
  Multiplexer #(.select(1), .width(5), .disabled("Z"), .enable("false")) multiplexer_6 (
    .in0(IR[25:21]), .in1(5'b00010), .out(multiplexer_6_out), .sel(Syscall));
  Multiplexer #(.select(1), .width(5), .disabled("Z"), .enable("false")) multiplexer_7 (
    .in0(IR[20:16]), .in1(5'b00100), .out(multiplexer_7_out), .sel(Syscall));
  Multiplexer #(.select(1), .width(5), .disabled("Z"), .enable("false")) multiplexer_8 (
    .in0(multiplexer_5_out), .in1({5{1'b1}}), .out(multiplexer_8_out), .sel(JAL));
  Multiplexer #(.select(1), .width(32), .disabled("Z"), .enable("false")) multiplexer_9 (
    .in0(bit_extender_1_out), .in1(bit_extender_2_out), .out(multiplexer_9_out), .sel(SignedExt));
  \单周期硬布线控制器  \u_单周期硬布线控制器_1  (
    .Func(IR[5:0]), .OP(IR[31:26]), .ALU_OP(\单周期硬布线控制器_1_alu_op ), .MemToReg(\单周期硬布线控制器_1_memtoreg ),
    .MemWrite(MemWrite), .ALU_SRC(\单周期硬布线控制器_1_alu_src ), .RegWrite(RegWrite), .SysCALL(Syscall),
    .SignedExt(SignedExt), .RegDst(RegDst), .JR(JR), .JMP(JMP), .Beq(\单周期硬布线控制器_1_beq ), .JAL(JAL),
    .Bne(\单周期硬布线控制器_1_bne ), .SLLV(SLLV), .LH(LH), .XORI(XORI), .BGTZ(BGTZ));  // open: M, MFC0, MTC0, ERET
  MIPS_Regifile mips_regifile_1 (
    .Din(RDin), .Clk(CLK), .R1(JR_address), .R2(MDin), .WE(RegWrite), .W_num(multiplexer_8_out),
    .R1_num(multiplexer_6_out), .R2_num(multiplexer_7_out));
  Shifter #(.width(32), .shift("ll")) shifter_1 (.in(bit_extender_2_out), .\dist (5'b00010), .out(shifter_1_out));
  Multiplexer #(.select(1), .width(32), .disabled("Z"), .enable("false")) multiplexer_10 (
    .in0(MDin), .in1(multiplexer_9_out), .out(multiplexer_10_out), .sel(\单周期硬布线控制器_1_alu_src ));
  Adder #(.width(32)) adder_2 (.a(shifter_1_out), .b({J_JAL, PC_4}), .out(J));  // open: cin, cout
  MIPS_ALU mips_alu_1 (
    .X(JR_address), .Y(multiplexer_10_out), .AluOP(\单周期硬布线控制器_1_alu_op ), .Equal(mips_alu_1_equal),
    .Result(mips_alu_1_result), .shamt(multiplexer_11_out));  // open: Result_2
  Multiplexer #(.select(1), .width(5), .disabled("Z"), .enable("false")) multiplexer_11 (
    .in0(IR[10:6]), .in1(JR_address[4:0]), .out(multiplexer_11_out), .sel(SLLV));
  and and_1 (and_1_out, mips_alu_1_equal, \单周期硬布线控制器_1_beq );
  not not_1 (not_1_out, mips_alu_1_equal);
  and and_2 (and_2_out, not_1_out, \单周期硬布线控制器_1_bne );
  // Probe on \单周期硬布线控制器_1_alu_op 
  // Probe on mips_alu_1_result
  or or_2 (\有条件分支 , and_1_out, JUMP, and_2_out);
  RAM #(.addrWidth(10), .dataWidth(32), .bus("separate"), .Select("high")) ram_1 (
    .addr(mips_alu_1_result[11:2]), .din(MDin), .data(ram_1_data), .str(MemWrite), .clk(CLK));  // open: sel, ld, clr
  Multiplexer #(.select(1), .width(32), .disabled("Z"), .enable("false")) multiplexer_12 (
    .in0(mips_alu_1_result), .in1(ram_1_data), .out(multiplexer_12_out), .sel(\单周期硬布线控制器_1_memtoreg ));
  Comparator #(.width(32), .mode("twosComplement")) comparator_2 (
    .a(JR_address), .b({32{1'b0}}), .gt(comparator_2_gt));  // open: eq, lt
  Multiplexer #(.select(1), .width(32), .disabled("Z"), .enable("false")) multiplexer_13 (
    .in0(multiplexer_12_out), .in1({J_JAL, PC_4}), .out(multiplexer_13_out), .sel(JAL));
  Multiplexer #(.select(1), .width(16), .disabled("Z"), .enable("false")) multiplexer_14 (
    .in0(multiplexer_12_out[15:0]), .in1(multiplexer_12_out[31:16]), .out(multiplexer_14_out),
    .sel(mips_alu_1_result[1]));
  and and_3 (JUMP, BGTZ, comparator_2_gt);
  Multiplexer #(.select(1), .width(32), .disabled("Z"), .enable("false")) multiplexer_15 (
    .in0(multiplexer_13_out), .in1(bit_extender_3_out), .out(RDin), .sel(LH));
  assign bit_extender_3_out = {{16{multiplexer_14_out[15]}}, multiplexer_14_out};  // Bit_Extender bit_extender_3

  // Other names for the same wires on the sheet: a0[31:0] = MDin; J_JAL[27:2] = IR[25:0]; shamt[4:0] = IR[10:6];
  //   SLLV_1[4:0] = JR_address[4:0]; PC_4[31:28] = J_JAL

  // Notes on the sheet:
  //   中断源
  //   中断等待指示
  //   总复位信号应将除ROM以外所有存储组件全部清零
  //   数码管输出
  //   指令存储器
  //   数码管输出应该用寄存器锁存，否则显示数据只能一闪而过
  //   contents of rom_1 (hex, n*v repeats v):
  //   20110001 8000c05 20110001 20120002 20130003 8000c09 20110001 20120002 20130003 8000c0d 20110001
  //   20120002 20130003 8000c11 20110001 20120002 20130003 c000cb8 20100001 20110001 118fc0 112020
  //   20020022 c 118882 12200001 8000c15 112020 20020022 c 20110001 118880 112020 20020022 c 12200001
  //   8000c1f 20110001 118fc0 112020 20020022 c 1188c3 112020 20020022 c 118903 112020 20020022 c 118903
  //   112020 20020022 c 118903 112020 20020022 c 118903 112020 20020022 c 118903 112020 20020022 c 118903
  //   112020 20020022 c 118903 112020 20020022 c 20100001 109fc0 139fc3 8021 2012000c 24160003 26100001
  //   3210000f 20080008 20090001 139900 2709825 132020 20020022 c 1094022 1500fff9 22100001 2018000f
  //   2188024 108700 20080008 20090001 139902 2709825 132021 20020022 c 1094022 1500fff9 108702 2c9b022
  //   12c00001 8000c50 4020 1084027 84400 3508ffff 82021 20020022 c 2010ffff 20110000 ae300000 22100001
  //   22310004 ae300000 22100001 22310004 ae300000 22100001 22310004 ae300000 22100001 22310004 ae300000
  //   22100001 22310004 ae300000 22100001 22310004 ae300000 22100001 22310004 ae300000 22100001 22310004
  //   ae300000 22100001 22310004 ae300000 22100001 22310004 ae300000 22100001 22310004 ae300000 22100001
  //   22310004 ae300000 22100001 22310004 ae300000 22100001 22310004 ae300000 22100001 22310004 ae300000
  //   22100001 22310004 22100001 8020 2011003c 8e130000 8e340000 274402a 11000002 ae330000 ae140000
  //   2231fffc 1611fff8 102020 20020022 c 22100004 2011003c 1611fff2 20020032 c 20100000 22100001 102020
  //   20020022 c 22100002 102020 20020022 c 22100003 102020 20020022 c 22100004 102020 20020022 c 22100005
  //   102020 20020022 c 22100006 102020 20020022 c 22100007 102020 20020022 c 22100008 102020 20020022
  //   20020022 c 3e00008
  //   OP
  //   Func
  //   rs
  //   指令字
  //   rt
  //   rd
  //   JMP
  //   JR
  //   OP
  //   Func
  //   为方便自动评测，需要输出PC，IR，寄存器文件写入端口RDin，内存写入端口MDin等信号
  //   Beq
  //   Bne
  //   MemToReg
  //   MemWrite
  //   AluOP
  //   AluSrcB
  //   RegWrite
  //   JAL
  //   RegDst
  //   Syscall
endmodule

module \单周期MIPS_单级中断  (
  input  IR1,
  input  IR2,
  input  IR3,
  output RegWrite,
  output MemWrite,
  output [31:0] PC,
  output [31:0] IR,
  output [31:0] RDin,
  output [31:0] MDin,
  output [31:0] LedData
);

  wire and_1_out, and_2_out, and_3_out, and_5_out, and_6_out, BGTZ, CLK, comparator_2_gt, comparator_3_eq,
       decoder_1_out1, decoder_1_out2, decoder_1_out3, ERET, Go, IR1_t, IR2_t, IR3_t, IRA, IRB, IRC, JAL,
       JMP, JR, JUMP, LH, mips_alu_1_equal, multiplexer_6_out, multiplexer_19_out, not_1_out, or_1_out,
       or_2_out, priority_encoder_1_gs, RegDst, register_2_q, SignedExt, SLLV, Start, Syscall, W1, W2, W3,
       XORI, \中断发生信号 , \中断按键参考电路_1_与中断屏蔽位与 , \中断按键参考电路_2_与中断屏蔽位与 , \中断按键参考电路_3_与中断屏蔽位与 , \中止 ,
       \单周期硬布线控制器_1_alu_src , \单周期硬布线控制器_1_beq , \单周期硬布线控制器_1_bne , \单周期硬布线控制器_1_memtoreg , \有条件分支 ;
  wire [1:0] INT_num, register_1_q;
  wire [3:0] \单周期硬布线控制器_1_alu_op ;
  wire [4:0] multiplexer_7_out, multiplexer_9_out, multiplexer_10_out, multiplexer_11_out, multiplexer_14_out;
  wire [15:0] multiplexer_17_out, \总周期数 ;
  wire [27:0] PC_4;
  wire [31:0] bit_extender_1_out, bit_extender_2_out, bit_extender_3_out, EPC_q, J, JR_address,
       mips_alu_1_result, multiplexer_1_out, multiplexer_2_out, multiplexer_3_out, multiplexer_4_out,
       multiplexer_5_out, multiplexer_12_out, multiplexer_13_out, multiplexer_15_out, multiplexer_16_out,
       ram_1_data, shifter_1_out, \服务地址 ;
  wire [31:28] J_JAL;

  Clock #(.highDuration(1), .lowDuration(1)) clock_1 (.out(CLK));
  Button _1 (.out(IRA));
  Button _2 (.out(IRB));
  Button _3 (.out(IRC));
  Button \u_继续运行  (.out(Go));
  LED #(.active("true")) led_1 (.in(W1));
  LED #(.active("true")) led_2 (.in(W2));
  LED #(.active("true")) led_3 (.in(W3));
  Multiplexer #(.select(1), .width(32), .disabled("Z"), .enable("false")) multiplexer_1 (
    .in0({J_JAL, PC_4}), .in1(J), .out(multiplexer_1_out), .sel(\有条件分支 ));
  Multiplexer #(.select(1), .width(32), .disabled("Z"), .enable("false")) multiplexer_2 (
    .in0({J_JAL, IR[25:0], 2'b00}), .in1(JR_address), .out(multiplexer_2_out), .sel(JR));
  Hex_Digit_Display hex_digit_display_1 (.value(LedData[31:28]));  // open: dp
  Multiplexer #(.select(1), .width(32), .disabled("Z"), .enable("false")) multiplexer_3 (
    .in0(multiplexer_1_out), .in1(multiplexer_2_out), .out(multiplexer_3_out), .sel(JMP));
  Register #(.width(2), .trigger("rising"), .Select("low")) register_1 (
    .D(INT_num), .en(\中断发生信号 ), .Q(register_1_q), .clk(CLK));  // open: clr
  Comparator #(.width(16), .mode("twosComplement")) comparator_1 (
    .a(\总周期数 ), .b({16{1'b0}}), .eq(Start));  // open: gt, lt
  Hex_Digit_Display hex_digit_display_2 (.value(LedData[27:24]));  // open: dp
  Hex_Digit_Display hex_digit_display_3 (.value(LedData[23:20]));  // open: dp
  Multiplexer #(.select(1), .width(32), .disabled("Z"), .enable("false")) multiplexer_4 (
    .in0(multiplexer_3_out), .in1(\服务地址 ), .out(multiplexer_4_out), .sel(\中断发生信号 ));
  Register #(.width(32), .trigger("rising"), .Select("low")) EPC (
    .D(multiplexer_3_out), .en(\中断发生信号 ), .Q(EPC_q), .clk(CLK));  // open: clr
  Decoder #(.select(2), .tristate("false"), .disabled("Z"), .enable("false")) decoder_1 (
    .out1(decoder_1_out1), .out2(decoder_1_out2), .out3(decoder_1_out3), .sel(register_1_q));  // open: out0
  Hex_Digit_Display hex_digit_display_4 (.value(LedData[15:12]));  // open: dp
  Hex_Digit_Display hex_digit_display_5 (.value(LedData[19:16]));  // open: dp
  Multiplexer #(.select(1), .width(32), .disabled("Z"), .enable("false")) multiplexer_5 (
    .in0(multiplexer_4_out), .in1(EPC_q), .out(multiplexer_5_out), .sel(ERET));
  and and_1 (and_1_out, ERET, decoder_1_out1);
  and and_2 (and_2_out, ERET, decoder_1_out2);
  and and_3 (and_3_out, ERET, decoder_1_out3);
  Hex_Digit_Display hex_digit_display_6 (.value(LedData[7:4]));  // open: dp
  Hex_Digit_Display hex_digit_display_7 (.value(LedData[11:8]));  // open: dp
  Counter #(.width(16), .max('hffff), .ongoal("wrap"), .trigger("rising"), .behavior("old")) counter_1 (
    .count(\中止 ), .Q(\总周期数 ), .clk(CLK));  // open: load, D, carry, clr, preset
  Register #(.width(32), .trigger("rising"), .Select("low")) u_PC (
    .D(multiplexer_5_out), .en(\中止 ), .Q(PC), .clk(CLK));  // open: clr
  Hex_Digit_Display hex_digit_display_8 (.value(LedData[3:0]));  // open: dp
  // Probe on \总周期数 
  \中断按键参考电路  \u_中断按键参考电路_1  (
    .\与中断屏蔽位与 (\中断按键参考电路_1_与中断屏蔽位与 ), .\同步清零信号 (and_1_out), .\中断号 (IR1_t), .\中断等待指示灯 (W1), .CLK(CLK));
  \中断按键参考电路  \u_中断按键参考电路_2  (
    .\与中断屏蔽位与 (\中断按键参考电路_2_与中断屏蔽位与 ), .\同步清零信号 (and_2_out), .\中断号 (IR2_t), .\中断等待指示灯 (W2), .CLK(CLK));
  \中断按键参考电路  \u_中断按键参考电路_3  (
    .\与中断屏蔽位与 (\中断按键参考电路_3_与中断屏蔽位与 ), .\同步清零信号 (and_3_out), .\中断号 (IR3_t), .\中断等待指示灯 (W3), .CLK(CLK));
  Multiplexer #(.select(1), .width(1), .disabled("Z"), .enable("false")) multiplexer_6 (
    .in0(1'b0), .in1(1'b1), .out(multiplexer_6_out), .sel(or_1_out));
  or or_1 (or_1_out, Start, ERET);
  ROM #(.addrWidth(10), .dataWidth(32), .Select("high")) rom_1 (.addr(PC[11:2]), .data(IR));
  Adder #(.width(32)) adder_1 (.a(PC), .b(32'h4), .out({J_JAL, PC_4}));  // open: cin, cout
  Register #(.width(1), .trigger("rising"), .Select("low")) register_2 (
    .D(multiplexer_6_out), .en(or_2_out), .Q(register_2_q), .clk(CLK));  // open: clr
  or or_2 (or_2_out, ERET, \中断发生信号 , Start);
  or or_3 (IR1_t, IR1, IRA);
  Priority_Encoder #(.select(2), .disabled("Z")) priority_encoder_1 (
    .in0(1'b0), .in1(\中断按键参考电路_1_与中断屏蔽位与 ), .in2(\中断按键参考电路_2_与中断屏蔽位与 ), .in3(\中断按键参考电路_3_与中断屏蔽位与 ),
    .out(INT_num), .gs(priority_encoder_1_gs));  // open: en_out, en_in
  or or_4 (IR2_t, IR2, IRB);
  Multiplexer #(.select(1), .width(5), .disabled("Z"), .enable("false")) multiplexer_7 (
    .in0(IR[20:16]), .in1(IR[15:11]), .out(multiplexer_7_out), .sel(RegDst));
  assign bit_extender_1_out = {{16{1'b0}}, IR[15:0]};  // Bit_Extender bit_extender_1
  assign bit_extender_2_out = {{16{IR[15]}}, IR[15:0]};  // Bit_Extender bit_extender_2
  // Probe on INT_num
  Multiplexer #(.select(2), .width(32), .disabled("Z"), .enable("false")) multiplexer_8 (
    .in1(32'h30ac), .in2(32'h3150), .in3(32'h31f4), .out(\服务地址 ), .sel(INT_num));  // open: in0
  and and_4 (\中断发生信号 , priority_encoder_1_gs, register_2_q);
  or or_5 (IR3_t, IR3, IRC);
  Multiplexer #(.select(1), .width(5), .disabled("Z"), .enable("false")) multiplexer_9 (
    .in0(IR[25:21]), .in1(5'b00010), .out(multiplexer_9_out), .sel(Syscall));
  Multiplexer #(.select(1), .width(5), .disabled("Z"), .enable("false")) multiplexer_10 (
    .in0(IR[20:16]), .in1(5'b00100), .out(multiplexer_10_out), .sel(Syscall));
  Multiplexer #(.select(1), .width(5), .disabled("Z"), .enable("false")) multiplexer_11 (
    .in0(multiplexer_7_out), .in1({5{1'b1}}), .out(multiplexer_11_out), .sel(JAL));
  Multiplexer #(.select(1), .width(32), .disabled("Z"), .enable("false")) multiplexer_12 (
    .in0(bit_extender_1_out), .in1(bit_extender_2_out), .out(multiplexer_12_out), .sel(SignedExt));
  \单周期硬布线控制器  \u_单周期硬布线控制器_1  (
    .Func(IR[5:0]), .OP(IR[31:26]), .ALU_OP(\单周期硬布线控制器_1_alu_op ), .MemToReg(\单周期硬布线控制器_1_memtoreg ),
    .MemWrite(MemWrite), .ALU_SRC(\单周期硬布线控制器_1_alu_src ), .RegWrite(RegWrite), .SysCALL(Syscall),
    .SignedExt(SignedExt), .RegDst(RegDst), .JR(JR), .JMP(JMP), .Beq(\单周期硬布线控制器_1_beq ), .JAL(JAL),
    .Bne(\单周期硬布线控制器_1_bne ), .SLLV(SLLV), .LH(LH), .XORI(XORI), .BGTZ(BGTZ), .M(IR[25:21]), .ERET(ERET));  // open: MFC0, MTC0
  MIPS_Regifile mips_regifile_1 (
    .Din(RDin), .Clk(CLK), .R1(JR_address), .R2(MDin), .WE(RegWrite), .W_num(multiplexer_11_out),
    .R1_num(multiplexer_9_out), .R2_num(multiplexer_10_out));
  Shifter #(.width(32), .shift("ll")) shifter_1 (.in(bit_extender_2_out), .\dist (5'b00010), .out(shifter_1_out));
  Multiplexer #(.select(1), .width(32), .disabled("Z"), .enable("false")) multiplexer_13 (
    .in0(MDin), .in1(multiplexer_12_out), .out(multiplexer_13_out), .sel(\单周期硬布线控制器_1_alu_src ));
  Adder #(.width(32)) adder_2 (.a(shifter_1_out), .b({J_JAL, PC_4}), .out(J));  // open: cin, cout
  not not_1 (not_1_out, mips_alu_1_equal);
  MIPS_ALU mips_alu_1 (
    .X(JR_address), .Y(multiplexer_13_out), .AluOP(\单周期硬布线控制器_1_alu_op ), .Equal(mips_alu_1_equal),
    .Result(mips_alu_1_result), .shamt(multiplexer_14_out));  // open: Result_2
  Multiplexer #(.select(1), .width(5), .disabled("Z"), .enable("false")) multiplexer_14 (
    .in0(IR[10:6]), .in1(JR_address[4:0]), .out(multiplexer_14_out), .sel(SLLV));
  and and_5 (and_5_out, mips_alu_1_equal, \单周期硬布线控制器_1_beq );
  and and_6 (and_6_out, not_1_out, \单周期硬布线控制器_1_bne );
  // Probe on \单周期硬布线控制器_1_alu_op 
  // Probe on mips_alu_1_result
  or or_6 (\有条件分支 , and_5_out, JUMP, and_6_out);
  Comparator #(.width(32), .mode("twosComplement")) comparator_2 (
    .a(JR_address), .b({32{1'b0}}), .gt(comparator_2_gt));  // open: eq, lt
  RAM #(.addrWidth(10), .dataWidth(32), .bus("separate"), .Select("high")) ram_1 (
    .addr(mips_alu_1_result[11:2]), .din(MDin), .data(ram_1_data), .str(MemWrite), .clk(CLK));  // open: sel, ld, clr
  and and_7 (JUMP, BGTZ, comparator_2_gt);
  Multiplexer #(.select(1), .width(32), .disabled("Z"), .enable("false")) multiplexer_15 (
    .in0(mips_alu_1_result), .in1(ram_1_data), .out(multiplexer_15_out), .sel(\单周期硬布线控制器_1_memtoreg ));
  Multiplexer #(.select(1), .width(32), .disabled("Z"), .enable("false")) multiplexer_16 (
    .in0(multiplexer_15_out), .in1({J_JAL, PC_4}), .out(multiplexer_16_out), .sel(JAL));
  Multiplexer #(.select(1), .width(16), .disabled("Z"), .enable("false")) multiplexer_17 (
    .in0(multiplexer_15_out[15:0]), .in1(multiplexer_15_out[31:16]), .out(multiplexer_17_out),
    .sel(mips_alu_1_result[1]));
  assign bit_extender_3_out = {{16{multiplexer_17_out[15]}}, multiplexer_17_out};  // Bit_Extender bit_extender_3
  Multiplexer #(.select(1), .width(32), .disabled("Z"), .enable("false")) multiplexer_18 (
    .in0(multiplexer_16_out), .in1(bit_extender_3_out), .out(RDin), .sel(LH));
  Multiplexer #(.select(1), .width(1), .disabled("Z"), .enable("false")) multiplexer_19 (
    .in0(1'b0), .in1(comparator_3_eq), .out(multiplexer_19_out), .sel(Syscall));
  Comparator #(.width(32), .mode("twosComplement")) comparator_3 (
    .a(JR_address), .b(32'h22), .eq(comparator_3_eq));  // open: gt, lt
  Register #(.width(32), .trigger("rising"), .Select("low")) register_3 (
    .D(MDin), .en(multiplexer_19_out), .Q(LedData), .clk(CLK));  // open: clr
  or or_7 (\中止 , multiplexer_19_out, Go, ~Syscall);  // OR_Gate

  // Other names for the same wires on the sheet: a0[31:0] = MDin; J_JAL[27:2] = IR[25:0]; shamt[4:0] = IR[10:6];
  //   M[4:0] = IR[25:21]; SLLV_1[4:0] = JR_address[4:0]; PC_4[31:28] = J_JAL

  // Notes on the sheet:
  //   中断源
  //   中断等待指示
  //   总复位信号应将除ROM以外所有存储组件全部清零
  //   数码管输出
  //   数码管输出应该用寄存器锁存，否则显示数据只能一闪而过
  //   指令存储器
  //   指令字
  //   contents of rom_1 (hex, n*v repeats v):
  //   201d07d0 20100001 109fc0 139fc3 8021 2012000c 24160008 26100001 3210000f 20080008 20090001 139900
  //   2709825 132020 20020022 c 1094022 1500fff9 22100001 2018000f 2188024 108700 20080008 20090001 139902
  //   2709825 132021 20020022 c 1094022 1500fff9 108702 2c9b022 12c00001 8000c07 4020 1084027 84400
  //   3508ffff 82021 20020022 c 8000c01 afa20000 23bd0004 afa40000 23bd0004 afb00000 23bd0004 afb30000
  //   23bd0004 afb40000 23bd0004 afb50000 23bd0004 afb60000 23bd0004 20160001 20140003 20150001 168020
  //   108100 2149825 132020 20020022 c 1600fffa 295a022 1680fff7 23bdfffc 8fb60000 23bdfffc 8fb50000
  //   23bdfffc 8fb40000 23bdfffc 8fb30000 23bdfffc 8fb00000 23bdfffc 8fa40000 23bdfffc 8fa20000 42000018
  //   afa20000 23bd0004 afa40000 23bd0004 afb00000 23bd0004 afb30000 23bd0004 afb40000 23bd0004 afb50000
  //   23bd0004 afb60000 23bd0004 20160002 20140003 20150001 168020 108100 2149825 132020 20020022 c
  //   1600fffa 295a022 1680fff7 23bdfffc 8fb60000 23bdfffc 8fb50000 23bdfffc 8fb40000 23bdfffc 8fb30000
  //   23bdfffc 8fb00000 23bdfffc 8fa40000 23bdfffc 8fa20000 42000018 afa20000 23bd0004 afa40000 23bd0004
  //   afb00000 23bd0004 afb30000 23bd0004 afb40000 23bd0004 afb50000 23bd0004 afb60000 23bd0004 20160003
  //   20140003 20150001 168020 108100 2149825 132020 20020022 c 1600fffa 295a022 1680fff7 23bdfffc
  //   8fb60000 23bdfffc 8fb50000 23bdfffc 8fb40000 23bdfffc 8fb30000 23bdfffc 8fb00000 23bdfffc 8fa40000
  //   23bdfffc 8fa20000 42000018
  //   OP
  //   Func
  //   rs
  //   rt
  //   rd
  //   JMP
  //   JR
  //   OP
  //   Func
  //   Beq
  //   Bne
  //   MemToReg
  //   MemWrite
  //   AluOP
  //   AluSrcB
  //   RegWrite
  //   JAL
  //   RegDst
  //   Syscall
  //   为方便自动评测，需要输出PC，IR，寄存器堆写如数据RDin
  //   RAM写使能MemWrite、RAM写入数据MDin等信号
endmodule

module \单周期MIPS_多级中断  (
  input  IR1,
  input  IR2,
  input  IR3,
  output RegWrite,
  output MemWrite,
  output [31:0] PC,
  output [31:0] IR,
  output [31:0] RDin,
  output [31:0] MDin,
  output [31:0] LedData
);

  wire _1, _2, _3, and_1_out, and_3_out, and_7_out, and_8_out, BGTZ, CLK, comparator_2_lt, comparator_3_lt,
       comparator_4_lt, comparator_5_gt, comparator_6_eq, d_ff_1_q, d_ff_2_q, d_ff_3_q, decoder_1_out1,
       decoder_1_out2, decoder_1_out3, demultiplexer_1_out1, demultiplexer_1_out2, demultiplexer_1_out3,
       ERET, Go, IE, IR1_t, IR2_t, IR3_t, IRA, IRB, IRC, JAL, JMP, JR, JUMP, LH, MFC0, mips_alu_1_equal,
       MTC0, multiplexer_6_out, multiplexer_9_out, multiplexer_16_out, multiplexer_26_out, not_1_out,
       or_1_out, or_3_out, or_4_out, or_5_out, or_7_out, RegDst, RST1, RST2, RST3, SignedExt, SLLV, Start,
       Status_1, Status_2, Status_3, Syscall, W1, W2, W3, XORI, \不处于中段 , \中止 , \优先级更高 ,
       \单周期硬布线控制器_1_alu_src , \单周期硬布线控制器_1_beq , \单周期硬布线控制器_1_bne , \单周期硬布线控制器_1_memtoreg , \处于中段1 , \处于中段2 ,
       \处于中段3 , \有条件分支 , \进入中断 ;
  wire [1:0] INT_num, multiplexer_19_out, multiplexer_20_out, multiplexer_21_out, priority_encoder_1_out,
       register_3_q, \中断替换 ;
  wire [3:0] \单周期硬布线控制器_1_alu_op ;
  wire [4:0] multiplexer_11_out, multiplexer_12_out, multiplexer_13_out, multiplexer_14_out,
       multiplexer_18_out;
  wire [15:0] multiplexer_24_out, \总周期数 ;
  wire [27:0] PC_4;
  wire [31:0] bit_extender_1_out, bit_extender_2_out, bit_extender_3_out, EPC__PC1, EPC__PC2, EPC__PC3, J,
       JR_address, mips_alu_1_result, multiplexer_1_out, multiplexer_2_out, multiplexer_4_out,
       multiplexer_5_out, multiplexer_7_out, multiplexer_15_out, multiplexer_17_out, multiplexer_22_out,
       multiplexer_23_out, PC__EPC, ram_1_data, shifter_1_out, \服务地址 ;
  wire [31:28] J_JAL;

  Clock #(.highDuration(1), .lowDuration(1)) clock_1 (.out(CLK));
  Button u__1 (.out(IRA));
  Button u__2 (.out(IRB));
  Button u__3 (.out(IRC));
  Button \u_继续运行  (.out(Go));
  LED #(.active("true")) led_1 (.in(W1));
  LED #(.active("true")) led_2 (.in(W2));
  LED #(.active("true")) led_3 (.in(W3));
  Multiplexer #(.select(1), .width(32), .disabled("Z"), .enable("false")) multiplexer_1 (
    .in0({J_JAL, PC_4}), .in1(J), .out(multiplexer_1_out), .sel(\有条件分支 ));
  Multiplexer #(.select(1), .width(32), .disabled("Z"), .enable("false")) multiplexer_2 (
    .in0({J_JAL, IR[25:0], 2'b00}), .in1(JR_address), .out(multiplexer_2_out), .sel(JR));
  Hex_Digit_Display hex_digit_display_1 (.value(LedData[31:28]));  // open: dp
  Multiplexer #(.select(1), .width(32), .disabled("Z"), .enable("false")) multiplexer_3 (
    .in0(multiplexer_1_out), .in1(multiplexer_2_out), .out(PC__EPC), .sel(JMP));
  Multiplexer #(.select(2), .width(32), .disabled("Z"), .enable("false")) multiplexer_4 (
    .in1(EPC__PC1), .in2(EPC__PC2), .in3(EPC__PC3), .out(multiplexer_4_out), .sel(INT_num));  // open: in0
  \中断按键参考电路  \u_中断按键参考电路_1  (.\与中断屏蔽位与 (_1), .\同步清零信号 (RST1), .\中断号 (IR1_t), .\中断等待指示灯 (W1), .CLK(CLK));
  \中断按键参考电路  \u_中断按键参考电路_2  (.\与中断屏蔽位与 (_2), .\同步清零信号 (RST2), .\中断号 (IR2_t), .\中断等待指示灯 (W2), .CLK(CLK));
  \中断按键参考电路  \u_中断按键参考电路_3  (.\与中断屏蔽位与 (_3), .\同步清零信号 (RST3), .\中断号 (IR3_t), .\中断等待指示灯 (W3), .CLK(CLK));
  Comparator #(.width(16), .mode("twosComplement")) comparator_1 (
    .a(\总周期数 ), .b({16{1'b0}}), .eq(Start));  // open: gt, lt
  Hex_Digit_Display hex_digit_display_2 (.value(LedData[27:24]));  // open: dp
  Hex_Digit_Display hex_digit_display_3 (.value(LedData[23:20]));  // open: dp
  Multiplexer #(.select(1), .width(32), .disabled("Z"), .enable("false")) multiplexer_5 (
    .in0(PC__EPC), .in1(\服务地址 ), .out(multiplexer_5_out), .sel(\进入中断 ));
  Multiplexer #(.select(1), .width(1), .disabled("Z"), .enable("false")) multiplexer_6 (
    .in0(1'b0), .in1(1'b1), .out(multiplexer_6_out), .sel(or_1_out));
  or or_1 (or_1_out, Start, MFC0, ERET);
  and and_1 (and_1_out, \优先级更高 , IE);
  or or_2 (\不处于中段 , \处于中段1 , \处于中段2 , \处于中段3 );
  Hex_Digit_Display hex_digit_display_4 (.value(LedData[15:12]));  // open: dp
  Hex_Digit_Display hex_digit_display_5 (.value(LedData[19:16]));  // open: dp
  Multiplexer #(.select(1), .width(32), .disabled("Z"), .enable("false")) multiplexer_7 (
    .in0(multiplexer_5_out), .in1(multiplexer_4_out), .out(multiplexer_7_out), .sel(ERET));
  Multiplexer #(.select(1), .width(2), .disabled("Z"), .enable("false")) multiplexer_8 (
    .in0(2'b00), .in1(priority_encoder_1_out), .out(INT_num), .sel(or_3_out));
  or or_3 (or_3_out, _1, _2, _3);
  Priority_Encoder #(.select(2), .disabled("Z")) priority_encoder_1 (
    .in0(1'b0), .in1(_1), .in2(_2), .in3(_3), .out(priority_encoder_1_out));  // open: gs, en_out, en_in
  Multiplexer #(.select(1), .width(1), .disabled("Z"), .enable("false")) multiplexer_9 (
    .in0(or_4_out), .in1(1'b1), .out(multiplexer_9_out), .sel(or_5_out));
  or or_4 (or_4_out, ERET, \进入中断 , Start);
  and and_2 (\进入中断 , and_1_out, \不处于中段 );
  Hex_Digit_Display hex_digit_display_6 (.value(LedData[7:4]));  // open: dp
  Hex_Digit_Display hex_digit_display_7 (.value(LedData[11:8]));  // open: dp
  // Probe on \总周期数 
  Counter #(.width(16), .max('hffff), .ongoal("wrap"), .trigger("rising"), .behavior("old")) counter_1 (
    .count(\中止 ), .Q(\总周期数 ), .clk(CLK));  // open: load, D, carry, clr, preset
  Register #(.width(32), .trigger("rising"), .Select("low")) u_PC (
    .D(multiplexer_7_out), .en(\中止 ), .Q(PC), .clk(CLK));  // open: clr
  // Probe on priority_encoder_1_out
  Register #(.width(1), .trigger("rising"), .Select("low")) register_1 (
    .D(multiplexer_6_out), .en(multiplexer_9_out), .Q(IE), .clk(CLK));  // open: clr
  or or_5 (or_5_out, MTC0, MFC0);
  Hex_Digit_Display hex_digit_display_8 (.value(LedData[3:0]));  // open: dp
  ROM #(.addrWidth(10), .dataWidth(32), .Select("high")) rom_1 (.addr(PC[11:2]), .data(IR));
  Adder #(.width(32)) adder_1 (.a(PC), .b(32'h4), .out({J_JAL, PC_4}));  // open: cin, cout
  Multiplexer #(.select(2), .width(32), .disabled("Z"), .enable("false")) multiplexer_10 (
    .in1(32'h30ac), .in2(32'h3158), .in3(32'h3204), .out(\服务地址 ), .sel(priority_encoder_1_out));  // open: in0
  and and_3 (and_3_out, \优先级更高 , IE);
  or or_6 (IR1_t, IR1, IRA);
  or or_7 (or_7_out, ERET, and_3_out);
  D_Flip_Flop #(.trigger("rising"), .Pre_Clr_Positions("LEGACY"), .NegatePresetClear("false"), .enable("true"), .NewFFLayout("false")) d_ff_1 (
    .clk(CLK), .D(RST1), .Q(d_ff_1_q));  // open: Qn, preset, en, reset
  or or_8 (IR2_t, IR2, IRB);
  Multiplexer #(.select(1), .width(5), .disabled("Z"), .enable("false")) multiplexer_11 (
    .in0(IR[20:16]), .in1(IR[15:11]), .out(multiplexer_11_out), .sel(RegDst));
  assign bit_extender_1_out = {{16{1'b0}}, IR[15:0]};  // Bit_Extender bit_extender_1
  assign bit_extender_2_out = {{16{IR[15]}}, IR[15:0]};  // Bit_Extender bit_extender_2
  Register #(.width(32), .trigger("falling"), .Select("low")) register_2 (
    .D(PC__EPC), .en(demultiplexer_1_out1), .Q(EPC__PC1), .clk(CLK), .clr(d_ff_1_q));
  Decoder #(.select(2), .tristate("false"), .disabled("Z"), .enable("false")) decoder_1 (
    .out1(decoder_1_out1), .out2(decoder_1_out2), .out3(decoder_1_out3), .sel(register_3_q));  // open: out0
  Register #(.width(2), .trigger("rising"), .Select("low")) register_3 (
    .D(INT_num), .en(or_7_out), .Q(register_3_q), .clk(CLK));  // open: clr
  Register #(.width(1), .trigger("rising"), .Select("low")) register_4 (
    .D(1'b1), .en(demultiplexer_1_out1), .Q(Status_1), .clk(CLK), .clr(d_ff_1_q));
  or or_9 (IR3_t, IR3, IRC);
  Multiplexer #(.select(1), .width(5), .disabled("Z"), .enable("false")) multiplexer_12 (
    .in0(IR[25:21]), .in1(5'b00010), .out(multiplexer_12_out), .sel(Syscall));
  Multiplexer #(.select(1), .width(5), .disabled("Z"), .enable("false")) multiplexer_13 (
    .in0(IR[20:16]), .in1(5'b00100), .out(multiplexer_13_out), .sel(Syscall));
  Multiplexer #(.select(1), .width(5), .disabled("Z"), .enable("false")) multiplexer_14 (
    .in0(multiplexer_11_out), .in1({5{1'b1}}), .out(multiplexer_14_out), .sel(JAL));
  Multiplexer #(.select(1), .width(32), .disabled("Z"), .enable("false")) multiplexer_15 (
    .in0(bit_extender_1_out), .in1(bit_extender_2_out), .out(multiplexer_15_out), .sel(SignedExt));
  D_Flip_Flop #(.trigger("rising"), .Pre_Clr_Positions("LEGACY"), .NegatePresetClear("false"), .enable("true"), .NewFFLayout("false")) d_ff_2 (
    .clk(CLK), .D(RST2), .Q(d_ff_2_q));  // open: Qn, preset, en, reset
  Demultiplexer #(.select(2), .width(1), .tristate("false"), .disabled("Z"), .enable("false")) demultiplexer_1 (
    .out1(demultiplexer_1_out1), .out2(demultiplexer_1_out2), .out3(demultiplexer_1_out3),
    .in(multiplexer_16_out), .sel(INT_num));  // open: out0
  Multiplexer #(.select(1), .width(1), .disabled("Z"), .enable("false")) multiplexer_16 (
    .in0(1'b0), .in1(1'b1), .out(multiplexer_16_out), .sel(\进入中断 ));
  \单周期硬布线控制器  \u_单周期硬布线控制器_1  (
    .Func(IR[5:0]), .OP(IR[31:26]), .ALU_OP(\单周期硬布线控制器_1_alu_op ), .MemToReg(\单周期硬布线控制器_1_memtoreg ),
    .MemWrite(MemWrite), .ALU_SRC(\单周期硬布线控制器_1_alu_src ), .RegWrite(RegWrite), .SysCALL(Syscall),
    .SignedExt(SignedExt), .RegDst(RegDst), .JR(JR), .JMP(JMP), .Beq(\单周期硬布线控制器_1_beq ), .JAL(JAL),
    .Bne(\单周期硬布线控制器_1_bne ), .SLLV(SLLV), .LH(LH), .XORI(XORI), .BGTZ(BGTZ), .M(IR[25:21]), .MFC0(MFC0),
    .MTC0(MTC0), .ERET(ERET));
  and and_4 (RST1, ERET, decoder_1_out1);
  and and_5 (RST2, ERET, decoder_1_out2);
  and and_6 (RST3, ERET, decoder_1_out3);
  Register #(.width(32), .trigger("falling"), .Select("low")) register_5 (
    .D(PC__EPC), .en(demultiplexer_1_out2), .Q(EPC__PC2), .clk(CLK), .clr(d_ff_2_q));
  Register #(.width(1), .trigger("rising"), .Select("low")) register_6 (
    .D(1'b1), .en(demultiplexer_1_out2), .Q(Status_2), .clk(CLK), .clr(d_ff_2_q));
  D_Flip_Flop #(.trigger("rising"), .Pre_Clr_Positions("LEGACY"), .NegatePresetClear("false"), .enable("true"), .NewFFLayout("false")) d_ff_3 (
    .clk(CLK), .D(RST3), .Q(d_ff_3_q));  // open: Qn, preset, en, reset
  MIPS_Regifile mips_regifile_1 (
    .Din(RDin), .Clk(CLK), .R1(JR_address), .R2(MDin), .WE(RegWrite), .W_num(multiplexer_14_out),
    .R1_num(multiplexer_12_out), .R2_num(multiplexer_13_out));
  Shifter #(.width(32), .shift("ll")) shifter_1 (.in(bit_extender_2_out), .\dist (5'b00010), .out(shifter_1_out));
  Register #(.width(32), .trigger("falling"), .Select("low")) register_7 (
    .D(PC__EPC), .en(demultiplexer_1_out3), .Q(EPC__PC3), .clk(CLK), .clr(d_ff_3_q));
  Multiplexer #(.select(1), .width(32), .disabled("Z"), .enable("false")) multiplexer_17 (
    .in0(MDin), .in1(multiplexer_15_out), .out(multiplexer_17_out), .sel(\单周期硬布线控制器_1_alu_src ));
  Adder #(.width(32)) adder_2 (.a(shifter_1_out), .b({J_JAL, PC_4}), .out(J));  // open: cin, cout
  Register #(.width(1), .trigger("rising"), .Select("low")) register_8 (
    .D(1'b1), .en(demultiplexer_1_out3), .Q(Status_3), .clk(CLK), .clr(d_ff_3_q));
  not not_1 (not_1_out, mips_alu_1_equal);
  MIPS_ALU mips_alu_1 (
    .X(JR_address), .Y(multiplexer_17_out), .AluOP(\单周期硬布线控制器_1_alu_op ), .Equal(mips_alu_1_equal),
    .Result(mips_alu_1_result), .shamt(multiplexer_18_out));  // open: Result_2
  Multiplexer #(.select(1), .width(5), .disabled("Z"), .enable("false")) multiplexer_18 (
    .in0(IR[10:6]), .in1(JR_address[4:0]), .out(multiplexer_18_out), .sel(SLLV));
  Register #(.width(2), .trigger("rising"), .Select("low")) register_9 (
    .D(INT_num), .en(\进入中断 ), .Q(\中断替换 ), .clk(CLK), .clr(ERET));
  Multiplexer #(.select(1), .width(2), .disabled("Z"), .enable("false")) multiplexer_19 (
    .in0(2'b00), .in1(2'b01), .out(multiplexer_19_out), .sel(_1));
  Multiplexer #(.select(1), .width(2), .disabled("Z"), .enable("false")) multiplexer_20 (
    .in0(2'b00), .in1(2'b10), .out(multiplexer_20_out), .sel(_2));
  // Probe on \中断替换 
  Multiplexer #(.select(1), .width(2), .disabled("Z"), .enable("false")) multiplexer_21 (
    .in0(2'b00), .in1(2'b11), .out(multiplexer_21_out), .sel(_3));
  // Probe on multiplexer_21_out
  and and_7 (and_7_out, mips_alu_1_equal, \单周期硬布线控制器_1_beq );
  and and_8 (and_8_out, not_1_out, \单周期硬布线控制器_1_bne );
  // Probe on \单周期硬布线控制器_1_alu_op 
  // Probe on mips_alu_1_result
  // Probe on MDin
  Comparator #(.width(2), .mode("unsigned")) comparator_2 (
    .a(\中断替换 ), .b(multiplexer_19_out), .lt(comparator_2_lt));  // open: gt, eq
  Comparator #(.width(2), .mode("unsigned")) comparator_3 (
    .a(\中断替换 ), .b(multiplexer_20_out), .lt(comparator_3_lt));  // open: gt, eq
  Comparator #(.width(2), .mode("unsigned")) comparator_4 (
    .a(\中断替换 ), .b(multiplexer_21_out), .lt(comparator_4_lt));  // open: gt, eq
  or or_10 (\有条件分支 , and_7_out, JUMP, and_8_out);
  and and_9 (\处于中段1 , ~Status_1, comparator_2_lt);  // AND_Gate
  and and_10 (\处于中段3 , comparator_4_lt, ~Status_3);  // AND_Gate
  and and_11 (\处于中段2 , comparator_3_lt, ~Status_2);  // AND_Gate
  Comparator #(.width(32), .mode("twosComplement")) comparator_5 (
    .a(JR_address), .b({32{1'b0}}), .gt(comparator_5_gt));  // open: eq, lt
  RAM #(.addrWidth(10), .dataWidth(32), .bus("separate"), .Select("high")) ram_1 (
    .addr(mips_alu_1_result[11:2]), .din(MDin), .data(ram_1_data), .str(MemWrite), .clk(CLK));  // open: sel, ld, clr
  or or_11 (\优先级更高 , comparator_2_lt, comparator_3_lt, comparator_4_lt);
  and and_12 (JUMP, BGTZ, comparator_5_gt);
  Multiplexer #(.select(1), .width(32), .disabled("Z"), .enable("false")) multiplexer_22 (
    .in0(mips_alu_1_result), .in1(ram_1_data), .out(multiplexer_22_out), .sel(\单周期硬布线控制器_1_memtoreg ));
  Multiplexer #(.select(1), .width(32), .disabled("Z"), .enable("false")) multiplexer_23 (
    .in0(multiplexer_22_out), .in1({J_JAL, PC_4}), .out(multiplexer_23_out), .sel(JAL));
  Multiplexer #(.select(1), .width(16), .disabled("Z"), .enable("false")) multiplexer_24 (
    .in0(multiplexer_22_out[15:0]), .in1(multiplexer_22_out[31:16]), .out(multiplexer_24_out),
    .sel(mips_alu_1_result[1]));
  assign bit_extender_3_out = {{16{multiplexer_24_out[15]}}, multiplexer_24_out};  // Bit_Extender bit_extender_3
  Multiplexer #(.select(1), .width(32), .disabled("Z"), .enable("false")) multiplexer_25 (
    .in0(multiplexer_23_out), .in1(bit_extender_3_out), .out(RDin), .sel(LH));
  Multiplexer #(.select(1), .width(1), .disabled("Z"), .enable("false")) multiplexer_26 (
    .in0(1'b0), .in1(comparator_6_eq), .out(multiplexer_26_out), .sel(Syscall));
  Comparator #(.width(32), .mode("twosComplement")) comparator_6 (
    .a(JR_address), .b(32'h22), .eq(comparator_6_eq));  // open: gt, lt
  Register #(.width(32), .trigger("rising"), .Select("low")) register_10 (
    .D(MDin), .en(multiplexer_26_out), .Q(LedData), .clk(CLK));  // open: clr
  or or_12 (\中止 , multiplexer_26_out, Go, ~Syscall);  // OR_Gate

  // Other names for the same wires on the sheet: a0[31:0] = MDin; J_JAL[27:2] = IR[25:0]; shamt[4:0] = IR[10:6];
  //   M[4:0] = IR[25:21]; SLLV_1[4:0] = JR_address[4:0]; PC_4[31:28] = J_JAL

  // Notes on the sheet:
  //   中断源
  //   中断等待指示
  //   总复位信号应将除ROM以外所有存储组件全部清零
  //   数码管输出
  //   数码管输出应该用寄存器锁存，否则显示数据只能一闪而过
  //   指令存储器
  //   指令字
  //   contents of rom_1 (hex, n*v repeats v):
  //   201d07d0 20100001 109fc0 139fc3 8021 2012000c 24160008 26100001 3210000f 20080008 20090001 139900
  //   2709825 132020 20020022 c 1094022 1500fff9 22100001 2018000f 2188024 108700 20080008 20090001 139902
  //   2709825 132021 20020022 c 1094022 1500fff9 108702 2c9b022 12c00001 8000c07 4020 1084027 84400
  //   3508ffff 82021 20020022 c 8000c01 afa20000 23bd0004 afa40000 23bd0004 afb00000 23bd0004 afb30000
  //   23bd0004 afb40000 23bd0004 afb50000 23bd0004 afb60000 23bd0004 40000000 20160001 20140003 20150001
  //   168020 108100 2149825 132020 20020022 c 1600fffa 295a022 1680fff7 40800000 23bdfffc 8fb60000
  //   23bdfffc 8fb50000 23bdfffc 8fb40000 23bdfffc 8fb30000 23bdfffc 8fb00000 23bdfffc 8fa40000 23bdfffc
  //   8fa20000 42000018 afa20000 23bd0004 afa40000 23bd0004 afb00000 23bd0004 afb30000 23bd0004 afb40000
  //   23bd0004 afb50000 23bd0004 afb60000 23bd0004 40000000 20160002 20140003 20150001 168020 108100
  //   2149825 132020 20020022 c 1600fffa 295a022 1680fff7 40800000 23bdfffc 8fb60000 23bdfffc 8fb50000
  //   23bdfffc 8fb40000 23bdfffc 8fb30000 23bdfffc 8fb00000 23bdfffc 8fa40000 23bdfffc 8fa20000 42000018
  //   afa20000 23bd0004 afa40000 23bd0004 afb00000 23bd0004 afb30000 23bd0004 afb40000 23bd0004 afb50000
  //   23bd0004 afb60000 23bd0004 40000000 20160003 20140003 20150001 168020 108100 2149825 132020 20020022
  //   c 1600fffa 295a022 1680fff7 40800000 23bdfffc 8fb60000 23bdfffc 8fb50000 23bdfffc 8fb40000 23bdfffc
  //   8fb30000 23bdfffc 8fb00000 23bdfffc 8fa40000 23bdfffc 8fa20000 42000018
  //   OP
  //   Func
  //   rs
  //   rt
  //   rd
  //   主要考虑问题：被返回的地址已经是某中断内此时不能再次跳转回改中断最初位置
  //   JMP
  //   JR
  //   OP
  //   Func
  //   Beq
  //   Bne
  //   MemToReg
  //   MemWrite
  //   AluOP
  //   AluSrcB
  //   RegWrite
  //   JAL
  //   RegDst
  //   Syscall
  //   保存各中断需要返回的地址
  //   为方便自动评测，需要输出PC，IR，寄存器堆写如数据RDin
  //   RAM写使能MemWrite、RAM写入数据MDin等信号
  //   比较是否出现优先级更高的中断信号
endmodule

// 单周期硬布线控制器
module \单周期硬布线控制器  (
  input  [5:0] OP,
  input  [5:0] Func,
  input  [4:0] M,
  output [3:0] ALU_OP,
  output MemToReg,
  output MemWrite,
  output ALU_SRC,
  output RegWrite,
  output SysCALL,
  output SignedExt,
  output RegDst,
  output Beq,
  output Bne,
  output JR,
  output JMP,
  output JAL,
  output SLLV,
  output XORI,
  output LH,
  output BGTZ,
  output MFC0,
  output MTC0,
  output ERET
);

  \运算控制器自动生成  \u_运算控制器自动生成_1  (
    .OP0(OP[0]), .OP1(OP[1]), .OP2(OP[2]), .OP3(OP[3]), .OP4(OP[4]), .OP5(OP[5]), .F0(Func[0]), .F1(Func[1]),
    .F2(Func[2]), .F3(Func[3]), .F4(Func[4]), .F5(Func[5]), .S0(ALU_OP[0]), .S1(ALU_OP[1]), .S2(ALU_OP[2]),
    .S3(ALU_OP[3]));
  \控制信号自动生成  \u_控制信号自动生成_1  (
    .OP0(OP[0]), .OP1(OP[1]), .OP2(OP[2]), .OP3(OP[3]), .OP4(OP[4]), .OP5(OP[5]), .F0(Func[0]), .F1(Func[1]),
    .F2(Func[2]), .F3(Func[3]), .F4(Func[4]), .F5(Func[5]), .MemToReg(MemToReg), .MemWrite(MemWrite),
    .ALU_SRC(ALU_SRC), .RegWrite(RegWrite), .SysCALL(SysCALL), .SignedExt(SignedExt), .RegDst(RegDst),
    .BEQ(Beq), .BNE(Bne), .JR(JR), .JMP(JMP), .JAL(JAL));
  \拓展指令信号  \u_拓展指令信号_1  (
    .OP0(OP[0]), .OP1(OP[1]), .OP2(OP[2]), .OP3(OP[3]), .OP4(OP[4]), .OP5(OP[5]), .F0(Func[0]), .F1(Func[1]),
    .F2(Func[2]), .F3(Func[3]), .F4(Func[4]), .F5(Func[5]), .SLLV(SLLV), .XORI(XORI), .LH(LH), .BGTZ(BGTZ));
  \中断指令信号  \u_中断指令信号_1  (
    .OP0(OP[0]), .OP1(OP[1]), .OP2(OP[2]), .MFC0(MFC0), .OP3(OP[3]), .OP4(OP[4]), .OP5(OP[5]), .F0(Func[0]),
    .F1(Func[1]), .F2(Func[2]), .MTC0(MTC0), .F3(Func[3]), .F4(Func[4]), .F5(Func[5]), .M0(M[0]), .M1(M[1]),
    .M2(M[2]), .ERET(ERET), .M3(M[3]), .M4(M[4]));

  // Other names for the same wires on the sheet: OP_CODE[5:0] = OP

  // Notes on the sheet:
  //   运算器控制器，根据指令生成运算器功能选择信号
  //   控制信号生成，产生数据通路需要的其他控制信号
endmodule

// 运算器控制器
module \运算控制器自动生成  (
  input  OP0,
  input  OP1,
  input  OP2,
  input  OP3,
  input  OP4,
  input  OP5,
  input  F0,
  input  F1,
  input  F2,
  input  F3,
  input  F4,
  input  F5,
  output S0,
  output S1,
  output S2,
  output S3
);

  wire and_1_out, and_2_out, and_3_out, and_4_out, and_5_out, and_6_out, and_7_out, and_8_out, and_9_out,
       and_10_out, and_11_out, and_12_out, and_13_out, and_14_out, and_15_out, and_16_out, and_17_out,
       and_18_out, and_19_out, and_20_out, and_21_out, and_22_out, and_23_out, and_24_out, and_25_out,
       and_26_out, and_27_out, and_28_out, and_29_out, and_30_out, and_31_out, and_32_out, and_33_out,
       and_34_out, and_35_out, and_36_out, and_37_out, and_38_out, and_39_out, and_40_out, not_1_out,
       not_2_out, not_3_out, not_4_out, not_5_out, not_6_out, not_7_out, not_8_out, not_9_out, not_10_out,
       not_11_out, not_12_out, not_13_out, not_14_out, not_15_out, not_16_out, not_17_out, not_18_out,
       not_19_out, not_20_out, not_21_out, not_22_out, not_23_out, not_24_out, not_25_out, not_26_out,
       not_27_out, not_28_out, not_29_out, not_30_out, not_31_out, not_32_out, not_33_out, not_34_out,
       not_35_out, not_36_out, not_37_out, not_38_out, not_39_out, not_40_out, not_41_out, not_42_out,
       not_43_out, not_44_out, not_45_out, not_46_out, not_47_out, not_48_out, not_49_out, not_50_out,
       not_51_out, not_52_out, not_53_out, not_54_out, not_55_out, not_56_out, not_57_out, not_58_out,
       not_59_out, not_60_out, not_61_out, not_62_out, not_63_out, not_64_out, not_65_out, not_66_out,
       not_67_out, not_68_out, not_69_out, not_70_out, not_71_out, not_72_out, not_73_out, not_74_out,
       not_75_out, not_76_out, not_77_out, not_78_out, not_79_out, not_80_out, not_81_out, not_82_out,
       not_83_out, not_84_out, not_85_out, not_86_out, not_87_out, not_88_out, not_89_out, not_90_out,
       not_91_out, not_92_out, not_93_out, not_94_out, not_95_out, not_96_out, not_97_out, not_98_out,
       not_99_out, not_100_out, not_101_out, not_102_out, not_103_out, not_104_out, not_105_out, not_106_out,
       not_107_out, not_108_out, not_109_out, not_110_out, not_111_out, not_112_out, not_113_out,
       not_114_out, not_115_out, not_116_out, not_117_out, not_118_out, not_119_out, not_120_out,
       not_121_out, not_122_out, not_123_out, not_124_out, not_125_out, not_126_out, not_127_out,
       not_128_out, not_129_out, not_130_out, not_131_out, not_132_out, not_133_out, not_134_out,
       not_135_out, not_136_out, not_137_out, not_138_out, not_139_out, not_140_out, not_141_out,
       not_142_out, not_143_out, not_144_out, not_145_out, not_146_out, not_147_out, not_148_out,
       not_149_out, not_150_out, not_151_out, not_152_out, not_153_out, not_154_out, not_155_out,
       not_156_out, not_157_out, not_158_out, not_159_out, not_160_out, not_161_out, not_162_out,
       not_163_out, not_164_out, not_165_out, not_166_out, not_167_out, not_168_out, not_169_out,
       not_170_out, not_171_out, not_172_out, not_173_out, not_174_out, not_175_out, not_176_out,
       not_177_out, not_178_out, not_179_out, not_180_out, not_181_out, not_182_out, not_183_out,
       not_184_out, not_185_out, not_186_out, not_187_out, not_188_out, not_189_out, not_190_out,
       not_191_out, not_192_out, not_193_out, not_194_out, not_195_out, not_196_out, not_197_out,
       not_198_out, not_199_out, not_200_out, not_201_out, not_202_out, not_203_out, not_204_out,
       not_205_out, not_206_out, not_207_out, not_208_out, not_209_out, not_210_out, not_211_out,
       not_212_out, not_213_out, not_214_out, not_215_out, not_216_out, not_217_out, not_218_out,
       not_219_out, not_220_out, not_221_out, not_222_out, not_223_out, not_224_out, not_225_out,
       not_226_out, not_227_out, not_228_out, not_229_out, not_230_out, not_231_out, not_232_out,
       not_233_out, not_234_out, not_235_out, not_236_out, not_237_out, not_238_out, not_239_out,
       not_240_out, not_241_out, not_242_out, not_243_out, not_244_out, not_245_out, not_246_out,
       not_247_out, not_248_out, not_249_out, not_250_out, not_251_out, not_252_out, not_253_out,
       not_254_out, not_255_out, not_256_out, not_257_out, not_258_out, not_259_out, not_260_out,
       not_261_out, not_262_out, not_263_out, not_264_out, not_265_out, not_266_out, not_267_out,
       not_268_out, not_269_out, not_270_out, not_271_out, not_272_out;

  not not_1 (not_1_out, OP5);
  not not_2 (not_2_out, OP4);
  not not_3 (not_3_out, OP3);
  not not_4 (not_4_out, OP2);
  not not_5 (not_5_out, OP1);
  not not_6 (not_6_out, OP0);
  not not_7 (not_7_out, F5);
  not not_8 (not_8_out, F4);
  not not_9 (not_9_out, F3);
  not not_10 (not_10_out, F2);
  not not_11 (not_11_out, OP5);
  not not_12 (not_12_out, OP4);
  not not_13 (not_13_out, OP3);
  not not_14 (not_14_out, OP2);
  not not_15 (not_15_out, OP1);
  not not_16 (not_16_out, OP0);
  not not_17 (not_17_out, F4);
  not not_18 (not_18_out, F3);
  not not_19 (not_19_out, F2);
  not not_20 (not_20_out, F1);
  not not_21 (not_21_out, F0);
  not not_22 (not_22_out, OP5);
  not not_23 (not_23_out, OP4);
  not not_24 (not_24_out, OP3);
  not not_25 (not_25_out, OP2);
  not not_26 (not_26_out, OP1);
  not not_27 (not_27_out, OP0);
  not not_28 (not_28_out, F4);
  not not_29 (not_29_out, F3);
  not not_30 (not_30_out, F2);
  not not_31 (not_31_out, F1);
  not not_32 (not_32_out, OP5);
  not not_33 (not_33_out, OP4);
  not not_34 (not_34_out, OP3);
  not not_35 (not_35_out, OP2);
  not not_36 (not_36_out, OP1);
  not not_37 (not_37_out, OP0);
  not not_38 (not_38_out, F4);
  not not_39 (not_39_out, F3);
  not not_40 (not_40_out, F1);
  not not_41 (not_41_out, F0);
  not not_42 (not_42_out, OP5);
  not not_43 (not_43_out, OP4);
  not not_44 (not_44_out, OP3);
  not not_45 (not_45_out, OP2);
  not not_46 (not_46_out, OP1);
  not not_47 (not_47_out, OP0);
  not not_48 (not_48_out, F4);
  not not_49 (not_49_out, F2);
  not not_50 (not_50_out, F0);
  not not_51 (not_51_out, OP5);
  not not_52 (not_52_out, OP4);
  not not_53 (not_53_out, OP3);
  not not_54 (not_54_out, OP2);
  not not_55 (not_55_out, OP1);
  not not_56 (not_56_out, OP0);
  not not_57 (not_57_out, F5);
  not not_58 (not_58_out, F4);
  not not_59 (not_59_out, F2);
  not not_60 (not_60_out, F1);
  not not_61 (not_61_out, F0);
  not not_62 (not_62_out, OP5);
  not not_63 (not_63_out, OP4);
  not not_64 (not_64_out, OP2);
  not not_65 (not_65_out, OP1);
  not not_66 (not_66_out, OP0);
  not not_67 (not_67_out, OP5);
  not not_68 (not_68_out, OP4);
  not not_69 (not_69_out, OP1);
  not not_70 (not_70_out, OP0);
  not not_71 (not_71_out, OP5);
  not not_72 (not_72_out, OP4);
  not not_73 (not_73_out, OP2);
  not not_74 (not_74_out, OP1);
  not not_75 (not_75_out, OP5);
  not not_76 (not_76_out, OP4);
  not not_77 (not_77_out, OP2);
  not not_78 (not_78_out, OP0);
  not not_79 (not_79_out, OP4);
  not not_80 (not_80_out, OP3);
  not not_81 (not_81_out, OP2);
  not not_82 (not_82_out, OP4);
  not not_83 (not_83_out, OP2);
  not not_84 (not_84_out, OP5);
  not not_85 (not_85_out, OP4);
  not not_86 (not_86_out, OP0);
  not not_87 (not_87_out, OP4);
  not not_88 (not_88_out, OP3);
  not not_89 (not_89_out, OP2);
  not not_90 (not_90_out, OP1);
  not not_91 (not_91_out, OP5);
  not not_92 (not_92_out, OP4);
  not not_93 (not_93_out, OP3);
  not not_94 (not_94_out, OP2);
  not not_95 (not_95_out, OP1);
  not not_96 (not_96_out, OP0);
  not not_97 (not_97_out, F5);
  not not_98 (not_98_out, F4);
  not not_99 (not_99_out, F3);
  not not_100 (not_100_out, F2);
  not not_101 (not_101_out, F0);
  not not_102 (not_102_out, OP5);
  not not_103 (not_103_out, OP4);
  not not_104 (not_104_out, OP3);
  not not_105 (not_105_out, OP2);
  not not_106 (not_106_out, OP1);
  not not_107 (not_107_out, OP0);
  not not_108 (not_108_out, F4);
  not not_109 (not_109_out, F3);
  not not_110 (not_110_out, F2);
  not not_111 (not_111_out, F0);
  not not_112 (not_112_out, OP5);
  not not_113 (not_113_out, OP4);
  not not_114 (not_114_out, OP3);
  not not_115 (not_115_out, OP2);
  not not_116 (not_116_out, OP1);
  not not_117 (not_117_out, OP0);
  not not_118 (not_118_out, F4);
  not not_119 (not_119_out, F3);
  not not_120 (not_120_out, F1);
  not not_121 (not_121_out, F0);
  not not_122 (not_122_out, OP5);
  not not_123 (not_123_out, OP4);
  not not_124 (not_124_out, OP3);
  not not_125 (not_125_out, OP2);
  not not_126 (not_126_out, OP1);
  not not_127 (not_127_out, OP0);
  not not_128 (not_128_out, F4);
  not not_129 (not_129_out, F3);
  not not_130 (not_130_out, OP5);
  not not_131 (not_131_out, OP4);
  not not_132 (not_132_out, OP3);
  not not_133 (not_133_out, OP2);
  not not_134 (not_134_out, OP1);
  not not_135 (not_135_out, OP0);
  not not_136 (not_136_out, F4);
  not not_137 (not_137_out, F2);
  not not_138 (not_138_out, F0);
  not not_139 (not_139_out, OP5);
  not not_140 (not_140_out, OP4);
  not not_141 (not_141_out, OP1);
  not not_142 (not_142_out, OP0);
  not not_143 (not_143_out, OP5);
  not not_144 (not_144_out, OP4);
  not not_145 (not_145_out, OP2);
  not not_146 (not_146_out, OP0);
  not not_147 (not_147_out, OP5);
  not not_148 (not_148_out, OP4);
  not not_149 (not_149_out, OP3);
  not not_150 (not_150_out, OP2);
  not not_151 (not_151_out, OP1);
  not not_152 (not_152_out, OP0);
  not not_153 (not_153_out, F4);
  not not_154 (not_154_out, F3);
  not not_155 (not_155_out, F2);
  not not_156 (not_156_out, F1);
  not not_157 (not_157_out, F0);
  not not_158 (not_158_out, OP5);
  not not_159 (not_159_out, OP4);
  not not_160 (not_160_out, OP3);
  not not_161 (not_161_out, OP2);
  not not_162 (not_162_out, OP1);
  not not_163 (not_163_out, OP0);
  not not_164 (not_164_out, F4);
  not not_165 (not_165_out, F3);
  not not_166 (not_166_out, F2);
  not not_167 (not_167_out, F1);
  not not_168 (not_168_out, OP5);
  not not_169 (not_169_out, OP4);
  not not_170 (not_170_out, OP3);
  not not_171 (not_171_out, OP2);
  not not_172 (not_172_out, OP1);
  not not_173 (not_173_out, OP0);
  not not_174 (not_174_out, F4);
  not not_175 (not_175_out, F3);
  not not_176 (not_176_out, F2);
  not not_177 (not_177_out, F0);
  not not_178 (not_178_out, OP5);
  not not_179 (not_179_out, OP4);
  not not_180 (not_180_out, OP3);
  not not_181 (not_181_out, OP2);
  not not_182 (not_182_out, OP1);
  not not_183 (not_183_out, OP0);
  not not_184 (not_184_out, F4);
  not not_185 (not_185_out, F3);
  not not_186 (not_186_out, F1);
  not not_187 (not_187_out, F0);
  not not_188 (not_188_out, OP5);
  not not_189 (not_189_out, OP4);
  not not_190 (not_190_out, OP3);
  not not_191 (not_191_out, OP2);
  not not_192 (not_192_out, OP1);
  not not_193 (not_193_out, OP0);
  not not_194 (not_194_out, F4);
  not not_195 (not_195_out, F2);
  not not_196 (not_196_out, OP5);
  not not_197 (not_197_out, OP4);
  not not_198 (not_198_out, OP3);
  not not_199 (not_199_out, OP2);
  not not_200 (not_200_out, OP1);
  not not_201 (not_201_out, OP0);
  not not_202 (not_202_out, F5);
  not not_203 (not_203_out, F4);
  not not_204 (not_204_out, F2);
  not not_205 (not_205_out, F1);
  not not_206 (not_206_out, F0);
  not not_207 (not_207_out, OP5);
  not not_208 (not_208_out, OP4);
  not not_209 (not_209_out, OP2);
  not not_210 (not_210_out, OP1);
  not not_211 (not_211_out, OP0);
  not not_212 (not_212_out, OP5);
  not not_213 (not_213_out, OP4);
  not not_214 (not_214_out, OP1);
  not not_215 (not_215_out, OP0);
  not not_216 (not_216_out, OP5);
  not not_217 (not_217_out, OP4);
  not not_218 (not_218_out, OP2);
  not not_219 (not_219_out, OP1);
  not not_220 (not_220_out, OP4);
  not not_221 (not_221_out, OP3);
  not not_222 (not_222_out, OP2);
  not not_223 (not_223_out, OP4);
  not not_224 (not_224_out, OP2);
  not not_225 (not_225_out, OP4);
  not not_226 (not_226_out, OP3);
  not not_227 (not_227_out, OP2);
  not not_228 (not_228_out, OP1);
  not not_229 (not_229_out, OP5);
  not not_230 (not_230_out, OP4);
  not not_231 (not_231_out, OP3);
  not not_232 (not_232_out, OP2);
  not not_233 (not_233_out, OP1);
  not not_234 (not_234_out, OP0);
  not not_235 (not_235_out, F4);
  not not_236 (not_236_out, F3);
  not not_237 (not_237_out, F1);
  not not_238 (not_238_out, OP5);
  not not_239 (not_239_out, OP4);
  not not_240 (not_240_out, OP3);
  not not_241 (not_241_out, OP2);
  not not_242 (not_242_out, OP1);
  not not_243 (not_243_out, OP0);
  not not_244 (not_244_out, F4);
  not not_245 (not_245_out, F3);
  not not_246 (not_246_out, OP5);
  not not_247 (not_247_out, OP4);
  not not_248 (not_248_out, OP3);
  not not_249 (not_249_out, OP2);
  not not_250 (not_250_out, OP1);
  not not_251 (not_251_out, OP0);
  not not_252 (not_252_out, F4);
  not not_253 (not_253_out, F2);
  not not_254 (not_254_out, F0);
  not not_255 (not_255_out, OP5);
  not not_256 (not_256_out, OP4);
  not not_257 (not_257_out, OP3);
  not not_258 (not_258_out, OP2);
  not not_259 (not_259_out, OP1);
  not not_260 (not_260_out, OP0);
  not not_261 (not_261_out, F4);
  not not_262 (not_262_out, F2);
  not not_263 (not_263_out, OP5);
  not not_264 (not_264_out, OP4);
  not not_265 (not_265_out, OP2);
  not not_266 (not_266_out, OP0);
  not not_267 (not_267_out, OP5);
  not not_268 (not_268_out, OP4);
  not not_269 (not_269_out, OP1);
  not not_270 (not_270_out, OP5);
  not not_271 (not_271_out, OP4);
  not not_272 (not_272_out, OP0);
  and and_1 (and_1_out, not_1_out, not_2_out, not_3_out, not_4_out, not_5_out, not_6_out, not_7_out, not_8_out, not_9_out, not_10_out, F1, F0);
  and and_2 (and_2_out, not_11_out, not_12_out, not_13_out, not_14_out, not_15_out, not_16_out, F5, not_17_out, not_18_out, not_19_out, not_20_out, not_21_out);
  and and_3 (and_3_out, not_22_out, not_23_out, not_24_out, not_25_out, not_26_out, not_27_out, F5, not_28_out, not_29_out, not_30_out, not_31_out, F0);
  and and_4 (and_4_out, not_32_out, not_33_out, not_34_out, not_35_out, not_36_out, not_37_out, F5, not_38_out, not_39_out, F2, not_40_out, not_41_out);
  and and_5 (and_5_out, not_42_out, not_43_out, not_44_out, not_45_out, not_46_out, not_47_out, F5, not_48_out, F3, not_49_out, F1, not_50_out);
  and and_6 (and_6_out, not_51_out, not_52_out, not_53_out, not_54_out, not_55_out, not_56_out, not_57_out, not_58_out, F3, not_59_out, not_60_out, not_61_out);
  and and_7 (and_7_out, not_62_out, not_63_out, OP3, not_64_out, not_65_out, not_66_out);
  and and_8 (and_8_out, not_67_out, not_68_out, OP3, OP2, not_69_out, not_70_out);
  and and_9 (and_9_out, not_71_out, not_72_out, OP3, not_73_out, not_74_out, OP0);
  and and_10 (and_10_out, not_75_out, not_76_out, OP3, not_77_out, OP1, not_78_out);
  and and_11 (and_11_out, OP5, not_79_out, not_80_out, not_81_out, OP1, OP0);
  and and_12 (and_12_out, OP5, not_82_out, OP3, not_83_out, OP1, OP0);
  and and_13 (and_13_out, not_84_out, not_85_out, OP3, OP2, OP1, not_86_out);
  and and_14 (and_14_out, OP5, not_87_out, not_88_out, not_89_out, not_90_out, OP0);
  and and_15 (and_15_out, not_91_out, not_92_out, not_93_out, not_94_out, not_95_out, not_96_out, not_97_out, not_98_out, not_99_out, not_100_out, F1, not_101_out);
  and and_16 (and_16_out, not_102_out, not_103_out, not_104_out, not_105_out, not_106_out, not_107_out, F5, not_108_out, not_109_out, not_110_out, F1, not_111_out);
  and and_17 (and_17_out, not_112_out, not_113_out, not_114_out, not_115_out, not_116_out, not_117_out, F5, not_118_out, not_119_out, F2, not_120_out, not_121_out);
  and and_18 (and_18_out, not_122_out, not_123_out, not_124_out, not_125_out, not_126_out, not_127_out, F5, not_128_out, not_129_out, F2, F1, F0);
  and and_19 (and_19_out, not_130_out, not_131_out, not_132_out, not_133_out, not_134_out, not_135_out, F5, not_136_out, F3, not_137_out, F1, not_138_out);
  and and_20 (and_20_out, not_139_out, not_140_out, OP3, OP2, not_141_out, not_142_out);
  and and_21 (and_21_out, not_143_out, not_144_out, OP3, not_145_out, OP1, not_146_out);
  and and_22 (and_22_out, not_147_out, not_148_out, not_149_out, not_150_out, not_151_out, not_152_out, F5, not_153_out, not_154_out, not_155_out, not_156_out, not_157_out);
  and and_23 (and_23_out, not_158_out, not_159_out, not_160_out, not_161_out, not_162_out, not_163_out, F5, not_164_out, not_165_out, not_166_out, not_167_out, F0);
  and and_24 (and_24_out, not_168_out, not_169_out, not_170_out, not_171_out, not_172_out, not_173_out, F5, not_174_out, not_175_out, not_176_out, F1, not_177_out);
  and and_25 (and_25_out, not_178_out, not_179_out, not_180_out, not_181_out, not_182_out, not_183_out, F5, not_184_out, not_185_out, F2, not_186_out, not_187_out);
  and and_26 (and_26_out, not_188_out, not_189_out, not_190_out, not_191_out, not_192_out, not_193_out, F5, not_194_out, F3, not_195_out, F1, F0);
  and and_27 (and_27_out, not_196_out, not_197_out, not_198_out, not_199_out, not_200_out, not_201_out, not_202_out, not_203_out, F3, not_204_out, not_205_out, not_206_out);
  and and_28 (and_28_out, not_207_out, not_208_out, OP3, not_209_out, not_210_out, not_211_out);
  and and_29 (and_29_out, not_212_out, not_213_out, OP3, OP2, not_214_out, not_215_out);
  and and_30 (and_30_out, not_216_out, not_217_out, OP3, not_218_out, not_219_out, OP0);
  and and_31 (and_31_out, OP5, not_220_out, not_221_out, not_222_out, OP1, OP0);
  and and_32 (and_32_out, OP5, not_223_out, OP3, not_224_out, OP1, OP0);
  and and_33 (and_33_out, OP5, not_225_out, not_226_out, not_227_out, not_228_out, OP0);
  and and_34 (and_34_out, not_229_out, not_230_out, not_231_out, not_232_out, not_233_out, not_234_out, F5, not_235_out, not_236_out, F2, not_237_out, F0);
  and and_35 (and_35_out, not_238_out, not_239_out, not_240_out, not_241_out, not_242_out, not_243_out, F5, not_244_out, not_245_out, F2, F1, F0);
  and and_36 (and_36_out, not_246_out, not_247_out, not_248_out, not_249_out, not_250_out, not_251_out, F5, not_252_out, F3, not_253_out, F1, not_254_out);
  and and_37 (and_37_out, not_255_out, not_256_out, not_257_out, not_258_out, not_259_out, not_260_out, F5, not_261_out, F3, not_262_out, F1, F0);
  and and_38 (and_38_out, not_263_out, not_264_out, OP3, not_265_out, OP1, not_266_out);
  and and_39 (and_39_out, not_267_out, not_268_out, OP3, OP2, not_269_out, OP0);
  and and_40 (and_40_out, not_270_out, not_271_out, OP3, OP2, OP1, not_272_out);
  or or_1 (S1, and_15_out, and_16_out, and_17_out, and_18_out, and_19_out, and_20_out, and_21_out);
  or or_2 (S3, and_34_out, and_35_out, and_36_out, and_37_out, and_38_out, and_39_out, and_40_out);
  or or_3 (S0, and_1_out, and_2_out, and_3_out, and_4_out, and_5_out, and_6_out, and_7_out, and_8_out, and_9_out, and_10_out, and_11_out, and_12_out, and_13_out, and_14_out);
  or or_4 (S2, and_22_out, and_23_out, and_24_out, and_25_out, and_26_out, and_27_out, and_28_out, and_29_out, and_30_out, and_31_out, and_32_out, and_33_out);
endmodule

// 控制信号生成
module \控制信号自动生成  (
  input  OP0,
  input  OP1,
  input  OP2,
  input  OP3,
  input  OP4,
  input  OP5,
  input  F0,
  input  F1,
  input  F2,
  input  F3,
  input  F4,
  input  F5,
  output MemToReg,
  output MemWrite,
  output ALU_SRC,
  output RegWrite,
  output SysCALL,
  output SignedExt,
  output RegDst,
  output BEQ,
  output BNE,
  output JR,
  output JMP,
  output JAL
);

  wire and_1_out, and_2_out, and_4_out, and_5_out, and_6_out, and_7_out, and_8_out, and_9_out, and_10_out,
       and_11_out, and_12_out, and_13_out, and_14_out, and_15_out, and_16_out, and_17_out, and_18_out,
       and_19_out, and_20_out, and_21_out, and_22_out, and_23_out, and_24_out, and_25_out, and_26_out,
       and_27_out, and_28_out, and_29_out, and_30_out, and_31_out, and_32_out, and_33_out, and_35_out,
       and_36_out, and_37_out, and_38_out, and_39_out, and_40_out, and_41_out, and_42_out, and_43_out,
       and_44_out, and_45_out, and_46_out, and_47_out, and_48_out, and_49_out, and_50_out, and_51_out,
       and_52_out, and_53_out, and_54_out, and_55_out, and_59_out, and_60_out, and_61_out, not_1_out,
       not_2_out, not_3_out, not_4_out, not_5_out, not_6_out, not_7_out, not_8_out, not_9_out, not_10_out,
       not_11_out, not_12_out, not_13_out, not_14_out, not_15_out, not_16_out, not_17_out, not_18_out,
       not_19_out, not_20_out, not_21_out, not_22_out, not_23_out, not_24_out, not_25_out, not_26_out,
       not_27_out, not_28_out, not_29_out, not_30_out, not_31_out, not_32_out, not_33_out, not_34_out,
       not_35_out, not_36_out, not_37_out, not_38_out, not_39_out, not_40_out, not_41_out, not_42_out,
       not_43_out, not_44_out, not_45_out, not_46_out, not_47_out, not_48_out, not_49_out, not_50_out,
       not_51_out, not_52_out, not_53_out, not_54_out, not_55_out, not_56_out, not_57_out, not_58_out,
       not_59_out, not_60_out, not_61_out, not_62_out, not_63_out, not_64_out, not_65_out, not_66_out,
       not_67_out, not_68_out, not_69_out, not_70_out, not_71_out, not_72_out, not_73_out, not_74_out,
       not_75_out, not_76_out, not_77_out, not_78_out, not_79_out, not_80_out, not_81_out, not_82_out,
       not_83_out, not_84_out, not_85_out, not_86_out, not_87_out, not_88_out, not_89_out, not_90_out,
       not_91_out, not_92_out, not_93_out, not_94_out, not_95_out, not_96_out, not_97_out, not_98_out,
       not_99_out, not_100_out, not_101_out, not_102_out, not_103_out, not_104_out, not_105_out, not_106_out,
       not_107_out, not_108_out, not_109_out, not_110_out, not_111_out, not_112_out, not_113_out,
       not_114_out, not_115_out, not_116_out, not_117_out, not_118_out, not_119_out, not_120_out,
       not_121_out, not_122_out, not_123_out, not_124_out, not_125_out, not_126_out, not_127_out,
       not_128_out, not_129_out, not_130_out, not_131_out, not_132_out, not_133_out, not_134_out,
       not_135_out, not_136_out, not_137_out, not_138_out, not_139_out, not_140_out, not_141_out,
       not_142_out, not_143_out, not_144_out, not_145_out, not_146_out, not_147_out, not_148_out,
       not_149_out, not_150_out, not_151_out, not_152_out, not_153_out, not_154_out, not_155_out,
       not_156_out, not_157_out, not_158_out, not_159_out, not_160_out, not_161_out, not_162_out,
       not_163_out, not_164_out, not_165_out, not_166_out, not_167_out, not_168_out, not_169_out,
       not_170_out, not_171_out, not_172_out, not_173_out, not_174_out, not_175_out, not_176_out,
       not_177_out, not_178_out, not_179_out, not_180_out, not_181_out, not_182_out, not_183_out,
       not_184_out, not_185_out, not_186_out, not_187_out, not_188_out, not_189_out, not_190_out,
       not_191_out, not_192_out, not_193_out, not_194_out, not_195_out, not_196_out, not_197_out,
       not_198_out, not_199_out, not_200_out, not_201_out, not_202_out, not_203_out, not_204_out,
       not_205_out, not_206_out, not_207_out, not_208_out, not_209_out, not_210_out, not_211_out,
       not_212_out, not_213_out, not_214_out, not_215_out, not_216_out, not_217_out, not_218_out,
       not_219_out, not_220_out, not_221_out, not_222_out, not_223_out, not_224_out, not_225_out,
       not_226_out, not_227_out, not_228_out, not_229_out, not_230_out, not_231_out, not_232_out,
       not_233_out, not_234_out, not_235_out, not_236_out, not_237_out, not_238_out, not_239_out,
       not_240_out, not_241_out, not_242_out, not_243_out, not_244_out, not_245_out, not_246_out,
       not_247_out, not_248_out, not_249_out, not_250_out, not_251_out, not_252_out, not_253_out,
       not_254_out, not_255_out, not_256_out, not_257_out, not_258_out, not_259_out, not_260_out,
       not_261_out, not_262_out, not_263_out, not_264_out, not_265_out, not_266_out, not_267_out,
       not_268_out, not_269_out, not_270_out, not_271_out, not_272_out, not_273_out, not_274_out,
       not_275_out, not_276_out, not_277_out, not_278_out, not_279_out, not_280_out, not_281_out,
       not_282_out, not_283_out, not_284_out, not_285_out, not_286_out, not_287_out, not_288_out,
       not_289_out, not_290_out, not_291_out, not_292_out, not_293_out, not_294_out, not_295_out,
       not_296_out, not_297_out, not_298_out, not_299_out, not_300_out, not_301_out, not_302_out,
       not_303_out, not_304_out, not_305_out, not_306_out, not_307_out, not_308_out, not_309_out,
       not_310_out, not_311_out, not_312_out, not_313_out, not_314_out, not_315_out, not_316_out,
       not_317_out, not_318_out, not_319_out, not_320_out, not_321_out, not_322_out, not_323_out,
       not_324_out, not_325_out, not_326_out, not_327_out, not_328_out, not_329_out, not_330_out,
       not_331_out, not_332_out, not_333_out, not_334_out, not_335_out, not_336_out, not_337_out,
       not_338_out, not_339_out, not_340_out, not_341_out, not_342_out, not_343_out, not_344_out,
       not_345_out, not_346_out, not_347_out, not_348_out, not_349_out, not_350_out, not_351_out,
       not_352_out, not_353_out, not_354_out, not_355_out, not_356_out, not_357_out, not_358_out,
       not_359_out, not_360_out, not_361_out, not_362_out, not_363_out, not_364_out, not_365_out,
       not_366_out, not_367_out, not_368_out, not_369_out, not_370_out, not_371_out, not_372_out,
       not_373_out, not_374_out, not_375_out, not_376_out, not_377_out, not_378_out, not_379_out,
       not_380_out, not_381_out, not_382_out, not_383_out, not_384_out, not_385_out, not_386_out,
       not_387_out, not_388_out, not_389_out, not_390_out, not_391_out, not_392_out, not_393_out,
       not_394_out, not_395_out, not_396_out, not_397_out, not_398_out, not_399_out, not_400_out,
       not_401_out, not_402_out, not_403_out, not_404_out, not_405_out, not_406_out, not_407_out, not_408_out;

  not not_1 (not_1_out, OP4);
  not not_2 (not_2_out, OP3);
  not not_3 (not_3_out, OP2);
  not not_4 (not_4_out, OP4);
  not not_5 (not_5_out, OP3);
  not not_6 (not_6_out, OP2);
  not not_7 (not_7_out, OP1);
  not not_8 (not_8_out, OP4);
  not not_9 (not_9_out, OP2);
  not not_10 (not_10_out, OP5);
  not not_11 (not_11_out, OP4);
  not not_12 (not_12_out, OP2);
  not not_13 (not_13_out, OP1);
  not not_14 (not_14_out, OP0);
  not not_15 (not_15_out, OP5);
  not not_16 (not_16_out, OP4);
  not not_17 (not_17_out, OP1);
  not not_18 (not_18_out, OP0);
  not not_19 (not_19_out, OP5);
  not not_20 (not_20_out, OP4);
  not not_21 (not_21_out, OP2);
  not not_22 (not_22_out, OP1);
  not not_23 (not_23_out, OP5);
  not not_24 (not_24_out, OP4);
  not not_25 (not_25_out, OP2);
  not not_26 (not_26_out, OP0);
  not not_27 (not_27_out, OP5);
  not not_28 (not_28_out, OP4);
  not not_29 (not_29_out, OP1);
  not not_30 (not_30_out, OP4);
  not not_31 (not_31_out, OP3);
  not not_32 (not_32_out, OP2);
  not not_33 (not_33_out, OP4);
  not not_34 (not_34_out, OP2);
  not not_35 (not_35_out, OP5);
  not not_36 (not_36_out, OP4);
  not not_37 (not_37_out, OP0);
  not not_38 (not_38_out, OP4);
  not not_39 (not_39_out, OP3);
  not not_40 (not_40_out, OP2);
  not not_41 (not_41_out, OP1);
  not not_42 (not_42_out, OP5);
  not not_43 (not_43_out, OP4);
  not not_44 (not_44_out, OP3);
  not not_45 (not_45_out, OP2);
  not not_46 (not_46_out, OP1);
  not not_47 (not_47_out, OP0);
  not not_48 (not_48_out, F5);
  not not_49 (not_49_out, F4);
  not not_50 (not_50_out, F3);
  not not_51 (not_51_out, F2);
  not not_52 (not_52_out, F1);
  not not_53 (not_53_out, F0);
  not not_54 (not_54_out, OP5);
  not not_55 (not_55_out, OP4);
  not not_56 (not_56_out, OP3);
  not not_57 (not_57_out, OP2);
  not not_58 (not_58_out, OP1);
  not not_59 (not_59_out, OP0);
  not not_60 (not_60_out, F5);
  not not_61 (not_61_out, F4);
  not not_62 (not_62_out, F3);
  not not_63 (not_63_out, F2);
  not not_64 (not_64_out, OP5);
  not not_65 (not_65_out, OP4);
  not not_66 (not_66_out, OP3);
  not not_67 (not_67_out, OP2);
  not not_68 (not_68_out, OP1);
  not not_69 (not_69_out, OP0);
  not not_70 (not_70_out, F5);
  not not_71 (not_71_out, F4);
  not not_72 (not_72_out, F3);
  not not_73 (not_73_out, F2);
  not not_74 (not_74_out, F0);
  not not_75 (not_75_out, OP5);
  not not_76 (not_76_out, OP4);
  not not_77 (not_77_out, OP3);
  not not_78 (not_78_out, OP2);
  not not_79 (not_79_out, OP1);
  not not_80 (not_80_out, OP0);
  not not_81 (not_81_out, F4);
  not not_82 (not_82_out, F3);
  not not_83 (not_83_out, F2);
  not not_84 (not_84_out, F1);
  not not_85 (not_85_out, F0);
  not not_86 (not_86_out, OP5);
  not not_87 (not_87_out, OP4);
  not not_88 (not_88_out, OP3);
  not not_89 (not_89_out, OP2);
  not not_90 (not_90_out, OP1);
  not not_91 (not_91_out, OP0);
  not not_92 (not_92_out, F4);
  not not_93 (not_93_out, F3);
  not not_94 (not_94_out, F2);
  not not_95 (not_95_out, F1);
  not not_96 (not_96_out, OP5);
  not not_97 (not_97_out, OP4);
  not not_98 (not_98_out, OP3);
  not not_99 (not_99_out, OP2);
  not not_100 (not_100_out, OP1);
  not not_101 (not_101_out, OP0);
  not not_102 (not_102_out, F4);
  not not_103 (not_103_out, F3);
  not not_104 (not_104_out, F2);
  not not_105 (not_105_out, F0);
  not not_106 (not_106_out, OP5);
  not not_107 (not_107_out, OP4);
  not not_108 (not_108_out, OP3);
  not not_109 (not_109_out, OP2);
  not not_110 (not_110_out, OP1);
  not not_111 (not_111_out, OP0);
  not not_112 (not_112_out, F4);
  not not_113 (not_113_out, F3);
  not not_114 (not_114_out, F1);
  not not_115 (not_115_out, F0);
  not not_116 (not_116_out, OP5);
  not not_117 (not_117_out, OP4);
  not not_118 (not_118_out, OP3);
  not not_119 (not_119_out, OP2);
  not not_120 (not_120_out, OP1);
  not not_121 (not_121_out, OP0);
  not not_122 (not_122_out, F4);
  not not_123 (not_123_out, F3);
  not not_124 (not_124_out, F1);
  not not_125 (not_125_out, OP5);
  not not_126 (not_126_out, OP4);
  not not_127 (not_127_out, OP3);
  not not_128 (not_128_out, OP2);
  not not_129 (not_129_out, OP1);
  not not_130 (not_130_out, OP0);
  not not_131 (not_131_out, F4);
  not not_132 (not_132_out, F3);
  not not_133 (not_133_out, OP5);
  not not_134 (not_134_out, OP4);
  not not_135 (not_135_out, OP3);
  not not_136 (not_136_out, OP2);
  not not_137 (not_137_out, OP1);
  not not_138 (not_138_out, OP0);
  not not_139 (not_139_out, F4);
  not not_140 (not_140_out, F2);
  not not_141 (not_141_out, F0);
  not not_142 (not_142_out, OP5);
  not not_143 (not_143_out, OP4);
  not not_144 (not_144_out, OP3);
  not not_145 (not_145_out, OP2);
  not not_146 (not_146_out, OP1);
  not not_147 (not_147_out, OP0);
  not not_148 (not_148_out, F4);
  not not_149 (not_149_out, F2);
  not not_150 (not_150_out, OP5);
  not not_151 (not_151_out, OP4);
  not not_152 (not_152_out, OP3);
  not not_153 (not_153_out, OP2);
  not not_154 (not_154_out, OP5);
  not not_155 (not_155_out, OP4);
  not not_156 (not_156_out, OP2);
  not not_157 (not_157_out, OP1);
  not not_158 (not_158_out, OP0);
  not not_159 (not_159_out, OP5);
  not not_160 (not_160_out, OP4);
  not not_161 (not_161_out, OP1);
  not not_162 (not_162_out, OP0);
  not not_163 (not_163_out, OP5);
  not not_164 (not_164_out, OP4);
  not not_165 (not_165_out, OP2);
  not not_166 (not_166_out, OP1);
  not not_167 (not_167_out, OP5);
  not not_168 (not_168_out, OP4);
  not not_169 (not_169_out, OP2);
  not not_170 (not_170_out, OP0);
  not not_171 (not_171_out, OP5);
  not not_172 (not_172_out, OP4);
  not not_173 (not_173_out, OP1);
  not not_174 (not_174_out, OP4);
  not not_175 (not_175_out, OP3);
  not not_176 (not_176_out, OP2);
  not not_177 (not_177_out, OP5);
  not not_178 (not_178_out, OP4);
  not not_179 (not_179_out, OP3);
  not not_180 (not_180_out, OP2);
  not not_181 (not_181_out, OP1);
  not not_182 (not_182_out, OP0);
  not not_183 (not_183_out, F5);
  not not_184 (not_184_out, F4);
  not not_185 (not_185_out, F3);
  not not_186 (not_186_out, F1);
  not not_187 (not_187_out, F0);
  not not_188 (not_188_out, OP5);
  not not_189 (not_189_out, OP4);
  not not_190 (not_190_out, OP0);
  not not_191 (not_191_out, OP4);
  not not_192 (not_192_out, OP3);
  not not_193 (not_193_out, OP2);
  not not_194 (not_194_out, OP1);
  not not_195 (not_195_out, OP5);
  not not_196 (not_196_out, OP4);
  not not_197 (not_197_out, OP3);
  not not_198 (not_198_out, OP2);
  not not_199 (not_199_out, OP1);
  not not_200 (not_200_out, OP0);
  not not_201 (not_201_out, F5);
  not not_202 (not_202_out, F4);
  not not_203 (not_203_out, F1);
  not not_204 (not_204_out, F0);
  not not_205 (not_205_out, OP5);
  not not_206 (not_206_out, OP4);
  not not_207 (not_207_out, OP3);
  not not_208 (not_208_out, OP1);
  not not_209 (not_209_out, OP0);
  not not_210 (not_210_out, OP5);
  not not_211 (not_211_out, OP4);
  not not_212 (not_212_out, OP3);
  not not_213 (not_213_out, OP1);
  not not_214 (not_214_out, OP5);
  not not_215 (not_215_out, OP4);
  not not_216 (not_216_out, OP2);
  not not_217 (not_217_out, OP1);
  not not_218 (not_218_out, OP0);
  not not_219 (not_219_out, OP5);
  not not_220 (not_220_out, OP4);
  not not_221 (not_221_out, OP2);
  not not_222 (not_222_out, OP1);
  not not_223 (not_223_out, OP5);
  not not_224 (not_224_out, OP4);
  not not_225 (not_225_out, OP2);
  not not_226 (not_226_out, OP0);
  not not_227 (not_227_out, OP4);
  not not_228 (not_228_out, OP3);
  not not_229 (not_229_out, OP2);
  not not_230 (not_230_out, OP4);
  not not_231 (not_231_out, OP2);
  not not_232 (not_232_out, OP5);
  not not_233 (not_233_out, OP4);
  not not_234 (not_234_out, OP3);
  not not_235 (not_235_out, OP5);
  not not_236 (not_236_out, OP4);
  not not_237 (not_237_out, OP3);
  not not_238 (not_238_out, OP2);
  not not_239 (not_239_out, OP1);
  not not_240 (not_240_out, OP0);
  not not_241 (not_241_out, F5);
  not not_242 (not_242_out, F4);
  not not_243 (not_243_out, F3);
  not not_244 (not_244_out, F2);
  not not_245 (not_245_out, F1);
  not not_246 (not_246_out, F0);
  not not_247 (not_247_out, OP5);
  not not_248 (not_248_out, OP4);
  not not_249 (not_249_out, OP3);
  not not_250 (not_250_out, OP2);
  not not_251 (not_251_out, OP1);
  not not_252 (not_252_out, OP0);
  not not_253 (not_253_out, F5);
  not not_254 (not_254_out, F4);
  not not_255 (not_255_out, F3);
  not not_256 (not_256_out, F2);
  not not_257 (not_257_out, OP5);
  not not_258 (not_258_out, OP4);
  not not_259 (not_259_out, OP3);
  not not_260 (not_260_out, OP2);
  not not_261 (not_261_out, OP1);
  not not_262 (not_262_out, OP0);
  not not_263 (not_263_out, F5);
  not not_264 (not_264_out, F4);
  not not_265 (not_265_out, F3);
  not not_266 (not_266_out, F2);
  not not_267 (not_267_out, F0);
  not not_268 (not_268_out, OP5);
  not not_269 (not_269_out, OP4);
  not not_270 (not_270_out, OP3);
  not not_271 (not_271_out, OP2);
  not not_272 (not_272_out, OP1);
  not not_273 (not_273_out, OP0);
  not not_274 (not_274_out, F4);
  not not_275 (not_275_out, F3);
  not not_276 (not_276_out, F2);
  not not_277 (not_277_out, F1);
  not not_278 (not_278_out, F0);
  not not_279 (not_279_out, OP5);
  not not_280 (not_280_out, OP4);
  not not_281 (not_281_out, OP3);
  not not_282 (not_282_out, OP2);
  not not_283 (not_283_out, OP1);
  not not_284 (not_284_out, OP0);
  not not_285 (not_285_out, F4);
  not not_286 (not_286_out, F3);
  not not_287 (not_287_out, F2);
  not not_288 (not_288_out, F1);
  not not_289 (not_289_out, OP5);
  not not_290 (not_290_out, OP4);
  not not_291 (not_291_out, OP3);
  not not_292 (not_292_out, OP2);
  not not_293 (not_293_out, OP1);
  not not_294 (not_294_out, OP0);
  not not_295 (not_295_out, F4);
  not not_296 (not_296_out, F3);
  not not_297 (not_297_out, F2);
  not not_298 (not_298_out, F0);
  not not_299 (not_299_out, OP5);
  not not_300 (not_300_out, OP4);
  not not_301 (not_301_out, OP3);
  not not_302 (not_302_out, OP2);
  not not_303 (not_303_out, OP1);
  not not_304 (not_304_out, OP0);
  not not_305 (not_305_out, F4);
  not not_306 (not_306_out, F3);
  not not_307 (not_307_out, F1);
  not not_308 (not_308_out, F0);
  not not_309 (not_309_out, OP5);
  not not_310 (not_310_out, OP4);
  not not_311 (not_311_out, OP3);
  not not_312 (not_312_out, OP2);
  not not_313 (not_313_out, OP1);
  not not_314 (not_314_out, OP0);
  not not_315 (not_315_out, F4);
  not not_316 (not_316_out, F3);
  not not_317 (not_317_out, F1);
  not not_318 (not_318_out, OP5);
  not not_319 (not_319_out, OP4);
  not not_320 (not_320_out, OP3);
  not not_321 (not_321_out, OP2);
  not not_322 (not_322_out, OP1);
  not not_323 (not_323_out, OP0);
  not not_324 (not_324_out, F4);
  not not_325 (not_325_out, F3);
  not not_326 (not_326_out, OP5);
  not not_327 (not_327_out, OP4);
  not not_328 (not_328_out, OP3);
  not not_329 (not_329_out, OP2);
  not not_330 (not_330_out, OP1);
  not not_331 (not_331_out, OP0);
  not not_332 (not_332_out, F4);
  not not_333 (not_333_out, F2);
  not not_334 (not_334_out, F0);
  not not_335 (not_335_out, OP5);
  not not_336 (not_336_out, OP4);
  not not_337 (not_337_out, OP3);
  not not_338 (not_338_out, OP2);
  not not_339 (not_339_out, OP1);
  not not_340 (not_340_out, OP0);
  not not_341 (not_341_out, F4);
  not not_342 (not_342_out, F2);
  not not_343 (not_343_out, OP5);
  not not_344 (not_344_out, OP4);
  not not_345 (not_345_out, OP3);
  not not_346 (not_346_out, OP2);
  not not_347 (not_347_out, OP1);
  not not_348 (not_348_out, OP0);
  not not_349 (not_349_out, F5);
  not not_350 (not_350_out, F4);
  not not_351 (not_351_out, F2);
  not not_352 (not_352_out, F1);
  not not_353 (not_353_out, F0);
  not not_354 (not_354_out, OP5);
  not not_355 (not_355_out, OP4);
  not not_356 (not_356_out, OP3);
  not not_357 (not_357_out, OP2);
  not not_358 (not_358_out, OP1);
  not not_359 (not_359_out, OP0);
  not not_360 (not_360_out, F5);
  not not_361 (not_361_out, F4);
  not not_362 (not_362_out, F3);
  not not_363 (not_363_out, F1);
  not not_364 (not_364_out, F0);
  not not_365 (not_365_out, OP5);
  not not_366 (not_366_out, OP4);
  not not_367 (not_367_out, OP3);
  not not_368 (not_368_out, OP1);
  not not_369 (not_369_out, OP0);
  not not_370 (not_370_out, OP5);
  not not_371 (not_371_out, OP4);
  not not_372 (not_372_out, OP3);
  not not_373 (not_373_out, OP1);
  not not_374 (not_374_out, OP5);
  not not_375 (not_375_out, OP4);
  not not_376 (not_376_out, OP3);
  not not_377 (not_377_out, OP2);
  not not_378 (not_378_out, OP1);
  not not_379 (not_379_out, OP0);
  not not_380 (not_380_out, F5);
  not not_381 (not_381_out, F4);
  not not_382 (not_382_out, F2);
  not not_383 (not_383_out, F1);
  not not_384 (not_384_out, F0);
  not not_385 (not_385_out, OP5);
  not not_386 (not_386_out, OP4);
  not not_387 (not_387_out, OP3);
  not not_388 (not_388_out, OP2);
  not not_389 (not_389_out, OP1);
  not not_390 (not_390_out, OP0);
  not not_391 (not_391_out, F5);
  not not_392 (not_392_out, F4);
  not not_393 (not_393_out, F2);
  not not_394 (not_394_out, F1);
  not not_395 (not_395_out, F0);
  not not_396 (not_396_out, OP5);
  not not_397 (not_397_out, OP4);
  not not_398 (not_398_out, OP3);
  not not_399 (not_399_out, OP2);
  not not_400 (not_400_out, OP0);
  not not_401 (not_401_out, OP5);
  not not_402 (not_402_out, OP4);
  not not_403 (not_403_out, OP3);
  not not_404 (not_404_out, OP2);
  not not_405 (not_405_out, OP5);
  not not_406 (not_406_out, OP4);
  not not_407 (not_407_out, OP3);
  not not_408 (not_408_out, OP2);
  and and_1 (and_1_out, OP5, not_1_out, not_2_out, not_3_out, OP1, OP0);
  and and_2 (and_2_out, OP5, not_4_out, not_5_out, not_6_out, not_7_out, OP0);
  and and_3 (MemWrite, OP5, not_8_out, OP3, not_9_out, OP1, OP0);
  and and_4 (and_4_out, not_10_out, not_11_out, OP3, not_12_out, not_13_out, not_14_out);
  and and_5 (and_5_out, not_15_out, not_16_out, OP3, OP2, not_17_out, not_18_out);
  and and_6 (and_6_out, not_19_out, not_20_out, OP3, not_21_out, not_22_out, OP0);
  and and_7 (and_7_out, not_23_out, not_24_out, OP3, not_25_out, OP1, not_26_out);
  and and_8 (and_8_out, not_27_out, not_28_out, OP3, OP2, not_29_out, OP0);
  and and_9 (and_9_out, OP5, not_30_out, not_31_out, not_32_out, OP1, OP0);
  and and_10 (and_10_out, OP5, not_33_out, OP3, not_34_out, OP1, OP0);
  and and_11 (and_11_out, not_35_out, not_36_out, OP3, OP2, OP1, not_37_out);
  and and_12 (and_12_out, OP5, not_38_out, not_39_out, not_40_out, not_41_out, OP0);
  and and_13 (and_13_out, not_42_out, not_43_out, not_44_out, not_45_out, not_46_out, not_47_out, not_48_out, not_49_out, not_50_out, not_51_out, not_52_out, not_53_out);
  and and_14 (and_14_out, not_54_out, not_55_out, not_56_out, not_57_out, not_58_out, not_59_out, not_60_out, not_61_out, not_62_out, not_63_out, F1, F0);
  and and_15 (and_15_out, not_64_out, not_65_out, not_66_out, not_67_out, not_68_out, not_69_out, not_70_out, not_71_out, not_72_out, not_73_out, F1, not_74_out);
  and and_16 (and_16_out, not_75_out, not_76_out, not_77_out, not_78_out, not_79_out, not_80_out, F5, not_81_out, not_82_out, not_83_out, not_84_out, not_85_out);
  and and_17 (and_17_out, not_86_out, not_87_out, not_88_out, not_89_out, not_90_out, not_91_out, F5, not_92_out, not_93_out, not_94_out, not_95_out, F0);
  and and_18 (and_18_out, not_96_out, not_97_out, not_98_out, not_99_out, not_100_out, not_101_out, F5, not_102_out, not_103_out, not_104_out, F1, not_105_out);
  and and_19 (and_19_out, not_106_out, not_107_out, not_108_out, not_109_out, not_110_out, not_111_out, F5, not_112_out, not_113_out, F2, not_114_out, not_115_out);
  and and_20 (and_20_out, not_116_out, not_117_out, not_118_out, not_119_out, not_120_out, not_121_out, F5, not_122_out, not_123_out, F2, not_124_out, F0);
  and and_21 (and_21_out, not_125_out, not_126_out, not_127_out, not_128_out, not_129_out, not_130_out, F5, not_131_out, not_132_out, F2, F1, F0);
  and and_22 (and_22_out, not_133_out, not_134_out, not_135_out, not_136_out, not_137_out, not_138_out, F5, not_139_out, F3, not_140_out, F1, not_141_out);
  and and_23 (and_23_out, not_142_out, not_143_out, not_144_out, not_145_out, not_146_out, not_147_out, F5, not_148_out, F3, not_149_out, F1, F0);
  and and_24 (and_24_out, not_150_out, not_151_out, not_152_out, not_153_out, OP1, OP0);
  and and_25 (and_25_out, not_154_out, not_155_out, OP3, not_156_out, not_157_out, not_158_out);
  and and_26 (and_26_out, not_159_out, not_160_out, OP3, OP2, not_161_out, not_162_out);
  and and_27 (and_27_out, not_163_out, not_164_out, OP3, not_165_out, not_166_out, OP0);
  and and_28 (and_28_out, not_167_out, not_168_out, OP3, not_169_out, OP1, not_170_out);
  and and_29 (and_29_out, not_171_out, not_172_out, OP3, OP2, not_173_out, OP0);
  and and_30 (and_30_out, OP5, not_174_out, not_175_out, not_176_out, OP1, OP0);
  and and_31 (and_31_out, not_177_out, not_178_out, not_179_out, not_180_out, not_181_out, not_182_out, not_183_out, not_184_out, not_185_out, F2, not_186_out, not_187_out);
  and and_32 (and_32_out, not_188_out, not_189_out, OP3, OP2, OP1, not_190_out);
  and and_33 (and_33_out, OP5, not_191_out, not_192_out, not_193_out, not_194_out, OP0);
  and and_34 (SysCALL, not_195_out, not_196_out, not_197_out, not_198_out, not_199_out, not_200_out, not_201_out, not_202_out, F3, F2, not_203_out, not_204_out);
  and and_35 (and_35_out, not_205_out, not_206_out, not_207_out, OP2, not_208_out, not_209_out);
  and and_36 (and_36_out, not_210_out, not_211_out, not_212_out, OP2, not_213_out, OP0);
  and and_37 (and_37_out, not_214_out, not_215_out, OP3, not_216_out, not_217_out, not_218_out);
  and and_38 (and_38_out, not_219_out, not_220_out, OP3, not_221_out, not_222_out, OP0);
  and and_39 (and_39_out, not_223_out, not_224_out, OP3, not_225_out, OP1, not_226_out);
  and and_40 (and_40_out, OP5, not_227_out, not_228_out, not_229_out, OP1, OP0);
  and and_41 (and_41_out, OP5, not_230_out, OP3, not_231_out, OP1, OP0);
  and and_42 (and_42_out, not_232_out, not_233_out, not_234_out, OP2, OP1, OP0);
  and and_43 (and_43_out, not_235_out, not_236_out, not_237_out, not_238_out, not_239_out, not_240_out, not_241_out, not_242_out, not_243_out, not_244_out, not_245_out, not_246_out);
  and and_44 (and_44_out, not_247_out, not_248_out, not_249_out, not_250_out, not_251_out, not_252_out, not_253_out, not_254_out, not_255_out, not_256_out, F1, F0);
  and and_45 (and_45_out, not_257_out, not_258_out, not_259_out, not_260_out, not_261_out, not_262_out, not_263_out, not_264_out, not_265_out, not_266_out, F1, not_267_out);
  and and_46 (and_46_out, not_268_out, not_269_out, not_270_out, not_271_out, not_272_out, not_273_out, F5, not_274_out, not_275_out, not_276_out, not_277_out, not_278_out);
  and and_47 (and_47_out, not_279_out, not_280_out, not_281_out, not_282_out, not_283_out, not_284_out, F5, not_285_out, not_286_out, not_287_out, not_288_out, F0);
  and and_48 (and_48_out, not_289_out, not_290_out, not_291_out, not_292_out, not_293_out, not_294_out, F5, not_295_out, not_296_out, not_297_out, F1, not_298_out);
  and and_49 (and_49_out, not_299_out, not_300_out, not_301_out, not_302_out, not_303_out, not_304_out, F5, not_305_out, not_306_out, F2, not_307_out, not_308_out);
  and and_50 (and_50_out, not_309_out, not_310_out, not_311_out, not_312_out, not_313_out, not_314_out, F5, not_315_out, not_316_out, F2, not_317_out, F0);
  and and_51 (and_51_out, not_318_out, not_319_out, not_320_out, not_321_out, not_322_out, not_323_out, F5, not_324_out, not_325_out, F2, F1, F0);
  and and_52 (and_52_out, not_326_out, not_327_out, not_328_out, not_329_out, not_330_out, not_331_out, F5, not_332_out, F3, not_333_out, F1, not_334_out);
  and and_53 (and_53_out, not_335_out, not_336_out, not_337_out, not_338_out, not_339_out, not_340_out, F5, not_341_out, F3, not_342_out, F1, F0);
  and and_54 (and_54_out, not_343_out, not_344_out, not_345_out, not_346_out, not_347_out, not_348_out, not_349_out, not_350_out, F3, not_351_out, not_352_out, not_353_out);
  and and_55 (and_55_out, not_354_out, not_355_out, not_356_out, not_357_out, not_358_out, not_359_out, not_360_out, not_361_out, not_362_out, F2, not_363_out, not_364_out);
  and and_56 (BEQ, not_365_out, not_366_out, not_367_out, OP2, not_368_out, not_369_out);
  and and_57 (BNE, not_370_out, not_371_out, not_372_out, OP2, not_373_out, OP0);
  and and_58 (JR, not_374_out, not_375_out, not_376_out, not_377_out, not_378_out, not_379_out, not_380_out, not_381_out, F3, not_382_out, not_383_out, not_384_out);
  and and_59 (and_59_out, not_385_out, not_386_out, not_387_out, not_388_out, not_389_out, not_390_out, not_391_out, not_392_out, F3, not_393_out, not_394_out, not_395_out);
  and and_60 (and_60_out, not_396_out, not_397_out, not_398_out, not_399_out, OP1, not_400_out);
  and and_61 (and_61_out, not_401_out, not_402_out, not_403_out, not_404_out, OP1, OP0);
  and and_62 (JAL, not_405_out, not_406_out, not_407_out, not_408_out, OP1, OP0);
  or or_1 (MemToReg, and_1_out, and_2_out);
  or or_2 (ALU_SRC, and_4_out, and_5_out, and_6_out, and_7_out, and_8_out, and_9_out, and_10_out, and_11_out, and_12_out);
  or or_3 (SignedExt, and_35_out, and_36_out, and_37_out, and_38_out, and_39_out, and_40_out, and_41_out, and_42_out);
  or or_4 (JMP, and_59_out, and_60_out, and_61_out);
  or or_5 (RegWrite, and_13_out, and_14_out, and_15_out, and_16_out, and_17_out, and_18_out, and_19_out, and_20_out, and_21_out, and_22_out, and_23_out, and_24_out, and_25_out, and_26_out, and_27_out, and_28_out, and_29_out, and_30_out, and_31_out, and_32_out, and_33_out);
  or or_6 (RegDst, and_43_out, and_44_out, and_45_out, and_46_out, and_47_out, and_48_out, and_49_out, and_50_out, and_51_out, and_52_out, and_53_out, and_54_out, and_55_out);
endmodule

// ALU
module MIPS_ALU (
  input  [4:0] shamt,
  input  [31:0] X,
  input  [31:0] Y,
  input  [3:0] AluOP,
  output Equal,
  output [31:0] Result,
  output [31:0] Result_2
);

  wire [0:0] comparator_1_lt, comparator_2_lt;
  wire [31:0] adder_1_out, AND_out, divider_1_out, divider_1_rem, multiplier_1_cout, multiplier_1_out,
       NOR_out, OR_out, shifter_1_out, shifter_2_out, shifter_3_out, subtractor_1_out, XOR_out;

  assign AND_out = X & Y;  // AND_Gate AND, 32 bits wide
  assign OR_out = X | Y;  // OR_Gate OR, 32 bits wide
  Shifter #(.width(32), .shift("ll")) shifter_1 (.in(Y), .\dist (shamt), .out(shifter_1_out));
  Shifter #(.width(32), .shift("ar")) shifter_2 (.in(Y), .\dist (shamt), .out(shifter_2_out));
  Shifter #(.width(32), .shift("lr")) shifter_3 (.in(Y), .\dist (shamt), .out(shifter_3_out));
  Multiplier #(.width(32)) multiplier_1 (.a(X), .b(Y), .out(multiplier_1_out), .cout(multiplier_1_cout));  // open: cin
  Divider #(.width(32)) divider_1 (.a(X), .b(Y), .out(divider_1_out), .rem(divider_1_rem));  // open: upper
  Adder #(.width(32)) adder_1 (.a(X), .b(Y), .out(adder_1_out));  // open: cin, cout
  Subtractor #(.width(32)) subtractor_1 (.a(X), .b(Y), .out(subtractor_1_out));  // open: bin, bout
  assign XOR_out = X ^ Y;  // XOR_Gate XOR, 32 bits wide
  assign NOR_out = ~(X | Y);  // NOR_Gate NOR, 32 bits wide
  Comparator #(.width(32), .mode("twosComplement")) comparator_1 (
    .a(X), .b(Y), .eq(Equal), .lt(comparator_1_lt[0]));  // open: gt
  Comparator #(.width(32), .mode("unsigned")) comparator_2 (.a(X), .b(Y), .lt(comparator_2_lt[0]));  // open: gt, eq
  Multiplexer #(.select(4), .width(32), .disabled("Z"), .enable("false")) multiplexer_1 (
    .in0(shifter_1_out), .in1(shifter_2_out), .in2(shifter_3_out), .in3(multiplier_1_out),
    .in4(divider_1_out), .in5(adder_1_out), .in6(subtractor_1_out), .in7(AND_out), .in8(OR_out),
    .in9(XOR_out), .in10(NOR_out), .in11({{31{1'b0}}, comparator_1_lt[0]}),
    .in12({{31{1'b0}}, comparator_2_lt[0]}), .in13({32{1'b0}}), .in14({32{1'b0}}), .in15({32{1'b0}}),
    .out(Result), .sel(AluOP));
  Multiplexer #(.select(4), .width(32), .disabled("Z"), .enable("false")) multiplexer_2 (
    .in0({32{1'b0}}), .in1({32{1'b0}}), .in2({32{1'b0}}), .in3(multiplier_1_cout), .in4(divider_1_rem),
    .in5({32{1'b0}}), .in6({32{1'b0}}), .in7({32{1'b0}}), .in8({32{1'b0}}), .in9({32{1'b0}}),
    .in10({32{1'b0}}), .in11({32{1'b0}}), .in12({32{1'b0}}), .in13({32{1'b0}}), .in14({32{1'b0}}),
    .in15({32{1'b0}}), .out(Result_2), .sel(AluOP));

  // Other names for the same wires on the sheet: Result2[31:0] = Result_2; S[3:0] = AluOP

  // Notes on the sheet:
  //   不要改变此引脚区域内容，也不要改变ALU封装形式
  //   输入引脚
  //   输出引脚
endmodule

module MIPS_Regifile (
  input  [31:0] Din,
  input  Clk,
  input  WE,
  input  [4:0] R1_num,
  input  [4:0] W_num,
  input  [4:0] R2_num,
  output [31:0] R1,
  output [31:0] R2
);

  // RegisterFile registerfile_1: pin names not known; wires that end beside it: Din, Clk, WE, W_num, R1_num, R2_num, R1, R2
endmodule
module \理想流水线  (
  output RegWrite,
  output MemWrite,
  output [31:0] IF_PC,
  output [31:0] ID_PC,
  output [31:0] EX_PC,
  output [31:0] M_PC,
  output [31:0] WB_PC,
  output [31:0] RDin,
  output [31:0] MDin,
  output [31:0] LedData
);

  wire and_1_out, and_2_out, and_4_out, and_5_out, and_6_out, and_7_out, and_8_out, BGTZ, BGTZ_EX, CLK,
       comparator_1_gt, comparator_2_eq, comparator_3_eq, d_ff_1_q, ex_mem_1_lh_2, ex_mem_1_mentoreg_2,
       ex_mem_1_stall_2, ex_mem_1_system_2, EX_WriteReg, Go, id_ex_1_alusrcb_2, id_ex_1_beq_2, id_ex_1_bne_2,
       id_ex_1_lh_2, id_ex_1_mentoreg_2, id_ex_1_menwrite_2, id_ex_1_stall_2, id_ex_1_system_2, IR1, IR2,
       IR3, JAL, JAL_EX, JAL_MEM, JMP, JMP_EX, JR, JR_EX, JUMP, LH, LH_WB, mem_wb_1_mentoreg_2, MEM_WriteReg,
       not_1_out, not_2_out, not_3_out, or_2_out, or_3_out, or_5_out, RegDst, RegDst_EX, RegDst_MEM, RST,
       SignedExt, SLLV, STALL_1, Stop, Sync, Syscall, Syscall_WB, tunnel, W1, W2, W3, XORI, \中止 ,
       \单周期硬布线控制器_1_alu_src , \单周期硬布线控制器_1_beq , \单周期硬布线控制器_1_bne , \单周期硬布线控制器_1_jal ,
       \单周期硬布线控制器_1_memtoreg , \单周期硬布线控制器_1_memwrite , \单周期硬布线控制器_1_regdst , \单周期硬布线控制器_1_regwrite , \数据相关 ,
       \有条件分支 ;
  wire [3:0] id_ex_1_aluop_2, \单周期硬布线控制器_1_alu_op ;
  wire [4:0] EX_WriteReg_num, id_ex_1_shame_2, MEM_WriteReg_num, multiplexer_1_out, multiplexer_2_out,
       multiplexer_8_out, multiplexer_11_out, multiplexer_13_out, R1__ID, R2__ID, Rd_back, Rd_EX, Rd_MEM,
       Rt_back, Rt_EX, Rt_MEM;
  wire [5:0] Func;
  wire [15:0] \LoadUse次数 , multiplexer_19_out, \总周期数 , \插入气泡数 , \无条件分支数 , \条件分支成功数 ;
  wire [31:0] a0, bit_extender_1_out, bit_extender_2_out, bit_extender_3_out, EX_IR, ex_mem_1_ir_2,
       ex_mem_1_result_2, EX_PC_4, id_ex_1_r2_2, IMM_EX, IR, J, JR_address, JR_address_EX, LED,
       mips_alu_1_result, multiplexer_5_out, multiplexer_6_out, multiplexer_7_out, multiplexer_12_out,
       multiplexer_14_out, multiplexer_15_out, multiplexer_16_out, multiplexer_17_out, multiplexer_18_out,
       PC_4, ram_1_data, shifter_1_out, v0, WB_IR, WB_PC_4;
  wire [31:6] IF_IR;

  Button \u_总复位  (.out(RST));
  Button _1 (.out(IR1));
  Button _2 (.out(IR2));
  Button _3 (.out(IR3));
  Button \u_继续运行  (.out(Go));
  LED #(.active("true")) led_1 (.in(W1));
  LED #(.active("true")) led_2 (.in(W2));
  LED #(.active("true")) led_3 (.in(W3));
  Multiplexer #(.select(1), .width(5), .disabled("Z"), .enable("false")) multiplexer_1 (
    .in0(Rt_EX), .in1(Rd_EX), .out(multiplexer_1_out), .sel(RegDst_EX));
  Multiplexer #(.select(1), .width(5), .disabled("Z"), .enable("false")) multiplexer_2 (
    .in0(Rt_MEM), .in1(Rd_MEM), .out(multiplexer_2_out), .sel(RegDst_MEM));
  Hex_Digit_Display hex_digit_display_1 (.value(LedData[31:28]));  // open: dp
  Multiplexer #(.select(1), .width(5), .disabled("Z"), .enable("false")) multiplexer_3 (
    .in0(multiplexer_1_out), .in1({5{1'b1}}), .out(EX_WriteReg_num), .sel(JAL_EX));
  Multiplexer #(.select(1), .width(5), .disabled("Z"), .enable("false")) multiplexer_4 (
    .in0(multiplexer_2_out), .in1({5{1'b1}}), .out(MEM_WriteReg_num), .sel(JAL_MEM));
  Multiplexer #(.select(1), .width(32), .disabled("Z"), .enable("false")) multiplexer_5 (
    .in0(PC_4), .in1(J), .out(multiplexer_5_out), .sel(\有条件分支 ));
  Multiplexer #(.select(1), .width(32), .disabled("Z"), .enable("false")) multiplexer_6 (
    .in0({EX_PC_4[31:28], EX_IR[25:0], 2'b00}), .in1(JR_address_EX), .out(multiplexer_6_out), .sel(JR_EX));
  Hex_Digit_Display hex_digit_display_2 (.value(LedData[23:20]));  // open: dp
  Hex_Digit_Display hex_digit_display_3 (.value(LedData[27:24]));  // open: dp
  Multiplexer #(.select(1), .width(32), .disabled("Z"), .enable("false")) multiplexer_7 (
    .in0(multiplexer_5_out), .in1(multiplexer_6_out), .out(multiplexer_7_out), .sel(JMP_EX));
  and and_1 (and_1_out, ~\数据相关 , \中止 );  // AND_Gate
  Hex_Digit_Display hex_digit_display_4 (.value(LedData[19:16]));  // open: dp
  Hex_Digit_Display hex_digit_display_5 (.value(LedData[15:12]));  // open: dp
  Register #(.width(32), .trigger("rising"), .Select("low")) PC (
    .D(multiplexer_7_out), .en(and_1_out), .Q(IF_PC), .clk(CLK));  // open: clr
  Hex_Digit_Display hex_digit_display_6 (.value(LedData[7:4]));  // open: dp
  Hex_Digit_Display hex_digit_display_7 (.value(LedData[11:8]));  // open: dp
  Clock #(.highDuration(1), .lowDuration(1)) clock_1 (.out(CLK));
  // Probe on IF_PC
  Adder #(.width(32)) adder_1 (.a(IF_PC), .b(32'h4), .out(PC_4));  // open: cin, cout
  Hex_Digit_Display hex_digit_display_8 (.value(LedData[3:0]));  // open: dp
  IF_ID if_id_1 (
    .IRin(IR), .IRout({IF_IR, Func}), .PCin(IF_PC), .PCout(ID_PC), .Sync(Sync), .STALL(and_2_out), .CLK(CLK),
    .STALL_2(STALL_1), .RST(RST));  // open: in_1, out_9, in_2, out_10
  ROM #(.addrWidth(10), .dataWidth(32), .Select("high")) rom_1 (.addr(IF_PC[11:2]), .data(IR));
  and and_2 (and_2_out, ~\数据相关 , \中止 );  // AND_Gate
  // Probe on \总周期数 
  // Probe on \无条件分支数 
  // Probe on \条件分支成功数 
  // Probe on \插入气泡数 
  // Probe on \LoadUse次数 
  \数据相关检测  \u_数据相关检测_1  (
    .OP(IF_IR[31:26]), .EX_WriteReg_num(EX_WriteReg_num), .MEM_WriteReg_num(MEM_WriteReg_num),
    .MEM_RegWrite(MEM_WriteReg), .Func(Func), .ID_R1_num(R1__ID), .ID_R2_num(R2__ID), .\数据相关 (\数据相关 ),
    .EX_RegWrite(EX_WriteReg));
  // Probe on IF_PC[11:0]
  // Probe on {IF_IR, Func}
  // Probe on ID_PC[11:0]
  // Probe on EX_PC[11:0]
  // Probe on M_PC[11:0]
  // Probe on IF_IR[25:21]
  Multiplexer #(.select(1), .width(5), .disabled("Z"), .enable("false")) multiplexer_8 (
    .in0(Rt_back), .in1(Rd_back), .out(multiplexer_8_out), .sel(RegDst));
  assign bit_extender_1_out = {{16{1'b0}}, {IF_IR[15:6], Func}};  // Bit_Extender bit_extender_1
  assign bit_extender_2_out = {{16{IF_IR[15]}}, {IF_IR[15:6], Func}};  // Bit_Extender bit_extender_2
  // Probe on WB_PC[11:0]
  or or_1 (Sync, \有条件分支 , JMP_EX);
  Shifter #(.width(32), .shift("ll")) shifter_1 (.in(IMM_EX), .\dist (5'b00010), .out(shifter_1_out));
  Adder #(.width(32)) adder_2 (.a(EX_PC), .b(32'h4), .out(EX_PC_4));  // open: cin, cout
  Adder #(.width(32)) adder_3 (.a(WB_PC), .b(32'h4), .out(WB_PC_4));  // open: cin, cout
  Multiplexer #(.select(1), .width(5), .disabled("Z"), .enable("false")) multiplexer_9 (
    .in0(IF_IR[25:21]), .in1(5'b00010), .out(R1__ID), .sel(Syscall));
  Multiplexer #(.select(1), .width(5), .disabled("Z"), .enable("false")) multiplexer_10 (
    .in0(IF_IR[20:16]), .in1(5'b00100), .out(R2__ID), .sel(Syscall));
  Multiplexer #(.select(1), .width(5), .disabled("Z"), .enable("false")) multiplexer_11 (
    .in0(multiplexer_8_out), .in1({5{1'b1}}), .out(multiplexer_11_out), .sel(JAL));
  Multiplexer #(.select(1), .width(32), .disabled("Z"), .enable("false")) multiplexer_12 (
    .in0(bit_extender_1_out), .in1(bit_extender_2_out), .out(multiplexer_12_out), .sel(SignedExt));
  Adder #(.width(32)) adder_4 (.a(shifter_1_out), .b(EX_PC_4), .out(J));  // open: cin, cout
  \单周期硬布线控制器  \u_单周期硬布线控制器_1  (
    .Func(Func), .OP(IF_IR[31:26]), .ALU_OP(\单周期硬布线控制器_1_alu_op ), .MemToReg(\单周期硬布线控制器_1_memtoreg ),
    .MemWrite(\单周期硬布线控制器_1_memwrite ), .ALU_SRC(\单周期硬布线控制器_1_alu_src ), .RegWrite(\单周期硬布线控制器_1_regwrite ),
    .SysCALL(Syscall), .SignedExt(SignedExt), .RegDst(\单周期硬布线控制器_1_regdst ), .JR(JR), .JMP(JMP),
    .Beq(\单周期硬布线控制器_1_beq ), .JAL(\单周期硬布线控制器_1_jal ), .Bne(\单周期硬布线控制器_1_bne ), .SLLV(SLLV), .LH(LH),
    .XORI(XORI), .BGTZ(BGTZ));  // open: M, MFC0, MTC0, ERET
  // Probe on R1__ID
  MIPS_Regifile mips_regifile_1 (
    .Din(RDin), .Clk(CLK), .R1(JR_address), .R2(LED), .WE(RegWrite), .W_num(multiplexer_11_out),
    .R1_num(R1__ID), .R2_num(R2__ID));
  or or_2 (or_2_out, \中止 , not_1_out);
  not not_1 (not_1_out, Syscall_WB);
  // Probe on JR_address
  Counter #(.width(16), .max('hffff), .ongoal("wrap"), .trigger("rising"), .behavior("old")) counter_1 (
    .count(or_2_out), .Q(\总周期数 ), .clk(CLK));  // open: load, D, carry, clr, preset
  Multiplexer #(.select(1), .width(5), .disabled("Z"), .enable("false")) multiplexer_13 (
    .in0(IF_IR[10:6]), .in1(JR_address[4:0]), .out(multiplexer_13_out), .sel(SLLV));
  ID_EX id_ex_1 (
    .in_10(IF_IR[20:16]), .in_11(IF_IR[15:11]), .Beq(\单周期硬布线控制器_1_beq ), .Bne(\单周期硬布线控制器_1_bne ),
    .MenToReg(\单周期硬布线控制器_1_memtoreg ), .MenWrite(\单周期硬布线控制器_1_memwrite ), .AluOP(\单周期硬布线控制器_1_alu_op ),
    .AluSrcB(\单周期硬布线控制器_1_alu_src ), .RegWrite(\单周期硬布线控制器_1_regwrite ), .JAL(\单周期硬布线控制器_1_jal ),
    .RegDst(\单周期硬布线控制器_1_regdst ), .IR({IF_IR, Func}), .PC(ID_PC), .R1(JR_address), .R2(LED),
    .IMM(multiplexer_12_out), .SHAME(multiplexer_13_out), .Rt(Rt_EX), .Rd(Rd_EX), .Beq_2(id_ex_1_beq_2),
    .Bne_2(id_ex_1_bne_2), .MenToReg_2(id_ex_1_mentoreg_2), .MenWrite_2(id_ex_1_menwrite_2),
    .AluOP_2(id_ex_1_aluop_2), .AluSrcB_2(id_ex_1_alusrcb_2), .RegWrite_2(EX_WriteReg), .JAL_2(JAL_EX),
    .RegDst_2(RegDst_EX), .IR_2(EX_IR), .PC_2(EX_PC), .R1_2(JR_address_EX), .R2_2(id_ex_1_r2_2),
    .IMM_2(IMM_EX), .SHAME_2(id_ex_1_shame_2), .Sync(or_3_out), .STALL(\中止 ), .CLK(CLK),
    .STALL_2(id_ex_1_stall_2), .RST(RST), .JR(JR), .JR_2(JR_EX), .JMP(JMP), .JMP_2(JMP_EX), .System(Syscall),
    .System_2(id_ex_1_system_2), .LH(LH), .LH_2(id_ex_1_lh_2), .BGTZ(BGTZ), .BGTZ_2(BGTZ_EX));  // open: A, A_2, B, B_2, in_1, out_31, in_2, out_32
  or or_3 (or_3_out, Sync, \数据相关 );
  Counter #(.width(16), .max('hffff), .ongoal("wrap"), .trigger("rising"), .behavior("old")) counter_2 (
    .count(JMP_EX), .Q(\无条件分支数 ), .clk(CLK), .clr(RST));  // open: load, D, carry, preset
  Multiplexer #(.select(1), .width(32), .disabled("Z"), .enable("false")) multiplexer_14 (
    .in0(id_ex_1_r2_2), .in1(IMM_EX), .out(multiplexer_14_out), .sel(id_ex_1_alusrcb_2));
  and and_3 (JUMP, BGTZ_EX, comparator_1_gt);
  Comparator #(.width(32), .mode("twosComplement")) comparator_1 (
    .a(JR_address_EX), .b({32{1'b0}}), .gt(comparator_1_gt));  // open: eq, lt
  and and_4 (and_4_out, tunnel, id_ex_1_beq_2);
  not not_2 (not_2_out, tunnel);
  and and_5 (and_5_out, not_2_out, id_ex_1_bne_2);
  MIPS_ALU mips_alu_1 (
    .X(JR_address_EX), .Y(multiplexer_14_out), .AluOP(id_ex_1_aluop_2), .Equal(tunnel),
    .Result(mips_alu_1_result), .shamt(id_ex_1_shame_2));  // open: Result_2
  or or_4 (\有条件分支 , and_4_out, JUMP, and_5_out);
  Counter #(.width(16), .max('hffff), .ongoal("wrap"), .trigger("rising"), .behavior("old")) counter_3 (
    .count(\有条件分支 ), .Q(\条件分支成功数 ), .clk(CLK), .clr(RST));  // open: load, D, carry, preset
  Multiplexer #(.select(1), .width(32), .disabled("Z"), .enable("false")) multiplexer_15 (
    .in0(mips_alu_1_result), .in1(JR_address_EX), .out(multiplexer_15_out), .sel(id_ex_1_system_2));
  EX_MEM ex_mem_1 (
    .in_3(Rt_EX), .in_4(Rd_EX), .MenToReg(id_ex_1_mentoreg_2), .MenWrite(id_ex_1_menwrite_2),
    .RegWrite(EX_WriteReg), .JAL(JAL_EX), .RegDst(RegDst_EX), .IR(EX_IR), .PC(EX_PC),
    .Result(multiplexer_15_out), .R2(id_ex_1_r2_2), .Rt(Rt_MEM), .Rd(Rd_MEM),
    .MenToReg_2(ex_mem_1_mentoreg_2), .MenWrite_2(MemWrite), .RegWrite_2(MEM_WriteReg), .JAL_2(JAL_MEM),
    .RegDst_2(RegDst_MEM), .IR_2(ex_mem_1_ir_2), .PC_2(M_PC), .Result_2(ex_mem_1_result_2), .R2_2(MDin),
    .RST(RST), .STALL(id_ex_1_stall_2), .CLK(CLK), .STALL_2(ex_mem_1_stall_2), .System(id_ex_1_system_2),
    .System_2(ex_mem_1_system_2), .LH(id_ex_1_lh_2), .LH_2(ex_mem_1_lh_2), .Sync(1'b0));
  and and_6 (and_6_out, \数据相关 , \中止 );
  Counter #(.width(16), .max('hffff), .ongoal("wrap"), .trigger("rising"), .behavior("old")) counter_4 (
    .count(and_6_out), .Q(\插入气泡数 ), .clk(CLK), .clr(RST));  // open: load, D, carry, preset
  RAM #(.addrWidth(10), .dataWidth(32), .bus("separate"), .Select("high")) ram_1 (
    .addr(ex_mem_1_result_2[11:2]), .din(MDin), .data(ram_1_data), .str(MemWrite), .clk(CLK));  // open: sel, ld, clr
  Comparator #(.width(32), .mode("twosComplement")) comparator_2 (
    .a(JR_address), .b(32'h22), .eq(comparator_2_eq));  // open: gt, lt
  Comparator #(.width(32), .mode("twosComplement")) comparator_3 (
    .a(v0), .b(32'h22), .eq(comparator_3_eq));  // open: gt, lt
  Multiplexer #(.select(1), .width(32), .disabled("Z"), .enable("false")) multiplexer_16 (
    .in0(ram_1_data), .in1(MDin), .out(multiplexer_16_out), .sel(ex_mem_1_system_2));
  not not_3 (not_3_out, comparator_3_eq);
  MEM_WB mem_wb_1 (
    .in_3(Rt_MEM), .in_4(Rd_MEM), .MenToReg(ex_mem_1_mentoreg_2), .RegWrite(MEM_WriteReg), .JAL(JAL_MEM),
    .RegDst(RegDst_MEM), .IR(ex_mem_1_ir_2), .PC(M_PC), .Result(ex_mem_1_result_2),
    .Mem_Res(multiplexer_16_out), .Rt(Rt_back), .Rd(Rd_back), .MenToReg_2(mem_wb_1_mentoreg_2),
    .RegWrite_2(RegWrite), .JAL_2(JAL), .RegDst_2(RegDst), .IR_2(WB_IR), .PC_2(WB_PC), .Result_2(v0),
    .Mem_Res_2(a0), .RST(RST), .STALL(ex_mem_1_stall_2), .CLK(CLK), .STALL_2(Stop),
    .System(ex_mem_1_system_2), .System_2(Syscall_WB), .LH(ex_mem_1_lh_2), .LH_2(LH_WB), .Sync(1'b0));
  and and_7 (and_7_out, comparator_2_eq, Syscall);
  and and_8 (and_8_out, Syscall_WB, not_3_out);
  Register #(.width(32), .trigger("rising"), .Select("low")) register_1 (
    .D(LED), .en(and_7_out), .Q(LedData), .clk(CLK));  // open: clr
  D_Flip_Flop #(.trigger("falling"), .Pre_Clr_Positions("LEGACY"), .NegatePresetClear("false"), .enable("true"), .NewFFLayout("false")) d_ff_1 (
    .clk(CLK), .D(and_8_out), .Q(d_ff_1_q), .reset(or_5_out));  // open: Qn, preset, en
  or or_5 (or_5_out, RST, Go);
  Multiplexer #(.select(1), .width(32), .disabled("Z"), .enable("false")) multiplexer_17 (
    .in0(v0), .in1(a0), .out(multiplexer_17_out), .sel(mem_wb_1_mentoreg_2));
  not not_4 (\中止 , d_ff_1_q);
  Multiplexer #(.select(1), .width(32), .disabled("Z"), .enable("false")) multiplexer_18 (
    .in0(multiplexer_17_out), .in1(WB_PC_4), .out(multiplexer_18_out), .sel(JAL));
  assign bit_extender_3_out = {{16{multiplexer_19_out[15]}}, multiplexer_19_out};  // Bit_Extender bit_extender_3
  Multiplexer #(.select(1), .width(16), .disabled("Z"), .enable("false")) multiplexer_19 (
    .in0(multiplexer_17_out[15:0]), .in1(multiplexer_17_out[31:16]), .out(multiplexer_19_out), .sel(v0[1]));
  Multiplexer #(.select(1), .width(32), .disabled("Z"), .enable("false")) multiplexer_20 (
    .in0(multiplexer_18_out), .in1(bit_extender_3_out), .out(RDin), .sel(LH_WB));

  // Other names for the same wires on the sheet: J_JAL[31:2] = {EX_PC_4[31:28], EX_IR[25:0]}; IF_IR[5:0] = Func;
  //   shamt[4:0] = IF_IR[10:6]; Rd[4:0] = IF_IR[15:11]; Rt[4:0] = IF_IR[20:16]; OP[5:0] = IF_IR[31:26];
  //   L[31:0] = JR_address; SLLV_1[4:0] = JR_address[4:0]; MEM_PC[31:0] = M_PC; PC[31:0] = IF_PC

  // Notes on the sheet:
  //   中断源
  //   中断等待指示
  //   总复位信号应将除ROM以外所有存储组件全部清零
  //   数码管输出
  //   数码管输出应该用寄存器锁存，否则显示数据只能一闪而过
  //   指令存储器
  //   指令字
  //   contents of rom_1 (hex, n*v repeats v):
  //   20100000 20110000 20120000 20130000 36100000 36310001 36520002 36730003 ae100000 ae110004 ae120008
  //   ae13000c 2002000a 20110000 20120000 20130000 c
  //   OP
  //   Func
  //   rs
  //   rt
  //   rd
  //   流水调试日志用
  //   JMP
  //   JR
  //   OP
  //   Func
  //   Beq
  //   Bne
  //   MemToReg
  //   MemWrite
  //   AluOP
  //   AluSrcB
  //   RegWrite
  //   JAL
  //   RegDst
  //   Syscall
  //   为方便自动评测，需要输出流水线各段保存的PC值，注意是PC不是PC+4，另外ID段寄存器写入信息，Mem段内存写入信息也要输出
endmodule

module \气泡流水线  (
  output RegWrite,
  output MemWrite,
  output [31:0] IF_PC,
  output [31:0] ID_PC,
  output [31:0] EX_PC,
  output [31:0] M_PC,
  output [31:0] WB_PC,
  output [31:0] RDin,
  output [31:0] MDin,
  output [31:0] LedData
);

  wire and_1_out, and_2_out, and_4_out, and_5_out, and_6_out, and_7_out, and_8_out, BGTZ, BGTZ_EX, CLK,
       comparator_1_gt, comparator_2_eq, comparator_3_eq, d_ff_1_q, ex_mem_1_lh_2, ex_mem_1_mentoreg_2,
       ex_mem_1_stall_2, ex_mem_1_system_2, EX_WriteReg, Go, id_ex_1_alusrcb_2, id_ex_1_beq_2, id_ex_1_bne_2,
       id_ex_1_lh_2, id_ex_1_mentoreg_2, id_ex_1_menwrite_2, id_ex_1_stall_2, id_ex_1_system_2, IR1, IR2,
       IR3, JAL, JAL_EX, JAL_MEM, JMP, JMP_EX, JR, JR_EX, JUMP, LH, LH_WB, mem_wb_1_mentoreg_2, MEM_WriteReg,
       not_1_out, not_2_out, not_3_out, or_2_out, or_3_out, or_5_out, RegDst, RegDst_EX, RegDst_MEM, RST,
       SignedExt, SLLV, STALL_1, Stop, Sync, Syscall, Syscall_WB, tunnel, W1, W2, W3, XORI, \中止 ,
       \单周期硬布线控制器_1_alu_src , \单周期硬布线控制器_1_beq , \单周期硬布线控制器_1_bne , \单周期硬布线控制器_1_jal ,
       \单周期硬布线控制器_1_memtoreg , \单周期硬布线控制器_1_memwrite , \单周期硬布线控制器_1_regdst , \单周期硬布线控制器_1_regwrite , \数据相关 ,
       \有条件分支 ;
  wire [3:0] id_ex_1_aluop_2, \单周期硬布线控制器_1_alu_op ;
  wire [4:0] EX_WriteReg_num, id_ex_1_shame_2, MEM_WriteReg_num, multiplexer_1_out, multiplexer_2_out,
       multiplexer_8_out, multiplexer_11_out, multiplexer_13_out, R1__ID, R2__ID, Rd_back, Rd_EX, Rd_MEM,
       Rt_back, Rt_EX, Rt_MEM;
  wire [5:0] Func;
  wire [15:0] \LoadUse次数 , multiplexer_19_out, \总周期数 , \插入气泡数 , \无条件分支数 , \条件分支成功数 ;
  wire [31:0] a0, bit_extender_1_out, bit_extender_2_out, bit_extender_3_out, EX_IR, ex_mem_1_ir_2,
       ex_mem_1_result_2, EX_PC_4, id_ex_1_r2_2, IMM_EX, IR, J, JR_address, JR_address_EX, LED,
       mips_alu_1_result, multiplexer_5_out, multiplexer_6_out, multiplexer_7_out, multiplexer_12_out,
       multiplexer_14_out, multiplexer_15_out, multiplexer_16_out, multiplexer_17_out, multiplexer_18_out,
       PC_4, ram_1_data, shifter_1_out, v0, WB_IR, WB_PC_4;
  wire [31:6] IF_IR;

  Button \u_总复位  (.out(RST));
  Button _1 (.out(IR1));
  Button _2 (.out(IR2));
  Button _3 (.out(IR3));
  Button \u_继续运行  (.out(Go));
  LED #(.active("true")) led_1 (.in(W1));
  LED #(.active("true")) led_2 (.in(W2));
  LED #(.active("true")) led_3 (.in(W3));
  Multiplexer #(.select(1), .width(5), .disabled("Z"), .enable("false")) multiplexer_1 (
    .in0(Rt_EX), .in1(Rd_EX), .out(multiplexer_1_out), .sel(RegDst_EX));
  Multiplexer #(.select(1), .width(5), .disabled("Z"), .enable("false")) multiplexer_2 (
    .in0(Rt_MEM), .in1(Rd_MEM), .out(multiplexer_2_out), .sel(RegDst_MEM));
  Hex_Digit_Display hex_digit_display_1 (.value(LedData[31:28]));  // open: dp
  Multiplexer #(.select(1), .width(5), .disabled("Z"), .enable("false")) multiplexer_3 (
    .in0(multiplexer_1_out), .in1({5{1'b1}}), .out(EX_WriteReg_num), .sel(JAL_EX));
  Multiplexer #(.select(1), .width(5), .disabled("Z"), .enable("false")) multiplexer_4 (
    .in0(multiplexer_2_out), .in1({5{1'b1}}), .out(MEM_WriteReg_num), .sel(JAL_MEM));
  Multiplexer #(.select(1), .width(32), .disabled("Z"), .enable("false")) multiplexer_5 (
    .in0(PC_4), .in1(J), .out(multiplexer_5_out), .sel(\有条件分支 ));
  Multiplexer #(.select(1), .width(32), .disabled("Z"), .enable("false")) multiplexer_6 (
    .in0({EX_PC_4[31:28], EX_IR[25:0], 2'b00}), .in1(JR_address_EX), .out(multiplexer_6_out), .sel(JR_EX));
  Hex_Digit_Display hex_digit_display_2 (.value(LedData[27:24]));  // open: dp
  Hex_Digit_Display hex_digit_display_3 (.value(LedData[23:20]));  // open: dp
  Multiplexer #(.select(1), .width(32), .disabled("Z"), .enable("false")) multiplexer_7 (
    .in0(multiplexer_5_out), .in1(multiplexer_6_out), .out(multiplexer_7_out), .sel(JMP_EX));
  and and_1 (and_1_out, ~\数据相关 , \中止 );  // AND_Gate
  Hex_Digit_Display hex_digit_display_4 (.value(LedData[19:16]));  // open: dp
  Hex_Digit_Display hex_digit_display_5 (.value(LedData[15:12]));  // open: dp
  Register #(.width(32), .trigger("rising"), .Select("low")) PC (
    .D(multiplexer_7_out), .en(and_1_out), .Q(IF_PC), .clk(CLK));  // open: clr
  Hex_Digit_Display hex_digit_display_6 (.value(LedData[11:8]));  // open: dp
  Hex_Digit_Display hex_digit_display_7 (.value(LedData[7:4]));  // open: dp
  Clock #(.highDuration(1), .lowDuration(1)) clock_1 (.out(CLK));
  // Probe on IF_PC
  Adder #(.width(32)) adder_1 (.a(IF_PC), .b(32'h4), .out(PC_4));  // open: cin, cout
  Hex_Digit_Display hex_digit_display_8 (.value(LedData[3:0]));  // open: dp
  IF_ID if_id_1 (
    .IRin(IR), .IRout({IF_IR, Func}), .PCin(IF_PC), .PCout(ID_PC), .Sync(Sync), .STALL(and_2_out), .CLK(CLK),
    .STALL_2(STALL_1), .RST(RST));  // open: in_1, out_9, in_2, out_10
  ROM #(.addrWidth(10), .dataWidth(32), .Select("high")) rom_1 (.addr(IF_PC[11:2]), .data(IR));
  and and_2 (and_2_out, ~\数据相关 , \中止 );  // AND_Gate
  // Probe on \总周期数 
  // Probe on \无条件分支数 
  // Probe on \条件分支成功数 
  // Probe on \插入气泡数 
  // Probe on \LoadUse次数 
  \数据相关检测  \u_数据相关检测_1  (
    .OP(IF_IR[31:26]), .EX_WriteReg_num(EX_WriteReg_num), .MEM_WriteReg_num(MEM_WriteReg_num),
    .MEM_RegWrite(MEM_WriteReg), .Func(Func), .ID_R1_num(R1__ID), .ID_R2_num(R2__ID), .\数据相关 (\数据相关 ),
    .EX_RegWrite(EX_WriteReg));
  // Probe on IF_PC[11:0]
  // Probe on {IF_IR, Func}
  // Probe on EX_PC[11:0]
  // Probe on ID_PC[11:0]
  // Probe on M_PC[11:0]
  // Probe on IF_IR[25:21]
  Multiplexer #(.select(1), .width(5), .disabled("Z"), .enable("false")) multiplexer_8 (
    .in0(Rt_back), .in1(Rd_back), .out(multiplexer_8_out), .sel(RegDst));
  assign bit_extender_1_out = {{16{1'b0}}, {IF_IR[15:6], Func}};  // Bit_Extender bit_extender_1
  assign bit_extender_2_out = {{16{IF_IR[15]}}, {IF_IR[15:6], Func}};  // Bit_Extender bit_extender_2
  // Probe on WB_PC[11:0]
  or or_1 (Sync, \有条件分支 , JMP_EX);
  Shifter #(.width(32), .shift("ll")) shifter_1 (.in(IMM_EX), .\dist (5'b00010), .out(shifter_1_out));
  Adder #(.width(32)) adder_2 (.a(EX_PC), .b(32'h4), .out(EX_PC_4));  // open: cin, cout
  Adder #(.width(32)) adder_3 (.a(WB_PC), .b(32'h4), .out(WB_PC_4));  // open: cin, cout
  Multiplexer #(.select(1), .width(5), .disabled("Z"), .enable("false")) multiplexer_9 (
    .in0(IF_IR[25:21]), .in1(5'b00010), .out(R1__ID), .sel(Syscall));
  Multiplexer #(.select(1), .width(5), .disabled("Z"), .enable("false")) multiplexer_10 (
    .in0(IF_IR[20:16]), .in1(5'b00100), .out(R2__ID), .sel(Syscall));
  Multiplexer #(.select(1), .width(5), .disabled("Z"), .enable("false")) multiplexer_11 (
    .in0(multiplexer_8_out), .in1({5{1'b1}}), .out(multiplexer_11_out), .sel(JAL));
  Multiplexer #(.select(1), .width(32), .disabled("Z"), .enable("false")) multiplexer_12 (
    .in0(bit_extender_1_out), .in1(bit_extender_2_out), .out(multiplexer_12_out), .sel(SignedExt));
  Adder #(.width(32)) adder_4 (.a(shifter_1_out), .b(EX_PC_4), .out(J));  // open: cin, cout
  \单周期硬布线控制器  \u_单周期硬布线控制器_1  (
    .Func(Func), .OP(IF_IR[31:26]), .ALU_OP(\单周期硬布线控制器_1_alu_op ), .MemToReg(\单周期硬布线控制器_1_memtoreg ),
    .MemWrite(\单周期硬布线控制器_1_memwrite ), .ALU_SRC(\单周期硬布线控制器_1_alu_src ), .RegWrite(\单周期硬布线控制器_1_regwrite ),
    .SysCALL(Syscall), .SignedExt(SignedExt), .RegDst(\单周期硬布线控制器_1_regdst ), .JR(JR), .JMP(JMP),
    .Beq(\单周期硬布线控制器_1_beq ), .JAL(\单周期硬布线控制器_1_jal ), .Bne(\单周期硬布线控制器_1_bne ), .SLLV(SLLV), .LH(LH),
    .XORI(XORI), .BGTZ(BGTZ));  // open: M, MFC0, MTC0, ERET
  // Probe on R1__ID
  MIPS_Regifile mips_regifile_1 (
    .Din(RDin), .Clk(CLK), .R1(JR_address), .R2(LED), .WE(RegWrite), .W_num(multiplexer_11_out),
    .R1_num(R1__ID), .R2_num(R2__ID));
  or or_2 (or_2_out, \中止 , not_1_out);
  not not_1 (not_1_out, Syscall_WB);
  // Probe on JR_address
  Counter #(.width(16), .max('hffff), .ongoal("wrap"), .trigger("rising"), .behavior("old")) counter_1 (
    .count(or_2_out), .Q(\总周期数 ), .clk(CLK));  // open: load, D, carry, clr, preset
  Multiplexer #(.select(1), .width(5), .disabled("Z"), .enable("false")) multiplexer_13 (
    .in0(IF_IR[10:6]), .in1(JR_address[4:0]), .out(multiplexer_13_out), .sel(SLLV));
  ID_EX id_ex_1 (
    .in_10(IF_IR[20:16]), .in_11(IF_IR[15:11]), .Beq(\单周期硬布线控制器_1_beq ), .Bne(\单周期硬布线控制器_1_bne ),
    .MenToReg(\单周期硬布线控制器_1_memtoreg ), .MenWrite(\单周期硬布线控制器_1_memwrite ), .AluOP(\单周期硬布线控制器_1_alu_op ),
    .AluSrcB(\单周期硬布线控制器_1_alu_src ), .RegWrite(\单周期硬布线控制器_1_regwrite ), .JAL(\单周期硬布线控制器_1_jal ),
    .RegDst(\单周期硬布线控制器_1_regdst ), .IR({IF_IR, Func}), .PC(ID_PC), .R1(JR_address), .R2(LED),
    .IMM(multiplexer_12_out), .SHAME(multiplexer_13_out), .Rt(Rt_EX), .Rd(Rd_EX), .Beq_2(id_ex_1_beq_2),
    .Bne_2(id_ex_1_bne_2), .MenToReg_2(id_ex_1_mentoreg_2), .MenWrite_2(id_ex_1_menwrite_2),
    .AluOP_2(id_ex_1_aluop_2), .AluSrcB_2(id_ex_1_alusrcb_2), .RegWrite_2(EX_WriteReg), .JAL_2(JAL_EX),
    .RegDst_2(RegDst_EX), .IR_2(EX_IR), .PC_2(EX_PC), .R1_2(JR_address_EX), .R2_2(id_ex_1_r2_2),
    .IMM_2(IMM_EX), .SHAME_2(id_ex_1_shame_2), .Sync(or_3_out), .STALL(\中止 ), .CLK(CLK),
    .STALL_2(id_ex_1_stall_2), .RST(RST), .JR(JR), .JR_2(JR_EX), .JMP(JMP), .JMP_2(JMP_EX), .System(Syscall),
    .System_2(id_ex_1_system_2), .LH(LH), .LH_2(id_ex_1_lh_2), .BGTZ(BGTZ), .BGTZ_2(BGTZ_EX));  // open: A, A_2, B, B_2, in_1, out_31, in_2, out_32
  or or_3 (or_3_out, Sync, \数据相关 );
  Counter #(.width(16), .max('hffff), .ongoal("wrap"), .trigger("rising"), .behavior("old")) counter_2 (
    .count(JMP_EX), .Q(\无条件分支数 ), .clk(CLK), .clr(RST));  // open: load, D, carry, preset
  Multiplexer #(.select(1), .width(32), .disabled("Z"), .enable("false")) multiplexer_14 (
    .in0(id_ex_1_r2_2), .in1(IMM_EX), .out(multiplexer_14_out), .sel(id_ex_1_alusrcb_2));
  and and_3 (JUMP, BGTZ_EX, comparator_1_gt);
  Comparator #(.width(32), .mode("twosComplement")) comparator_1 (
    .a(JR_address_EX), .b({32{1'b0}}), .gt(comparator_1_gt));  // open: eq, lt
  and and_4 (and_4_out, tunnel, id_ex_1_beq_2);
  not not_2 (not_2_out, tunnel);
  and and_5 (and_5_out, not_2_out, id_ex_1_bne_2);
  MIPS_ALU mips_alu_1 (
    .X(JR_address_EX), .Y(multiplexer_14_out), .AluOP(id_ex_1_aluop_2), .Equal(tunnel),
    .Result(mips_alu_1_result), .shamt(id_ex_1_shame_2));  // open: Result_2
  or or_4 (\有条件分支 , and_4_out, JUMP, and_5_out);
  Counter #(.width(16), .max('hffff), .ongoal("wrap"), .trigger("rising"), .behavior("old")) counter_3 (
    .count(\有条件分支 ), .Q(\条件分支成功数 ), .clk(CLK), .clr(RST));  // open: load, D, carry, preset
  Multiplexer #(.select(1), .width(32), .disabled("Z"), .enable("false")) multiplexer_15 (
    .in0(mips_alu_1_result), .in1(JR_address_EX), .out(multiplexer_15_out), .sel(id_ex_1_system_2));
  EX_MEM ex_mem_1 (
    .in_3(Rt_EX), .in_4(Rd_EX), .MenToReg(id_ex_1_mentoreg_2), .MenWrite(id_ex_1_menwrite_2),
    .RegWrite(EX_WriteReg), .JAL(JAL_EX), .RegDst(RegDst_EX), .IR(EX_IR), .PC(EX_PC),
    .Result(multiplexer_15_out), .R2(id_ex_1_r2_2), .Rt(Rt_MEM), .Rd(Rd_MEM),
    .MenToReg_2(ex_mem_1_mentoreg_2), .MenWrite_2(MemWrite), .RegWrite_2(MEM_WriteReg), .JAL_2(JAL_MEM),
    .RegDst_2(RegDst_MEM), .IR_2(ex_mem_1_ir_2), .PC_2(M_PC), .Result_2(ex_mem_1_result_2), .R2_2(MDin),
    .RST(RST), .STALL(id_ex_1_stall_2), .CLK(CLK), .STALL_2(ex_mem_1_stall_2), .System(id_ex_1_system_2),
    .System_2(ex_mem_1_system_2), .LH(id_ex_1_lh_2), .LH_2(ex_mem_1_lh_2), .Sync(1'b0));
  and and_6 (and_6_out, \数据相关 , \中止 );
  Counter #(.width(16), .max('hffff), .ongoal("wrap"), .trigger("rising"), .behavior("old")) counter_4 (
    .count(and_6_out), .Q(\插入气泡数 ), .clk(CLK), .clr(RST));  // open: load, D, carry, preset
  RAM #(.addrWidth(10), .dataWidth(32), .bus("separate"), .Select("high")) ram_1 (
    .addr(ex_mem_1_result_2[11:2]), .din(MDin), .data(ram_1_data), .str(MemWrite), .clk(CLK));  // open: sel, ld, clr
  Comparator #(.width(32), .mode("twosComplement")) comparator_2 (
    .a(JR_address), .b(32'h22), .eq(comparator_2_eq));  // open: gt, lt
  Comparator #(.width(32), .mode("twosComplement")) comparator_3 (
    .a(v0), .b(32'h22), .eq(comparator_3_eq));  // open: gt, lt
  Multiplexer #(.select(1), .width(32), .disabled("Z"), .enable("false")) multiplexer_16 (
    .in0(ram_1_data), .in1(MDin), .out(multiplexer_16_out), .sel(ex_mem_1_system_2));
  not not_3 (not_3_out, comparator_3_eq);
  MEM_WB mem_wb_1 (
    .in_3(Rt_MEM), .in_4(Rd_MEM), .MenToReg(ex_mem_1_mentoreg_2), .RegWrite(MEM_WriteReg), .JAL(JAL_MEM),
    .RegDst(RegDst_MEM), .IR(ex_mem_1_ir_2), .PC(M_PC), .Result(ex_mem_1_result_2),
    .Mem_Res(multiplexer_16_out), .Rt(Rt_back), .Rd(Rd_back), .MenToReg_2(mem_wb_1_mentoreg_2),
    .RegWrite_2(RegWrite), .JAL_2(JAL), .RegDst_2(RegDst), .IR_2(WB_IR), .PC_2(WB_PC), .Result_2(v0),
    .Mem_Res_2(a0), .RST(RST), .STALL(ex_mem_1_stall_2), .CLK(CLK), .STALL_2(Stop),
    .System(ex_mem_1_system_2), .System_2(Syscall_WB), .LH(ex_mem_1_lh_2), .LH_2(LH_WB), .Sync(1'b0));
  and and_7 (and_7_out, comparator_2_eq, Syscall);
  and and_8 (and_8_out, Syscall_WB, not_3_out);
  Register #(.width(32), .trigger("rising"), .Select("low")) register_1 (
    .D(LED), .en(and_7_out), .Q(LedData), .clk(CLK));  // open: clr
  D_Flip_Flop #(.trigger("falling"), .Pre_Clr_Positions("LEGACY"), .NegatePresetClear("false"), .enable("true"), .NewFFLayout("false")) d_ff_1 (
    .clk(CLK), .D(and_8_out), .Q(d_ff_1_q), .reset(or_5_out));  // open: Qn, preset, en
  or or_5 (or_5_out, RST, Go);
  Multiplexer #(.select(1), .width(32), .disabled("Z"), .enable("false")) multiplexer_17 (
    .in0(v0), .in1(a0), .out(multiplexer_17_out), .sel(mem_wb_1_mentoreg_2));
  not not_4 (\中止 , d_ff_1_q);
  Multiplexer #(.select(1), .width(32), .disabled("Z"), .enable("false")) multiplexer_18 (
    .in0(multiplexer_17_out), .in1(WB_PC_4), .out(multiplexer_18_out), .sel(JAL));
  Multiplexer #(.select(1), .width(16), .disabled("Z"), .enable("false")) multiplexer_19 (
    .in0(multiplexer_17_out[15:0]), .in1(multiplexer_17_out[31:16]), .out(multiplexer_19_out), .sel(v0[1]));
  assign bit_extender_3_out = {{16{multiplexer_19_out[15]}}, multiplexer_19_out};  // Bit_Extender bit_extender_3
  Multiplexer #(.select(1), .width(32), .disabled("Z"), .enable("false")) multiplexer_20 (
    .in0(multiplexer_18_out), .in1(bit_extender_3_out), .out(RDin), .sel(LH_WB));

  // Other names for the same wires on the sheet: J_JAL[31:2] = {EX_PC_4[31:28], EX_IR[25:0]}; IF_IR[5:0] = Func;
  //   shamt[4:0] = IF_IR[10:6]; Rd[4:0] = IF_IR[15:11]; Rt[4:0] = IF_IR[20:16]; OP[5:0] = IF_IR[31:26];
  //   L[31:0] = JR_address; SLLV_1[4:0] = JR_address[4:0]; MEM_PC[31:0] = M_PC; PC[31:0] = IF_PC

  // Notes on the sheet:
  //   中断源
  //   中断等待指示
  //   总复位信号应将除ROM以外所有存储组件全部清零
  //   数码管输出
  //   数码管输出应该用寄存器锁存，否则显示数据只能一闪而过
  //   指令存储器
  //   指令字
  //   contents of rom_1 (hex, n*v repeats v):
  //   20110001 8000c05 20110001 20120002 20130003 8000c09 20110001 20120002 20130003 8000c0d 20110001
  //   20120002 20130003 8000c11 20110001 20120002 20130003 c000cb8 20100001 20110001 118fc0 112020
  //   20020022 c 118882 12200001 8000c15 112020 20020022 c 20110001 118880 112020 20020022 c 12200001
  //   8000c1f 20110001 118fc0 112020 20020022 c 1188c3 112020 20020022 c 118903 112020 20020022 c 118903
  //   112020 20020022 c 118903 112020 20020022 c 118903 112020 20020022 c 118903 112020 20020022 c 118903
  //   112020 20020022 c 118903 112020 20020022 c 20100001 109fc0 139fc3 8021 2012000c 24160003 26100001
  //   3210000f 20080008 20090001 139900 2709825 132020 20020022 c 1094022 1500fff9 22100001 2018000f
  //   2188024 108700 20080008 20090001 139902 2709825 132021 20020022 c 1094022 1500fff9 108702 2c9b022
  //   12c00001 8000c50 4020 1084027 84400 3508ffff 82021 20020022 c 2010ffff 20110000 ae300000 22100001
  //   22310004 ae300000 22100001 22310004 ae300000 22100001 22310004 ae300000 22100001 22310004 ae300000
  //   22100001 22310004 ae300000 22100001 22310004 ae300000 22100001 22310004 ae300000 22100001 22310004
  //   ae300000 22100001 22310004 ae300000 22100001 22310004 ae300000 22100001 22310004 ae300000 22100001
  //   22310004 ae300000 22100001 22310004 ae300000 22100001 22310004 ae300000 22100001 22310004 ae300000
  //   22100001 22310004 22100001 8020 2011003c 8e130000 8e340000 274402a 11000002 ae330000 ae140000
  //   2231fffc 1611fff8 102020 20020022 c 22100004 2011003c 1611fff2 20020032 c 20100000 22100001 102020
  //   20020022 c 22100002 102020 20020022 c 22100003 102020 20020022 c 22100004 102020 20020022 c 22100005
  //   102020 20020022 c 22100006 102020 20020022 c 22100007 102020 20020022 c 22100008 102020 20020022
  //   20020022 c 3e00008
  //   OP
  //   Func
  //   rs
  //   rt
  //   rd
  //   流水调试日志用
  //   JMP
  //   JR
  //   OP
  //   Func
  //   Beq
  //   Bne
  //   MemToReg
  //   MemWrite
  //   AluOP
  //   AluSrcB
  //   RegWrite
  //   JAL
  //   RegDst
  //   Syscall
  //   为方便自动评测，需要输出流水线各段保存的PC值，注意是PC不是PC+4，另外ID段寄存器写入信息，Mem段内存写入信息也要输出
endmodule

module \重定向流水线  (
  output RegWrite,
  output MemWrite,
  output [31:0] IF_PC,
  output [31:0] ID_PC,
  output [31:0] EX_PC,
  output [31:0] M_PC,
  output [31:0] WB_PC,
  output [31:0] RDin,
  output [31:0] MDin,
  output [31:0] LedData
);

  wire and_1_out, and_2_out, and_3_out, and_4_out, and_6_out, and_7_out, and_8_out, BGTZ, BGTZ_EX, CLK,
       comparator_1_gt, comparator_2_eq, comparator_3_eq, d_ff_1_q, ex_mem_1_lh_2, ex_mem_1_mentoreg_2,
       ex_mem_1_stall_2, ex_mem_1_system_2, EX_WriteReg, Go, id_ex_1_alusrcb_2, id_ex_1_beq_2, id_ex_1_bne_2,
       id_ex_1_lh_2, id_ex_1_menwrite_2, id_ex_1_stall_2, IR1, IR2, IR3, JAL, JAL_EX, JAL_MEM, JMP, JMP_EX,
       JR, JR_EX, JUMP, LH, LH_WB, mem_wb_1_mentoreg_2, MEM_WriteReg, MemToReg_EX, mips_alu_1_equal,
       not_1_out, not_2_out, not_3_out, or_2_out, or_3_out, or_5_out, RegDst, RegDst_EX, RegDst_MEM, RST,
       SignedExt, SLLV, STALL_1, Stop, Sync, Syscall, Syscall_EX, Syscall_WB, Used_1, Used_2, W1, W2, W3,
       XORI, \中止 , \单周期硬布线控制器_1_alu_src , \单周期硬布线控制器_1_beq , \单周期硬布线控制器_1_bne , \单周期硬布线控制器_1_jal ,
       \单周期硬布线控制器_1_memtoreg , \单周期硬布线控制器_1_memwrite , \单周期硬布线控制器_1_regdst , \单周期硬布线控制器_1_regwrite , \数据相关 ,
       \有条件分支 ;
  wire [1:0] FowardA, FowardB, \重定向数据检测_1_fowarda , \重定向数据检测_1_fowardb ;
  wire [3:0] id_ex_1_aluop_2, \单周期硬布线控制器_1_alu_op ;
  wire [4:0] EX_WriteReg_num, id_ex_1_shame_2, mem_wb_1_rd, mem_wb_1_rt, MEM_WriteReg_num, multiplexer_1_out,
       multiplexer_2_out, multiplexer_8_out, multiplexer_11_out, multiplexer_13_out, R1__ID, R2__ID, Rd_EX,
       Rd_MEM, Rt_EX, Rt_MEM;
  wire [5:0] Func;
  wire [15:0] \LoadUse次数 , multiplexer_21_out, \总周期数 , \无条件分支数 , \条件分支成功数 ;
  wire [31:0] a0, bit_extender_1_out, bit_extender_2_out, bit_extender_3_out, EX_IR, ex_mem_1_ir_2,
       ex_mem_1_result_2, EX_PC_4, id_ex_1_r1_2, id_ex_1_r2_2, IMM_EX, IR, J, JR_address, JR_address_EX, LED,
       mips_alu_1_result, mips_regifile_1_r2, multiplexer_3_out, multiplexer_4_out, multiplexer_7_out,
       multiplexer_12_out, multiplexer_16_out, multiplexer_17_out, multiplexer_18_out, multiplexer_19_out,
       multiplexer_20_out, PC_4, ram_1_data, shifter_1_out, v0, WB_IR, WB_PC_4;
  wire [31:6] IF_IR;

  Button \u_总复位  (.out(RST));
  Button _1 (.out(IR1));
  Button _2 (.out(IR2));
  Button _3 (.out(IR3));
  Button \u_继续运行  (.out(Go));
  LED #(.active("true")) led_1 (.in(W1));
  LED #(.active("true")) led_2 (.in(W2));
  LED #(.active("true")) led_3 (.in(W3));
  Hex_Digit_Display hex_digit_display_1 (.value(LedData[31:28]));  // open: dp
  Multiplexer #(.select(1), .width(5), .disabled("Z"), .enable("false")) multiplexer_1 (
    .in0(Rt_EX), .in1(Rd_EX), .out(multiplexer_1_out), .sel(RegDst_EX));
  Multiplexer #(.select(1), .width(5), .disabled("Z"), .enable("false")) multiplexer_2 (
    .in0(Rt_MEM), .in1(Rd_MEM), .out(multiplexer_2_out), .sel(RegDst_MEM));
  Multiplexer #(.select(1), .width(32), .disabled("Z"), .enable("false")) multiplexer_3 (
    .in0(PC_4), .in1(J), .out(multiplexer_3_out), .sel(\有条件分支 ));
  Multiplexer #(.select(1), .width(32), .disabled("Z"), .enable("false")) multiplexer_4 (
    .in0({EX_PC_4[31:28], EX_IR[25:0], 2'b00}), .in1(JR_address_EX), .out(multiplexer_4_out), .sel(JR_EX));
  Hex_Digit_Display hex_digit_display_2 (.value(LedData[23:20]));  // open: dp
  Hex_Digit_Display hex_digit_display_3 (.value(LedData[27:24]));  // open: dp
  Multiplexer #(.select(1), .width(5), .disabled("Z"), .enable("false")) multiplexer_5 (
    .in0(multiplexer_1_out), .in1({5{1'b1}}), .out(EX_WriteReg_num), .sel(JAL_EX));
  Multiplexer #(.select(1), .width(5), .disabled("Z"), .enable("false")) multiplexer_6 (
    .in0(multiplexer_2_out), .in1({5{1'b1}}), .out(MEM_WriteReg_num), .sel(JAL_MEM));
  Multiplexer #(.select(1), .width(32), .disabled("Z"), .enable("false")) multiplexer_7 (
    .in0(multiplexer_3_out), .in1(multiplexer_4_out), .out(multiplexer_7_out), .sel(JMP_EX));
  and and_1 (and_1_out, ~\数据相关 , \中止 );  // AND_Gate
  Hex_Digit_Display hex_digit_display_4 (.value(LedData[15:12]));  // open: dp
  Hex_Digit_Display hex_digit_display_5 (.value(LedData[19:16]));  // open: dp
  Register #(.width(32), .trigger("rising"), .Select("low")) PC (
    .D(multiplexer_7_out), .en(and_1_out), .Q(IF_PC), .clk(CLK), .clr(RST));
  Hex_Digit_Display hex_digit_display_6 (.value(LedData[7:4]));  // open: dp
  Hex_Digit_Display hex_digit_display_7 (.value(LedData[11:8]));  // open: dp
  Clock #(.highDuration(1), .lowDuration(1)) clock_1 (.out(CLK));
  // Probe on IF_PC
  Adder #(.width(32)) adder_1 (.a(IF_PC), .b(32'h4), .out(PC_4));  // open: cin, cout
  Hex_Digit_Display hex_digit_display_8 (.value(LedData[3:0]));  // open: dp
  or or_1 (Sync, \有条件分支 , JMP_EX);
  Shifter #(.width(32), .shift("ll")) shifter_1 (.in(IMM_EX), .\dist (5'b00010), .out(shifter_1_out));
  Adder #(.width(32)) adder_2 (.a(EX_PC), .b(32'h4), .out(EX_PC_4));  // open: cin, cout
  Adder #(.width(32)) adder_3 (.a(WB_PC), .b(32'h4), .out(WB_PC_4));  // open: cin, cout
  IF_ID if_id_1 (
    .IRin(IR), .IRout({IF_IR, Func}), .PCin(IF_PC), .PCout(ID_PC), .Sync(Sync), .STALL(and_2_out), .CLK(CLK),
    .STALL_2(STALL_1), .RST(RST));  // open: in_1, out_9, in_2, out_10
  ROM #(.addrWidth(10), .dataWidth(32), .Select("high")) rom_1 (.addr(IF_PC[11:2]), .data(IR));
  and and_2 (and_2_out, ~\数据相关 , \中止 );  // AND_Gate
  // Probe on \总周期数 
  // Probe on \无条件分支数 
  // Probe on \条件分支成功数 
  // Probe on \LoadUse次数 
  // Probe on \LoadUse次数 
  // Probe on IF_PC[11:0]
  Adder #(.width(32)) adder_4 (.a(shifter_1_out), .b(EX_PC_4), .out(J));  // open: cin, cout
  // Probe on {IF_IR, Func}
  // Probe on EX_PC[11:0]
  // Probe on ID_PC[11:0]
  assign bit_extender_1_out = {{16{1'b0}}, {IF_IR[15:6], Func}};  // Bit_Extender bit_extender_1
  assign bit_extender_2_out = {{16{IF_IR[15]}}, {IF_IR[15:6], Func}};  // Bit_Extender bit_extender_2
  // Probe on M_PC[11:0]
  // Probe on IF_IR[31:26]
  // Probe on Func
  // Probe on IF_IR[25:21]
  Multiplexer #(.select(1), .width(5), .disabled("Z"), .enable("false")) multiplexer_8 (
    .in0(mem_wb_1_rt), .in1(mem_wb_1_rd), .out(multiplexer_8_out), .sel(RegDst));
  // Probe on WB_PC[11:0]
  Multiplexer #(.select(1), .width(5), .disabled("Z"), .enable("false")) multiplexer_9 (
    .in0(IF_IR[25:21]), .in1(5'b00010), .out(R1__ID), .sel(Syscall));
  Multiplexer #(.select(1), .width(5), .disabled("Z"), .enable("false")) multiplexer_10 (
    .in0(IF_IR[20:16]), .in1(5'b00100), .out(R2__ID), .sel(Syscall));
  Multiplexer #(.select(1), .width(5), .disabled("Z"), .enable("false")) multiplexer_11 (
    .in0(multiplexer_8_out), .in1({5{1'b1}}), .out(multiplexer_11_out), .sel(JAL));
  Multiplexer #(.select(1), .width(32), .disabled("Z"), .enable("false")) multiplexer_12 (
    .in0(bit_extender_1_out), .in1(bit_extender_2_out), .out(multiplexer_12_out), .sel(SignedExt));
  \源寄存器使用检测  \u_源寄存器使用检测_1  (
    .OP0(IF_IR[26]), .OP1(IF_IR[27]), .OP2(IF_IR[28]), .OP3(IF_IR[29]), .OP4(IF_IR[30]), .OP5(IF_IR[31]),
    .F0(Func[0]), .F1(Func[1]), .F2(Func[2]), .F3(Func[3]), .F4(Func[4]), .F5(Func[5]), .R1_Used(Used_1),
    .R2_Used(Used_2));
  \单周期硬布线控制器  \u_单周期硬布线控制器_1  (
    .Func(Func), .OP(IF_IR[31:26]), .ALU_OP(\单周期硬布线控制器_1_alu_op ), .MemToReg(\单周期硬布线控制器_1_memtoreg ),
    .MemWrite(\单周期硬布线控制器_1_memwrite ), .ALU_SRC(\单周期硬布线控制器_1_alu_src ), .RegWrite(\单周期硬布线控制器_1_regwrite ),
    .SysCALL(Syscall), .SignedExt(SignedExt), .RegDst(\单周期硬布线控制器_1_regdst ), .JR(JR), .JMP(JMP),
    .Beq(\单周期硬布线控制器_1_beq ), .JAL(\单周期硬布线控制器_1_jal ), .Bne(\单周期硬布线控制器_1_bne ), .SLLV(SLLV), .LH(LH),
    .XORI(XORI), .BGTZ(BGTZ));  // open: M, MFC0, MTC0, ERET
  // Probe on R1__ID
  or or_2 (or_2_out, \中止 , not_1_out);
  not not_1 (not_1_out, Syscall_WB);
  MIPS_Regifile mips_regifile_1 (
    .Din(RDin), .Clk(CLK), .R1(JR_address), .R2(mips_regifile_1_r2), .WE(RegWrite),
    .W_num(multiplexer_11_out), .R1_num(R1__ID), .R2_num(R2__ID));
  Counter #(.width(16), .max('hffff), .ongoal("wrap"), .trigger("rising"), .behavior("old")) counter_1 (
    .count(or_2_out), .Q(\总周期数 ), .clk(CLK), .clr(RST));  // open: load, D, carry, preset
  \重定向数据检测  \u_重定向数据检测_1  (
    .EX_LD(MemToReg_EX), .R1Used(Used_1), .R1_num(R1__ID), .R2_num(R2__ID), .EX_W_num(EX_WriteReg_num),
    .Mem_W_num(MEM_WriteReg_num), .EX_RegWrite(EX_WriteReg), .Mem_WriteReg(MEM_WriteReg), .R2Used(Used_2),
    .Bubble(\数据相关 ), .FowardA(\重定向数据检测_1_fowarda ), .FowardB(\重定向数据检测_1_fowardb ));
  // Probe on \重定向数据检测_1_fowarda 
  // Probe on \重定向数据检测_1_fowardb 
  Multiplexer #(.select(1), .width(5), .disabled("Z"), .enable("false")) multiplexer_13 (
    .in0(IF_IR[10:6]), .in1(JR_address[4:0]), .out(multiplexer_13_out), .sel(SLLV));
  Counter #(.width(16), .max('hffff), .ongoal("wrap"), .trigger("rising"), .behavior("old")) counter_2 (
    .count(JMP_EX), .Q(\无条件分支数 ), .clk(CLK), .clr(RST));  // open: load, D, carry, preset
  ID_EX id_ex_1 (
    .in_10(IF_IR[20:16]), .in_11(IF_IR[15:11]), .Beq(\单周期硬布线控制器_1_beq ), .Bne(\单周期硬布线控制器_1_bne ),
    .MenToReg(\单周期硬布线控制器_1_memtoreg ), .MenWrite(\单周期硬布线控制器_1_memwrite ), .AluOP(\单周期硬布线控制器_1_alu_op ),
    .AluSrcB(\单周期硬布线控制器_1_alu_src ), .RegWrite(\单周期硬布线控制器_1_regwrite ), .JAL(\单周期硬布线控制器_1_jal ),
    .RegDst(\单周期硬布线控制器_1_regdst ), .IR({IF_IR, Func}), .PC(ID_PC), .R1(JR_address), .R2(mips_regifile_1_r2),
    .IMM(multiplexer_12_out), .SHAME(multiplexer_13_out), .Rt(Rt_EX), .Rd(Rd_EX), .Beq_2(id_ex_1_beq_2),
    .Bne_2(id_ex_1_bne_2), .MenToReg_2(MemToReg_EX), .MenWrite_2(id_ex_1_menwrite_2),
    .AluOP_2(id_ex_1_aluop_2), .AluSrcB_2(id_ex_1_alusrcb_2), .RegWrite_2(EX_WriteReg), .JAL_2(JAL_EX),
    .RegDst_2(RegDst_EX), .IR_2(EX_IR), .PC_2(EX_PC), .R1_2(id_ex_1_r1_2), .R2_2(id_ex_1_r2_2),
    .IMM_2(IMM_EX), .SHAME_2(id_ex_1_shame_2), .Sync(or_3_out), .STALL(\中止 ), .CLK(CLK),
    .STALL_2(id_ex_1_stall_2), .RST(RST), .JR(JR), .JR_2(JR_EX), .JMP(JMP), .JMP_2(JMP_EX), .System(Syscall),
    .System_2(Syscall_EX), .LH(LH), .LH_2(id_ex_1_lh_2), .BGTZ(BGTZ), .BGTZ_2(BGTZ_EX),
    .A(\重定向数据检测_1_fowarda ), .A_2(FowardA), .B(\重定向数据检测_1_fowardb ), .B_2(FowardB));  // open: in_1, out_31, in_2, out_32
  or or_3 (or_3_out, Sync, \数据相关 );
  Multiplexer #(.select(2), .width(32), .disabled("Z"), .enable("false")) multiplexer_14 (
    .in0(id_ex_1_r1_2), .in1(RDin), .in2(ex_mem_1_result_2), .in3(ex_mem_1_result_2), .out(JR_address_EX),
    .sel(FowardA));
  Multiplexer #(.select(2), .width(32), .disabled("Z"), .enable("false")) multiplexer_15 (
    .in0(id_ex_1_r2_2), .in1(RDin), .in2(ex_mem_1_result_2), .in3(ex_mem_1_result_2), .out(LED), .sel(FowardB));
  not not_2 (not_2_out, mips_alu_1_equal);
  Multiplexer #(.select(1), .width(32), .disabled("Z"), .enable("false")) multiplexer_16 (
    .in0(LED), .in1(IMM_EX), .out(multiplexer_16_out), .sel(id_ex_1_alusrcb_2));
  Counter #(.width(16), .max('hffff), .ongoal("wrap"), .trigger("rising"), .behavior("old")) counter_3 (
    .count(\有条件分支 ), .Q(\条件分支成功数 ), .clk(CLK), .clr(RST));  // open: load, D, carry, preset
  and and_3 (and_3_out, mips_alu_1_equal, id_ex_1_beq_2);
  and and_4 (and_4_out, not_2_out, id_ex_1_bne_2);
  MIPS_ALU mips_alu_1 (
    .X(JR_address_EX), .Y(multiplexer_16_out), .AluOP(id_ex_1_aluop_2), .Equal(mips_alu_1_equal),
    .Result(mips_alu_1_result), .shamt(id_ex_1_shame_2));  // open: Result_2
  Comparator #(.width(32), .mode("twosComplement")) comparator_1 (
    .a(JR_address_EX), .b({32{1'b0}}), .gt(comparator_1_gt));  // open: eq, lt
  or or_4 (\有条件分支 , and_3_out, JUMP, and_4_out);
  and and_5 (JUMP, BGTZ_EX, comparator_1_gt);
  Multiplexer #(.select(1), .width(32), .disabled("Z"), .enable("false")) multiplexer_17 (
    .in0(mips_alu_1_result), .in1(JR_address_EX), .out(multiplexer_17_out), .sel(Syscall_EX));
  and and_6 (and_6_out, \数据相关 , \中止 );
  EX_MEM ex_mem_1 (
    .in_3(Rt_EX), .in_4(Rd_EX), .MenToReg(MemToReg_EX), .MenWrite(id_ex_1_menwrite_2),
    .RegWrite(EX_WriteReg), .JAL(JAL_EX), .RegDst(RegDst_EX), .IR(EX_IR), .PC(EX_PC),
    .Result(multiplexer_17_out), .R2(LED), .Rt(Rt_MEM), .Rd(Rd_MEM), .MenToReg_2(ex_mem_1_mentoreg_2),
    .MenWrite_2(MemWrite), .RegWrite_2(MEM_WriteReg), .JAL_2(JAL_MEM), .RegDst_2(RegDst_MEM),
    .IR_2(ex_mem_1_ir_2), .PC_2(M_PC), .Result_2(ex_mem_1_result_2), .R2_2(MDin), .RST(RST),
    .STALL(id_ex_1_stall_2), .CLK(CLK), .STALL_2(ex_mem_1_stall_2), .System(Syscall_EX),
    .System_2(ex_mem_1_system_2), .LH(id_ex_1_lh_2), .LH_2(ex_mem_1_lh_2), .Sync(1'b0));
  Counter #(.width(16), .max('hffff), .ongoal("wrap"), .trigger("rising"), .behavior("old")) counter_4 (
    .count(and_6_out), .Q(\LoadUse次数 ), .clk(CLK), .clr(RST));  // open: load, D, carry, preset
  // Probe on ex_mem_1_result_2
  RAM #(.addrWidth(10), .dataWidth(32), .bus("separate"), .Select("high")) ram_1 (
    .addr(ex_mem_1_result_2[11:2]), .din(MDin), .data(ram_1_data), .str(MemWrite), .clk(CLK));  // open: sel, ld, clr
  Comparator #(.width(32), .mode("twosComplement")) comparator_2 (
    .a(JR_address_EX), .b(32'h22), .eq(comparator_2_eq));  // open: gt, lt
  Comparator #(.width(32), .mode("twosComplement")) comparator_3 (
    .a(v0), .b(32'h22), .eq(comparator_3_eq));  // open: gt, lt
  Multiplexer #(.select(1), .width(32), .disabled("Z"), .enable("false")) multiplexer_18 (
    .in0(ram_1_data), .in1(MDin), .out(multiplexer_18_out), .sel(ex_mem_1_system_2));
  not not_3 (not_3_out, comparator_3_eq);
  MEM_WB mem_wb_1 (
    .in_3(Rt_MEM), .in_4(Rd_MEM), .MenToReg(ex_mem_1_mentoreg_2), .RegWrite(MEM_WriteReg), .JAL(JAL_MEM),
    .RegDst(RegDst_MEM), .IR(ex_mem_1_ir_2), .PC(M_PC), .Result(ex_mem_1_result_2),
    .Mem_Res(multiplexer_18_out), .Rt(mem_wb_1_rt), .Rd(mem_wb_1_rd), .MenToReg_2(mem_wb_1_mentoreg_2),
    .RegWrite_2(RegWrite), .JAL_2(JAL), .RegDst_2(RegDst), .IR_2(WB_IR), .PC_2(WB_PC), .Result_2(v0),
    .Mem_Res_2(a0), .RST(RST), .STALL(ex_mem_1_stall_2), .CLK(CLK), .STALL_2(Stop),
    .System(ex_mem_1_system_2), .System_2(Syscall_WB), .LH(ex_mem_1_lh_2), .LH_2(LH_WB), .Sync(1'b0));
  and and_7 (and_7_out, comparator_2_eq, Syscall_EX);
  and and_8 (and_8_out, Syscall_WB, not_3_out);
  Register #(.width(32), .trigger("rising"), .Select("low")) register_1 (
    .D(LED), .en(and_7_out), .Q(LedData), .clk(CLK), .clr(RST));
  D_Flip_Flop #(.trigger("falling"), .Pre_Clr_Positions("LEGACY"), .NegatePresetClear("false"), .enable("true"), .NewFFLayout("false")) d_ff_1 (
    .clk(CLK), .D(and_8_out), .Q(d_ff_1_q), .reset(or_5_out));  // open: Qn, preset, en
  or or_5 (or_5_out, RST, Go);
  Multiplexer #(.select(1), .width(32), .disabled("Z"), .enable("false")) multiplexer_19 (
    .in0(v0), .in1(a0), .out(multiplexer_19_out), .sel(mem_wb_1_mentoreg_2));
  not not_4 (\中止 , d_ff_1_q);
  Multiplexer #(.select(1), .width(32), .disabled("Z"), .enable("false")) multiplexer_20 (
    .in0(multiplexer_19_out), .in1(WB_PC_4), .out(multiplexer_20_out), .sel(JAL));
  Multiplexer #(.select(1), .width(16), .disabled("Z"), .enable("false")) multiplexer_21 (
    .in0(multiplexer_19_out[15:0]), .in1(multiplexer_19_out[31:16]), .out(multiplexer_21_out), .sel(v0[1]));
  assign bit_extender_3_out = {{16{multiplexer_21_out[15]}}, multiplexer_21_out};  // Bit_Extender bit_extender_3
  Multiplexer #(.select(1), .width(32), .disabled("Z"), .enable("false")) multiplexer_22 (
    .in0(multiplexer_20_out), .in1(bit_extender_3_out), .out(RDin), .sel(LH_WB));

  // Other names for the same wires on the sheet: J_JAL[31:2] = {EX_PC_4[31:28], EX_IR[25:0]}; IF_IR[5:0] = Func;
  //   shamt[4:0] = IF_IR[10:6]; Rd[4:0] = IF_IR[15:11]; Rt[4:0] = IF_IR[20:16]; OP[5:0] = IF_IR[31:26];
  //   SLLV_1[4:0] = JR_address[4:0]; L[31:0] = JR_address_EX; MEM_PC[31:0] = M_PC; PC[31:0] = IF_PC;
  //   插入气泡数[15:0] = \LoadUse次数 

  // Notes on the sheet:
  //   中断源
  //   中断等待指示
  //   数码管输出
  //   指令存储器
  //   指令字
  //   contents of rom_1 (hex, n*v repeats v):
  //   20110001 8000c05 20110001 20120002 20130003 8000c09 20110001 20120002 20130003 8000c0d 20110001
  //   20120002 20130003 8000c11 20110001 20120002 20130003 c000cb8 20100001 20110001 118fc0 112020
  //   20020022 c 118882 12200001 8000c15 112020 20020022 c 20110001 118880 112020 20020022 c 12200001
  //   8000c1f 20110001 118fc0 112020 20020022 c 1188c3 112020 20020022 c 118903 112020 20020022 c 118903
  //   112020 20020022 c 118903 112020 20020022 c 118903 112020 20020022 c 118903 112020 20020022 c 118903
  //   112020 20020022 c 118903 112020 20020022 c 20100001 109fc0 139fc3 8021 2012000c 24160003 26100001
  //   3210000f 20080008 20090001 139900 2709825 132020 20020022 c 1094022 1500fff9 22100001 2018000f
  //   2188024 108700 20080008 20090001 139902 2709825 132021 20020022 c 1094022 1500fff9 108702 2c9b022
  //   12c00001 8000c50 4020 1084027 84400 3508ffff 82021 20020022 c 2010ffff 20110000 ae300000 22100001
  //   22310004 ae300000 22100001 22310004 ae300000 22100001 22310004 ae300000 22100001 22310004 ae300000
  //   22100001 22310004 ae300000 22100001 22310004 ae300000 22100001 22310004 ae300000 22100001 22310004
  //   ae300000 22100001 22310004 ae300000 22100001 22310004 ae300000 22100001 22310004 ae300000 22100001
  //   22310004 ae300000 22100001 22310004 ae300000 22100001 22310004 ae300000 22100001 22310004 ae300000
  //   22100001 22310004 22100001 8020 2011003c 8e130000 8e340000 274402a 11000002 ae330000 ae140000
  //   2231fffc 1611fff8 102020 20020022 c 22100004 2011003c 1611fff2 20020032 c 20100000 22100001 102020
  //   20020022 c 22100002 102020 20020022 c 22100003 102020 20020022 c 22100004 102020 20020022 c 22100005
  //   102020 20020022 c 22100006 102020 20020022 c 22100007 102020 20020022 c 22100008 102020 20020022
  //   20020022 c 3e00008
  //   OP
  //   Func
  //   rs
  //   rt
  //   rd
  //   流水调试日志用
  //   JMP
  //   JR
  //   OP
  //   Func
  //   Beq
  //   Bne
  //   MemToReg
  //   MemWrite
  //   AluOP
  //   AluSrcB
  //   RegWrite
  //   JAL
  //   RegDst
  //   Syscall
  //   为方便自动评测，需要输出流水线各段保存的PC值，注意是PC不是PC+4，另外ID段寄存器写入信息，Mem段内存写入信息也要输出
endmodule

module \重定向流水线_单级中断  (
  input  IR1,
  input  IR2,
  input  IR3,
  output RegWrite,
  output MemWrite,
  output [31:0] IF_PC,
  output [31:0] ID_PC,
  output [31:0] EX_PC,
  output [31:0] M_PC,
  output [31:0] WB_PC,
  output [31:0] RDin,
  output [31:0] MDin,
  output [31:0] LedData
);

  wire and_1_out, and_2_out, and_3_out, and_4_out, and_5_out, and_8_out, and_9_out, and_11_out, and_12_out,
       and_13_out, BGTZ, BGTZ_EX, CLK, comparator_2_eq, comparator_3_eq, comparator_4_eq, comparator_5_eq,
       comparator_6_eq, comparator_7_gt, comparator_8_eq, comparator_9_eq, d_ff_1_q, d_ff_2_q,
       decoder_1_out1, decoder_1_out2, decoder_1_out3, ERET, ex_mem_1_lh_2, ex_mem_1_mentoreg_2,
       ex_mem_1_stall_2, ex_mem_1_system_2, EX_WriteReg, Go, id_ex_1_alusrcb_2, id_ex_1_beq_2, id_ex_1_bne_2,
       id_ex_1_lh_2, id_ex_1_menwrite_2, id_ex_1_stall_2, IR1_t, IR2_t, IR3_t, IRA, IRB, IRC, JAL, JAL_EX,
       JAL_MEM, JMP, JMP_EX, JR, JR_EX, JUMP, LH, LH_WB, mem_wb_1_mentoreg_2, MEM_WriteReg, MemToReg_EX,
       mips_alu_1_equal, multiplexer_10_out, multiplexer_13_out, not_1_out, not_2_out, not_3_out, or_4_out,
       or_5_out, or_7_out, or_8_out, or_9_out, or_10_out, or_11_out, or_13_out, or_14_out, or_15_out,
       priority_encoder_1_gs, RegDst, RegDst_EX, RegDst_MEM, register_2_q, RST, SignedExt, SLLV, STALL_1,
       Start, Stop, Sync, Syscall, Syscall_EX, Syscall_WB, Used_1, Used_2, W1, W2, W3, XORI, \中断发生信号 ,
       \中断按键参考电路_1_与中断屏蔽位与 , \中断按键参考电路_2_与中断屏蔽位与 , \中断按键参考电路_3_与中断屏蔽位与 , \中止 , \单周期硬布线控制器_1_alu_src ,
       \单周期硬布线控制器_1_beq , \单周期硬布线控制器_1_bne , \单周期硬布线控制器_1_jal , \单周期硬布线控制器_1_memtoreg ,
       \单周期硬布线控制器_1_memwrite , \单周期硬布线控制器_1_regdst , \单周期硬布线控制器_1_regwrite , \数据相关 , \有条件分支 , \进入中断 ;
  wire [1:0] FowardA, FowardB, INT_num, register_1_q, \重定向数据检测_1_fowarda , \重定向数据检测_1_fowardb ;
  wire [3:0] id_ex_1_aluop_2, \单周期硬布线控制器_1_alu_op ;
  wire [4:0] EX_WriteReg_num, id_ex_1_shame_2, mem_wb_1_rd, mem_wb_1_rt, MEM_WriteReg_num, multiplexer_3_out,
       multiplexer_4_out, multiplexer_12_out, multiplexer_16_out, multiplexer_18_out, R1__ID, R2__ID, Rd_EX,
       Rd_MEM, Rt_EX, Rt_MEM;
  wire [5:0] Func;
  wire [15:0] \LoadUse次数 , multiplexer_26_out, \总周期数 , \无条件分支数 , \条件分支成功数 ;
  wire [31:0] a0, bit_extender_1_out, bit_extender_2_out, bit_extender_3_out, EPC_q, EX_IR, ex_mem_1_ir_2,
       ex_mem_1_result_2, EX_PC_4, id_ex_1_r1_2, id_ex_1_r2_2, IMM_EX, IR, J, JR_address, JR_address_EX, LED,
       mips_alu_1_result, mips_regifile_1_r2, multiplexer_1_out, multiplexer_2_out, multiplexer_5_out,
       multiplexer_8_out, multiplexer_9_out, multiplexer_17_out, multiplexer_21_out, multiplexer_22_out,
       multiplexer_23_out, multiplexer_24_out, multiplexer_25_out, PC_4, ram_1_data, shifter_1_out, v0,
       WB_IR, WB_PC_4, \服务地址 ;
  wire [31:6] IF_IR;

  Button \u_总复位  (.out(RST));
  Button \u_继续运行  (.out(Go));
  LED #(.active("true")) led_1 (.in(W1));
  LED #(.active("true")) led_2 (.in(W2));
  LED #(.active("true")) led_3 (.in(W3));
  or or_1 (IR1_t, IR1, IRA);
  Multiplexer #(.select(1), .width(32), .disabled("Z"), .enable("false")) multiplexer_1 (
    .in0(PC_4), .in1(J), .out(multiplexer_1_out), .sel(\有条件分支 ));
  Multiplexer #(.select(1), .width(32), .disabled("Z"), .enable("false")) multiplexer_2 (
    .in0({EX_PC_4[31:28], EX_IR[25:0], 2'b00}), .in1(JR_address_EX), .out(multiplexer_2_out), .sel(JR_EX));
  Hex_Digit_Display hex_digit_display_1 (.value(LedData[31:28]));  // open: dp
  or or_2 (IR2_t, IR2, IRB);
  Multiplexer #(.select(1), .width(5), .disabled("Z"), .enable("false")) multiplexer_3 (
    .in0(Rt_EX), .in1(Rd_EX), .out(multiplexer_3_out), .sel(RegDst_EX));
  Multiplexer #(.select(1), .width(5), .disabled("Z"), .enable("false")) multiplexer_4 (
    .in0(Rt_MEM), .in1(Rd_MEM), .out(multiplexer_4_out), .sel(RegDst_MEM));
  Multiplexer #(.select(1), .width(32), .disabled("Z"), .enable("false")) multiplexer_5 (
    .in0(multiplexer_1_out), .in1(multiplexer_2_out), .out(multiplexer_5_out), .sel(JMP_EX));
  Register #(.width(2), .trigger("rising"), .Select("low")) register_1 (
    .D(INT_num), .en(\中断发生信号 ), .Q(register_1_q), .clk(CLK));  // open: clr
  Comparator #(.width(16), .mode("twosComplement")) comparator_1 (
    .a(\总周期数 ), .b({16{1'b0}}), .eq(Start));  // open: gt, lt
  Hex_Digit_Display hex_digit_display_2 (.value(LedData[23:20]));  // open: dp
  Hex_Digit_Display hex_digit_display_3 (.value(LedData[27:24]));  // open: dp
  Multiplexer #(.select(1), .width(5), .disabled("Z"), .enable("false")) multiplexer_6 (
    .in0(multiplexer_3_out), .in1({5{1'b1}}), .out(EX_WriteReg_num), .sel(JAL_EX));
  Multiplexer #(.select(1), .width(5), .disabled("Z"), .enable("false")) multiplexer_7 (
    .in0(multiplexer_4_out), .in1({5{1'b1}}), .out(MEM_WriteReg_num), .sel(JAL_MEM));
  Decoder #(.select(2), .tristate("false"), .disabled("Z"), .enable("false")) decoder_1 (
    .out1(decoder_1_out1), .out2(decoder_1_out2), .out3(decoder_1_out3), .sel(register_1_q));  // open: out0
  Hex_Digit_Display hex_digit_display_4 (.value(LedData[19:16]));  // open: dp
  Hex_Digit_Display hex_digit_display_5 (.value(LedData[15:12]));  // open: dp
  or or_3 (IR3_t, IR3, IRC);
  Multiplexer #(.select(1), .width(32), .disabled("Z"), .enable("false")) multiplexer_8 (
    .in0(multiplexer_5_out), .in1(\服务地址 ), .out(multiplexer_8_out), .sel(\进入中断 ));
  Register #(.width(32), .trigger("rising"), .Select("low")) EPC (
    .D(M_PC), .en(\进入中断 ), .Q(EPC_q), .clk(CLK));  // open: clr
  and and_1 (and_1_out, ERET, decoder_1_out1);
  and and_2 (and_2_out, ERET, decoder_1_out2);
  and and_3 (and_3_out, ERET, decoder_1_out3);
  Hex_Digit_Display hex_digit_display_6 (.value(LedData[11:8]));  // open: dp
  Hex_Digit_Display hex_digit_display_7 (.value(LedData[7:4]));  // open: dp
  Clock #(.highDuration(1), .lowDuration(1)) clock_1 (.out(CLK));
  Multiplexer #(.select(1), .width(32), .disabled("Z"), .enable("false")) multiplexer_9 (
    .in0(multiplexer_8_out), .in1(EPC_q), .out(multiplexer_9_out), .sel(ERET));
  and and_4 (and_4_out, ~\数据相关 , \中止 );  // AND_Gate
  Hex_Digit_Display hex_digit_display_8 (.value(LedData[3:0]));  // open: dp
  Register #(.width(32), .trigger("rising"), .Select("low")) PC (
    .D(multiplexer_9_out), .en(and_4_out), .Q(IF_PC), .clk(CLK), .clr(RST));
  \中断按键参考电路  \u_中断按键参考电路_1  (
    .\与中断屏蔽位与 (\中断按键参考电路_1_与中断屏蔽位与 ), .\同步清零信号 (and_1_out), .\中断号 (IR1_t), .\中断等待指示灯 (W1), .CLK(CLK));
  \中断按键参考电路  \u_中断按键参考电路_2  (
    .\与中断屏蔽位与 (\中断按键参考电路_2_与中断屏蔽位与 ), .\同步清零信号 (and_2_out), .\中断号 (IR2_t), .\中断等待指示灯 (W2), .CLK(CLK));
  \中断按键参考电路  \u_中断按键参考电路_3  (
    .\与中断屏蔽位与 (\中断按键参考电路_3_与中断屏蔽位与 ), .\同步清零信号 (and_3_out), .\中断号 (IR3_t), .\中断等待指示灯 (W3), .CLK(CLK));
  Multiplexer #(.select(1), .width(1), .disabled("Z"), .enable("false")) multiplexer_10 (
    .in0(1'b0), .in1(1'b1), .out(multiplexer_10_out), .sel(or_4_out));
  or or_4 (or_4_out, Start, ERET);
  // Probe on IF_PC
  Adder #(.width(32)) adder_1 (.a(IF_PC), .b(32'h4), .out(PC_4));  // open: cin, cout
  or or_5 (or_5_out, ERET, \中断发生信号 , Start);
  // Probe on \总周期数 
  // Probe on \无条件分支数 
  // Probe on \条件分支成功数 
  // Probe on \LoadUse次数 
  // Probe on \LoadUse次数 
  ROM #(.addrWidth(10), .dataWidth(32), .Select("high")) rom_1 (.addr(IF_PC[11:2]), .data(IR));
  Priority_Encoder #(.select(2), .disabled("Z")) priority_encoder_1 (
    .in0(1'b0), .in1(\中断按键参考电路_1_与中断屏蔽位与 ), .in2(\中断按键参考电路_2_与中断屏蔽位与 ), .in3(\中断按键参考电路_3_与中断屏蔽位与 ),
    .out(INT_num), .gs(priority_encoder_1_gs));  // open: en_out, en_in
  Register #(.width(1), .trigger("rising"), .Select("low")) register_2 (
    .D(multiplexer_10_out), .en(or_5_out), .Q(register_2_q), .clk(CLK));  // open: clr
  // Probe on IF_PC[11:0]
  or or_6 (Sync, \有条件分支 , JMP_EX);
  Shifter #(.width(32), .shift("ll")) shifter_1 (.in(IMM_EX), .\dist (5'b00010), .out(shifter_1_out));
  Adder #(.width(32)) adder_2 (.a(EX_PC), .b(32'h4), .out(EX_PC_4));  // open: cin, cout
  Adder #(.width(32)) adder_3 (.a(WB_PC), .b(32'h4), .out(WB_PC_4));  // open: cin, cout
  IF_ID if_id_1 (
    .IRin(IR), .IRout({IF_IR, Func}), .PCin(IF_PC), .PCout(ID_PC), .Sync(or_7_out), .STALL(and_5_out),
    .CLK(CLK), .STALL_2(STALL_1), .RST(RST));  // open: in_1, out_9, in_2, out_10
  and and_5 (and_5_out, ~\数据相关 , \中止 );  // AND_Gate
  // Probe on INT_num
  // Probe on EX_PC[11:0]
  // Probe on ID_PC[11:0]
  Adder #(.width(32)) adder_4 (.a(shifter_1_out), .b(EX_PC_4), .out(J));  // open: cin, cout
  or or_7 (or_7_out, Sync, \进入中断 , ERET);
  and and_6 (\中断发生信号 , priority_encoder_1_gs, register_2_q);
  // Probe on M_PC[11:0]
  // Probe on {IF_IR, Func}
  Multiplexer #(.select(2), .width(32), .disabled("Z"), .enable("false")) multiplexer_11 (
    .in1(32'h30ac), .in2(32'h3150), .in3(32'h31f4), .out(\服务地址 ), .sel(INT_num));  // open: in0
  // Probe on WB_PC[11:0]
  assign bit_extender_1_out = {{16{1'b0}}, {IF_IR[15:6], Func}};  // Bit_Extender bit_extender_1
  assign bit_extender_2_out = {{16{IF_IR[15]}}, {IF_IR[15:6], Func}};  // Bit_Extender bit_extender_2
  // Probe on IF_IR[31:26]
  // Probe on Func
  // Probe on IF_IR[25:21]
  Multiplexer #(.select(1), .width(5), .disabled("Z"), .enable("false")) multiplexer_12 (
    .in0(mem_wb_1_rt), .in1(mem_wb_1_rd), .out(multiplexer_12_out), .sel(RegDst));
  Multiplexer #(.select(1), .width(1), .disabled("Z"), .enable("false")) multiplexer_13 (
    .in0(1'b1), .in1(1'b0), .out(multiplexer_13_out), .sel(\进入中断 ));
  \单周期硬布线控制器  \u_单周期硬布线控制器_1  (
    .Func(Func), .OP(IF_IR[31:26]), .ALU_OP(\单周期硬布线控制器_1_alu_op ), .MemToReg(\单周期硬布线控制器_1_memtoreg ),
    .MemWrite(\单周期硬布线控制器_1_memwrite ), .ALU_SRC(\单周期硬布线控制器_1_alu_src ), .RegWrite(\单周期硬布线控制器_1_regwrite ),
    .SysCALL(Syscall), .SignedExt(SignedExt), .RegDst(\单周期硬布线控制器_1_regdst ), .JR(JR), .JMP(JMP),
    .Beq(\单周期硬布线控制器_1_beq ), .JAL(\单周期硬布线控制器_1_jal ), .Bne(\单周期硬布线控制器_1_bne ), .SLLV(SLLV), .LH(LH),
    .XORI(XORI), .BGTZ(BGTZ), .M(IF_IR[25:21]), .ERET(ERET));  // open: MFC0, MTC0
  Multiplexer #(.select(1), .width(5), .disabled("Z"), .enable("false")) multiplexer_14 (
    .in0(IF_IR[25:21]), .in1(5'b00010), .out(R1__ID), .sel(Syscall));
  Multiplexer #(.select(1), .width(5), .disabled("Z"), .enable("false")) multiplexer_15 (
    .in0(IF_IR[20:16]), .in1(5'b00100), .out(R2__ID), .sel(Syscall));
  Multiplexer #(.select(1), .width(5), .disabled("Z"), .enable("false")) multiplexer_16 (
    .in0(multiplexer_12_out), .in1({5{1'b1}}), .out(multiplexer_16_out), .sel(JAL));
  Multiplexer #(.select(1), .width(32), .disabled("Z"), .enable("false")) multiplexer_17 (
    .in0(bit_extender_1_out), .in1(bit_extender_2_out), .out(multiplexer_17_out), .sel(SignedExt));
  D_Flip_Flop #(.trigger("rising"), .Pre_Clr_Positions("LEGACY"), .NegatePresetClear("false"), .enable("true"), .NewFFLayout("false")) d_ff_1 (
    .clk(CLK), .D(multiplexer_13_out), .Q(d_ff_1_q), .en(or_8_out));  // open: Qn, preset, reset
  or or_8 (or_8_out, \进入中断 , \中断发生信号 );
  \源寄存器使用检测  \u_源寄存器使用检测_1  (
    .OP0(IF_IR[26]), .OP1(IF_IR[27]), .OP2(IF_IR[28]), .OP3(IF_IR[29]), .OP4(IF_IR[30]), .OP5(IF_IR[31]),
    .F0(Func[0]), .F1(Func[1]), .F2(Func[2]), .F3(Func[3]), .F4(Func[4]), .F5(Func[5]), .R1_Used(Used_1),
    .R2_Used(Used_2));
  // Probe on R1__ID
  not not_1 (not_1_out, Syscall_WB);
  Comparator #(.width(32), .mode("unsigned")) comparator_2 (
    .a({32{1'b0}}), .b(M_PC), .eq(comparator_2_eq));  // open: gt, lt
  or or_9 (or_9_out, \中止 , not_1_out);
  MIPS_Regifile mips_regifile_1 (
    .Din(RDin), .Clk(CLK), .R1(JR_address), .R2(mips_regifile_1_r2), .WE(RegWrite),
    .W_num(multiplexer_16_out), .R1_num(R1__ID), .R2_num(R2__ID));
  and and_7 (\进入中断 , d_ff_1_q, ~comparator_2_eq);  // AND_Gate
  Counter #(.width(16), .max('hffff), .ongoal("wrap"), .trigger("rising"), .behavior("old")) counter_1 (
    .count(or_9_out), .Q(\总周期数 ), .clk(CLK), .clr(RST));  // open: load, D, carry, preset
  \重定向数据检测  \u_重定向数据检测_1  (
    .EX_LD(MemToReg_EX), .R1Used(Used_1), .R1_num(R1__ID), .R2_num(R2__ID), .EX_W_num(EX_WriteReg_num),
    .Mem_W_num(MEM_WriteReg_num), .EX_RegWrite(EX_WriteReg), .Mem_WriteReg(MEM_WriteReg), .R2Used(Used_2),
    .Bubble(\数据相关 ), .FowardA(\重定向数据检测_1_fowarda ), .FowardB(\重定向数据检测_1_fowardb ));
  // Probe on \重定向数据检测_1_fowarda 
  // Probe on \重定向数据检测_1_fowardb 
  ID_EX id_ex_1 (
    .in_10(IF_IR[20:16]), .in_11(IF_IR[15:11]), .Beq(\单周期硬布线控制器_1_beq ), .Bne(\单周期硬布线控制器_1_bne ),
    .MenToReg(\单周期硬布线控制器_1_memtoreg ), .MenWrite(\单周期硬布线控制器_1_memwrite ), .AluOP(\单周期硬布线控制器_1_alu_op ),
    .AluSrcB(\单周期硬布线控制器_1_alu_src ), .RegWrite(\单周期硬布线控制器_1_regwrite ), .JAL(\单周期硬布线控制器_1_jal ),
    .RegDst(\单周期硬布线控制器_1_regdst ), .IR({IF_IR, Func}), .PC(ID_PC), .R1(JR_address), .R2(mips_regifile_1_r2),
    .IMM(multiplexer_17_out), .SHAME(multiplexer_18_out), .Rt(Rt_EX), .Rd(Rd_EX), .Beq_2(id_ex_1_beq_2),
    .Bne_2(id_ex_1_bne_2), .MenToReg_2(MemToReg_EX), .MenWrite_2(id_ex_1_menwrite_2),
    .AluOP_2(id_ex_1_aluop_2), .AluSrcB_2(id_ex_1_alusrcb_2), .RegWrite_2(EX_WriteReg), .JAL_2(JAL_EX),
    .RegDst_2(RegDst_EX), .IR_2(EX_IR), .PC_2(EX_PC), .R1_2(id_ex_1_r1_2), .R2_2(id_ex_1_r2_2),
    .IMM_2(IMM_EX), .SHAME_2(id_ex_1_shame_2), .Sync(or_10_out), .STALL(\中止 ), .CLK(CLK),
    .STALL_2(id_ex_1_stall_2), .RST(RST), .JR(JR), .JR_2(JR_EX), .JMP(JMP), .JMP_2(JMP_EX), .System(Syscall),
    .System_2(Syscall_EX), .LH(LH), .LH_2(id_ex_1_lh_2), .BGTZ(BGTZ), .BGTZ_2(BGTZ_EX),
    .A(\重定向数据检测_1_fowarda ), .A_2(FowardA), .B(\重定向数据检测_1_fowardb ), .B_2(FowardB));  // open: in_1, out_31, in_2, out_32
  Multiplexer #(.select(1), .width(5), .disabled("Z"), .enable("false")) multiplexer_18 (
    .in0(IF_IR[10:6]), .in1(JR_address[4:0]), .out(multiplexer_18_out), .sel(SLLV));
  Counter #(.width(16), .max('hffff), .ongoal("wrap"), .trigger("rising"), .behavior("old")) counter_2 (
    .count(JMP_EX), .Q(\无条件分支数 ), .clk(CLK), .clr(RST));  // open: load, D, carry, preset
  or or_10 (or_10_out, ERET, Sync, \进入中断 , \数据相关 );
  Comparator #(.width(16), .mode("twosComplement")) comparator_3 (
    .a(16'h258), .b(\总周期数 ), .eq(comparator_3_eq));  // open: gt, lt
  Comparator #(.width(16), .mode("twosComplement")) comparator_4 (
    .a(\总周期数 ), .b(16'h1), .eq(comparator_4_eq));  // open: gt, lt
  Comparator #(.width(16), .mode("twosComplement")) comparator_5 (
    .a(\总周期数 ), .b(16'h4), .eq(comparator_5_eq));  // open: gt, lt
  Comparator #(.width(16), .mode("twosComplement")) comparator_6 (
    .a(\总周期数 ), .b(16'h7), .eq(comparator_6_eq));  // open: gt, lt
  Multiplexer #(.select(2), .width(32), .disabled("Z"), .enable("false")) multiplexer_19 (
    .in0(id_ex_1_r1_2), .in1(RDin), .in2(ex_mem_1_result_2), .in3(ex_mem_1_result_2), .out(JR_address_EX),
    .sel(FowardA));
  Multiplexer #(.select(2), .width(32), .disabled("Z"), .enable("false")) multiplexer_20 (
    .in0(id_ex_1_r2_2), .in1(RDin), .in2(ex_mem_1_result_2), .in3(ex_mem_1_result_2), .out(LED), .sel(FowardB));
  or or_11 (or_11_out, comparator_3_eq, comparator_4_eq);
  assign IRA = or_11_out ? ~CLK : 1'bz;  // Controlled_Inverter controlled_inverter_1
  assign IRB = comparator_5_eq ? ~CLK : 1'bz;  // Controlled_Inverter controlled_inverter_2
  assign IRC = comparator_6_eq ? ~CLK : 1'bz;  // Controlled_Inverter controlled_inverter_3
  Multiplexer #(.select(1), .width(32), .disabled("Z"), .enable("false")) multiplexer_21 (
    .in0(LED), .in1(IMM_EX), .out(multiplexer_21_out), .sel(id_ex_1_alusrcb_2));
  Counter #(.width(16), .max('hffff), .ongoal("wrap"), .trigger("rising"), .behavior("old")) counter_3 (
    .count(\有条件分支 ), .Q(\条件分支成功数 ), .clk(CLK), .clr(RST));  // open: load, D, carry, preset
  and and_8 (and_8_out, mips_alu_1_equal, id_ex_1_beq_2);
  not not_2 (not_2_out, mips_alu_1_equal);
  and and_9 (and_9_out, not_2_out, id_ex_1_bne_2);
  MIPS_ALU mips_alu_1 (
    .X(JR_address_EX), .Y(multiplexer_21_out), .AluOP(id_ex_1_aluop_2), .Equal(mips_alu_1_equal),
    .Result(mips_alu_1_result), .shamt(id_ex_1_shame_2));  // open: Result_2
  Comparator #(.width(32), .mode("twosComplement")) comparator_7 (
    .a(JR_address_EX), .b({32{1'b0}}), .gt(comparator_7_gt));  // open: eq, lt
  or or_12 (\有条件分支 , and_8_out, JUMP, and_9_out);
  Multiplexer #(.select(1), .width(32), .disabled("Z"), .enable("false")) multiplexer_22 (
    .in0(mips_alu_1_result), .in1(JR_address_EX), .out(multiplexer_22_out), .sel(Syscall_EX));
  or or_13 (or_13_out, ERET, \进入中断 );
  and and_10 (JUMP, BGTZ_EX, comparator_7_gt);
  EX_MEM ex_mem_1 (
    .in_3(Rt_EX), .in_4(Rd_EX), .MenToReg(MemToReg_EX), .MenWrite(id_ex_1_menwrite_2),
    .RegWrite(EX_WriteReg), .JAL(JAL_EX), .RegDst(RegDst_EX), .IR(EX_IR), .PC(EX_PC),
    .Result(multiplexer_22_out), .R2(LED), .Rt(Rt_MEM), .Rd(Rd_MEM), .MenToReg_2(ex_mem_1_mentoreg_2),
    .MenWrite_2(MemWrite), .RegWrite_2(MEM_WriteReg), .JAL_2(JAL_MEM), .RegDst_2(RegDst_MEM),
    .IR_2(ex_mem_1_ir_2), .PC_2(M_PC), .Result_2(ex_mem_1_result_2), .R2_2(MDin), .RST(RST),
    .STALL(id_ex_1_stall_2), .CLK(CLK), .STALL_2(ex_mem_1_stall_2), .System(Syscall_EX),
    .System_2(ex_mem_1_system_2), .LH(id_ex_1_lh_2), .LH_2(ex_mem_1_lh_2), .Sync(or_13_out));
  Counter #(.width(16), .max('hffff), .ongoal("wrap"), .trigger("rising"), .behavior("old")) counter_4 (
    .count(and_11_out), .Q(\LoadUse次数 ), .clk(CLK), .clr(RST));  // open: load, D, carry, preset
  and and_11 (and_11_out, \数据相关 , \中止 );
  // Probe on ex_mem_1_result_2
  Comparator #(.width(32), .mode("twosComplement")) comparator_8 (
    .a(JR_address_EX), .b(32'h22), .eq(comparator_8_eq));  // open: gt, lt
  Comparator #(.width(32), .mode("twosComplement")) comparator_9 (
    .a(v0), .b(32'h22), .eq(comparator_9_eq));  // open: gt, lt
  RAM #(.addrWidth(10), .dataWidth(32), .bus("separate"), .Select("high")) ram_1 (
    .addr(ex_mem_1_result_2[11:2]), .din(MDin), .data(ram_1_data), .str(MemWrite), .clk(CLK));  // open: sel, ld, clr
  or or_14 (or_14_out, ERET, \进入中断 );
  Multiplexer #(.select(1), .width(32), .disabled("Z"), .enable("false")) multiplexer_23 (
    .in0(ram_1_data), .in1(MDin), .out(multiplexer_23_out), .sel(ex_mem_1_system_2));
  and and_12 (and_12_out, comparator_8_eq, Syscall_EX);
  and and_13 (and_13_out, Syscall_WB, not_3_out);
  not not_3 (not_3_out, comparator_9_eq);
  MEM_WB mem_wb_1 (
    .in_3(Rt_MEM), .in_4(Rd_MEM), .MenToReg(ex_mem_1_mentoreg_2), .RegWrite(MEM_WriteReg), .JAL(JAL_MEM),
    .RegDst(RegDst_MEM), .IR(ex_mem_1_ir_2), .PC(M_PC), .Result(ex_mem_1_result_2),
    .Mem_Res(multiplexer_23_out), .Rt(mem_wb_1_rt), .Rd(mem_wb_1_rd), .MenToReg_2(mem_wb_1_mentoreg_2),
    .RegWrite_2(RegWrite), .JAL_2(JAL), .RegDst_2(RegDst), .IR_2(WB_IR), .PC_2(WB_PC), .Result_2(v0),
    .Mem_Res_2(a0), .RST(RST), .STALL(ex_mem_1_stall_2), .CLK(CLK), .STALL_2(Stop),
    .System(ex_mem_1_system_2), .System_2(Syscall_WB), .LH(ex_mem_1_lh_2), .LH_2(LH_WB), .Sync(or_14_out));
  Register #(.width(32), .trigger("rising"), .Select("low")) register_3 (
    .D(LED), .en(and_12_out), .Q(LedData), .clk(CLK), .clr(RST));
  D_Flip_Flop #(.trigger("falling"), .Pre_Clr_Positions("LEGACY"), .NegatePresetClear("false"), .enable("true"), .NewFFLayout("false")) d_ff_2 (
    .clk(CLK), .D(and_13_out), .Q(d_ff_2_q), .reset(or_15_out));  // open: Qn, preset, en
  not not_4 (\中止 , d_ff_2_q);
  or or_15 (or_15_out, RST, Go);
  Multiplexer #(.select(1), .width(32), .disabled("Z"), .enable("false")) multiplexer_24 (
    .in0(v0), .in1(a0), .out(multiplexer_24_out), .sel(mem_wb_1_mentoreg_2));
  Multiplexer #(.select(1), .width(32), .disabled("Z"), .enable("false")) multiplexer_25 (
    .in0(multiplexer_24_out), .in1(WB_PC_4), .out(multiplexer_25_out), .sel(JAL));
  Multiplexer #(.select(1), .width(16), .disabled("Z"), .enable("false")) multiplexer_26 (
    .in0(multiplexer_24_out[15:0]), .in1(multiplexer_24_out[31:16]), .out(multiplexer_26_out), .sel(v0[1]));
  assign bit_extender_3_out = {{16{multiplexer_26_out[15]}}, multiplexer_26_out};  // Bit_Extender bit_extender_3
  Multiplexer #(.select(1), .width(32), .disabled("Z"), .enable("false")) multiplexer_27 (
    .in0(multiplexer_25_out), .in1(bit_extender_3_out), .out(RDin), .sel(LH_WB));

  // Other names for the same wires on the sheet: J_JAL[31:2] = {EX_PC_4[31:28], EX_IR[25:0]}; IF_IR[5:0] = Func;
  //   shamt[4:0] = IF_IR[10:6]; Rd[4:0] = IF_IR[15:11]; Rt[4:0] = IF_IR[20:16]; OP[5:0] = IF_IR[31:26];
  //   SLLV_1[4:0] = JR_address[4:0]; L[31:0] = JR_address_EX; MEM_PC[31:0] = M_PC; PC[31:0] = IF_PC;
  //   插入气泡数[15:0] = \LoadUse次数 

  // Notes on the sheet:
  //   中断源
  //   中断等待指示
  //   数码管输出
  //   指令存储器
  //   指令字
  //   contents of rom_1 (hex, n*v repeats v):
  //   201d07d0 20100001 109fc0 139fc3 8021 2012000c 24160008 26100001 3210000f 20080008 20090001 139900
  //   2709825 132020 20020022 c 1094022 1500fff9 22100001 2018000f 2188024 108700 20080008 20090001 139902
  //   2709825 132021 20020022 c 1094022 1500fff9 108702 2c9b022 12c00001 8000c07 4020 1084027 84400
  //   3508ffff 82021 20020022 c 8000c01 afa20000 23bd0004 afa40000 23bd0004 afb00000 23bd0004 afb30000
  //   23bd0004 afb40000 23bd0004 afb50000 23bd0004 afb60000 23bd0004 20160001 20140003 20150001 168020
  //   108100 2149825 132020 20020022 c 1600fffa 295a022 1680fff7 23bdfffc 8fb60000 23bdfffc 8fb50000
  //   23bdfffc 8fb40000 23bdfffc 8fb30000 23bdfffc 8fb00000 23bdfffc 8fa40000 23bdfffc 8fa20000 42000018
  //   afa20000 23bd0004 afa40000 23bd0004 afb00000 23bd0004 afb30000 23bd0004 afb40000 23bd0004 afb50000
  //   23bd0004 afb60000 23bd0004 20160002 20140003 20150001 168020 108100 2149825 132020 20020022 c
  //   1600fffa 295a022 1680fff7 23bdfffc 8fb60000 23bdfffc 8fb50000 23bdfffc 8fb40000 23bdfffc 8fb30000
  //   23bdfffc 8fb00000 23bdfffc 8fa40000 23bdfffc 8fa20000 42000018 afa20000 23bd0004 afa40000 23bd0004
  //   afb00000 23bd0004 afb30000 23bd0004 afb40000 23bd0004 afb50000 23bd0004 afb60000 23bd0004 20160003
  //   20140003 20150001 168020 108100 2149825 132020 20020022 c 1600fffa 295a022 1680fff7 23bdfffc
  //   8fb60000 23bdfffc 8fb50000 23bdfffc 8fb40000 23bdfffc 8fb30000 23bdfffc 8fb00000 23bdfffc 8fa40000
  //   23bdfffc 8fa20000 42000018
  //   流水调试日志用
  //   OP
  //   Func
  //   rs
  //   rt
  //   rd
  //   JMP
  //   JR
  //   OP
  //   Func
  //   Beq
  //   Bne
  //   MemToReg
  //   MemWrite
  //   AluOP
  //   AluSrcB
  //   RegWrite
  //   JAL
  //   RegDst
  //   Syscall
  //   为方便自动评测，需要输出流水线各段保存的PC值，注意是PC不是PC+4，另外ID段寄存器写入信息，Mem段内存写入信息也要输出
  //   先断开三个按钮和IRA~IRC的连接
  //   再加入这个电路
endmodule

module \重定向流水线_动态分支预测  (
  output RegWrite,
  output MemWrite,
  output [31:0] IF_PC,
  output [31:0] ID_PC,
  output [31:0] EX_PC,
  output [31:0] M_PC,
  output [31:0] WB_PC,
  output [31:0] RDin,
  output [31:0] MDin,
  output [31:0] LedData
);

  wire and_1_out, and_2_out, and_3_out, and_4_out, and_6_out, and_7_out, and_8_out, BGTZ, BGTZ_EX, CLK,
       comparator_1_gt, comparator_2_eq, comparator_3_eq, d_ff_1_q, EX_CerJump, EX_Have, ex_mem_1_lh_2,
       ex_mem_1_mentoreg_2, ex_mem_1_stall_2, ex_mem_1_system_2, EX_ProJump, EX_WriteReg, Go,
       id_ex_1_alusrcb_2, id_ex_1_beq_2, id_ex_1_bne_2, id_ex_1_lh_2, id_ex_1_menwrite_2, id_ex_1_stall_2,
       ID_Have, IR1, IR2, IR3, JAL, JAL_EX, JAL_MEM, JMP, JMP_EX, JR, JR_EX, JUMP, LH, LH_WB,
       mem_wb_1_mentoreg_2, MEM_WriteReg, MemToReg_EX, mips_alu_1_equal, NewClear, not_1_out, not_2_out,
       not_3_out, not_4_out, or_3_out, or_4_out, or_7_out, RegDst, RegDst_EX, RegDst_MEM, RST, SignedExt,
       SLLV, STALL_1, Stop, Sync, Syscall, Syscall_EX, Syscall_WB, Used_1, Used_2, W1, W2, W3, XORI, \中止 ,
       \单周期硬布线控制器_1_alu_src , \单周期硬布线控制器_1_beq , \单周期硬布线控制器_1_bne , \单周期硬布线控制器_1_jal ,
       \单周期硬布线控制器_1_memtoreg , \单周期硬布线控制器_1_memwrite , \单周期硬布线控制器_1_regdst , \单周期硬布线控制器_1_regwrite , \数据相关 ,
       \有条件分支 ;
  wire [1:0] \bht_1_双预测位输出 , \EX_双位预测 , FowardA, FowardB, \ID_双位预测 , multiplexer_9_out, multiplexer_10_out,
       \双位预测状态机_1_新的状态位 , \重定向数据检测_1_fowarda , \重定向数据检测_1_fowardb ;
  wire [2:0] if_id_1_out_9;
  wire [3:0] id_ex_1_aluop_2, \单周期硬布线控制器_1_alu_op ;
  wire [4:0] EX_WriteReg_num, id_ex_1_shame_2, mem_wb_1_rd, mem_wb_1_rt, MEM_WriteReg_num, multiplexer_2_out,
       multiplexer_3_out, multiplexer_12_out, multiplexer_15_out, multiplexer_21_out, R1__ID, R2__ID, Rd_EX,
       Rd_MEM, Rt_EX, Rt_MEM;
  wire [5:0] Func;
  wire [15:0] \LoadUse次数 , multiplexer_29_out, \总周期数 , \无条件分支数 , \条件分支成功数 ;
  wire [31:0] a0, \bht_1_分支目标地址_2 , bit_extender_1_out, bit_extender_2_out, bit_extender_3_out, EX_IR,
       ex_mem_1_ir_2, ex_mem_1_result_2, EX_NPC, EX_PC_4, id_ex_1_r1_2, id_ex_1_r2_2, ID_NPC, if_id_1_out_10,
       IMM_EX, IR, J, JR_address, JR_address_EX, LED, mips_alu_1_result, mips_regifile_1_r2,
       multiplexer_1_out, multiplexer_4_out, multiplexer_5_out, multiplexer_11_out, multiplexer_16_out,
       multiplexer_18_out, multiplexer_19_out, multiplexer_24_out, multiplexer_25_out, multiplexer_26_out,
       multiplexer_27_out, multiplexer_28_out, NPC_R, PC_4, ram_1_data, shifter_1_out, v0, WB_IR, WB_PC_4;
  wire [31:6] IF_IR;

  Button \u_总复位  (.out(RST));
  Button _1 (.out(IR1));
  Button _2 (.out(IR2));
  Button _3 (.out(IR3));
  Button \u_继续运行  (.out(Go));
  LED #(.active("true")) led_1 (.in(W1));
  LED #(.active("true")) led_2 (.in(W2));
  LED #(.active("true")) led_3 (.in(W3));
  Multiplexer #(.select(1), .width(32), .disabled("Z"), .enable("false")) multiplexer_1 (
    .in0(PC_4), .in1(EX_PC_4), .out(multiplexer_1_out), .sel(NewClear));
  Hex_Digit_Display hex_digit_display_1 (.value(LedData[31:28]));  // open: dp
  Multiplexer #(.select(1), .width(5), .disabled("Z"), .enable("false")) multiplexer_2 (
    .in0(Rt_EX), .in1(Rd_EX), .out(multiplexer_2_out), .sel(RegDst_EX));
  Multiplexer #(.select(1), .width(5), .disabled("Z"), .enable("false")) multiplexer_3 (
    .in0(Rt_MEM), .in1(Rd_MEM), .out(multiplexer_3_out), .sel(RegDst_MEM));
  or or_1 (EX_CerJump, JMP_EX, \有条件分支 );
  Multiplexer #(.select(1), .width(32), .disabled("Z"), .enable("false")) multiplexer_4 (
    .in0(multiplexer_1_out), .in1(J), .out(multiplexer_4_out), .sel(\有条件分支 ));
  Multiplexer #(.select(1), .width(32), .disabled("Z"), .enable("false")) multiplexer_5 (
    .in0({EX_PC_4[31:28], EX_IR[25:0], 2'b00}), .in1(JR_address_EX), .out(multiplexer_5_out), .sel(JR_EX));
  Hex_Digit_Display hex_digit_display_2 (.value(LedData[27:24]));  // open: dp
  Hex_Digit_Display hex_digit_display_3 (.value(LedData[23:20]));  // open: dp
  Multiplexer #(.select(1), .width(5), .disabled("Z"), .enable("false")) multiplexer_6 (
    .in0(multiplexer_2_out), .in1({5{1'b1}}), .out(EX_WriteReg_num), .sel(JAL_EX));
  Multiplexer #(.select(1), .width(5), .disabled("Z"), .enable("false")) multiplexer_7 (
    .in0(multiplexer_3_out), .in1({5{1'b1}}), .out(MEM_WriteReg_num), .sel(JAL_MEM));
  Multiplexer #(.select(1), .width(32), .disabled("Z"), .enable("false")) multiplexer_8 (
    .in0(multiplexer_4_out), .in1(multiplexer_5_out), .out(NPC_R), .sel(JMP_EX));
  and and_1 (and_1_out, ~\数据相关 , \中止 );  // AND_Gate
  Hex_Digit_Display hex_digit_display_4 (.value(LedData[15:12]));  // open: dp
  Hex_Digit_Display hex_digit_display_5 (.value(LedData[19:16]));  // open: dp
  Register #(.width(32), .trigger("rising"), .Select("low")) PC (
    .D(ID_NPC), .en(and_1_out), .Q(IF_PC), .clk(CLK), .clr(RST));
  Hex_Digit_Display hex_digit_display_6 (.value(LedData[11:8]));  // open: dp
  Hex_Digit_Display hex_digit_display_7 (.value(LedData[7:4]));  // open: dp
  Clock #(.highDuration(1), .lowDuration(1)) clock_1 (.out(CLK));
  // Probe on IF_PC
  Adder #(.width(32)) adder_1 (.a(IF_PC), .b(32'h4), .out(PC_4));  // open: cin, cout
  Multiplexer #(.select(1), .width(2), .disabled("Z"), .enable("false")) multiplexer_9 (
    .in0(2'b10), .in1(2'b11), .out(multiplexer_9_out), .sel(\有条件分支 ));
  Hex_Digit_Display hex_digit_display_8 (.value(LedData[3:0]));  // open: dp
  or or_2 (Sync, \有条件分支 , JMP_EX);
  Shifter #(.width(32), .shift("ll")) shifter_1 (.in(IMM_EX), .\dist (5'b00010), .out(shifter_1_out));
  Adder #(.width(32)) adder_2 (.a(EX_PC), .b(32'h4), .out(EX_PC_4));  // open: cin, cout
  Adder #(.width(32)) adder_3 (.a(WB_PC), .b(32'h4), .out(WB_PC_4));  // open: cin, cout
  IF_ID if_id_1 (
    .IRin(IR), .IRout({IF_IR, Func}), .PCin(IF_PC), .PCout(ID_PC), .Sync(NewClear), .STALL(and_2_out),
    .CLK(CLK), .STALL_2(STALL_1), .RST(RST), .in_1({ID_Have, \ID_双位预测 }), .out_9(if_id_1_out_9),
    .in_2(ID_NPC), .out_10(if_id_1_out_10));
  ROM #(.addrWidth(10), .dataWidth(32), .Select("high")) rom_1 (.addr(IF_PC[11:2]), .data(IR));
  and and_2 (and_2_out, ~\数据相关 , \中止 );  // AND_Gate
  \双位预测状态机  \u_双位预测状态机_1  (.\初始预测位 (\EX_双位预测 ), .\实际跳转情况 (EX_CerJump), .\新的状态位 (\双位预测状态机_1_新的状态位 ));
  // Probe on \总周期数 
  // Probe on \无条件分支数 
  // Probe on \条件分支成功数 
  // Probe on \LoadUse次数 
  // Probe on \LoadUse次数 
  Multiplexer #(.select(1), .width(2), .disabled("Z"), .enable("false")) multiplexer_10 (
    .in0(multiplexer_9_out), .in1(\双位预测状态机_1_新的状态位 ), .out(multiplexer_10_out), .sel(EX_Have));
  // Probe on IF_PC[11:0]
  Adder #(.width(32)) adder_4 (.a(shifter_1_out), .b(EX_PC_4), .out(J));  // open: cin, cout
  // Probe on {IF_IR, Func}
  // Probe on ID_PC[11:0]
  // Probe on EX_PC[11:0]
  assign bit_extender_1_out = {{16{1'b0}}, {IF_IR[15:6], Func}};  // Bit_Extender bit_extender_1
  assign bit_extender_2_out = {{16{IF_IR[15]}}, {IF_IR[15:6], Func}};  // Bit_Extender bit_extender_2
  Multiplexer #(.select(1), .width(32), .disabled("Z"), .enable("false")) multiplexer_11 (
    .in0(NPC_R), .in1(EX_NPC), .out(multiplexer_11_out), .sel(EX_Have));
  // Probe on M_PC[11:0]
  // Probe on IF_IR[31:26]
  // Probe on Func
  // Probe on IF_IR[25:21]
  Multiplexer #(.select(1), .width(5), .disabled("Z"), .enable("false")) multiplexer_12 (
    .in0(mem_wb_1_rt), .in1(mem_wb_1_rd), .out(multiplexer_12_out), .sel(RegDst));
  // Probe on WB_PC[11:0]
  Multiplexer #(.select(1), .width(5), .disabled("Z"), .enable("false")) multiplexer_13 (
    .in0(IF_IR[25:21]), .in1(5'b00010), .out(R1__ID), .sel(Syscall));
  Multiplexer #(.select(1), .width(5), .disabled("Z"), .enable("false")) multiplexer_14 (
    .in0(IF_IR[20:16]), .in1(5'b00100), .out(R2__ID), .sel(Syscall));
  Multiplexer #(.select(1), .width(5), .disabled("Z"), .enable("false")) multiplexer_15 (
    .in0(multiplexer_12_out), .in1({5{1'b1}}), .out(multiplexer_15_out), .sel(JAL));
  Multiplexer #(.select(1), .width(32), .disabled("Z"), .enable("false")) multiplexer_16 (
    .in0(bit_extender_1_out), .in1(bit_extender_2_out), .out(multiplexer_16_out), .sel(SignedExt));
  BHT bht_1 (
    .EX_PC(EX_PC), .\分支目标地址 (multiplexer_11_out), .IF_PC(IF_PC), .\双预测位 (multiplexer_10_out),
    .BlkDataReady(EX_ProJump), .CLK(CLK), .Have(ID_Have), .\分支目标地址_2 (\bht_1_分支目标地址_2 ),
    .\双预测位输出 (\bht_1_双预测位输出 ));
  \源寄存器使用检测  \u_源寄存器使用检测_1  (
    .OP0(IF_IR[26]), .OP1(IF_IR[27]), .OP2(IF_IR[28]), .OP3(IF_IR[29]), .OP4(IF_IR[30]), .OP5(IF_IR[31]),
    .F0(Func[0]), .F1(Func[1]), .F2(Func[2]), .F3(Func[3]), .F4(Func[4]), .F5(Func[5]), .R1_Used(Used_1),
    .R2_Used(Used_2));
  \单周期硬布线控制器  \u_单周期硬布线控制器_1  (
    .Func(Func), .OP(IF_IR[31:26]), .ALU_OP(\单周期硬布线控制器_1_alu_op ), .MemToReg(\单周期硬布线控制器_1_memtoreg ),
    .MemWrite(\单周期硬布线控制器_1_memwrite ), .ALU_SRC(\单周期硬布线控制器_1_alu_src ), .RegWrite(\单周期硬布线控制器_1_regwrite ),
    .SysCALL(Syscall), .SignedExt(SignedExt), .RegDst(\单周期硬布线控制器_1_regdst ), .JR(JR), .JMP(JMP),
    .Beq(\单周期硬布线控制器_1_beq ), .JAL(\单周期硬布线控制器_1_jal ), .Bne(\单周期硬布线控制器_1_bne ), .SLLV(SLLV), .LH(LH),
    .XORI(XORI), .BGTZ(BGTZ));  // open: M, MFC0, MTC0, ERET
  // Probe on R1__ID
  Multiplexer #(.select(1), .width(2), .disabled("Z"), .enable("false")) multiplexer_17 (
    .in0(2'b00), .in1(\bht_1_双预测位输出 ), .out(\ID_双位预测 ), .sel(ID_Have));
  Multiplexer #(.select(2), .width(32), .disabled("Z"), .enable("false")) multiplexer_18 (
    .in0(PC_4), .in1(PC_4), .in2(\bht_1_分支目标地址_2 ), .in3(\bht_1_分支目标地址_2 ), .out(multiplexer_18_out),
    .sel(\bht_1_双预测位输出 ));
  or or_3 (or_3_out, \中止 , not_1_out);
  not not_1 (not_1_out, Syscall_WB);
  MIPS_Regifile mips_regifile_1 (
    .Din(RDin), .Clk(CLK), .R1(JR_address), .R2(mips_regifile_1_r2), .WE(RegWrite),
    .W_num(multiplexer_15_out), .R1_num(R1__ID), .R2_num(R2__ID));
  not not_2 (not_2_out, ID_Have);
  Multiplexer #(.select(1), .width(32), .disabled("Z"), .enable("false")) multiplexer_19 (
    .in0(multiplexer_18_out), .in1(PC_4), .out(multiplexer_19_out), .sel(not_2_out));
  Counter #(.width(16), .max('hffff), .ongoal("wrap"), .trigger("rising"), .behavior("old")) counter_1 (
    .count(or_3_out), .Q(\总周期数 ), .clk(CLK), .clr(RST));  // open: load, D, carry, preset
  Multiplexer #(.select(1), .width(32), .disabled("Z"), .enable("false")) multiplexer_20 (
    .in0(multiplexer_19_out), .in1(NPC_R), .out(ID_NPC), .sel(NewClear));
  xor xor_1 (NewClear, \EX_双位预测 [1], EX_CerJump);
  \重定向数据检测  \u_重定向数据检测_1  (
    .EX_LD(MemToReg_EX), .R1Used(Used_1), .R1_num(R1__ID), .R2_num(R2__ID), .EX_W_num(EX_WriteReg_num),
    .Mem_W_num(MEM_WriteReg_num), .EX_RegWrite(EX_WriteReg), .Mem_WriteReg(MEM_WriteReg), .R2Used(Used_2),
    .Bubble(\数据相关 ), .FowardA(\重定向数据检测_1_fowarda ), .FowardB(\重定向数据检测_1_fowardb ));
  // Probe on \重定向数据检测_1_fowarda 
  // Probe on \重定向数据检测_1_fowardb 
  Multiplexer #(.select(1), .width(5), .disabled("Z"), .enable("false")) multiplexer_21 (
    .in0(IF_IR[10:6]), .in1(JR_address[4:0]), .out(multiplexer_21_out), .sel(SLLV));
  Counter #(.width(16), .max('hffff), .ongoal("wrap"), .trigger("rising"), .behavior("old")) counter_2 (
    .count(JMP_EX), .Q(\无条件分支数 ), .clk(CLK), .clr(RST));  // open: load, D, carry, preset
  ID_EX id_ex_1 (
    .in_10(IF_IR[20:16]), .in_11(IF_IR[15:11]), .Beq(\单周期硬布线控制器_1_beq ), .Bne(\单周期硬布线控制器_1_bne ),
    .MenToReg(\单周期硬布线控制器_1_memtoreg ), .MenWrite(\单周期硬布线控制器_1_memwrite ), .AluOP(\单周期硬布线控制器_1_alu_op ),
    .AluSrcB(\单周期硬布线控制器_1_alu_src ), .RegWrite(\单周期硬布线控制器_1_regwrite ), .JAL(\单周期硬布线控制器_1_jal ),
    .RegDst(\单周期硬布线控制器_1_regdst ), .IR({IF_IR, Func}), .PC(ID_PC), .R1(JR_address), .R2(mips_regifile_1_r2),
    .IMM(multiplexer_16_out), .SHAME(multiplexer_21_out), .Rt(Rt_EX), .Rd(Rd_EX), .Beq_2(id_ex_1_beq_2),
    .Bne_2(id_ex_1_bne_2), .MenToReg_2(MemToReg_EX), .MenWrite_2(id_ex_1_menwrite_2),
    .AluOP_2(id_ex_1_aluop_2), .AluSrcB_2(id_ex_1_alusrcb_2), .RegWrite_2(EX_WriteReg), .JAL_2(JAL_EX),
    .RegDst_2(RegDst_EX), .IR_2(EX_IR), .PC_2(EX_PC), .R1_2(id_ex_1_r1_2), .R2_2(id_ex_1_r2_2),
    .IMM_2(IMM_EX), .SHAME_2(id_ex_1_shame_2), .Sync(or_4_out), .STALL(\中止 ), .CLK(CLK),
    .STALL_2(id_ex_1_stall_2), .RST(RST), .JR(JR), .JR_2(JR_EX), .JMP(JMP), .JMP_2(JMP_EX), .System(Syscall),
    .System_2(Syscall_EX), .LH(LH), .LH_2(id_ex_1_lh_2), .BGTZ(BGTZ), .BGTZ_2(BGTZ_EX),
    .A(\重定向数据检测_1_fowarda ), .A_2(FowardA), .B(\重定向数据检测_1_fowardb ), .B_2(FowardB), .in_1(if_id_1_out_9),
    .out_31({EX_Have, \EX_双位预测 }), .in_2(if_id_1_out_10), .out_32(EX_NPC));
  or or_4 (or_4_out, NewClear, \数据相关 );
  or or_5 (EX_ProJump, id_ex_1_beq_2, id_ex_1_bne_2, JAL_EX, JMP_EX, JR_EX, BGTZ_EX);
  Multiplexer #(.select(2), .width(32), .disabled("Z"), .enable("false")) multiplexer_22 (
    .in0(id_ex_1_r1_2), .in1(RDin), .in2(ex_mem_1_result_2), .in3(ex_mem_1_result_2), .out(JR_address_EX),
    .sel(FowardA));
  Multiplexer #(.select(2), .width(32), .disabled("Z"), .enable("false")) multiplexer_23 (
    .in0(id_ex_1_r2_2), .in1(RDin), .in2(ex_mem_1_result_2), .in3(ex_mem_1_result_2), .out(LED), .sel(FowardB));
  not not_3 (not_3_out, mips_alu_1_equal);
  Multiplexer #(.select(1), .width(32), .disabled("Z"), .enable("false")) multiplexer_24 (
    .in0(LED), .in1(IMM_EX), .out(multiplexer_24_out), .sel(id_ex_1_alusrcb_2));
  Counter #(.width(16), .max('hffff), .ongoal("wrap"), .trigger("rising"), .behavior("old")) counter_3 (
    .count(\有条件分支 ), .Q(\条件分支成功数 ), .clk(CLK), .clr(RST));  // open: load, D, carry, preset
  and and_3 (and_3_out, mips_alu_1_equal, id_ex_1_beq_2);
  and and_4 (and_4_out, not_3_out, id_ex_1_bne_2);
  MIPS_ALU mips_alu_1 (
    .X(JR_address_EX), .Y(multiplexer_24_out), .AluOP(id_ex_1_aluop_2), .Equal(mips_alu_1_equal),
    .Result(mips_alu_1_result), .shamt(id_ex_1_shame_2));  // open: Result_2
  Comparator #(.width(32), .mode("twosComplement")) comparator_1 (
    .a(JR_address_EX), .b({32{1'b0}}), .gt(comparator_1_gt));  // open: eq, lt
  or or_6 (\有条件分支 , and_3_out, JUMP, and_4_out);
  and and_5 (JUMP, BGTZ_EX, comparator_1_gt);
  Multiplexer #(.select(1), .width(32), .disabled("Z"), .enable("false")) multiplexer_25 (
    .in0(mips_alu_1_result), .in1(JR_address_EX), .out(multiplexer_25_out), .sel(Syscall_EX));
  and and_6 (and_6_out, \数据相关 , \中止 );
  EX_MEM ex_mem_1 (
    .in_3(Rt_EX), .in_4(Rd_EX), .MenToReg(MemToReg_EX), .MenWrite(id_ex_1_menwrite_2),
    .RegWrite(EX_WriteReg), .JAL(JAL_EX), .RegDst(RegDst_EX), .IR(EX_IR), .PC(EX_PC),
    .Result(multiplexer_25_out), .R2(LED), .Rt(Rt_MEM), .Rd(Rd_MEM), .MenToReg_2(ex_mem_1_mentoreg_2),
    .MenWrite_2(MemWrite), .RegWrite_2(MEM_WriteReg), .JAL_2(JAL_MEM), .RegDst_2(RegDst_MEM),
    .IR_2(ex_mem_1_ir_2), .PC_2(M_PC), .Result_2(ex_mem_1_result_2), .R2_2(MDin), .RST(RST),
    .STALL(id_ex_1_stall_2), .CLK(CLK), .STALL_2(ex_mem_1_stall_2), .System(Syscall_EX),
    .System_2(ex_mem_1_system_2), .LH(id_ex_1_lh_2), .LH_2(ex_mem_1_lh_2), .Sync(1'b0));
  Counter #(.width(16), .max('hffff), .ongoal("wrap"), .trigger("rising"), .behavior("old")) counter_4 (
    .count(and_6_out), .Q(\LoadUse次数 ), .clk(CLK), .clr(RST));  // open: load, D, carry, preset
  // Probe on ex_mem_1_result_2
  RAM #(.addrWidth(10), .dataWidth(32), .bus("separate"), .Select("high")) ram_1 (
    .addr(ex_mem_1_result_2[11:2]), .din(MDin), .data(ram_1_data), .str(MemWrite), .clk(CLK));  // open: sel, ld, clr
  Comparator #(.width(32), .mode("twosComplement")) comparator_2 (
    .a(JR_address_EX), .b(32'h22), .eq(comparator_2_eq));  // open: gt, lt
  Comparator #(.width(32), .mode("twosComplement")) comparator_3 (
    .a(v0), .b(32'h22), .eq(comparator_3_eq));  // open: gt, lt
  Multiplexer #(.select(1), .width(32), .disabled("Z"), .enable("false")) multiplexer_26 (
    .in0(ram_1_data), .in1(MDin), .out(multiplexer_26_out), .sel(ex_mem_1_system_2));
  not not_4 (not_4_out, comparator_3_eq);
  MEM_WB mem_wb_1 (
    .in_3(Rt_MEM), .in_4(Rd_MEM), .MenToReg(ex_mem_1_mentoreg_2), .RegWrite(MEM_WriteReg), .JAL(JAL_MEM),
    .RegDst(RegDst_MEM), .IR(ex_mem_1_ir_2), .PC(M_PC), .Result(ex_mem_1_result_2),
    .Mem_Res(multiplexer_26_out), .Rt(mem_wb_1_rt), .Rd(mem_wb_1_rd), .MenToReg_2(mem_wb_1_mentoreg_2),
    .RegWrite_2(RegWrite), .JAL_2(JAL), .RegDst_2(RegDst), .IR_2(WB_IR), .PC_2(WB_PC), .Result_2(v0),
    .Mem_Res_2(a0), .RST(RST), .STALL(ex_mem_1_stall_2), .CLK(CLK), .STALL_2(Stop),
    .System(ex_mem_1_system_2), .System_2(Syscall_WB), .LH(ex_mem_1_lh_2), .LH_2(LH_WB), .Sync(1'b0));
  and and_7 (and_7_out, comparator_2_eq, Syscall_EX);
  and and_8 (and_8_out, Syscall_WB, not_4_out);
  Register #(.width(32), .trigger("rising"), .Select("low")) register_1 (
    .D(LED), .en(and_7_out), .Q(LedData), .clk(CLK), .clr(RST));
  D_Flip_Flop #(.trigger("falling"), .Pre_Clr_Positions("LEGACY"), .NegatePresetClear("false"), .enable("true"), .NewFFLayout("false")) d_ff_1 (
    .clk(CLK), .D(and_8_out), .Q(d_ff_1_q), .reset(or_7_out));  // open: Qn, preset, en
  or or_7 (or_7_out, RST, Go);
  Multiplexer #(.select(1), .width(32), .disabled("Z"), .enable("false")) multiplexer_27 (
    .in0(v0), .in1(a0), .out(multiplexer_27_out), .sel(mem_wb_1_mentoreg_2));
  not not_5 (\中止 , d_ff_1_q);
  Multiplexer #(.select(1), .width(32), .disabled("Z"), .enable("false")) multiplexer_28 (
    .in0(multiplexer_27_out), .in1(WB_PC_4), .out(multiplexer_28_out), .sel(JAL));
  assign bit_extender_3_out = {{16{multiplexer_29_out[15]}}, multiplexer_29_out};  // Bit_Extender bit_extender_3
  Multiplexer #(.select(1), .width(16), .disabled("Z"), .enable("false")) multiplexer_29 (
    .in0(multiplexer_27_out[15:0]), .in1(multiplexer_27_out[31:16]), .out(multiplexer_29_out), .sel(v0[1]));
  Multiplexer #(.select(1), .width(32), .disabled("Z"), .enable("false")) multiplexer_30 (
    .in0(multiplexer_28_out), .in1(bit_extender_3_out), .out(RDin), .sel(LH_WB));

  // Other names for the same wires on the sheet: J_JAL[31:2] = {EX_PC_4[31:28], EX_IR[25:0]}; IF_IR[5:0] = Func;
  //   shamt[4:0] = IF_IR[10:6]; Rd[4:0] = IF_IR[15:11]; Rt[4:0] = IF_IR[20:16]; OP[5:0] = IF_IR[31:26];
  //   SLLV_1[4:0] = JR_address[4:0]; L[31:0] = JR_address_EX; MEM_PC[31:0] = M_PC; Next_PC_2[31:0] = EX_PC;
  //   PC[31:0] = IF_PC; 插入气泡数[15:0] = \LoadUse次数 

  // Notes on the sheet:
  //   中断源
  //   中断等待指示
  //   数码管输出
  //   指令存储器
  //   指令字
  //   contents of rom_1 (hex, n*v repeats v):
  //   20110001 8000c05 20110001 20120002 20130003 8000c09 20110001 20120002 20130003 8000c0d 20110001
  //   20120002 20130003 8000c11 20110001 20120002 20130003 c000cf8 20100001 20110001 118fc0 112020
  //   20020022 c 118882 12200001 8000c15 112020 20020022 c 20110001 118880 112020 20020022 c 12200001
  //   8000c1f 20110001 118fc0 112020 20020022 c 1188c3 112020 20020022 c 118903 112020 20020022 c 118903
  //   112020 20020022 c 118903 112020 20020022 c 118903 112020 20020022 c 118903 112020 20020022 c 118903
  //   112020 20020022 c 118903 112020 20020022 c 20100001 109fc0 139fc3 8021 2012000c 24160003 26100001
  //   3210000f 20080008 20090001 139900 2709825 132020 20020022 c 1094022 1500fff9 22100001 2018000f
  //   2188024 108700 20080008 20090001 139902 2709825 132021 20020022 c 1094022 1500fff9 108702 2c9b022
  //   12c00001 8000c50 4020 1084027 84400 3508ffff 82021 20020022 c 2010ffff 20110000 ae300000 22100001
  //   22310004 ae300000 22100001 22310004 ae300000 22100001 22310004 ae300000 22100001 22310004 ae300000
  //   22100001 22310004 ae300000 22100001 22310004 ae300000 22100001 22310004 ae300000 22100001 22310004
  //   ae300000 22100001 22310004 ae300000 22100001 22310004 ae300000 22100001 22310004 ae300000 22100001
  //   22310004 ae300000 22100001 22310004 ae300000 22100001 22310004 ae300000 22100001 22310004 ae300000
  //   22100001 22310004 22100001 8020 2011003c 8e130000 8e340000 274402a 11000002 ae330000 ae140000
  //   2231fffc 1611fff8 102020 20020022 c 22100004 2011003c 1611fff2 20020032 c 20080001 20090003 20110876
  //   112020 20020022 c 200b0008 1118804 1318804 112020 20020022 c 216bffff 1560fff9 2002000a c 2008ffff
  //   20117777 112020 20020022 c 200b0010 3a31ffff 112020 20020022 c 216bffff 1560fffa 2002000a c 20090000
  //   200b0010 34118483 20120404 118c00 129400 36318281 22520404 ad310000 2328820 21290004 216bffff
  //   1560fffb 200b0020 20090000 85310000 112020 20020022 c 21290002 216bffff 1560fff9 2002000a c 2011000f
  //   112020 20020022 c 2231ffff 1e20fffb 2002000a c 2002000a c 20100000 22100001 102020 20020022 c
  //   22100002 102020 20020022 c 22100003 102020 20020022 c 22100004 102020 20020022 c 22100005 102020
  //   20020022 c 22100006 102020 20020022 c 22100007 102020 20020022 c 22100008 102020 20020022 20020022 c
  //   3e00008
  //   OP
  //   Func
  //   rs
  //   rt
  //   rd
  //   流水调试日志用
  //   JMP
  //   JR
  //   OP
  //   Func
  //   Beq
  //   Bne
  //   MemToReg
  //   MemWrite
  //   AluOP
  //   AluSrcB
  //   RegWrite
  //   JAL
  //   RegDst
  //   Syscall
  //   避免取Cache的第一行双位预测
  //   预测情况与实际情况相反
  //   为方便自动评测，需要输出流水线各段保存的PC值，注意是PC不是PC+4，另外ID段寄存器写入信息，Mem段内存写入信息也要输出
endmodule

// 中断
module \中断按键参考电路  (
  input  CLK,
  input  \中断号 ,
  input  \同步清零信号 ,
  output \与中断屏蔽位与 ,
  output \中断等待指示灯 
);

  wire and_1_out, d_ff_1_q, or_2_out;

  or or_1 (\中断等待指示灯 , \与中断屏蔽位与 , d_ff_1_q);
  D_Flip_Flop #(.trigger("rising"), .Pre_Clr_Positions("LEGACY"), .NegatePresetClear("false"), .enable("true"), .NewFFLayout("false")) d_ff_1 (
    .clk(\中断号 ), .D(1'b1), .Q(d_ff_1_q), .reset(\与中断屏蔽位与 ));  // open: Qn, preset, en
  or or_2 (or_2_out, d_ff_1_q, \与中断屏蔽位与 );
  and and_1 (and_1_out, or_2_out, ~\同步清零信号 );  // AND_Gate
  D_Flip_Flop #(.trigger("rising"), .Pre_Clr_Positions("LEGACY"), .NegatePresetClear("false"), .enable("true"), .NewFFLayout("false")) IR1 (
    .clk(CLK), .D(and_1_out), .Q(\与中断屏蔽位与 ));  // open: Qn, preset, en, reset

  // Notes on the sheet:
  //   中断信号采样参考电路
  //   Reset 
endmodule

// 拓展指令信号
module \拓展指令信号  (
  input  OP0,
  input  OP1,
  input  OP2,
  input  OP3,
  input  OP4,
  input  OP5,
  input  F0,
  input  F1,
  input  F2,
  input  F3,
  input  F4,
  input  F5,
  output SLLV,
  output XORI,
  output LH,
  output BGTZ
);

  wire not_1_out, not_2_out, not_3_out, not_4_out, not_5_out, not_6_out, not_7_out, not_8_out, not_9_out,
       not_10_out, not_11_out, not_12_out, not_13_out, not_14_out, not_15_out, not_16_out, not_17_out,
       not_18_out, not_19_out, not_20_out, not_21_out;

  not not_1 (not_1_out, OP5);
  not not_2 (not_2_out, OP4);
  not not_3 (not_3_out, OP3);
  not not_4 (not_4_out, OP2);
  not not_5 (not_5_out, OP1);
  not not_6 (not_6_out, OP0);
  not not_7 (not_7_out, F5);
  not not_8 (not_8_out, F4);
  not not_9 (not_9_out, F3);
  not not_10 (not_10_out, F1);
  not not_11 (not_11_out, F0);
  not not_12 (not_12_out, OP5);
  not not_13 (not_13_out, OP4);
  not not_14 (not_14_out, OP0);
  not not_15 (not_15_out, OP4);
  not not_16 (not_16_out, OP3);
  not not_17 (not_17_out, OP2);
  not not_18 (not_18_out, OP1);
  not not_19 (not_19_out, OP5);
  not not_20 (not_20_out, OP4);
  not not_21 (not_21_out, OP3);
  and and_1 (SLLV, not_1_out, not_2_out, not_3_out, not_4_out, not_5_out, not_6_out, not_7_out, not_8_out, not_9_out, F2, not_10_out, not_11_out);
  and and_2 (XORI, not_12_out, not_13_out, OP3, OP2, OP1, not_14_out);
  and and_3 (LH, OP5, not_15_out, not_16_out, not_17_out, not_18_out, OP0);
  and and_4 (BGTZ, not_19_out, not_20_out, not_21_out, OP2, OP1, OP0);
endmodule

// 中断指令信号
module \中断指令信号  (
  input  OP0,
  input  OP1,
  input  OP2,
  input  OP3,
  input  OP4,
  input  OP5,
  input  F0,
  input  F1,
  input  F2,
  input  F3,
  input  F4,
  input  F5,
  input  M0,
  input  M1,
  input  M2,
  input  M3,
  input  M4,
  output MFC0,
  output MTC0,
  output ERET
);

  wire not_1_out, not_2_out, not_3_out, not_4_out, not_5_out, not_6_out, not_7_out, not_8_out, not_9_out,
       not_10_out, not_11_out, not_12_out, not_13_out, not_14_out, not_15_out, not_16_out, not_17_out,
       not_18_out, not_19_out, not_20_out, not_21_out, not_22_out, not_23_out, not_24_out, not_25_out,
       not_26_out, not_27_out, not_28_out;

  not not_1 (not_1_out, OP0);
  not not_2 (not_2_out, OP1);
  not not_3 (not_3_out, OP2);
  not not_4 (not_4_out, OP3);
  not not_5 (not_5_out, OP5);
  not not_6 (not_6_out, M0);
  not not_7 (not_7_out, M1);
  not not_8 (not_8_out, M2);
  not not_9 (not_9_out, M3);
  not not_10 (not_10_out, M4);
  not not_11 (not_11_out, OP0);
  not not_12 (not_12_out, OP1);
  not not_13 (not_13_out, OP2);
  not not_14 (not_14_out, OP3);
  not not_15 (not_15_out, OP5);
  not not_16 (not_16_out, M0);
  not not_17 (not_17_out, M1);
  not not_18 (not_18_out, M3);
  not not_19 (not_19_out, M4);
  not not_20 (not_20_out, OP0);
  not not_21 (not_21_out, OP1);
  not not_22 (not_22_out, OP2);
  not not_23 (not_23_out, OP3);
  not not_24 (not_24_out, OP5);
  not not_25 (not_25_out, F0);
  not not_26 (not_26_out, F1);
  not not_27 (not_27_out, F2);
  not not_28 (not_28_out, F5);
  and and_1 (MFC0, not_1_out, not_2_out, not_3_out, not_4_out, OP4, not_5_out, not_6_out, not_7_out, not_8_out, not_9_out, not_10_out);
  and and_2 (MTC0, not_11_out, not_12_out, not_13_out, not_14_out, OP4, not_15_out, not_16_out, not_17_out, M2, not_18_out, not_19_out);
  and and_3 (ERET, not_20_out, not_21_out, not_22_out, not_23_out, OP4, not_24_out, not_25_out, not_26_out, not_27_out, F3, F4, not_28_out, M4);
endmodule

module IF_ID (
  input  [2:0] in_1,
  input  [31:0] in_2,
  input  [31:0] IRin,
  input  [31:0] PCin,
  input  Sync,
  input  STALL,
  input  CLK,
  input  RST,
  output [2:0] out_9,
  output [31:0] out_10,
  output [31:0] IRout,
  output [31:0] PCout,
  output STALL_2
);

  wire [2:0] multiplexer_1_out;
  wire [31:0] multiplexer_2_out, multiplexer_3_out, multiplexer_4_out;

  Multiplexer #(.select(1), .width(3), .disabled("Z"), .enable("false")) multiplexer_1 (
    .in0(in_1), .in1(3'b000), .out(multiplexer_1_out), .sel(Sync));
  Multiplexer #(.select(1), .width(32), .disabled("Z"), .enable("false")) multiplexer_2 (
    .in0(in_2), .in1({32{1'b0}}), .out(multiplexer_2_out), .sel(Sync));
  Multiplexer #(.select(1), .width(32), .disabled("Z"), .enable("false")) multiplexer_3 (
    .in0(IRin), .in1({32{1'b0}}), .out(multiplexer_3_out), .sel(Sync));
  Multiplexer #(.select(1), .width(32), .disabled("Z"), .enable("false")) multiplexer_4 (
    .in0(PCin), .in1({32{1'b0}}), .out(multiplexer_4_out), .sel(Sync));
  Register #(.width(3), .trigger("rising"), .Select("low")) register_1 (
    .D(multiplexer_1_out), .en(STALL), .Q(out_9), .clk(CLK), .clr(RST));
  Register #(.width(32), .trigger("rising"), .Select("low")) register_2 (
    .D(multiplexer_2_out), .en(STALL), .Q(out_10), .clk(CLK), .clr(RST));
  Register #(.width(32), .trigger("rising"), .Select("low")) IR (
    .D(multiplexer_3_out), .en(STALL), .Q(IRout), .clk(CLK), .clr(RST));
  Register #(.width(32), .trigger("rising"), .Select("low")) PC (
    .D(multiplexer_4_out), .en(STALL), .Q(PCout), .clk(CLK), .clr(RST));

  assign STALL_2 = STALL;
endmodule
module ID_EX (
  input  [2:0] in_1,
  input  [31:0] in_2,
  input  [1:0] A,
  input  [1:0] B,
  input  LH,
  input  BGTZ,
  input  System,
  input  JMP,
  input  JR,
  input  [4:0] in_10,
  input  [4:0] in_11,
  input  Beq,
  input  Bne,
  input  MenToReg,
  input  MenWrite,
  input  [3:0] AluOP,
  input  AluSrcB,
  input  RegWrite,
  input  JAL,
  input  RegDst,
  input  [31:0] IR,
  input  [31:0] PC,
  input  [31:0] R1,
  input  [31:0] R2,
  input  [31:0] IMM,
  input  [4:0] SHAME,
  input  Sync,
  input  RST,
  input  STALL,
  input  CLK,
  output [2:0] out_31,
  output [31:0] out_32,
  output [1:0] A_2,
  output [1:0] B_2,
  output LH_2,
  output BGTZ_2,
  output System_2,
  output JMP_2,
  output JR_2,
  output [4:0] Rt,
  output [4:0] Rd,
  output Beq_2,
  output Bne_2,
  output MenToReg_2,
  output MenWrite_2,
  output [3:0] AluOP_2,
  output AluSrcB_2,
  output RegWrite_2,
  output JAL_2,
  output RegDst_2,
  output [31:0] IR_2,
  output [31:0] PC_2,
  output [31:0] R1_2,
  output [31:0] R2_2,
  output [31:0] IMM_2,
  output [4:0] SHAME_2,
  output STALL_2
);

  wire multiplexer_5_out, multiplexer_6_out, multiplexer_7_out, multiplexer_8_out, multiplexer_9_out,
       multiplexer_12_out, multiplexer_13_out, multiplexer_14_out, multiplexer_15_out, multiplexer_17_out,
       multiplexer_18_out, multiplexer_19_out, multiplexer_20_out;
  wire [1:0] multiplexer_3_out, multiplexer_4_out;
  wire [2:0] multiplexer_1_out;
  wire [3:0] multiplexer_16_out;
  wire [4:0] multiplexer_10_out, multiplexer_11_out, multiplexer_26_out;
  wire [31:0] multiplexer_2_out, multiplexer_21_out, multiplexer_22_out, multiplexer_23_out,
       multiplexer_24_out, multiplexer_25_out;

  Multiplexer #(.select(1), .width(3), .disabled("Z"), .enable("false")) multiplexer_1 (
    .in0(in_1), .in1(3'b000), .out(multiplexer_1_out), .sel(Sync));
  Multiplexer #(.select(1), .width(32), .disabled("Z"), .enable("false")) multiplexer_2 (
    .in0(in_2), .in1({32{1'b0}}), .out(multiplexer_2_out), .sel(Sync));
  Multiplexer #(.select(1), .width(2), .disabled("Z"), .enable("false")) multiplexer_3 (
    .in0(A), .in1(2'b00), .out(multiplexer_3_out), .sel(Sync));
  Multiplexer #(.select(1), .width(2), .disabled("Z"), .enable("false")) multiplexer_4 (
    .in0(B), .in1(2'b00), .out(multiplexer_4_out), .sel(Sync));
  Multiplexer #(.select(1), .width(1), .disabled("Z"), .enable("false")) multiplexer_5 (
    .in0(LH), .in1(1'b0), .out(multiplexer_5_out), .sel(Sync));
  Multiplexer #(.select(1), .width(1), .disabled("Z"), .enable("false")) multiplexer_6 (
    .in0(BGTZ), .in1(1'b0), .out(multiplexer_6_out), .sel(Sync));
  Multiplexer #(.select(1), .width(1), .disabled("Z"), .enable("false")) multiplexer_7 (
    .in0(System), .in1(1'b0), .out(multiplexer_7_out), .sel(Sync));
  Multiplexer #(.select(1), .width(1), .disabled("Z"), .enable("false")) multiplexer_8 (
    .in0(JMP), .in1(1'b0), .out(multiplexer_8_out), .sel(Sync));
  Multiplexer #(.select(1), .width(1), .disabled("Z"), .enable("false")) multiplexer_9 (
    .in0(JR), .in1(1'b0), .out(multiplexer_9_out), .sel(Sync));
  Multiplexer #(.select(1), .width(5), .disabled("Z"), .enable("false")) multiplexer_10 (
    .in0(in_10), .in1({5{1'b0}}), .out(multiplexer_10_out), .sel(Sync));
  Multiplexer #(.select(1), .width(5), .disabled("Z"), .enable("false")) multiplexer_11 (
    .in0(in_11), .in1({5{1'b0}}), .out(multiplexer_11_out), .sel(Sync));
  Multiplexer #(.select(1), .width(1), .disabled("Z"), .enable("false")) multiplexer_12 (
    .in0(Beq), .in1(1'b0), .out(multiplexer_12_out), .sel(Sync));
  Multiplexer #(.select(1), .width(1), .disabled("Z"), .enable("false")) multiplexer_13 (
    .in0(Bne), .in1(1'b0), .out(multiplexer_13_out), .sel(Sync));
  Multiplexer #(.select(1), .width(1), .disabled("Z"), .enable("false")) multiplexer_14 (
    .in0(MenToReg), .in1(1'b0), .out(multiplexer_14_out), .sel(Sync));
  Multiplexer #(.select(1), .width(1), .disabled("Z"), .enable("false")) multiplexer_15 (
    .in0(MenWrite), .in1(1'b0), .out(multiplexer_15_out), .sel(Sync));
  Multiplexer #(.select(1), .width(4), .disabled("Z"), .enable("false")) multiplexer_16 (
    .in0(AluOP), .in1(4'b0000), .out(multiplexer_16_out), .sel(Sync));
  Multiplexer #(.select(1), .width(1), .disabled("Z"), .enable("false")) multiplexer_17 (
    .in0(AluSrcB), .in1(1'b0), .out(multiplexer_17_out), .sel(Sync));
  Multiplexer #(.select(1), .width(1), .disabled("Z"), .enable("false")) multiplexer_18 (
    .in0(RegWrite), .in1(1'b0), .out(multiplexer_18_out), .sel(Sync));
  Multiplexer #(.select(1), .width(1), .disabled("Z"), .enable("false")) multiplexer_19 (
    .in0(JAL), .in1(1'b0), .out(multiplexer_19_out), .sel(Sync));
  Multiplexer #(.select(1), .width(1), .disabled("Z"), .enable("false")) multiplexer_20 (
    .in0(RegDst), .in1(1'b0), .out(multiplexer_20_out), .sel(Sync));
  Multiplexer #(.select(1), .width(32), .disabled("Z"), .enable("false")) multiplexer_21 (
    .in0(IR), .in1({32{1'b0}}), .out(multiplexer_21_out), .sel(Sync));
  Multiplexer #(.select(1), .width(32), .disabled("Z"), .enable("false")) multiplexer_22 (
    .in0(PC), .in1({32{1'b0}}), .out(multiplexer_22_out), .sel(Sync));
  Multiplexer #(.select(1), .width(32), .disabled("Z"), .enable("false")) multiplexer_23 (
    .in0(R1), .in1({32{1'b0}}), .out(multiplexer_23_out), .sel(Sync));
  Multiplexer #(.select(1), .width(32), .disabled("Z"), .enable("false")) multiplexer_24 (
    .in0(R2), .in1({32{1'b0}}), .out(multiplexer_24_out), .sel(Sync));
  Multiplexer #(.select(1), .width(32), .disabled("Z"), .enable("false")) multiplexer_25 (
    .in0(IMM), .in1({32{1'b0}}), .out(multiplexer_25_out), .sel(Sync));
  Multiplexer #(.select(1), .width(5), .disabled("Z"), .enable("false")) multiplexer_26 (
    .in0(SHAME), .out(multiplexer_26_out), .sel(Sync));  // open: in1
  Register #(.width(3), .trigger("rising"), .Select("low")) register_1 (
    .D(multiplexer_1_out), .en(STALL), .Q(out_31), .clk(CLK), .clr(RST));
  Register #(.width(32), .trigger("rising"), .Select("low")) register_2 (
    .D(multiplexer_2_out), .en(STALL), .Q(out_32), .clk(CLK), .clr(RST));
  Register #(.width(2), .trigger("rising"), .Select("low")) u_A (
    .D(multiplexer_3_out), .en(STALL), .Q(A_2), .clk(CLK), .clr(RST));
  Register #(.width(2), .trigger("rising"), .Select("low")) u_B (
    .D(multiplexer_4_out), .en(STALL), .Q(B_2), .clk(CLK), .clr(RST));
  Register #(.width(1), .trigger("rising"), .Select("low")) u_LH (
    .D(multiplexer_5_out), .en(STALL), .Q(LH_2), .clk(CLK), .clr(RST));
  Register #(.width(1), .trigger("rising"), .Select("low")) u_BGTZ (
    .D(multiplexer_6_out), .en(STALL), .Q(BGTZ_2), .clk(CLK), .clr(RST));
  Register #(.width(1), .trigger("rising"), .Select("low")) u_System (
    .D(multiplexer_7_out), .en(STALL), .Q(System_2), .clk(CLK), .clr(RST));
  Register #(.width(1), .trigger("rising"), .Select("low")) u_JMP (
    .D(multiplexer_8_out), .en(STALL), .Q(JMP_2), .clk(CLK), .clr(RST));
  Register #(.width(1), .trigger("rising"), .Select("low")) u_JR (
    .D(multiplexer_9_out), .en(STALL), .Q(JR_2), .clk(CLK), .clr(RST));
  Register #(.width(5), .trigger("rising"), .Select("low")) u_Rt (
    .D(multiplexer_10_out), .en(STALL), .Q(Rt), .clk(CLK), .clr(RST));
  Register #(.width(5), .trigger("rising"), .Select("low")) u_Rd (
    .D(multiplexer_11_out), .en(STALL), .Q(Rd), .clk(CLK), .clr(RST));
  Register #(.width(1), .trigger("rising"), .Select("low")) u_Beq (
    .D(multiplexer_12_out), .en(STALL), .Q(Beq_2), .clk(CLK), .clr(RST));
  Register #(.width(1), .trigger("rising"), .Select("low")) u_Bne (
    .D(multiplexer_13_out), .en(STALL), .Q(Bne_2), .clk(CLK), .clr(RST));
  Register #(.width(1), .trigger("rising"), .Select("low")) u_MenToReg (
    .D(multiplexer_14_out), .en(STALL), .Q(MenToReg_2), .clk(CLK), .clr(RST));
  Register #(.width(1), .trigger("rising"), .Select("low")) u_MenWrite (
    .D(multiplexer_15_out), .en(STALL), .Q(MenWrite_2), .clk(CLK), .clr(RST));
  Register #(.width(4), .trigger("rising"), .Select("low")) u_AluOP (
    .D(multiplexer_16_out), .en(STALL), .Q(AluOP_2), .clk(CLK), .clr(RST));
  Register #(.width(1), .trigger("rising"), .Select("low")) u_AluSrcB (
    .D(multiplexer_17_out), .en(STALL), .Q(AluSrcB_2), .clk(CLK), .clr(RST));
  Register #(.width(1), .trigger("rising"), .Select("low")) u_RegWrite (
    .D(multiplexer_18_out), .en(STALL), .Q(RegWrite_2), .clk(CLK), .clr(RST));
  Register #(.width(1), .trigger("rising"), .Select("low")) u_JAL (
    .D(multiplexer_19_out), .en(STALL), .Q(JAL_2), .clk(CLK), .clr(RST));
  Register #(.width(1), .trigger("rising"), .Select("low")) u_RegDst (
    .D(multiplexer_20_out), .en(STALL), .Q(RegDst_2), .clk(CLK), .clr(RST));
  Register #(.width(32), .trigger("rising"), .Select("low")) u_IR (
    .D(multiplexer_21_out), .en(STALL), .Q(IR_2), .clk(CLK), .clr(RST));
  Register #(.width(32), .trigger("rising"), .Select("low")) u_PC (
    .D(multiplexer_22_out), .en(STALL), .Q(PC_2), .clk(CLK), .clr(RST));
  Register #(.width(32), .trigger("rising"), .Select("low")) u_R1 (
    .D(multiplexer_23_out), .en(STALL), .Q(R1_2), .clk(CLK), .clr(RST));
  Register #(.width(32), .trigger("rising"), .Select("low")) u_R2 (
    .D(multiplexer_24_out), .en(STALL), .Q(R2_2), .clk(CLK), .clr(RST));
  Register #(.width(32), .trigger("rising"), .Select("low")) u_IMM (
    .D(multiplexer_25_out), .en(STALL), .Q(IMM_2), .clk(CLK), .clr(RST));
  Register #(.width(5), .trigger("rising"), .Select("low")) u_SHAME (
    .D(multiplexer_26_out), .en(STALL), .Q(SHAME_2), .clk(CLK), .clr(RST));

  assign STALL_2 = STALL;
endmodule

module EX_MEM (
  input  LH,
  input  System,
  input  [4:0] in_3,
  input  [4:0] in_4,
  input  MenToReg,
  input  MenWrite,
  input  RegWrite,
  input  JAL,
  input  RegDst,
  input  [31:0] IR,
  input  [31:0] PC,
  input  [31:0] Result,
  input  [31:0] R2,
  input  Sync,
  input  RST,
  input  STALL,
  input  CLK,
  output LH_2,
  output System_2,
  output [4:0] Rt,
  output [4:0] Rd,
  output MenToReg_2,
  output MenWrite_2,
  output RegWrite_2,
  output JAL_2,
  output RegDst_2,
  output [31:0] IR_2,
  output [31:0] PC_2,
  output [31:0] Result_2,
  output [31:0] R2_2,
  output STALL_2
);

  wire multiplexer_1_out, multiplexer_2_out, multiplexer_5_out, multiplexer_6_out, multiplexer_7_out,
       multiplexer_8_out, multiplexer_9_out;
  wire [4:0] multiplexer_3_out, multiplexer_4_out;
  wire [31:0] multiplexer_10_out, multiplexer_11_out, multiplexer_12_out, multiplexer_13_out;

  Multiplexer #(.select(1), .width(1), .disabled("Z"), .enable("false")) multiplexer_1 (
    .in0(LH), .in1(1'b0), .out(multiplexer_1_out), .sel(Sync));
  Multiplexer #(.select(1), .width(1), .disabled("Z"), .enable("false")) multiplexer_2 (
    .in0(System), .in1(1'b0), .out(multiplexer_2_out), .sel(Sync));
  Multiplexer #(.select(1), .width(5), .disabled("Z"), .enable("false")) multiplexer_3 (
    .in0(in_3), .in1({5{1'b0}}), .out(multiplexer_3_out), .sel(Sync));
  Multiplexer #(.select(1), .width(5), .disabled("Z"), .enable("false")) multiplexer_4 (
    .in0(in_4), .in1({5{1'b0}}), .out(multiplexer_4_out), .sel(Sync));
  Multiplexer #(.select(1), .width(1), .disabled("Z"), .enable("false")) multiplexer_5 (
    .in0(MenToReg), .in1(1'b0), .out(multiplexer_5_out), .sel(Sync));
  Multiplexer #(.select(1), .width(1), .disabled("Z"), .enable("false")) multiplexer_6 (
    .in0(MenWrite), .in1(1'b0), .out(multiplexer_6_out), .sel(Sync));
  Multiplexer #(.select(1), .width(1), .disabled("Z"), .enable("false")) multiplexer_7 (
    .in0(RegWrite), .in1(1'b0), .out(multiplexer_7_out), .sel(Sync));
  Multiplexer #(.select(1), .width(1), .disabled("Z"), .enable("false")) multiplexer_8 (
    .in0(JAL), .in1(1'b0), .out(multiplexer_8_out), .sel(Sync));
  Multiplexer #(.select(1), .width(1), .disabled("Z"), .enable("false")) multiplexer_9 (
    .in0(RegDst), .in1(1'b0), .out(multiplexer_9_out), .sel(Sync));
  Multiplexer #(.select(1), .width(32), .disabled("Z"), .enable("false")) multiplexer_10 (
    .in0(IR), .in1({32{1'b0}}), .out(multiplexer_10_out), .sel(Sync));
  Multiplexer #(.select(1), .width(32), .disabled("Z"), .enable("false")) multiplexer_11 (
    .in0(PC), .in1({32{1'b0}}), .out(multiplexer_11_out), .sel(Sync));
  Multiplexer #(.select(1), .width(32), .disabled("Z"), .enable("false")) multiplexer_12 (
    .in0(Result), .in1({32{1'b0}}), .out(multiplexer_12_out), .sel(Sync));
  Multiplexer #(.select(1), .width(32), .disabled("Z"), .enable("false")) multiplexer_13 (
    .in0(R2), .in1({32{1'b0}}), .out(multiplexer_13_out), .sel(Sync));
  Register #(.width(1), .trigger("rising"), .Select("low")) u_LH (
    .D(multiplexer_1_out), .en(STALL), .Q(LH_2), .clk(CLK), .clr(RST));
  Register #(.width(1), .trigger("rising"), .Select("low")) u_System (
    .D(multiplexer_2_out), .en(STALL), .Q(System_2), .clk(CLK), .clr(RST));
  Register #(.width(5), .trigger("rising"), .Select("low")) u_Rt (
    .D(multiplexer_3_out), .en(STALL), .Q(Rt), .clk(CLK), .clr(RST));
  Register #(.width(5), .trigger("rising"), .Select("low")) u_Rd (
    .D(multiplexer_4_out), .en(STALL), .Q(Rd), .clk(CLK), .clr(RST));
  Register #(.width(1), .trigger("rising"), .Select("low")) u_MenToReg (
    .D(multiplexer_5_out), .en(STALL), .Q(MenToReg_2), .clk(CLK), .clr(RST));
  Register #(.width(1), .trigger("rising"), .Select("low")) u_MenWrite (
    .D(multiplexer_6_out), .en(STALL), .Q(MenWrite_2), .clk(CLK), .clr(RST));
  Register #(.width(1), .trigger("rising"), .Select("low")) u_RegWrite (
    .D(multiplexer_7_out), .en(STALL), .Q(RegWrite_2), .clk(CLK), .clr(RST));
  Register #(.width(1), .trigger("rising"), .Select("low")) u_JAL (
    .D(multiplexer_8_out), .en(STALL), .Q(JAL_2), .clk(CLK), .clr(RST));
  Register #(.width(1), .trigger("rising"), .Select("low")) u_RegDst (
    .D(multiplexer_9_out), .en(STALL), .Q(RegDst_2), .clk(CLK), .clr(RST));
  Register #(.width(32), .trigger("rising"), .Select("low")) u_IR (
    .D(multiplexer_10_out), .en(STALL), .Q(IR_2), .clk(CLK), .clr(RST));
  Register #(.width(32), .trigger("rising"), .Select("low")) u_PC (
    .D(multiplexer_11_out), .en(STALL), .Q(PC_2), .clk(CLK), .clr(RST));
  Register #(.width(32), .trigger("rising"), .Select("low")) u_Result (
    .D(multiplexer_12_out), .en(STALL), .Q(Result_2), .clk(CLK), .clr(RST));
  Register #(.width(32), .trigger("rising"), .Select("low")) u_R2 (
    .D(multiplexer_13_out), .en(STALL), .Q(R2_2), .clk(CLK), .clr(RST));

  assign STALL_2 = STALL;
endmodule

module MEM_WB (
  input  LH,
  input  System,
  input  [4:0] in_3,
  input  [4:0] in_4,
  input  MenToReg,
  input  RegWrite,
  input  JAL,
  input  RegDst,
  input  [31:0] IR,
  input  [31:0] PC,
  input  [31:0] Result,
  input  [31:0] Mem_Res,
  input  Sync,
  input  RST,
  input  STALL,
  input  CLK,
  output LH_2,
  output System_2,
  output [4:0] Rt,
  output [4:0] Rd,
  output MenToReg_2,
  output RegWrite_2,
  output JAL_2,
  output RegDst_2,
  output [31:0] IR_2,
  output [31:0] PC_2,
  output [31:0] Result_2,
  output [31:0] Mem_Res_2,
  output STALL_2
);

  wire multiplexer_1_out, multiplexer_2_out, multiplexer_5_out, multiplexer_6_out, multiplexer_7_out,
       multiplexer_8_out;
  wire [4:0] multiplexer_3_out, multiplexer_4_out;
  wire [31:0] multiplexer_9_out, multiplexer_10_out, multiplexer_11_out, multiplexer_12_out;

  Multiplexer #(.select(1), .width(1), .disabled("Z"), .enable("false")) multiplexer_1 (
    .in0(LH), .in1(1'b0), .out(multiplexer_1_out), .sel(Sync));
  Multiplexer #(.select(1), .width(1), .disabled("Z"), .enable("false")) multiplexer_2 (
    .in0(System), .in1(1'b0), .out(multiplexer_2_out), .sel(Sync));
  Multiplexer #(.select(1), .width(5), .disabled("Z"), .enable("false")) multiplexer_3 (
    .in0(in_3), .in1({5{1'b0}}), .out(multiplexer_3_out), .sel(Sync));
  Multiplexer #(.select(1), .width(5), .disabled("Z"), .enable("false")) multiplexer_4 (
    .in0(in_4), .in1({5{1'b0}}), .out(multiplexer_4_out), .sel(Sync));
  Multiplexer #(.select(1), .width(1), .disabled("Z"), .enable("false")) multiplexer_5 (
    .in0(MenToReg), .in1(1'b0), .out(multiplexer_5_out), .sel(Sync));
  Multiplexer #(.select(1), .width(1), .disabled("Z"), .enable("false")) multiplexer_6 (
    .in0(RegWrite), .in1(1'b0), .out(multiplexer_6_out), .sel(Sync));
  Multiplexer #(.select(1), .width(1), .disabled("Z"), .enable("false")) multiplexer_7 (
    .in0(JAL), .in1(1'b0), .out(multiplexer_7_out), .sel(Sync));
  Multiplexer #(.select(1), .width(1), .disabled("Z"), .enable("false")) multiplexer_8 (
    .in0(RegDst), .in1(1'b0), .out(multiplexer_8_out), .sel(Sync));
  Multiplexer #(.select(1), .width(32), .disabled("Z"), .enable("false")) multiplexer_9 (
    .in0(IR), .in1({32{1'b0}}), .out(multiplexer_9_out), .sel(Sync));
  Multiplexer #(.select(1), .width(32), .disabled("Z"), .enable("false")) multiplexer_10 (
    .in0(PC), .in1({32{1'b0}}), .out(multiplexer_10_out), .sel(Sync));
  Multiplexer #(.select(1), .width(32), .disabled("Z"), .enable("false")) multiplexer_11 (
    .in0(Result), .in1({32{1'b0}}), .out(multiplexer_11_out), .sel(Sync));
  Multiplexer #(.select(1), .width(32), .disabled("Z"), .enable("false")) multiplexer_12 (
    .in0(Mem_Res), .in1({32{1'b0}}), .out(multiplexer_12_out), .sel(Sync));
  Register #(.width(1), .trigger("rising"), .Select("low")) u_LH (
    .D(multiplexer_1_out), .en(STALL), .Q(LH_2), .clk(CLK), .clr(RST));
  Register #(.width(1), .trigger("rising"), .Select("low")) u_System (
    .D(multiplexer_2_out), .en(STALL), .Q(System_2), .clk(CLK), .clr(RST));
  Register #(.width(5), .trigger("rising"), .Select("low")) u_Rt (
    .D(multiplexer_3_out), .en(STALL), .Q(Rt), .clk(CLK), .clr(RST));
  Register #(.width(5), .trigger("rising"), .Select("low")) u_Rd (
    .D(multiplexer_4_out), .en(STALL), .Q(Rd), .clk(CLK), .clr(RST));
  Register #(.width(1), .trigger("rising"), .Select("low")) u_MenToReg (
    .D(multiplexer_5_out), .en(STALL), .Q(MenToReg_2), .clk(CLK), .clr(RST));
  Register #(.width(1), .trigger("rising"), .Select("low")) u_RegWrite (
    .D(multiplexer_6_out), .en(STALL), .Q(RegWrite_2), .clk(CLK), .clr(RST));
  Register #(.width(1), .trigger("rising"), .Select("low")) u_JAL (
    .D(multiplexer_7_out), .en(STALL), .Q(JAL_2), .clk(CLK), .clr(RST));
  Register #(.width(1), .trigger("rising"), .Select("low")) u_RegDst (
    .D(multiplexer_8_out), .en(STALL), .Q(RegDst_2), .clk(CLK), .clr(RST));
  Register #(.width(32), .trigger("rising"), .Select("low")) u_IR (
    .D(multiplexer_9_out), .en(STALL), .Q(IR_2), .clk(CLK), .clr(RST));
  Register #(.width(32), .trigger("rising"), .Select("low")) u_PC (
    .D(multiplexer_10_out), .en(STALL), .Q(PC_2), .clk(CLK), .clr(RST));
  Register #(.width(32), .trigger("rising"), .Select("low")) u_Result (
    .D(multiplexer_11_out), .en(STALL), .Q(Result_2), .clk(CLK), .clr(RST));
  Register #(.width(32), .trigger("rising"), .Select("low")) u_Mem_Res (
    .D(multiplexer_12_out), .en(STALL), .Q(Mem_Res_2), .clk(CLK), .clr(RST));

  assign STALL_2 = STALL;
endmodule

module \数据相关检测  (
  input  [5:0] OP,
  input  [5:0] Func,
  input  [4:0] ID_R1_num,
  input  MEM_RegWrite,
  input  [4:0] MEM_WriteReg_num,
  input  [4:0] EX_WriteReg_num,
  input  EX_RegWrite,
  input  [4:0] ID_R2_num,
  output \数据相关 
);

  wire and_1_out, and_2_out, and_3_out, and_4_out, and_5_out, and_6_out, and_7_out, and_8_out,
       comparator_1_eq, comparator_2_eq, comparator_3_eq, comparator_4_eq, comparator_5_eq, comparator_6_eq,
       not_1_out, not_2_out, or_1_out, or_2_out, R1_Used, R2_Used;

  \源寄存器使用检测  \u_源寄存器使用检测_1  (
    .OP0(OP[0]), .OP1(OP[1]), .OP2(OP[2]), .OP3(OP[3]), .OP4(OP[4]), .OP5(OP[5]), .F0(Func[0]), .F1(Func[1]),
    .F2(Func[2]), .F3(Func[3]), .F4(Func[4]), .F5(Func[5]), .R1_Used(R1_Used), .R2_Used(R2_Used));
  Comparator #(.width(5), .mode("twosComplement")) comparator_1 (
    .a(ID_R1_num), .b(MEM_WriteReg_num), .eq(comparator_1_eq));  // open: gt, lt
  Comparator #(.width(5), .mode("twosComplement")) comparator_2 (
    .a(ID_R1_num), .b(EX_WriteReg_num), .eq(comparator_2_eq));  // open: gt, lt
  Comparator #(.width(5), .mode("twosComplement")) comparator_3 (
    .a(ID_R2_num), .b(MEM_WriteReg_num), .eq(comparator_3_eq));  // open: gt, lt
  Comparator #(.width(5), .mode("twosComplement")) comparator_4 (
    .a(ID_R2_num), .b(EX_WriteReg_num), .eq(comparator_4_eq));  // open: gt, lt
  and and_1 (and_1_out, MEM_RegWrite, comparator_1_eq);
  and and_2 (and_2_out, comparator_2_eq, EX_RegWrite);
  and and_3 (and_3_out, MEM_RegWrite, comparator_3_eq);
  and and_4 (and_4_out, comparator_4_eq, EX_RegWrite);
  Comparator #(.width(5), .mode("twosComplement")) comparator_5 (
    .a(ID_R1_num), .b({5{1'b0}}), .eq(comparator_5_eq));  // open: gt, lt
  not not_1 (not_1_out, comparator_5_eq);
  or or_1 (or_1_out, and_1_out, and_2_out);
  not not_2 (not_2_out, comparator_6_eq);
  Comparator #(.width(5), .mode("twosComplement")) comparator_6 (
    .a(ID_R2_num), .b({5{1'b0}}), .eq(comparator_6_eq));  // open: gt, lt
  or or_2 (or_2_out, and_3_out, and_4_out);
  and and_5 (and_5_out, or_1_out, R1_Used);
  and and_6 (and_6_out, or_2_out, R2_Used);
  and and_7 (and_7_out, not_1_out, and_5_out);
  and and_8 (and_8_out, not_2_out, and_6_out);
  or or_3 (\数据相关 , and_7_out, and_8_out);
endmodule

// 源寄存器使用检测
module \源寄存器使用检测  (
  input  OP0,
  input  OP1,
  input  OP2,
  input  OP3,
  input  OP4,
  input  OP5,
  input  F0,
  input  F1,
  input  F2,
  input  F3,
  input  F4,
  input  F5,
  output R1_Used,
  output R2_Used
);

  wire and_1_out, and_2_out, and_3_out, and_4_out, and_5_out, and_6_out, and_7_out, and_8_out, and_9_out,
       and_10_out, and_11_out, and_12_out, and_13_out, and_14_out, and_15_out, and_16_out, and_17_out,
       and_18_out, and_19_out, and_20_out, and_21_out, and_22_out, and_23_out, and_24_out, and_25_out,
       and_26_out, and_27_out, and_28_out, and_29_out, and_30_out, and_31_out, and_32_out, and_33_out,
       and_34_out, and_35_out, and_36_out, and_37_out, and_38_out, and_39_out, not_1_out, not_2_out,
       not_3_out, not_4_out, not_5_out, not_6_out, not_7_out, not_8_out, not_9_out, not_10_out, not_11_out,
       not_12_out, not_13_out, not_14_out, not_15_out, not_16_out, not_17_out, not_18_out, not_19_out,
       not_20_out, not_21_out, not_22_out, not_23_out, not_24_out, not_25_out, not_26_out, not_27_out,
       not_28_out, not_29_out, not_30_out, not_31_out, not_32_out, not_33_out, not_34_out, not_35_out,
       not_36_out, not_37_out, not_38_out, not_39_out, not_40_out, not_41_out, not_42_out, not_43_out,
       not_44_out, not_45_out, not_46_out, not_47_out, not_48_out, not_49_out, not_50_out, not_51_out,
       not_52_out, not_53_out, not_54_out, not_55_out, not_56_out, not_57_out, not_58_out, not_59_out,
       not_60_out, not_61_out, not_62_out, not_63_out, not_64_out, not_65_out, not_66_out, not_67_out,
       not_68_out, not_69_out, not_70_out, not_71_out, not_72_out, not_73_out, not_74_out, not_75_out,
       not_76_out, not_77_out, not_78_out, not_79_out, not_80_out, not_81_out, not_82_out, not_83_out,
       not_84_out, not_85_out, not_86_out, not_87_out, not_88_out, not_89_out, not_90_out, not_91_out,
       not_92_out, not_93_out, not_94_out, not_95_out, not_96_out, not_97_out, not_98_out, not_99_out,
       not_100_out, not_101_out, not_102_out, not_103_out, not_104_out, not_105_out, not_106_out,
       not_107_out, not_108_out, not_109_out, not_110_out, not_111_out, not_112_out, not_113_out,
       not_114_out, not_115_out, not_116_out, not_117_out, not_118_out, not_119_out, not_120_out,
       not_121_out, not_122_out, not_123_out, not_124_out, not_125_out, not_126_out, not_127_out,
       not_128_out, not_129_out, not_130_out, not_131_out, not_132_out, not_133_out, not_134_out,
       not_135_out, not_136_out, not_137_out, not_138_out, not_139_out, not_140_out, not_141_out,
       not_142_out, not_143_out, not_144_out, not_145_out, not_146_out, not_147_out, not_148_out,
       not_149_out, not_150_out, not_151_out, not_152_out, not_153_out, not_154_out, not_155_out,
       not_156_out, not_157_out, not_158_out, not_159_out, not_160_out, not_161_out, not_162_out,
       not_163_out, not_164_out, not_165_out, not_166_out, not_167_out, not_168_out, not_169_out,
       not_170_out, not_171_out, not_172_out, not_173_out, not_174_out, not_175_out, not_176_out,
       not_177_out, not_178_out, not_179_out, not_180_out, not_181_out, not_182_out, not_183_out,
       not_184_out, not_185_out, not_186_out, not_187_out, not_188_out, not_189_out, not_190_out,
       not_191_out, not_192_out, not_193_out, not_194_out, not_195_out, not_196_out, not_197_out,
       not_198_out, not_199_out, not_200_out, not_201_out, not_202_out, not_203_out, not_204_out,
       not_205_out, not_206_out, not_207_out, not_208_out, not_209_out, not_210_out, not_211_out,
       not_212_out, not_213_out, not_214_out, not_215_out, not_216_out, not_217_out, not_218_out,
       not_219_out, not_220_out, not_221_out, not_222_out, not_223_out, not_224_out, not_225_out,
       not_226_out, not_227_out, not_228_out, not_229_out, not_230_out, not_231_out, not_232_out,
       not_233_out, not_234_out, not_235_out, not_236_out, not_237_out, not_238_out, not_239_out,
       not_240_out, not_241_out, not_242_out, not_243_out, not_244_out, not_245_out, not_246_out,
       not_247_out, not_248_out, not_249_out, not_250_out, not_251_out, not_252_out, not_253_out,
       not_254_out, not_255_out, not_256_out, not_257_out, not_258_out, not_259_out, not_260_out,
       not_261_out, not_262_out, not_263_out, not_264_out, not_265_out, not_266_out, not_267_out,
       not_268_out, not_269_out, not_270_out, not_271_out, not_272_out, not_273_out, not_274_out,
       not_275_out, not_276_out, not_277_out, not_278_out, not_279_out, not_280_out, not_281_out,
       not_282_out, not_283_out, not_284_out, not_285_out, not_286_out, not_287_out, not_288_out,
       not_289_out, not_290_out, not_291_out;

  not not_1 (not_1_out, OP5);
  not not_2 (not_2_out, OP4);
  not not_3 (not_3_out, OP3);
  not not_4 (not_4_out, OP2);
  not not_5 (not_5_out, OP1);
  not not_6 (not_6_out, OP0);
  not not_7 (not_7_out, F4);
  not not_8 (not_8_out, F3);
  not not_9 (not_9_out, F2);
  not not_10 (not_10_out, F1);
  not not_11 (not_11_out, F0);
  not not_12 (not_12_out, OP5);
  not not_13 (not_13_out, OP4);
  not not_14 (not_14_out, OP3);
  not not_15 (not_15_out, OP2);
  not not_16 (not_16_out, OP1);
  not not_17 (not_17_out, OP0);
  not not_18 (not_18_out, F4);
  not not_19 (not_19_out, F3);
  not not_20 (not_20_out, F2);
  not not_21 (not_21_out, F1);
  not not_22 (not_22_out, OP5);
  not not_23 (not_23_out, OP4);
  not not_24 (not_24_out, OP3);
  not not_25 (not_25_out, OP2);
  not not_26 (not_26_out, OP1);
  not not_27 (not_27_out, OP0);
  not not_28 (not_28_out, F4);
  not not_29 (not_29_out, F3);
  not not_30 (not_30_out, F2);
  not not_31 (not_31_out, F0);
  not not_32 (not_32_out, OP5);
  not not_33 (not_33_out, OP4);
  not not_34 (not_34_out, OP3);
  not not_35 (not_35_out, OP2);
  not not_36 (not_36_out, OP1);
  not not_37 (not_37_out, OP0);
  not not_38 (not_38_out, F4);
  not not_39 (not_39_out, F3);
  not not_40 (not_40_out, F1);
  not not_41 (not_41_out, F0);
  not not_42 (not_42_out, OP5);
  not not_43 (not_43_out, OP4);
  not not_44 (not_44_out, OP3);
  not not_45 (not_45_out, OP2);
  not not_46 (not_46_out, OP1);
  not not_47 (not_47_out, OP0);
  not not_48 (not_48_out, F4);
  not not_49 (not_49_out, F3);
  not not_50 (not_50_out, F1);
  not not_51 (not_51_out, OP5);
  not not_52 (not_52_out, OP4);
  not not_53 (not_53_out, OP3);
  not not_54 (not_54_out, OP2);
  not not_55 (not_55_out, OP1);
  not not_56 (not_56_out, OP0);
  not not_57 (not_57_out, F4);
  not not_58 (not_58_out, F3);
  not not_59 (not_59_out, OP5);
  not not_60 (not_60_out, OP4);
  not not_61 (not_61_out, OP3);
  not not_62 (not_62_out, OP2);
  not not_63 (not_63_out, OP1);
  not not_64 (not_64_out, OP0);
  not not_65 (not_65_out, F4);
  not not_66 (not_66_out, F2);
  not not_67 (not_67_out, F0);
  not not_68 (not_68_out, OP5);
  not not_69 (not_69_out, OP4);
  not not_70 (not_70_out, OP3);
  not not_71 (not_71_out, OP2);
  not not_72 (not_72_out, OP1);
  not not_73 (not_73_out, OP0);
  not not_74 (not_74_out, F4);
  not not_75 (not_75_out, F2);
  not not_76 (not_76_out, OP5);
  not not_77 (not_77_out, OP4);
  not not_78 (not_78_out, OP3);
  not not_79 (not_79_out, OP2);
  not not_80 (not_80_out, OP1);
  not not_81 (not_81_out, OP0);
  not not_82 (not_82_out, F5);
  not not_83 (not_83_out, F4);
  not not_84 (not_84_out, F2);
  not not_85 (not_85_out, F1);
  not not_86 (not_86_out, F0);
  not not_87 (not_87_out, OP5);
  not not_88 (not_88_out, OP4);
  not not_89 (not_89_out, OP3);
  not not_90 (not_90_out, OP2);
  not not_91 (not_91_out, OP1);
  not not_92 (not_92_out, OP0);
  not not_93 (not_93_out, F5);
  not not_94 (not_94_out, F4);
  not not_95 (not_95_out, F1);
  not not_96 (not_96_out, F0);
  not not_97 (not_97_out, OP5);
  not not_98 (not_98_out, OP4);
  not not_99 (not_99_out, OP3);
  not not_100 (not_100_out, OP1);
  not not_101 (not_101_out, OP0);
  not not_102 (not_102_out, OP5);
  not not_103 (not_103_out, OP4);
  not not_104 (not_104_out, OP3);
  not not_105 (not_105_out, OP1);
  not not_106 (not_106_out, OP5);
  not not_107 (not_107_out, OP4);
  not not_108 (not_108_out, OP2);
  not not_109 (not_109_out, OP1);
  not not_110 (not_110_out, OP0);
  not not_111 (not_111_out, OP5);
  not not_112 (not_112_out, OP4);
  not not_113 (not_113_out, OP1);
  not not_114 (not_114_out, OP0);
  not not_115 (not_115_out, OP5);
  not not_116 (not_116_out, OP4);
  not not_117 (not_117_out, OP2);
  not not_118 (not_118_out, OP1);
  not not_119 (not_119_out, OP5);
  not not_120 (not_120_out, OP4);
  not not_121 (not_121_out, OP2);
  not not_122 (not_122_out, OP0);
  not not_123 (not_123_out, OP5);
  not not_124 (not_124_out, OP4);
  not not_125 (not_125_out, OP1);
  not not_126 (not_126_out, OP4);
  not not_127 (not_127_out, OP3);
  not not_128 (not_128_out, OP2);
  not not_129 (not_129_out, OP4);
  not not_130 (not_130_out, OP2);
  not not_131 (not_131_out, OP5);
  not not_132 (not_132_out, OP4);
  not not_133 (not_133_out, OP3);
  not not_134 (not_134_out, OP2);
  not not_135 (not_135_out, OP1);
  not not_136 (not_136_out, OP0);
  not not_137 (not_137_out, F5);
  not not_138 (not_138_out, F4);
  not not_139 (not_139_out, F3);
  not not_140 (not_140_out, F1);
  not not_141 (not_141_out, F0);
  not not_142 (not_142_out, OP5);
  not not_143 (not_143_out, OP4);
  not not_144 (not_144_out, OP0);
  not not_145 (not_145_out, OP4);
  not not_146 (not_146_out, OP3);
  not not_147 (not_147_out, OP2);
  not not_148 (not_148_out, OP1);
  not not_149 (not_149_out, OP5);
  not not_150 (not_150_out, OP4);
  not not_151 (not_151_out, OP3);
  not not_152 (not_152_out, OP5);
  not not_153 (not_153_out, OP4);
  not not_154 (not_154_out, OP3);
  not not_155 (not_155_out, OP2);
  not not_156 (not_156_out, OP1);
  not not_157 (not_157_out, OP0);
  not not_158 (not_158_out, F5);
  not not_159 (not_159_out, F4);
  not not_160 (not_160_out, F3);
  not not_161 (not_161_out, F2);
  not not_162 (not_162_out, F1);
  not not_163 (not_163_out, F0);
  not not_164 (not_164_out, OP5);
  not not_165 (not_165_out, OP4);
  not not_166 (not_166_out, OP3);
  not not_167 (not_167_out, OP2);
  not not_168 (not_168_out, OP1);
  not not_169 (not_169_out, OP0);
  not not_170 (not_170_out, F5);
  not not_171 (not_171_out, F4);
  not not_172 (not_172_out, F3);
  not not_173 (not_173_out, F2);
  not not_174 (not_174_out, OP5);
  not not_175 (not_175_out, OP4);
  not not_176 (not_176_out, OP3);
  not not_177 (not_177_out, OP2);
  not not_178 (not_178_out, OP1);
  not not_179 (not_179_out, OP0);
  not not_180 (not_180_out, F5);
  not not_181 (not_181_out, F4);
  not not_182 (not_182_out, F3);
  not not_183 (not_183_out, F2);
  not not_184 (not_184_out, F0);
  not not_185 (not_185_out, OP5);
  not not_186 (not_186_out, OP4);
  not not_187 (not_187_out, OP3);
  not not_188 (not_188_out, OP2);
  not not_189 (not_189_out, OP1);
  not not_190 (not_190_out, OP0);
  not not_191 (not_191_out, F4);
  not not_192 (not_192_out, F3);
  not not_193 (not_193_out, F2);
  not not_194 (not_194_out, F1);
  not not_195 (not_195_out, F0);
  not not_196 (not_196_out, OP5);
  not not_197 (not_197_out, OP4);
  not not_198 (not_198_out, OP3);
  not not_199 (not_199_out, OP2);
  not not_200 (not_200_out, OP1);
  not not_201 (not_201_out, OP0);
  not not_202 (not_202_out, F4);
  not not_203 (not_203_out, F3);
  not not_204 (not_204_out, F2);
  not not_205 (not_205_out, F1);
  not not_206 (not_206_out, OP5);
  not not_207 (not_207_out, OP4);
  not not_208 (not_208_out, OP3);
  not not_209 (not_209_out, OP2);
  not not_210 (not_210_out, OP1);
  not not_211 (not_211_out, OP0);
  not not_212 (not_212_out, F4);
  not not_213 (not_213_out, F3);
  not not_214 (not_214_out, F2);
  not not_215 (not_215_out, F0);
  not not_216 (not_216_out, OP5);
  not not_217 (not_217_out, OP4);
  not not_218 (not_218_out, OP3);
  not not_219 (not_219_out, OP2);
  not not_220 (not_220_out, OP1);
  not not_221 (not_221_out, OP0);
  not not_222 (not_222_out, F4);
  not not_223 (not_223_out, F3);
  not not_224 (not_224_out, F1);
  not not_225 (not_225_out, F0);
  not not_226 (not_226_out, OP5);
  not not_227 (not_227_out, OP4);
  not not_228 (not_228_out, OP3);
  not not_229 (not_229_out, OP2);
  not not_230 (not_230_out, OP1);
  not not_231 (not_231_out, OP0);
  not not_232 (not_232_out, F4);
  not not_233 (not_233_out, F3);
  not not_234 (not_234_out, F1);
  not not_235 (not_235_out, OP5);
  not not_236 (not_236_out, OP4);
  not not_237 (not_237_out, OP3);
  not not_238 (not_238_out, OP2);
  not not_239 (not_239_out, OP1);
  not not_240 (not_240_out, OP0);
  not not_241 (not_241_out, F4);
  not not_242 (not_242_out, F3);
  not not_243 (not_243_out, OP5);
  not not_244 (not_244_out, OP4);
  not not_245 (not_245_out, OP3);
  not not_246 (not_246_out, OP2);
  not not_247 (not_247_out, OP1);
  not not_248 (not_248_out, OP0);
  not not_249 (not_249_out, F4);
  not not_250 (not_250_out, F2);
  not not_251 (not_251_out, F0);
  not not_252 (not_252_out, OP5);
  not not_253 (not_253_out, OP4);
  not not_254 (not_254_out, OP3);
  not not_255 (not_255_out, OP2);
  not not_256 (not_256_out, OP1);
  not not_257 (not_257_out, OP0);
  not not_258 (not_258_out, F4);
  not not_259 (not_259_out, F2);
  not not_260 (not_260_out, OP5);
  not not_261 (not_261_out, OP4);
  not not_262 (not_262_out, OP3);
  not not_263 (not_263_out, OP2);
  not not_264 (not_264_out, OP1);
  not not_265 (not_265_out, OP0);
  not not_266 (not_266_out, F5);
  not not_267 (not_267_out, F4);
  not not_268 (not_268_out, F1);
  not not_269 (not_269_out, F0);
  not not_270 (not_270_out, OP5);
  not not_271 (not_271_out, OP4);
  not not_272 (not_272_out, OP3);
  not not_273 (not_273_out, OP1);
  not not_274 (not_274_out, OP0);
  not not_275 (not_275_out, OP5);
  not not_276 (not_276_out, OP4);
  not not_277 (not_277_out, OP3);
  not not_278 (not_278_out, OP1);
  not not_279 (not_279_out, OP4);
  not not_280 (not_280_out, OP2);
  not not_281 (not_281_out, OP5);
  not not_282 (not_282_out, OP4);
  not not_283 (not_283_out, OP3);
  not not_284 (not_284_out, OP2);
  not not_285 (not_285_out, OP1);
  not not_286 (not_286_out, OP0);
  not not_287 (not_287_out, F5);
  not not_288 (not_288_out, F4);
  not not_289 (not_289_out, F3);
  not not_290 (not_290_out, F1);
  not not_291 (not_291_out, F0);
  and and_1 (and_1_out, not_1_out, not_2_out, not_3_out, not_4_out, not_5_out, not_6_out, F5, not_7_out, not_8_out, not_9_out, not_10_out, not_11_out);
  and and_2 (and_2_out, not_12_out, not_13_out, not_14_out, not_15_out, not_16_out, not_17_out, F5, not_18_out, not_19_out, not_20_out, not_21_out, F0);
  and and_3 (and_3_out, not_22_out, not_23_out, not_24_out, not_25_out, not_26_out, not_27_out, F5, not_28_out, not_29_out, not_30_out, F1, not_31_out);
  and and_4 (and_4_out, not_32_out, not_33_out, not_34_out, not_35_out, not_36_out, not_37_out, F5, not_38_out, not_39_out, F2, not_40_out, not_41_out);
  and and_5 (and_5_out, not_42_out, not_43_out, not_44_out, not_45_out, not_46_out, not_47_out, F5, not_48_out, not_49_out, F2, not_50_out, F0);
  and and_6 (and_6_out, not_51_out, not_52_out, not_53_out, not_54_out, not_55_out, not_56_out, F5, not_57_out, not_58_out, F2, F1, F0);
  and and_7 (and_7_out, not_59_out, not_60_out, not_61_out, not_62_out, not_63_out, not_64_out, F5, not_65_out, F3, not_66_out, F1, not_67_out);
  and and_8 (and_8_out, not_68_out, not_69_out, not_70_out, not_71_out, not_72_out, not_73_out, F5, not_74_out, F3, not_75_out, F1, F0);
  and and_9 (and_9_out, not_76_out, not_77_out, not_78_out, not_79_out, not_80_out, not_81_out, not_82_out, not_83_out, F3, not_84_out, not_85_out, not_86_out);
  and and_10 (and_10_out, not_87_out, not_88_out, not_89_out, not_90_out, not_91_out, not_92_out, not_93_out, not_94_out, F3, F2, not_95_out, not_96_out);
  and and_11 (and_11_out, not_97_out, not_98_out, not_99_out, OP2, not_100_out, not_101_out);
  and and_12 (and_12_out, not_102_out, not_103_out, not_104_out, OP2, not_105_out, OP0);
  and and_13 (and_13_out, not_106_out, not_107_out, OP3, not_108_out, not_109_out, not_110_out);
  and and_14 (and_14_out, not_111_out, not_112_out, OP3, OP2, not_113_out, not_114_out);
  and and_15 (and_15_out, not_115_out, not_116_out, OP3, not_117_out, not_118_out, OP0);
  and and_16 (and_16_out, not_119_out, not_120_out, OP3, not_121_out, OP1, not_122_out);
  and and_17 (and_17_out, not_123_out, not_124_out, OP3, OP2, not_125_out, OP0);
  and and_18 (and_18_out, OP5, not_126_out, not_127_out, not_128_out, OP1, OP0);
  and and_19 (and_19_out, OP5, not_129_out, OP3, not_130_out, OP1, OP0);
  and and_20 (and_20_out, not_131_out, not_132_out, not_133_out, not_134_out, not_135_out, not_136_out, not_137_out, not_138_out, not_139_out, F2, not_140_out, not_141_out);
  and and_21 (and_21_out, not_142_out, not_143_out, OP3, OP2, OP1, not_144_out);
  and and_22 (and_22_out, OP5, not_145_out, not_146_out, not_147_out, not_148_out, OP0);
  and and_23 (and_23_out, not_149_out, not_150_out, not_151_out, OP2, OP1, OP0);
  and and_24 (and_24_out, not_152_out, not_153_out, not_154_out, not_155_out, not_156_out, not_157_out, not_158_out, not_159_out, not_160_out, not_161_out, not_162_out, not_163_out);
  and and_25 (and_25_out, not_164_out, not_165_out, not_166_out, not_167_out, not_168_out, not_169_out, not_170_out, not_171_out, not_172_out, not_173_out, F1, F0);
  and and_26 (and_26_out, not_174_out, not_175_out, not_176_out, not_177_out, not_178_out, not_179_out, not_180_out, not_181_out, not_182_out, not_183_out, F1, not_184_out);
  and and_27 (and_27_out, not_185_out, not_186_out, not_187_out, not_188_out, not_189_out, not_190_out, F5, not_191_out, not_192_out, not_193_out, not_194_out, not_195_out);
  and and_28 (and_28_out, not_196_out, not_197_out, not_198_out, not_199_out, not_200_out, not_201_out, F5, not_202_out, not_203_out, not_204_out, not_205_out, F0);
  and and_29 (and_29_out, not_206_out, not_207_out, not_208_out, not_209_out, not_210_out, not_211_out, F5, not_212_out, not_213_out, not_214_out, F1, not_215_out);
  and and_30 (and_30_out, not_216_out, not_217_out, not_218_out, not_219_out, not_220_out, not_221_out, F5, not_222_out, not_223_out, F2, not_224_out, not_225_out);
  and and_31 (and_31_out, not_226_out, not_227_out, not_228_out, not_229_out, not_230_out, not_231_out, F5, not_232_out, not_233_out, F2, not_234_out, F0);
  and and_32 (and_32_out, not_235_out, not_236_out, not_237_out, not_238_out, not_239_out, not_240_out, F5, not_241_out, not_242_out, F2, F1, F0);
  and and_33 (and_33_out, not_243_out, not_244_out, not_245_out, not_246_out, not_247_out, not_248_out, F5, not_249_out, F3, not_250_out, F1, not_251_out);
  and and_34 (and_34_out, not_252_out, not_253_out, not_254_out, not_255_out, not_256_out, not_257_out, F5, not_258_out, F3, not_259_out, F1, F0);
  and and_35 (and_35_out, not_260_out, not_261_out, not_262_out, not_263_out, not_264_out, not_265_out, not_266_out, not_267_out, F3, F2, not_268_out, not_269_out);
  and and_36 (and_36_out, not_270_out, not_271_out, not_272_out, OP2, not_273_out, not_274_out);
  and and_37 (and_37_out, not_275_out, not_276_out, not_277_out, OP2, not_278_out, OP0);
  and and_38 (and_38_out, OP5, not_279_out, OP3, not_280_out, OP1, OP0);
  and and_39 (and_39_out, not_281_out, not_282_out, not_283_out, not_284_out, not_285_out, not_286_out, not_287_out, not_288_out, not_289_out, F2, not_290_out, not_291_out);
  or or_1 (R1_Used, and_1_out, and_2_out, and_3_out, and_4_out, and_5_out, and_6_out, and_7_out, and_8_out, and_9_out, and_10_out, and_11_out, and_12_out, and_13_out, and_14_out, and_15_out, and_16_out, and_17_out, and_18_out, and_19_out, and_20_out, and_21_out, and_22_out, and_23_out);
  or or_2 (R2_Used, and_24_out, and_25_out, and_26_out, and_27_out, and_28_out, and_29_out, and_30_out, and_31_out, and_32_out, and_33_out, and_34_out, and_35_out, and_36_out, and_37_out, and_38_out, and_39_out);
endmodule

module \重定向数据检测  (
  input  EX_LD,
  input  R1Used,
  input  [4:0] R1_num,
  input  [4:0] R2_num,
  input  [4:0] EX_W_num,
  input  [4:0] Mem_W_num,
  input  EX_RegWrite,
  input  Mem_WriteReg,
  input  R2Used,
  output Bubble,
  output [1:0] FowardA,
  output [1:0] FowardB
);

  wire and_1_out, and_2_out, and_3_out, and_4_out, and_9_out, and_10_out, comparator_1_eq, comparator_2_eq,
       comparator_3_eq, comparator_4_eq, comparator_5_eq, comparator_6_eq;

  Comparator #(.width(5), .mode("twosComplement")) comparator_1 (
    .a(R1_num), .b(EX_W_num), .eq(comparator_1_eq));  // open: gt, lt
  Comparator #(.width(5), .mode("twosComplement")) comparator_2 (
    .a(R1_num), .b(Mem_W_num), .eq(comparator_2_eq));  // open: gt, lt
  Comparator #(.width(5), .mode("twosComplement")) comparator_3 (
    .a(R1_num), .b({5{1'b0}}), .eq(comparator_3_eq));  // open: gt, lt
  Comparator #(.width(5), .mode("twosComplement")) comparator_4 (
    .a({5{1'b0}}), .b(R2_num), .eq(comparator_4_eq));  // open: gt, lt
  Comparator #(.width(5), .mode("twosComplement")) comparator_5 (
    .a(R2_num), .b(EX_W_num), .eq(comparator_5_eq));  // open: gt, lt
  Comparator #(.width(5), .mode("twosComplement")) comparator_6 (
    .a(R2_num), .b(Mem_W_num), .eq(comparator_6_eq));  // open: gt, lt
  and and_1 (and_1_out, comparator_1_eq, EX_RegWrite);
  and and_2 (and_2_out, comparator_2_eq, Mem_WriteReg);
  and and_3 (and_3_out, comparator_5_eq, EX_RegWrite);
  and and_4 (and_4_out, comparator_6_eq, Mem_WriteReg);
  and and_5 (FowardA[1], and_1_out, R1Used, ~comparator_3_eq);  // AND_Gate
  and and_6 (FowardA[0], and_2_out, R1Used, ~comparator_3_eq);  // AND_Gate
  and and_7 (FowardB[1], ~comparator_4_eq, R2Used, and_3_out);  // AND_Gate
  and and_8 (FowardB[0], ~comparator_4_eq, R2Used, and_4_out);  // AND_Gate
  and and_9 (and_9_out, EX_LD, FowardA[1]);
  and and_10 (and_10_out, EX_LD, FowardB[1]);
  or or_1 (Bubble, and_9_out, and_10_out);
endmodule

// BHT
module BHT (
  input  [31:0] EX_PC,
  input  [31:0] \分支目标地址 ,
  input  [31:0] IF_PC,
  input  [1:0] \双预测位 ,
  input  BlkDataReady,
  input  CLK,
  output Have,
  output [31:0] \分支目标地址_2 ,
  output [1:0] \双预测位输出 
);

  wire and_9_out, comparator_1_eq, comparator_2_eq, comparator_3_eq, comparator_4_eq, comparator_5_eq,
       comparator_6_eq, comparator_7_eq, comparator_8_eq, comparator_9_eq, comparator_10_eq,
       comparator_11_eq, comparator_12_eq, comparator_13_eq, comparator_14_eq, comparator_15_eq,
       comparator_16_eq, decoder_1_out0, decoder_1_out1, decoder_1_out2, decoder_1_out3, decoder_1_out4,
       decoder_1_out5, decoder_1_out6, decoder_1_out7, not_1_out, not_2_out, not_3_out, not_4_out, not_5_out,
       not_6_out, not_7_out, not_8_out, priority_encoder_1_gs, priority_encoder_2_gs, S0, S1, S2, S3, S4, S5,
       S6, S7, Shoot, V0, V1, V2, V3, V4, V5, V6, V7, W0, W1, W2, W3, W4, W5, W6, W7, Write0, Write1, Write2,
       Write3, Write4, Write5, Write6, Write7;
  wire [1:0] \双预测位输出0 , \双预测位输出1 , \双预测位输出2 , \双预测位输出3 , \双预测位输出4 , \双预测位输出5 , \双预测位输出6 , \双预测位输出7 ;
  wire [2:0] \max2_归并比较_1_max_num , \max2_归并比较_2_max_num , \max2_归并比较_3_max_num , \max2_归并比较_4_max_num ,
       \max2_归并比较_5_max_num , \max2_归并比较_6_max_num , \max2_归并比较_7_max_num , multiplexer_1_out,
       multiplexer_2_out, priority_encoder_1_out, priority_encoder_2_out;
  wire [15:0] LRU0, LRU1, LRU2, LRU3, LRU4, LRU5, LRU6, LRU7, \max2_归并比较_1_max , \max2_归并比较_2_max ,
       \max2_归并比较_3_max , \max2_归并比较_4_max , \max2_归并比较_5_max , \max2_归并比较_6_max ;
  wire [31:0] Tag0, Tag1, Tag2, Tag3, Tag4, Tag5, Tag6, Tag7, \分支地址输出0 , \分支地址输出1 , \分支地址输出2 , \分支地址输出3 ,
       \分支地址输出4 , \分支地址输出5 , \分支地址输出6 , \分支地址输出7 ;

  Register #(.width(1), .trigger("rising"), .Select("low")) valid (
    .D(1'b1), .en(Write0), .Q(V0), .clk(CLK));  // open: clr
  Register #(.width(1), .trigger("rising"), .Select("low")) valid_2 (
    .D(1'b1), .en(Write1), .Q(V1), .clk(CLK));  // open: clr
  Register #(.width(1), .trigger("rising"), .Select("low")) valid_3 (
    .D(1'b1), .en(Write2), .Q(V2), .clk(CLK));  // open: clr
  Register #(.width(1), .trigger("rising"), .Select("low")) valid_4 (
    .D(1'b1), .en(Write3), .Q(V3), .clk(CLK));  // open: clr
  Register #(.width(1), .trigger("rising"), .Select("low")) valid_5 (
    .D(1'b1), .en(Write4), .Q(V4), .clk(CLK));  // open: clr
  Register #(.width(1), .trigger("rising"), .Select("low")) valid_6 (
    .D(1'b1), .en(Write5), .Q(V5), .clk(CLK));  // open: clr
  Register #(.width(1), .trigger("rising"), .Select("low")) valid_7 (
    .D(1'b1), .en(Write6), .Q(V6), .clk(CLK));  // open: clr
  Register #(.width(1), .trigger("rising"), .Select("low")) valid_8 (
    .D(1'b1), .en(Write7), .Q(V7), .clk(CLK));  // open: clr
  Register #(.width(32), .trigger("rising"), .Select("low")) \u_分支指令地址  (
    .D(EX_PC), .en(Write0), .Q(Tag0), .clk(CLK));  // open: clr
  Register #(.width(32), .trigger("rising"), .Select("low")) \u_分支指令地址_2  (
    .D(EX_PC), .en(Write1), .Q(Tag1), .clk(CLK));  // open: clr
  Register #(.width(32), .trigger("rising"), .Select("low")) \u_分支指令地址_3  (
    .D(EX_PC), .en(Write2), .Q(Tag2), .clk(CLK));  // open: clr
  Register #(.width(32), .trigger("rising"), .Select("low")) \u_分支指令地址_4  (
    .D(EX_PC), .en(Write3), .Q(Tag3), .clk(CLK));  // open: clr
  Register #(.width(32), .trigger("rising"), .Select("low")) \u_分支指令地址_5  (
    .D(EX_PC), .en(Write4), .Q(Tag4), .clk(CLK));  // open: clr
  Register #(.width(32), .trigger("rising"), .Select("low")) \u_分支指令地址_6  (
    .D(EX_PC), .en(Write5), .Q(Tag5), .clk(CLK));  // open: clr
  Register #(.width(32), .trigger("rising"), .Select("low")) \u_分支指令地址_7  (
    .D(EX_PC), .en(Write6), .Q(Tag6), .clk(CLK));  // open: clr
  Register #(.width(32), .trigger("rising"), .Select("low")) \u_分支指令地址_8  (
    .D(EX_PC), .en(Write7), .Q(Tag7), .clk(CLK));  // open: clr
  Register #(.width(32), .trigger("rising"), .Select("low")) \u_分支目标地址  (
    .D(\分支目标地址 ), .en(Write0), .Q(\分支地址输出0 ), .clk(CLK));  // open: clr
  Register #(.width(32), .trigger("rising"), .Select("low")) \u_分支目标地址_2  (
    .D(\分支目标地址 ), .en(Write1), .Q(\分支地址输出1 ), .clk(CLK));  // open: clr
  Register #(.width(32), .trigger("rising"), .Select("low")) \u_分支目标地址_3  (
    .D(\分支目标地址 ), .en(Write2), .Q(\分支地址输出2 ), .clk(CLK));  // open: clr
  Register #(.width(32), .trigger("rising"), .Select("low")) \u_分支目标地址_4  (
    .D(\分支目标地址 ), .en(Write3), .Q(\分支地址输出3 ), .clk(CLK));  // open: clr
  Register #(.width(32), .trigger("rising"), .Select("low")) \u_分支目标地址_5  (
    .D(\分支目标地址 ), .en(Write4), .Q(\分支地址输出4 ), .clk(CLK));  // open: clr
  Register #(.width(32), .trigger("rising"), .Select("low")) \u_分支目标地址_6  (
    .D(\分支目标地址 ), .en(Write5), .Q(\分支地址输出5 ), .clk(CLK));  // open: clr
  Register #(.width(32), .trigger("rising"), .Select("low")) \u_分支目标地址_7  (
    .D(\分支目标地址 ), .en(Write6), .Q(\分支地址输出6 ), .clk(CLK));  // open: clr
  Register #(.width(32), .trigger("rising"), .Select("low")) \u_分支目标地址_8  (
    .D(\分支目标地址 ), .en(Write7), .Q(\分支地址输出7 ), .clk(CLK));  // open: clr
  Register #(.width(2), .trigger("rising"), .Select("low")) \u_双预测位  (
    .D(\双预测位 ), .en(Write0), .Q(\双预测位输出0 ), .clk(CLK));  // open: clr
  Register #(.width(2), .trigger("rising"), .Select("low")) \u_双预测位_2  (
    .D(\双预测位 ), .en(Write1), .Q(\双预测位输出1 ), .clk(CLK));  // open: clr
  Register #(.width(2), .trigger("rising"), .Select("low")) \u_双预测位_3  (
    .D(\双预测位 ), .en(Write2), .Q(\双预测位输出2 ), .clk(CLK));  // open: clr
  Register #(.width(2), .trigger("rising"), .Select("low")) \u_双预测位_4  (
    .D(\双预测位 ), .en(Write3), .Q(\双预测位输出3 ), .clk(CLK));  // open: clr
  Register #(.width(2), .trigger("rising"), .Select("low")) \u_双预测位_5  (
    .D(\双预测位 ), .en(Write4), .Q(\双预测位输出4 ), .clk(CLK));  // open: clr
  Register #(.width(2), .trigger("rising"), .Select("low")) \u_双预测位_6  (
    .D(\双预测位 ), .en(Write5), .Q(\双预测位输出5 ), .clk(CLK));  // open: clr
  Register #(.width(2), .trigger("rising"), .Select("low")) \u_双预测位_7  (
    .D(\双预测位 ), .en(Write6), .Q(\双预测位输出6 ), .clk(CLK));  // open: clr
  Register #(.width(2), .trigger("rising"), .Select("low")) \u_双预测位_8  (
    .D(\双预测位 ), .en(Write7), .Q(\双预测位输出7 ), .clk(CLK));  // open: clr
  not not_1 (not_1_out, W0);
  not not_2 (not_2_out, W1);
  not not_3 (not_3_out, W2);
  not not_4 (not_4_out, W3);
  not not_5 (not_5_out, W4);
  not not_6 (not_6_out, W5);
  not not_7 (not_7_out, W6);
  not not_8 (not_8_out, W7);
  Counter #(.width(16), .max('hffff), .ongoal("wrap"), .trigger("rising"), .behavior("old")) \u_淘汰标志位  (
    .count(not_1_out), .Q(LRU0), .clk(CLK), .clr(W0));  // open: load, D, carry, preset
  Counter #(.width(16), .max('hffff), .ongoal("wrap"), .trigger("rising"), .behavior("old")) \u_淘汰标志位_2  (
    .count(not_2_out), .Q(LRU1), .clk(CLK), .clr(W1));  // open: load, D, carry, preset
  Counter #(.width(16), .max('hffff), .ongoal("wrap"), .trigger("rising"), .behavior("old")) \u_淘汰标志位_3  (
    .count(not_3_out), .Q(LRU2), .clk(CLK), .clr(W2));  // open: load, D, carry, preset
  Counter #(.width(16), .max('hffff), .ongoal("wrap"), .trigger("rising"), .behavior("old")) \u_淘汰标志位_4  (
    .count(not_4_out), .Q(LRU3), .clk(CLK), .clr(W3));  // open: load, D, carry, preset
  Counter #(.width(16), .max('hffff), .ongoal("wrap"), .trigger("rising"), .behavior("old")) \u_淘汰标志位_5  (
    .count(not_5_out), .Q(LRU4), .clk(CLK), .clr(W4));  // open: load, D, carry, preset
  Counter #(.width(16), .max('hffff), .ongoal("wrap"), .trigger("rising"), .behavior("old")) \u_淘汰标志位_6  (
    .count(not_6_out), .Q(LRU5), .clk(CLK), .clr(W5));  // open: load, D, carry, preset
  Counter #(.width(16), .max('hffff), .ongoal("wrap"), .trigger("rising"), .behavior("old")) \u_淘汰标志位_7  (
    .count(not_7_out), .Q(LRU6), .clk(CLK), .clr(W6));  // open: load, D, carry, preset
  Counter #(.width(16), .max('hffff), .ongoal("wrap"), .trigger("rising"), .behavior("old")) \u_淘汰标志位_8  (
    .count(not_8_out), .Q(LRU7), .clk(CLK), .clr(W7));  // open: load, D, carry, preset
  \Max2_归并比较  \max2_归并比较_1  (
    .Y(LRU1), .X(LRU0), .Y_num(3'b001), .X_num(3'b000), .MAX(\max2_归并比较_1_max ),
    .Max_num(\max2_归并比较_1_max_num ));
  \Max2_归并比较  \max2_归并比较_2  (
    .Y(LRU3), .X(LRU2), .Y_num(3'b011), .X_num(3'b010), .MAX(\max2_归并比较_2_max ),
    .Max_num(\max2_归并比较_2_max_num ));
  \Max2_归并比较  \max2_归并比较_3  (
    .Y(LRU5), .X(LRU4), .Y_num(3'b101), .X_num(3'b100), .MAX(\max2_归并比较_3_max ),
    .Max_num(\max2_归并比较_3_max_num ));
  \Max2_归并比较  \max2_归并比较_4  (
    .Y(LRU7), .X(LRU6), .Y_num(3'b111), .X_num(3'b110), .MAX(\max2_归并比较_4_max ),
    .Max_num(\max2_归并比较_4_max_num ));
  \Max2_归并比较  \max2_归并比较_5  (
    .Y(\max2_归并比较_2_max ), .X(\max2_归并比较_1_max ), .Y_num(\max2_归并比较_2_max_num ),
    .X_num(\max2_归并比较_1_max_num ), .MAX(\max2_归并比较_5_max ), .Max_num(\max2_归并比较_5_max_num ));
  \Max2_归并比较  \max2_归并比较_6  (
    .Y(\max2_归并比较_4_max ), .X(\max2_归并比较_3_max ), .Y_num(\max2_归并比较_4_max_num ),
    .X_num(\max2_归并比较_3_max_num ), .MAX(\max2_归并比较_6_max ), .Max_num(\max2_归并比较_6_max_num ));
  and and_1 (W0, V0, comparator_1_eq);
  Comparator #(.width(32), .mode("twosComplement")) comparator_1 (
    .a(Tag0), .b(EX_PC), .eq(comparator_1_eq));  // open: gt, lt
  and and_2 (W1, V1, comparator_2_eq);
  Comparator #(.width(32), .mode("twosComplement")) comparator_2 (
    .a(Tag1), .b(EX_PC), .eq(comparator_2_eq));  // open: gt, lt
  and and_3 (W2, V2, comparator_3_eq);
  Comparator #(.width(32), .mode("twosComplement")) comparator_3 (
    .a(Tag2), .b(EX_PC), .eq(comparator_3_eq));  // open: gt, lt
  and and_4 (W3, V3, comparator_4_eq);
  Comparator #(.width(32), .mode("twosComplement")) comparator_4 (
    .a(Tag3), .b(EX_PC), .eq(comparator_4_eq));  // open: gt, lt
  and and_5 (W4, V4, comparator_5_eq);
  Comparator #(.width(32), .mode("twosComplement")) comparator_5 (
    .a(Tag4), .b(EX_PC), .eq(comparator_5_eq));  // open: gt, lt
  and and_6 (W5, V5, comparator_6_eq);
  Comparator #(.width(32), .mode("twosComplement")) comparator_6 (
    .a(Tag5), .b(EX_PC), .eq(comparator_6_eq));  // open: gt, lt
  and and_7 (W6, V6, comparator_7_eq);
  Comparator #(.width(32), .mode("twosComplement")) comparator_7 (
    .a(Tag6), .b(EX_PC), .eq(comparator_7_eq));  // open: gt, lt
  and and_8 (W7, V7, comparator_8_eq);
  Comparator #(.width(32), .mode("twosComplement")) comparator_8 (
    .a(Tag7), .b(EX_PC), .eq(comparator_8_eq));  // open: gt, lt
  \Max2_归并比较  \max2_归并比较_7  (
    .Y(\max2_归并比较_6_max ), .X(\max2_归并比较_5_max ), .Y_num(\max2_归并比较_6_max_num ),
    .X_num(\max2_归并比较_5_max_num ), .Max_num(\max2_归并比较_7_max_num ));  // open: MAX
  and and_9 (and_9_out, priority_encoder_1_gs, Shoot);
  Priority_Encoder #(.select(3), .disabled("Z")) priority_encoder_1 (
    .in0(W0), .in1(W1), .in2(W2), .in3(W3), .in4(W4), .in5(W5), .in6(W6), .in7(W7),
    .out(priority_encoder_1_out), .gs(priority_encoder_1_gs));  // open: en_out, en_in
  Decoder #(.select(3), .tristate("false"), .disabled("Z"), .enable("false")) decoder_1 (
    .out0(decoder_1_out0), .out1(decoder_1_out1), .out2(decoder_1_out2), .out3(decoder_1_out3),
    .out4(decoder_1_out4), .out5(decoder_1_out5), .out6(decoder_1_out6), .out7(decoder_1_out7),
    .sel(multiplexer_1_out));
  Multiplexer #(.select(1), .width(3), .disabled("Z"), .enable("false")) multiplexer_1 (
    .in0(\max2_归并比较_7_max_num ), .in1(priority_encoder_1_out), .out(multiplexer_1_out), .sel(and_9_out));
  or or_1 (Shoot, W0, W1, W2, W3, W4, W5, W6, W7);
  and and_10 (Write0, BlkDataReady, decoder_1_out0);
  and and_11 (Write1, BlkDataReady, decoder_1_out1);
  and and_12 (Write2, BlkDataReady, decoder_1_out2);
  and and_13 (Write5, decoder_1_out5, BlkDataReady);
  and and_14 (Write6, decoder_1_out6, BlkDataReady);
  and and_15 (Write7, decoder_1_out7, BlkDataReady);
  and and_16 (Write3, BlkDataReady, decoder_1_out3);
  and and_17 (Write4, decoder_1_out4, BlkDataReady);
  and and_18 (S0, V0, comparator_9_eq);
  Comparator #(.width(32), .mode("twosComplement")) comparator_9 (
    .a(Tag0), .b(IF_PC), .eq(comparator_9_eq));  // open: gt, lt
  and and_19 (S1, V1, comparator_10_eq);
  Comparator #(.width(32), .mode("twosComplement")) comparator_10 (
    .a(Tag1), .b(IF_PC), .eq(comparator_10_eq));  // open: gt, lt
  and and_20 (S2, V2, comparator_11_eq);
  Comparator #(.width(32), .mode("twosComplement")) comparator_11 (
    .a(Tag2), .b(IF_PC), .eq(comparator_11_eq));  // open: gt, lt
  and and_21 (S3, V3, comparator_12_eq);
  Comparator #(.width(32), .mode("twosComplement")) comparator_12 (
    .a(Tag3), .b(IF_PC), .eq(comparator_12_eq));  // open: gt, lt
  and and_22 (S4, V4, comparator_13_eq);
  Comparator #(.width(32), .mode("twosComplement")) comparator_13 (
    .a(Tag4), .b(IF_PC), .eq(comparator_13_eq));  // open: gt, lt
  and and_23 (S5, V5, comparator_14_eq);
  Comparator #(.width(32), .mode("twosComplement")) comparator_14 (
    .a(Tag5), .b(IF_PC), .eq(comparator_14_eq));  // open: gt, lt
  and and_24 (S6, V6, comparator_15_eq);
  Comparator #(.width(32), .mode("twosComplement")) comparator_15 (
    .a(Tag6), .b(IF_PC), .eq(comparator_15_eq));  // open: gt, lt
  and and_25 (S7, V7, comparator_16_eq);
  Comparator #(.width(32), .mode("twosComplement")) comparator_16 (
    .a(Tag7), .b(IF_PC), .eq(comparator_16_eq));  // open: gt, lt
  or or_2 (Have, S0, S1, S2, S3, S4, S5, S6, S7);
  Priority_Encoder #(.select(3), .disabled("Z")) priority_encoder_2 (
    .in0(S0), .in1(S1), .in2(S2), .in3(S3), .in4(S4), .in5(S5), .in6(S6), .in7(S7),
    .out(priority_encoder_2_out), .gs(priority_encoder_2_gs));  // open: en_out, en_in
  Multiplexer #(.select(1), .width(3), .disabled("Z"), .enable("false")) multiplexer_2 (
    .in0(3'b000), .in1(priority_encoder_2_out), .out(multiplexer_2_out), .sel(priority_encoder_2_gs));
  Multiplexer #(.select(3), .width(32), .disabled("Z"), .enable("false")) multiplexer_3 (
    .in0(\分支地址输出0 ), .in1(\分支地址输出1 ), .in2(\分支地址输出2 ), .in3(\分支地址输出3 ), .in4(\分支地址输出4 ), .in5(\分支地址输出5 ),
    .in6(\分支地址输出6 ), .in7(\分支地址输出7 ), .out(\分支目标地址_2 ), .sel(multiplexer_2_out));
  Multiplexer #(.select(3), .width(2), .disabled("Z"), .enable("false")) multiplexer_4 (
    .in0(\双预测位输出0 ), .in1(\双预测位输出1 ), .in2(\双预测位输出2 ), .in3(\双预测位输出3 ), .in4(\双预测位输出4 ), .in5(\双预测位输出5 ),
    .in6(\双预测位输出6 ), .in7(\双预测位输出7 ), .out(\双预测位输出 ), .sel(multiplexer_2_out));

  // Other names for the same wires on the sheet: Blk[31:0] = \分支目标地址 ; BlkReady = BlkDataReady;
  //   分支地址输出[31:0] = \分支目标地址_2 ; 分支指令地址Search[31:0] = IF_PC; 分支指令地址Write[31:0] = EX_PC

  // Notes on the sheet:
  //   输入引脚区
  //   (用于区分查找和写入)
  //   输出引脚区
  //   写阶段/命中阶段
  //   读阶段
  //   查
endmodule

module \双位预测状态机  (
  input  [1:0] \初始预测位 ,
  input  \实际跳转情况 ,
  output [1:0] \新的状态位 
);

  wire [1:0] multiplexer_1_out, multiplexer_2_out;

  Multiplexer #(.select(2), .width(2), .disabled("Z"), .enable("false")) multiplexer_1 (
    .in0(2'b00), .in1(2'b00), .in2(2'b11), .in3(2'b00), .out(multiplexer_1_out), .sel(\初始预测位 ));
  Multiplexer #(.select(2), .width(2), .disabled("Z"), .enable("false")) multiplexer_2 (
    .in0(2'b01), .in1(2'b10), .in2(2'b10), .in3(2'b10), .out(multiplexer_2_out), .sel(\初始预测位 ));
  Multiplexer #(.select(1), .width(2), .disabled("Z"), .enable("false")) multiplexer_3 (
    .in0(multiplexer_1_out), .in1(multiplexer_2_out), .out(\新的状态位 ), .sel(\实际跳转情况 ));
endmodule

module \Max2_归并比较  (
  input  [15:0] Y,
  input  [15:0] X,
  input  [2:0] Y_num,
  input  [2:0] X_num,
  output [15:0] MAX,
  output [2:0] Max_num
);

  wire comparator_1_eq, comparator_1_gt, or_1_out;

  Multiplexer #(.select(1), .width(16), .disabled("Z"), .enable("false")) multiplexer_1 (
    .in0(Y), .in1(X), .out(MAX), .sel(or_1_out));
  Comparator #(.width(16), .mode("unsigned")) comparator_1 (
    .a(X), .b(Y), .gt(comparator_1_gt), .eq(comparator_1_eq));  // open: lt
  or or_1 (or_1_out, comparator_1_gt, comparator_1_eq);
  Multiplexer #(.select(1), .width(3), .disabled("Z"), .enable("false")) multiplexer_2 (
    .in0(Y_num), .in1(X_num), .out(Max_num), .sel(or_1_out));

  // Notes on the sheet:
  //   输出两个输入中的较大值，并输出较大值的3位编号
endmodule

module \测试  (
);

  wire CLK, comparator_1_eq, comparator_2_eq, comparator_3_eq, comparator_4_eq, comparator_5_eq, IRA, IRB,
       IRC, or_1_out, or_2_out;
  wire [15:0] \总周期数 ;

  Comparator #(.width(16), .mode("twosComplement")) comparator_1 (
    .a(16'h258), .b(\总周期数 ), .eq(comparator_1_eq));  // open: gt, lt
  Comparator #(.width(16), .mode("twosComplement")) comparator_2 (
    .a(\总周期数 ), .b(16'h1), .eq(comparator_2_eq));  // open: gt, lt
  Comparator #(.width(16), .mode("twosComplement")) comparator_3 (
    .a(\总周期数 ), .b(16'h4), .eq(comparator_3_eq));  // open: gt, lt
  Comparator #(.width(16), .mode("twosComplement")) comparator_4 (
    .a(\总周期数 ), .b(16'h7), .eq(comparator_4_eq));  // open: gt, lt
  or or_1 (or_1_out, comparator_4_eq, comparator_5_eq);
  Comparator #(.width(16), .mode("twosComplement")) comparator_5 (
    .a(\总周期数 ), .b(16'h241), .eq(comparator_5_eq));  // open: gt, lt
  or or_2 (or_2_out, comparator_1_eq, comparator_2_eq);
  Pull_Resistor #(.pull(0)) pull_resistor_1 (.node(IRA));
  assign IRA = or_2_out ? ~CLK : 1'bz;  // Controlled_Inverter controlled_inverter_1
  Pull_Resistor #(.pull(0)) pull_resistor_2 (.node(IRB));
  assign IRB = comparator_3_eq ? ~CLK : 1'bz;  // Controlled_Inverter controlled_inverter_2
  Pull_Resistor #(.pull(0)) pull_resistor_3 (.node(IRC));
  assign IRC = or_1_out ? ~CLK : 1'bz;  // Controlled_Inverter controlled_inverter_3

  // Notes on the sheet:
  //   多级中断信号产生
endmodule
